// Logisim project 组合逻辑电路设计 - 学生.circ as structural Verilog
module \多路分配器  (
  input  D,
  input  A1,
  input  A0,
  output f0,
  output f1,
  output f2,
  output f3
);

  wire and_1_out, and_2_out, and_3_out, and_4_out, not_1_out, not_2_out;

  not not_1 (not_1_out, A1);
  not not_2 (not_2_out, A0);
  and and_1 (and_1_out, not_1_out, not_2_out);
  and and_2 (and_2_out, not_1_out, A0);
  and and_3 (and_3_out, A1, not_2_out);
  and and_4 (and_4_out, A0, A1);
  and and_5 (f0, D, and_1_out);
  and and_6 (f1, D, and_2_out);
  and and_7 (f2, D, and_3_out);
  and and_8 (f3, D, and_4_out);
endmodule

module \多路选择器  (
  input  D0,
  input  D1,
  input  D2,
  input  D3,
  input  A1,
  input  A0,
  output Y
);

  wire and_1_out, and_2_out, and_3_out, and_4_out, and_5_out, and_6_out, and_7_out, and_8_out, not_1_out,
       not_2_out;

  not not_1 (not_1_out, A1);
  not not_2 (not_2_out, A0);
  and and_1 (and_1_out, not_1_out, not_2_out);
  and and_2 (and_2_out, not_1_out, A0);
  and and_3 (and_3_out, A1, not_2_out);
  and and_4 (and_4_out, A0, A1);
  and and_5 (and_5_out, D0, and_1_out);
  and and_6 (and_6_out, D1, and_2_out);
  and and_7 (and_7_out, D2, and_3_out);
  and and_8 (and_8_out, D3, and_4_out);
  or or_1 (Y, and_5_out, and_6_out, and_7_out, and_8_out);
endmodule

module \七段显示译码器  (
  input  A3,
  input  A2,
  input  A1,
  input  A0,
  output a,
  output b,
  output c,
  output d,
  output e,
  output f,
  output g
);

  wire and_1_out, and_2_out, and_3_out, and_4_out, and_5_out, and_6_out, and_7_out, and_8_out, and_9_out,
       and_10_out, and_11_out, and_12_out, and_13_out, and_14_out, and_15_out, and_16_out, and_17_out,
       not_1_out, not_2_out, not_3_out, not_4_out, not_5_out, not_6_out, not_7_out, not_8_out, not_9_out,
       not_10_out, not_11_out, not_12_out, not_13_out, not_14_out, not_15_out, not_16_out, not_17_out,
       not_18_out, not_19_out, not_20_out, not_21_out, not_22_out;

  not not_1 (not_1_out, A2);
  and and_1 (and_1_out, not_1_out, not_2_out);
  not not_2 (not_2_out, A0);
  not not_3 (not_3_out, A2);
  and and_2 (and_2_out, not_3_out, A1);
  and and_3 (and_3_out, A2, A0);
  not not_4 (not_4_out, A2);
  not not_5 (not_5_out, A1);
  and and_4 (and_4_out, not_5_out, not_6_out);
  not not_6 (not_6_out, A0);
  and and_5 (and_5_out, A1, A0);
  not not_7 (not_7_out, A1);
  or or_1 (c, not_7_out, A0, A2);
  not not_8 (not_8_out, A2);
  and and_6 (and_6_out, not_8_out, not_9_out);
  not not_9 (not_9_out, A0);
  not not_10 (not_10_out, A2);
  and and_7 (and_7_out, not_10_out, A1);
  and and_8 (and_8_out, A1, not_11_out);
  not not_11 (not_11_out, A0);
  and and_9 (and_9_out, A2, not_12_out, A0);
  not not_12 (not_12_out, A1);
  not not_13 (not_13_out, A2);
  and and_10 (and_10_out, not_13_out, not_14_out);
  not not_14 (not_14_out, A0);
  and and_11 (and_11_out, A1, not_15_out);
  not not_15 (not_15_out, A0);
  not not_16 (not_16_out, A1);
  and and_12 (and_12_out, not_16_out, not_17_out);
  not not_17 (not_17_out, A0);
  and and_13 (and_13_out, A2, not_18_out);
  not not_18 (not_18_out, A1);
  and and_14 (and_14_out, A2, not_19_out);
  not not_19 (not_19_out, A0);
  not not_20 (not_20_out, A2);
  and and_15 (and_15_out, not_20_out, A1);
  and and_16 (and_16_out, A2, not_21_out);
  not not_21 (not_21_out, A1);
  and and_17 (and_17_out, A2, not_22_out);
  not not_22 (not_22_out, A0);
  or or_2 (a, and_1_out, and_2_out, and_3_out, A3);
  or or_3 (b, not_4_out, and_4_out, and_5_out);
  or or_4 (d, and_6_out, and_7_out, and_8_out, and_9_out);
  or or_5 (e, and_10_out, and_11_out);
  or or_6 (f, and_12_out, and_13_out, and_14_out, A3);
  or or_7 (g, and_15_out, and_16_out, and_17_out, A3);
endmodule

module \七段显示译码器测试  (
  input  in_1,
  input  in_2,
  input  in_3,
  input  in_4
);

  wire \七段显示译码器_1_a , \七段显示译码器_1_b , \七段显示译码器_1_c , \七段显示译码器_1_d , \七段显示译码器_1_e , \七段显示译码器_1_f ,
       \七段显示译码器_1_g ;

  \七段显示译码器  \u_七段显示译码器_1  (
    .A3(in_1), .A2(in_2), .A1(in_3), .A0(in_4), .a(\七段显示译码器_1_a ), .b(\七段显示译码器_1_b ), .c(\七段显示译码器_1_c ),
    .d(\七段显示译码器_1_d ), .e(\七段显示译码器_1_e ), .f(\七段显示译码器_1_f ), .g(\七段显示译码器_1_g ));
  _7_Segment_Display #(.active("true")) u_7_segment_display_1 (
    .g(\七段显示译码器_1_g ), .f(\七段显示译码器_1_f ), .a(\七段显示译码器_1_a ), .b(\七段显示译码器_1_b ), .e(\七段显示译码器_1_e ),
    .d(\七段显示译码器_1_d ), .c(\七段显示译码器_1_c ));  // open: dp
endmodule

module \险象  (
  input  B,
  input  C,
  output F
);

  wire A_out, and_1_out, and_2_out, not_1_out;

  Clock #(.highDuration(1), .lowDuration(1)) A (.out(A_out));
  and and_1 (and_1_out, A_out, B);
  not not_1 (not_1_out, A_out);
  and and_2 (and_2_out, not_1_out, C);
  or or_1 (F, and_1_out, and_2_out);
  Counter #(.width(1), .max('h1), .ongoal("wrap"), .trigger("rising"), .behavior("new")) counter_1 (.clk(F));  // open: load, D, count, Q, carry, clr, preset, down
endmodule

module \少数服从多数  (
  input  A,
  input  B,
  input  C,
  output F
);

  wire and_1_out, and_2_out, and_3_out;

  and and_1 (and_1_out, A, B);
  and and_2 (and_2_out, B, C);
  and and_3 (and_3_out, C, A);
  or or_1 (F, and_1_out, and_2_out, and_3_out);
endmodule

module \少数服从多数与非门  (
  input  A,
  input  B,
  input  C,
  output F
);

  wire nand_1_out, nand_2_out, nand_3_out;

  nand nand_1 (nand_1_out, A, B);
  nand nand_2 (nand_2_out, B, C);
  nand nand_3 (nand_3_out, A, C);
  nand nand_4 (F, nand_1_out, nand_2_out, nand_3_out);
endmodule

module \不一致电路  (
  input  A,
  input  B,
  input  C,
  output F
);

  wire and_1_out, and_2_out, and_3_out, not_1_out, not_2_out, not_3_out;

  not not_1 (not_1_out, A);
  not not_2 (not_2_out, C);
  not not_3 (not_3_out, B);
  and and_1 (and_1_out, not_1_out, C);
  and and_2 (and_2_out, B, not_2_out);
  and and_3 (and_3_out, A, not_3_out);
  or or_1 (F, and_1_out, and_2_out, and_3_out);
endmodule

module \不一致电路真值表自动生成  (
  input  A,
  input  B,
  input  C,
  output F
);

  wire and_1_out, and_2_out, and_3_out, and_4_out, not_1_out, not_2_out, not_3_out, not_4_out;

  not not_1 (not_1_out, A);
  not not_2 (not_2_out, A);
  not not_3 (not_3_out, B);
  not not_4 (not_4_out, C);
  and and_1 (and_1_out, not_1_out, C);
  and and_2 (and_2_out, not_2_out, B);
  and and_3 (and_3_out, A, not_3_out);
  and and_4 (and_4_out, A, not_4_out);
  or or_1 (F, and_1_out, and_2_out, and_3_out, and_4_out);
endmodule

module \一票否决投票  (
  input  A,
  input  B,
  input  C,
  output F
);

  and and_1 (F, A, B, C);
endmodule

module \集中制投票  (
  input  A,
  input  B,
  input  C,
  output F
);

  buf buffer_1 (F, A);
endmodule

module \无关最小项投票器  (
  input  A,
  input  B,
  input  C,
  input  D,
  output F
);

  wire and_1_out, and_2_out, and_3_out, and_4_out, and_5_out;

  and and_1 (and_1_out, A, C);
  and and_2 (and_2_out, A, D);
  and and_3 (and_3_out, C, D);
  and and_4 (and_4_out, B, D);
  and and_5 (and_5_out, B, C);
  or or_1 (F, and_1_out, and_2_out, and_3_out, and_4_out, and_5_out);
endmodule

module \无效投票  (
  input  A,
  input  B,
  input  C,
  input  D,
  output F
);

  wire and_1_out, and_2_out, and_3_out;

  and and_1 (and_1_out, B, C);
  and and_2 (and_2_out, B, D);
  and and_3 (and_3_out, C, D);
  or or_1 (F, and_1_out, and_2_out, and_3_out);
endmodule

module \综合投票器  (
  input  A,
  input  B,
  input  C,
  input  X,
  input  Y,
  output W,
  output X_2,
  output Y_2,
  output Z
);

  wire \一票否决投票_1_f , \不一致电路_1_f , \多路选择器_1_y , \少数服从多数_1_f , \集中制投票_1_f ;

  \少数服从多数  \u_少数服从多数_1  (.A(A), .B(B), .C(C), .F(\少数服从多数_1_f ));
  \一票否决投票  \u_一票否决投票_1  (.A(A), .B(B), .C(C), .F(\一票否决投票_1_f ));
  \集中制投票  \u_集中制投票_1  (.A(A), .B(B), .C(C), .F(\集中制投票_1_f ));
  \不一致电路  \u_不一致电路_1  (.A(A), .B(B), .C(C), .F(\不一致电路_1_f ));
  \多路选择器  \u_多路选择器_1  (
    .A1(X), .A0(Y), .Y(\多路选择器_1_y ), .D0(\少数服从多数_1_f ), .D1(\一票否决投票_1_f ), .D2(\集中制投票_1_f ), .D3(\不一致电路_1_f ));
  \多路分配器  \u_多路分配器_1  (.D(\多路选择器_1_y ), .A1(X), .A0(Y), .f0(W), .f1(X_2), .f2(Y_2), .f3(Z));
endmodule

module \全加器  (
  input  Ci_1,
  input  B,
  input  A,
  output Si,
  output Ci
);

  wire and_1_out, and_2_out, xor_1_out;

  xor xor_1 (xor_1_out, Ci_1, B);
  and and_1 (and_1_out, xor_1_out, A);
  and and_2 (and_2_out, B, Ci_1);
  xor xor_2 (Si, xor_1_out, A);
  or or_1 (Ci, and_1_out, and_2_out);
endmodule

module \全减器  (
  input  G_1,
  input  B,
  input  A,
  output Di,
  output Gi
);

  wire and_1_out, and_2_out, not_1_out, xor_1_out;

  xor xor_1 (xor_1_out, G_1, B);
  and and_1 (and_1_out, xor_1_out, not_1_out);
  not not_1 (not_1_out, A);
  and and_2 (and_2_out, B, G_1);
  xor xor_2 (Di, xor_1_out, A);
  or or_1 (Gi, and_1_out, and_2_out);
endmodule

module \全加_全减器  (
  input  Ci_1_Gi_1,
  input  B,
  input  A,
  input  M,
  output Si_Di,
  output Ci_Gi
);

  wire \全减器_1_gi , \全加器_1_ci ;

  \全加器  \u_全加器_1  (.Ci_1(Ci_1_Gi_1), .B(B), .A(A), .Si(Si_Di), .Ci(\全加器_1_ci ));
  \全减器  \u_全减器_1  (.G_1(Ci_1_Gi_1), .B(B), .A(A), .Gi(\全减器_1_gi ));  // open: Di
  \_2选1  \u_2选1_1  (.A(\全加器_1_ci ), .M(M), .B(\全减器_1_gi ), .F(Ci_Gi));
endmodule

module \_2选1_险象  (
  input  A,
  input  M,
  input  B,
  output F
);

  wire and_1_out, and_2_out, not_1_out;

  and and_1 (and_1_out, A, not_1_out);
  not not_1 (not_1_out, M);
  and and_2 (and_2_out, M, B);
  or or_1 (F, and_1_out, and_2_out);
endmodule

module \_2选1  (
  input  A,
  input  M,
  input  B,
  output F
);

  wire and_1_out, and_2_out, and_3_out, not_1_out;

  and and_1 (and_1_out, A, not_1_out);
  not not_1 (not_1_out, M);
  and and_2 (and_2_out, M, B);
  and and_3 (and_3_out, A, B);
  or or_1 (F, and_1_out, and_2_out, and_3_out);
endmodule

module \_16进制转10进制  (
  input  A,
  input  B,
  input  C,
  input  D,
  input  E,
  output F,
  output W,
  output X,
  output Y,
  output Z
);
endmodule
