// Logisim project 习题6.6.circ as structural Verilog: 1 circuit, main circuit 习题6.6
module \习题6_6  (
  input  x1,
  input  x2,
  output z
);

  wire and_1_out, and_2_out, or_1_out, t_ff_1_q, t_ff_1_qn;

  and and_1 (and_1_out, t_ff_1_q, x2);
  and and_2 (and_2_out, x1, t_ff_1_qn);
  or or_1 (or_1_out, and_1_out, and_2_out);
  T_Flip_Flop #(.trigger("rising"), .Pre_Clr_Positions("ABOVE_BELOW"), .NegatePresetClear("false"), .enable("false"), .NewFFLayout("true")) t_ff_1 (
    .clk(or_1_out), .T(1'b1), .Q(t_ff_1_q), .Qn(t_ff_1_qn));  // open: preset, reset
  and and_3 (z, x2, t_ff_1_q);
endmodule
