// Logisim project 实验3-ACM1901-U201915035-邹雅.circ as structural Verilog: 6 circuits, main circuit 四位乘法器
module \四位乘法器  (
  input  [3:0] b,
  input  [3:0] a,
  output [7:0] out_3
);

  wire [7:0] adder_1_out, adder_2_out, adder_3_out, adder_4_out, bit_extender_1_out, multiplexer_1_out,
       multiplexer_2_out, multiplexer_3_out, shifter_1_out, shifter_2_out, shifter_3_out, shifter_4_out;

  assign bit_extender_1_out = {{4{1'b0}}, b};  // Bit_Extender bit_extender_1
  Adder #(.width(8)) adder_1 (.a({8{1'b0}}), .b(bit_extender_1_out), .out(adder_1_out));  // open: cin, cout
  Shifter #(.width(8), .shift("ll")) shifter_1 (.in(bit_extender_1_out), .\dist (3'b001), .out(shifter_1_out));
  Multiplexer #(.select(1), .width(8), .disabled("Z"), .enable("false")) multiplexer_1 (
    .in0({8{1'b0}}), .in1(adder_1_out), .out(multiplexer_1_out), .sel(a[0]));
  Shifter #(.width(8), .shift("ll")) shifter_2 (.in(shifter_1_out), .\dist (3'b001), .out(shifter_2_out));
  Adder #(.width(8)) adder_2 (.a(multiplexer_1_out), .b(shifter_1_out), .out(adder_2_out));  // open: cin, cout
  Multiplexer #(.select(1), .width(8), .disabled("Z"), .enable("false")) multiplexer_2 (
    .in0(multiplexer_1_out), .in1(adder_2_out), .out(multiplexer_2_out), .sel(a[1]));
  Shifter #(.width(8), .shift("ll")) shifter_3 (.in(shifter_2_out), .\dist (3'b001), .out(shifter_3_out));
  Adder #(.width(8)) adder_3 (.a(multiplexer_2_out), .b(shifter_2_out), .out(adder_3_out));  // open: cin, cout
  Multiplexer #(.select(1), .width(8), .disabled("Z"), .enable("false")) multiplexer_3 (
    .in0(multiplexer_2_out), .in1(adder_3_out), .out(multiplexer_3_out), .sel(a[2]));
  Shifter #(.width(8), .shift("ll")) shifter_4 (.in(shifter_3_out), .\dist (3'b001), .out(shifter_4_out));
  Adder #(.width(8)) adder_4 (.a(multiplexer_3_out), .b(shifter_3_out), .out(adder_4_out));  // open: cin, cout
  Multiplexer #(.select(1), .width(8), .disabled("Z"), .enable("false")) multiplexer_4 (
    .in0(multiplexer_3_out), .in1(adder_4_out), .out(out_3), .sel(a[3]));
endmodule

module \四位乘法器测试电路  (
  input  [3:0] in_1,
  input  [3:0] in_2,
  output [7:0] out_3
);

  \四位乘法器  \u_四位乘法器_1  (.b(in_2), .out_3(out_3), .a(in_1));
endmodule

module \_32X4乘法器  (
  input  [31:0] b,
  input  [3:0] a,
  output [31:0] hl,
  output [31:0] ph
);

  wire adder_9_cout;
  wire [31:0] adder_1_out, adder_2_out, adder_3_out, adder_4_out, adder_5_out, adder_6_out, adder_7_out,
       adder_8_out, bit_extender_1_out, bit_extender_2_out, bit_extender_3_out, bit_extender_4_out,
       multiplexer_1_out, multiplexer_2_out, multiplexer_3_out, multiplexer_4_out, multiplexer_5_out,
       multiplexer_6_out, multiplexer_7_out, multiplexer_8_out, shifter_1_out, shifter_2_out, shifter_3_out,
       shifter_4_out, shifter_5_out, shifter_6_out, shifter_7_out;

  assign bit_extender_1_out = {{16{1'b0}}, b[15:0]};  // Bit_Extender bit_extender_1
  assign bit_extender_2_out = {{16{1'b0}}, b[31:16]};  // Bit_Extender bit_extender_2
  Adder #(.width(32)) adder_1 (.a({32{1'b0}}), .b(bit_extender_1_out), .out(adder_1_out));  // open: cin, cout
  Shifter #(.width(32), .shift("ll")) shifter_1 (.in(bit_extender_1_out), .\dist (5'b00001), .out(shifter_1_out));
  Adder #(.width(32)) adder_2 (.a({32{1'b0}}), .b(bit_extender_2_out), .out(adder_2_out));  // open: cin, cout
  Shifter #(.width(32), .shift("ll")) shifter_2 (.in(bit_extender_2_out), .\dist (5'b00001), .out(shifter_2_out));
  Multiplexer #(.select(1), .width(32), .disabled("Z"), .enable("false")) multiplexer_1 (
    .in0({32{1'b0}}), .in1(adder_1_out), .out(multiplexer_1_out), .sel(a[0]));
  Multiplexer #(.select(1), .width(32), .disabled("Z"), .enable("false")) multiplexer_2 (
    .in0({32{1'b0}}), .in1(adder_2_out), .out(multiplexer_2_out), .sel(a[0]));
  Shifter #(.width(32), .shift("ll")) shifter_3 (.in(shifter_1_out), .\dist (5'b00001), .out(shifter_3_out));
  Shifter #(.width(32), .shift("ll")) shifter_4 (.in(shifter_2_out), .\dist (5'b00001), .out(shifter_4_out));
  Adder #(.width(32)) adder_3 (.a(multiplexer_1_out), .b(shifter_1_out), .out(adder_3_out));  // open: cin, cout
  Adder #(.width(32)) adder_4 (.a(multiplexer_2_out), .b(shifter_2_out), .out(adder_4_out));  // open: cin, cout
  Multiplexer #(.select(1), .width(32), .disabled("Z"), .enable("false")) multiplexer_3 (
    .in0(multiplexer_1_out), .in1(adder_3_out), .out(multiplexer_3_out), .sel(a[1]));
  Shifter #(.width(32), .shift("ll")) shifter_5 (.in(shifter_3_out), .\dist (5'b00001), .out(shifter_5_out));
  Multiplexer #(.select(1), .width(32), .disabled("Z"), .enable("false")) multiplexer_4 (
    .in0(multiplexer_2_out), .in1(adder_4_out), .out(multiplexer_4_out), .sel(a[1]));
  Adder #(.width(32)) adder_5 (.a(multiplexer_3_out), .b(shifter_3_out), .out(adder_5_out));  // open: cin, cout
  Shifter #(.width(32), .shift("ll")) shifter_6 (.in(shifter_4_out), .\dist (5'b00001), .out(shifter_6_out));
  Multiplexer #(.select(1), .width(32), .disabled("Z"), .enable("false")) multiplexer_5 (
    .in0(multiplexer_3_out), .in1(adder_5_out), .out(multiplexer_5_out), .sel(a[2]));
  Adder #(.width(32)) adder_6 (.a(multiplexer_4_out), .b(shifter_4_out), .out(adder_6_out));  // open: cin, cout
  Multiplexer #(.select(1), .width(32), .disabled("Z"), .enable("false")) multiplexer_6 (
    .in0(multiplexer_4_out), .in1(adder_6_out), .out(multiplexer_6_out), .sel(a[2]));
  Adder #(.width(32)) adder_7 (.a(multiplexer_5_out), .b(shifter_5_out), .out(adder_7_out));  // open: cin, cout
  Adder #(.width(32)) adder_8 (.a(multiplexer_6_out), .b(shifter_6_out), .out(adder_8_out));  // open: cin, cout
  Multiplexer #(.select(1), .width(32), .disabled("Z"), .enable("false")) multiplexer_7 (
    .in0(multiplexer_5_out), .in1(adder_7_out), .out(multiplexer_7_out), .sel(a[3]));
  Multiplexer #(.select(1), .width(32), .disabled("Z"), .enable("false")) multiplexer_8 (
    .in0(multiplexer_6_out), .in1(adder_8_out), .out(multiplexer_8_out), .sel(a[3]));
  assign bit_extender_3_out = {{16{1'b0}}, multiplexer_8_out[15:0]};  // Bit_Extender bit_extender_3
  Shifter #(.width(32), .shift("ll")) shifter_7 (.in(bit_extender_3_out), .\dist (5'b10000), .out(shifter_7_out));
  assign bit_extender_4_out = {{16{1'b0}}, multiplexer_8_out[31:16]};  // Bit_Extender bit_extender_4
  Adder #(.width(32)) adder_9 (.a(multiplexer_7_out), .b(shifter_7_out), .out(hl), .cout(adder_9_cout));  // open: cin
  Adder #(.width(32)) adder_10 (.a(bit_extender_4_out), .b({32{1'b0}}), .out(ph), .cin(adder_9_cout));  // open: cout
endmodule

module \_32X4乘法器测试电路  (
  input  [3:0] in_1,
  input  [31:0] in_2,
  output [31:0] out_3,
  output [31:0] out_4
);

  \_32X4乘法器  \u_32x4乘法器_1  (.b(in_2), .ph(out_4), .a(in_1), .hl(out_3));
endmodule

module \_32X32乘法器  (
  input  [31:0] a,
  input  [31:0] b,
  output [31:0] pl,
  output [31:0] ph
);

  wire adder_1_cout, adder_3_cout, adder_5_cout, adder_7_cout, adder_9_cout, adder_11_cout, adder_13_cout;
  wire [3:0] \n32x4乘法器_2_ph , \n32x4乘法器_2_ph_3 , \n32x4乘法器_2_ph_4 , \n32x4乘法器_2_ph_5 , \n32x4乘法器_3_ph ,
       \n32x4乘法器_3_ph_2 , \n32x4乘法器_3_ph_4 , \n32x4乘法器_4_ph , \n32x4乘法器_4_ph_2 , \n32x4乘法器_4_ph_3 ,
       \n32x4乘法器_5_ph_2 , \n32x4乘法器_5_ph_3 , \n32x4乘法器_5_ph_4 , \n32x4乘法器_6_ph_2 , \n32x4乘法器_6_ph_3 ,
       \n32x4乘法器_6_ph_4 , \n32x4乘法器_7_ph_2 , \n32x4乘法器_7_ph_3 , \n32x4乘法器_7_ph_4 , \n32x4乘法器_8_ph_2 ,
       \n32x4乘法器_8_ph_3 , \n32x4乘法器_8_ph_4 ;
  wire [15:0] \n32x4乘法器_2_ph_2 ;
  wire [19:0] \n32x4乘法器_3_ph_3 , \n32x4乘法器_4_ph_4 , \n32x4乘法器_5_ph , \n32x4乘法器_6_ph , \n32x4乘法器_7_ph ,
       \n32x4乘法器_8_ph ;
  wire [31:0] adder_1_out, adder_2_out, adder_3_out, adder_4_out, adder_5_out, adder_6_out, adder_7_out,
       adder_8_out, adder_9_out, adder_10_out, adder_11_out, adder_12_out, \n32x4乘法器_1_hl , \n32x4乘法器_1_ph ,
       \n32x4乘法器_2_hl , \n32x4乘法器_4_hl , \n32x4乘法器_5_hl , \n32x4乘法器_6_hl , \n32x4乘法器_7_hl , \n32x4乘法器_8_hl ;
  wire [31:8] \n32x4乘法器_3_hl_2 ;
  wire [31:24] \n32x4乘法器_3_hl ;

  \_32X4乘法器  \u_32x4乘法器_1  (.b(b), .ph(\n32x4乘法器_1_ph ), .a(a[3:0]), .hl(\n32x4乘法器_1_hl ));
  \_32X4乘法器  \u_32x4乘法器_2  (
    .b(b),
    .ph({\n32x4乘法器_2_ph , \n32x4乘法器_2_ph_5 , \n32x4乘法器_2_ph_4 , \n32x4乘法器_2_ph_3 , \n32x4乘法器_2_ph_2 }),
    .a(a[7:4]), .hl(\n32x4乘法器_2_hl ));
  Adder #(.width(32)) adder_1 (
    .a({\n32x4乘法器_2_hl [27:0], 4'b0000}), .b(\n32x4乘法器_1_hl ), .out(adder_1_out), .cin(1'b0),
    .cout(adder_1_cout));
  Adder #(.width(32)) adder_2 (
    .a({\n32x4乘法器_2_ph_5 , \n32x4乘法器_2_ph_4 , \n32x4乘法器_2_ph_3 , \n32x4乘法器_2_ph_2 , \n32x4乘法器_2_hl [31:28]}),
    .b(\n32x4乘法器_1_ph ), .out(adder_2_out), .cin(adder_1_cout));  // open: cout
  \_32X4乘法器  \u_32x4乘法器_3  (
    .b(b), .ph({\n32x4乘法器_3_ph_2 , \n32x4乘法器_3_ph , \n32x4乘法器_3_ph_4 , \n32x4乘法器_3_ph_3 }), .a(a[11:8]),
    .hl({\n32x4乘法器_3_hl , \n32x4乘法器_3_hl_2 }));
  Adder #(.width(32)) adder_3 (
    .a(adder_1_out), .b({\n32x4乘法器_3_hl_2 , {8{1'b0}}}), .out(adder_3_out), .cin(1'b0), .cout(adder_3_cout));
  Adder #(.width(32)) adder_4 (
    .a({\n32x4乘法器_3_ph_4 , \n32x4乘法器_3_ph_3 , \n32x4乘法器_3_hl }), .b(adder_2_out), .out(adder_4_out),
    .cin(adder_3_cout));  // open: cout
  \_32X4乘法器  \u_32x4乘法器_4  (
    .b(b), .ph({\n32x4乘法器_4_ph_3 , \n32x4乘法器_4_ph_2 , \n32x4乘法器_4_ph , \n32x4乘法器_4_ph_4 }), .a(a[15:12]),
    .hl(\n32x4乘法器_4_hl ));
  Adder #(.width(32)) adder_5 (
    .a({\n32x4乘法器_4_hl [19:0], {12{1'b0}}}), .b(adder_3_out), .out(adder_5_out), .cin(1'b0),
    .cout(adder_5_cout));
  Adder #(.width(32)) adder_6 (
    .a(adder_4_out), .b({\n32x4乘法器_4_ph_4 , \n32x4乘法器_4_hl [31:20]}), .out(adder_6_out), .cin(adder_5_cout));  // open: cout
  \_32X4乘法器  \u_32x4乘法器_5  (
    .b(b), .ph({\n32x4乘法器_5_ph_4 , \n32x4乘法器_5_ph_3 , \n32x4乘法器_5_ph_2 , \n32x4乘法器_5_ph }), .a(a[19:16]),
    .hl(\n32x4乘法器_5_hl ));
  Adder #(.width(32)) adder_7 (
    .a({\n32x4乘法器_5_hl [15:0], {16{1'b0}}}), .b(adder_5_out), .out(adder_7_out), .cin(1'b0),
    .cout(adder_7_cout));
  Adder #(.width(32)) adder_8 (
    .a(adder_6_out), .b({\n32x4乘法器_5_ph [15:0], \n32x4乘法器_5_hl [31:16]}), .out(adder_8_out),
    .cin(adder_7_cout));  // open: cout
  \_32X4乘法器  \u_32x4乘法器_6  (
    .b(b), .ph({\n32x4乘法器_6_ph_4 , \n32x4乘法器_6_ph_3 , \n32x4乘法器_6_ph_2 , \n32x4乘法器_6_ph }), .a(a[23:20]),
    .hl(\n32x4乘法器_6_hl ));
  Adder #(.width(32)) adder_9 (
    .a({\n32x4乘法器_6_hl [11:0], {20{1'b0}}}), .b(adder_7_out), .out(adder_9_out), .cin(1'b0),
    .cout(adder_9_cout));
  Adder #(.width(32)) adder_10 (
    .a({\n32x4乘法器_6_ph [11:0], \n32x4乘法器_6_hl [31:12]}), .b(adder_8_out), .out(adder_10_out),
    .cin(adder_9_cout));  // open: cout
  \_32X4乘法器  \u_32x4乘法器_7  (
    .b(b), .ph({\n32x4乘法器_7_ph_4 , \n32x4乘法器_7_ph_3 , \n32x4乘法器_7_ph_2 , \n32x4乘法器_7_ph }), .a(a[27:24]),
    .hl(\n32x4乘法器_7_hl ));
  Adder #(.width(32)) adder_11 (
    .a({\n32x4乘法器_7_hl [7:0], {24{1'b0}}}), .b(adder_9_out), .out(adder_11_out), .cin(1'b0),
    .cout(adder_11_cout));
  Adder #(.width(32)) adder_12 (
    .a({\n32x4乘法器_7_ph [7:0], \n32x4乘法器_7_hl [31:8]}), .b(adder_10_out), .out(adder_12_out),
    .cin(adder_11_cout));  // open: cout
  \_32X4乘法器  \u_32x4乘法器_8  (
    .b(b), .ph({\n32x4乘法器_8_ph_4 , \n32x4乘法器_8_ph_3 , \n32x4乘法器_8_ph_2 , \n32x4乘法器_8_ph }), .a(a[31:28]),
    .hl(\n32x4乘法器_8_hl ));
  Adder #(.width(32)) adder_13 (
    .a(adder_11_out), .b({\n32x4乘法器_8_hl [3:0], {28{1'b0}}}), .out(pl), .cin(1'b0), .cout(adder_13_cout));
  Adder #(.width(32)) adder_14 (
    .a({\n32x4乘法器_8_ph [3:0], \n32x4乘法器_8_hl [31:4]}), .b(adder_12_out), .out(ph), .cin(adder_13_cout));  // open: cout
endmodule

module \_32X32乘法器测试电路  (
  input  [31:0] in_1,
  input  [31:0] in_2,
  output [31:0] out_3,
  output [31:0] out_4
);

  \_32X32乘法器  \u_32x32乘法器_1  (.a(in_1), .b(in_2), .pl(out_3), .ph(out_4));
endmodule
