// Logisim project 实验2-ACM1901-U201915035-邹雅.circ as structural Verilog: 9 circuits, main circuit 四位二进制可逆计数器
module \四位二进制可逆计数器  (
  input  A,
  input  B,
  input  C,
  input  D,
  input  nLD,
  input  CLR,
  input  CPu,
  input  CPd,
  output QA,
  output QB,
  output QC,
  output QD
);

  wire and_1_out, and_2_out, and_3_out, and_4_out, and_5_out, and_6_out, and_7_out, and_8_out, and_9_out,
       and_10_out, and_11_out, and_12_out, and_13_out, and_14_out, d_ff_1_qn, d_ff_2_qn, d_ff_3_qn,
       d_ff_4_qn, not_1_out, not_2_out, not_3_out, not_4_out, not_5_out, or_1_out, or_2_out, or_3_out,
       or_4_out, or_5_out, or_6_out, or_7_out, or_8_out;

  not not_1 (not_1_out, A);
  and and_1 (and_1_out, not_1_out, not_5_out);
  or or_1 (or_1_out, CPu, CPd);
  and and_2 (and_2_out, A, not_5_out);
  D_Flip_Flop #(.trigger("falling"), .Pre_Clr_Positions("ABOVE_BELOW"), .NegatePresetClear("false"), .enable("false"), .NewFFLayout("true")) d_ff_1 (
    .clk(or_1_out), .D(d_ff_1_qn), .Q(QA), .Qn(d_ff_1_qn), .preset(and_2_out), .reset(or_2_out));
  or or_2 (or_2_out, and_1_out, CLR);
  not not_2 (not_2_out, B);
  or or_3 (or_3_out, and_3_out, and_6_out);
  and and_3 (and_3_out, QA, CPu);
  and and_4 (and_4_out, B, not_5_out);
  D_Flip_Flop #(.trigger("falling"), .Pre_Clr_Positions("ABOVE_BELOW"), .NegatePresetClear("false"), .enable("false"), .NewFFLayout("true")) d_ff_2 (
    .clk(or_3_out), .D(d_ff_2_qn), .Q(QB), .Qn(d_ff_2_qn), .preset(and_4_out), .reset(or_4_out));
  or or_4 (or_4_out, and_5_out, CLR);
  and and_5 (and_5_out, not_2_out, not_5_out);
  and and_6 (and_6_out, d_ff_1_qn, CPd);
  or or_5 (or_5_out, and_7_out, and_10_out);
  and and_7 (and_7_out, CPu, QA, QB);
  not not_3 (not_3_out, C);
  and and_8 (and_8_out, C, not_5_out);
  or or_6 (or_6_out, and_9_out, CLR);
  and and_9 (and_9_out, not_3_out, not_5_out);
  and and_10 (and_10_out, CPd, d_ff_1_qn, d_ff_2_qn);
  D_Flip_Flop #(.trigger("falling"), .Pre_Clr_Positions("ABOVE_BELOW"), .NegatePresetClear("false"), .enable("false"), .NewFFLayout("true")) d_ff_3 (
    .clk(or_5_out), .D(d_ff_3_qn), .Q(QC), .Qn(d_ff_3_qn), .preset(and_8_out), .reset(or_6_out));
  not not_4 (not_4_out, D);
  and and_11 (and_11_out, not_4_out, not_5_out);
  or or_7 (or_7_out, and_12_out, and_14_out);
  and and_12 (and_12_out, CPu, QA, QB, QC);
  and and_13 (and_13_out, D, not_5_out);
  D_Flip_Flop #(.trigger("falling"), .Pre_Clr_Positions("ABOVE_BELOW"), .NegatePresetClear("false"), .enable("false"), .NewFFLayout("true")) d_ff_4 (
    .clk(or_7_out), .D(d_ff_4_qn), .Q(QD), .Qn(d_ff_4_qn), .preset(and_13_out), .reset(or_8_out));
  or or_8 (or_8_out, and_11_out, CLR);
  and and_14 (and_14_out, CPd, d_ff_1_qn, d_ff_2_qn, d_ff_3_qn);
  not not_5 (not_5_out, nLD);
endmodule

module \四位二进制可逆计数器测试电路  (
  input  in_1,
  input  in_2,
  input  in_3,
  input  in_4,
  input  in_5,
  input  in_6,
  input  in_7,
  input  in_8,
  output out_9,
  output out_10,
  output out_11,
  output out_12
);

  \四位二进制可逆计数器  \u_四位二进制可逆计数器_1  (
    .CPu(in_1), .CPd(in_3), .nLD(in_8), .QA(out_12), .QB(out_11), .QC(out_10), .QD(out_9), .CLR(in_2),
    .A(in_7), .B(in_6), .C(in_5), .D(in_4));
endmodule

module \二进制转8421码电路  (
  input  A3,
  input  A2,
  input  A1,
  input  A0,
  output S80,
  output S40,
  output S20,
  output S10,
  output S8,
  output S4,
  output S2,
  output S1
);

  wire and_1_out, or_1_out;

  \先行进位并行加法器  \u_先行进位并行加法器_1  (
    .C0(1'b0), .A3(A3), .B3(1'b0), .A2(A2), .B2(and_1_out), .A1(A1), .B1(and_1_out), .A0(A0), .B0(1'b0),
    .C4(S10), .S3(S8), .S2(S4), .S1(S2), .S0(S1));
  or or_1 (or_1_out, A1, A2);
  and and_1 (and_1_out, A3, or_1_out);

  assign S20 = 1'b0;
  assign S40 = 1'b0;
  assign S80 = 1'b0;
endmodule

module \二进制转8421码测试电路  (
  input  in_1,
  input  in_2,
  input  in_3,
  input  in_4,
  output out_5,
  output out_6,
  output out_7,
  output out_8,
  output out_9,
  output out_10,
  output out_11,
  output out_12
);

  \二进制转8421码电路  \u_二进制转8421码电路_1  (
    .S80(out_5), .S40(out_6), .S20(out_7), .S10(out_8), .S8(out_9), .S4(out_10), .S2(out_11), .S1(out_12),
    .A3(in_1), .A2(in_2), .A1(in_3), .A0(in_4));
endmodule

module \显示电路  (
  input  A3,
  input  A2,
  input  A1,
  input  A0,
  output a,
  output b,
  output c,
  output d,
  output e,
  output f,
  output g
);

  wire and_1_out, and_2_out, and_3_out, and_4_out, and_5_out, and_6_out, and_7_out, and_8_out, and_9_out,
       and_10_out, and_11_out, and_12_out, and_13_out, and_14_out, and_15_out, and_16_out, and_17_out,
       and_18_out, and_19_out, and_20_out, and_21_out, and_22_out, and_23_out, and_24_out, and_25_out,
       not_1_out, not_2_out, not_3_out, not_4_out;

  not not_1 (not_1_out, A3);
  not not_2 (not_2_out, A2);
  not not_3 (not_3_out, A1);
  not not_4 (not_4_out, A0);
  and and_1 (and_1_out, A0, not_3_out, A3);
  and and_2 (and_2_out, A0, A2, not_1_out);
  and and_3 (and_3_out, A1, not_2_out, not_1_out);
  and and_4 (and_4_out, not_2_out, not_3_out, not_4_out);
  and and_5 (and_5_out, A0, A1, not_1_out);
  and and_6 (and_6_out, not_3_out, not_2_out);
  and and_7 (and_7_out, not_3_out, not_4_out);
  and and_8 (and_8_out, not_1_out, not_2_out);
  and and_9 (and_9_out, A0, not_2_out);
  and and_10 (and_10_out, not_3_out, not_2_out);
  and and_11 (and_11_out, not_1_out, A2);
  and and_12 (and_12_out, not_4_out, A1, A2);
  and and_13 (and_13_out, A0, A1, not_2_out);
  and and_14 (and_14_out, not_4_out, not_2_out);
  and and_15 (and_15_out, A0, not_3_out, A2);
  and and_16 (and_16_out, not_4_out, not_2_out);
  and and_17 (and_17_out, not_4_out, A1);
  and and_18 (and_18_out, not_4_out, A2);
  and and_19 (and_19_out, not_3_out, not_2_out, A3);
  and and_20 (and_20_out, not_3_out, A2);
  and and_21 (and_21_out, not_4_out, not_3_out);
  and and_22 (and_22_out, not_4_out, A1);
  and and_23 (and_23_out, A1, not_2_out);
  and and_24 (and_24_out, not_2_out, A3);
  and and_25 (and_25_out, not_3_out, A2);
  or or_1 (a, and_1_out, and_2_out, and_3_out, and_4_out);
  or or_2 (b, and_5_out, and_6_out, and_7_out, and_8_out);
  or or_3 (c, and_9_out, and_10_out, and_11_out);
  or or_4 (d, and_12_out, and_13_out, and_14_out, and_15_out);
  or or_5 (e, and_16_out, and_17_out);
  or or_6 (f, and_18_out, and_19_out, and_20_out, and_21_out);
  or or_7 (g, and_22_out, and_23_out, and_24_out, and_25_out);
endmodule

module \显示电路测试电路  (
  input  in_1,
  input  in_2,
  input  in_3,
  input  in_4
);

  wire \二进制转8421码电路_1_s1 , \二进制转8421码电路_1_s2 , \二进制转8421码电路_1_s4 , \二进制转8421码电路_1_s8 , \二进制转8421码电路_1_s10 ,
       \二进制转8421码电路_1_s20 , \二进制转8421码电路_1_s40 , \二进制转8421码电路_1_s80 , \显示电路_1_a , \显示电路_1_b , \显示电路_1_c ,
       \显示电路_1_d , \显示电路_1_e , \显示电路_1_f , \显示电路_1_g , \显示电路_2_a , \显示电路_2_b , \显示电路_2_c , \显示电路_2_d ,
       \显示电路_2_e , \显示电路_2_f , \显示电路_2_g ;

  _7_Segment_Display #(.active("true")) u_7_segment_display_1 (
    .g(\显示电路_1_g ), .f(\显示电路_1_f ), .a(\显示电路_1_a ), .b(\显示电路_1_b ), .e(\显示电路_1_e ), .d(\显示电路_1_d ),
    .c(\显示电路_1_c ));  // open: dp
  \显示电路  \u_显示电路_1  (
    .A3(\二进制转8421码电路_1_s80 ), .A2(\二进制转8421码电路_1_s40 ), .A1(\二进制转8421码电路_1_s20 ), .A0(\二进制转8421码电路_1_s10 ),
    .a(\显示电路_1_a ), .b(\显示电路_1_b ), .c(\显示电路_1_c ), .d(\显示电路_1_d ), .e(\显示电路_1_e ), .f(\显示电路_1_f ),
    .g(\显示电路_1_g ));
  \二进制转8421码电路  \u_二进制转8421码电路_1  (
    .S80(\二进制转8421码电路_1_s80 ), .S40(\二进制转8421码电路_1_s40 ), .S20(\二进制转8421码电路_1_s20 ),
    .S10(\二进制转8421码电路_1_s10 ), .S8(\二进制转8421码电路_1_s8 ), .S4(\二进制转8421码电路_1_s4 ), .S2(\二进制转8421码电路_1_s2 ),
    .S1(\二进制转8421码电路_1_s1 ), .A3(in_1), .A2(in_2), .A1(in_3), .A0(in_4));
  \显示电路  \u_显示电路_2  (
    .A3(\二进制转8421码电路_1_s8 ), .A2(\二进制转8421码电路_1_s4 ), .A1(\二进制转8421码电路_1_s2 ), .A0(\二进制转8421码电路_1_s1 ),
    .a(\显示电路_2_a ), .b(\显示电路_2_b ), .c(\显示电路_2_c ), .d(\显示电路_2_d ), .e(\显示电路_2_e ), .f(\显示电路_2_f ),
    .g(\显示电路_2_g ));
  _7_Segment_Display #(.active("true")) u_7_segment_display_2 (
    .g(\显示电路_2_g ), .f(\显示电路_2_f ), .a(\显示电路_2_a ), .b(\显示电路_2_b ), .e(\显示电路_2_e ), .d(\显示电路_2_d ),
    .c(\显示电路_2_c ));  // open: dp
endmodule

module \报警电路  (
  input  QD,
  input  QC,
  input  QB,
  input  QA,
  input  CPu,
  input  CPd,
  output Alarm,
  output CPu1,
  output CPd1
);

  wire and_1_out, not_1_out, or_1_out;

  and and_1 (and_1_out, QD, QC, QB, QA);
  or or_1 (or_1_out, QD, QC, QB, QB);
  not not_1 (not_1_out, and_1_out);
  and and_2 (Alarm, CPu, and_1_out);
  and and_3 (CPu1, not_1_out, CPu);
  and and_4 (CPd1, or_1_out, CPd);
endmodule

module \小型实验室门禁系统  (
  input  CPu,
  input  CPd,
  input  CLR,
  output a1,
  output b1,
  output c1,
  output d1,
  output e1,
  output f1,
  output g1,
  output a,
  output b,
  output c,
  output d,
  output e,
  output f,
  output g,
  output \报警 
);

  wire \二进制转8421码电路_1_s1 , \二进制转8421码电路_1_s2 , \二进制转8421码电路_1_s4 , \二进制转8421码电路_1_s8 , \二进制转8421码电路_1_s10 ,
       \二进制转8421码电路_1_s20 , \二进制转8421码电路_1_s40 , \二进制转8421码电路_1_s80 , \四位二进制可逆计数器_1_qa , \四位二进制可逆计数器_1_qb ,
       \四位二进制可逆计数器_1_qc , \四位二进制可逆计数器_1_qd , \报警电路_1_cpd1 , \报警电路_1_cpu1 ;

  \报警电路  \u_报警电路_1  (
    .QD(\四位二进制可逆计数器_1_qd ), .QC(\四位二进制可逆计数器_1_qc ), .QB(\四位二进制可逆计数器_1_qb ), .QA(\四位二进制可逆计数器_1_qa ),
    .CPu(CPu), .CPd(CPd), .Alarm(\报警 ), .CPu1(\报警电路_1_cpu1 ), .CPd1(\报警电路_1_cpd1 ));
  \显示电路  \u_显示电路_1  (
    .A3(\二进制转8421码电路_1_s80 ), .A2(\二进制转8421码电路_1_s40 ), .A1(\二进制转8421码电路_1_s20 ), .A0(\二进制转8421码电路_1_s10 ),
    .a(a1), .b(b1), .c(c1), .d(d1), .e(e1), .f(f1), .g(g1));
  \二进制转8421码电路  \u_二进制转8421码电路_1  (
    .S80(\二进制转8421码电路_1_s80 ), .S40(\二进制转8421码电路_1_s40 ), .S20(\二进制转8421码电路_1_s20 ),
    .S10(\二进制转8421码电路_1_s10 ), .S8(\二进制转8421码电路_1_s8 ), .S4(\二进制转8421码电路_1_s4 ), .S2(\二进制转8421码电路_1_s2 ),
    .S1(\二进制转8421码电路_1_s1 ), .A3(\四位二进制可逆计数器_1_qd ), .A2(\四位二进制可逆计数器_1_qc ), .A1(\四位二进制可逆计数器_1_qb ),
    .A0(\四位二进制可逆计数器_1_qa ));
  \四位二进制可逆计数器  \u_四位二进制可逆计数器_1  (
    .CPu(\报警电路_1_cpu1 ), .CPd(\报警电路_1_cpd1 ), .nLD(1'b1), .QA(\四位二进制可逆计数器_1_qa ), .QB(\四位二进制可逆计数器_1_qb ),
    .QC(\四位二进制可逆计数器_1_qc ), .QD(\四位二进制可逆计数器_1_qd ), .CLR(CLR), .A(1'b0), .B(1'b0), .C(1'b0), .D(1'b0));
  \显示电路  \u_显示电路_2  (
    .A3(\二进制转8421码电路_1_s8 ), .A2(\二进制转8421码电路_1_s4 ), .A1(\二进制转8421码电路_1_s2 ), .A0(\二进制转8421码电路_1_s1 ),
    .a(a), .b(b), .c(c), .d(d), .e(e), .f(f), .g(g));
endmodule

module \小型实验室门禁系统封装  (
  input  in_1,
  input  in_2,
  input  in_3,
  output out_4
);

  wire \小型实验室门禁系统_1_a , \小型实验室门禁系统_1_a1 , \小型实验室门禁系统_1_b , \小型实验室门禁系统_1_b1 , \小型实验室门禁系统_1_c ,
       \小型实验室门禁系统_1_c1 , \小型实验室门禁系统_1_d , \小型实验室门禁系统_1_d1 , \小型实验室门禁系统_1_e , \小型实验室门禁系统_1_e1 ,
       \小型实验室门禁系统_1_f , \小型实验室门禁系统_1_f1 , \小型实验室门禁系统_1_g , \小型实验室门禁系统_1_g1 ;

  _7_Segment_Display #(.active("true")) u_7_segment_display_1 (
    .g(\小型实验室门禁系统_1_g1 ), .f(\小型实验室门禁系统_1_f1 ), .a(\小型实验室门禁系统_1_a1 ), .b(\小型实验室门禁系统_1_b1 ),
    .e(\小型实验室门禁系统_1_e1 ), .d(\小型实验室门禁系统_1_d1 ), .c(\小型实验室门禁系统_1_c1 ));  // open: dp
  _7_Segment_Display #(.active("true")) u_7_segment_display_2 (
    .g(\小型实验室门禁系统_1_g ), .f(\小型实验室门禁系统_1_f ), .a(\小型实验室门禁系统_1_a ), .b(\小型实验室门禁系统_1_b ), .e(\小型实验室门禁系统_1_e ),
    .d(\小型实验室门禁系统_1_d ), .c(\小型实验室门禁系统_1_c ));  // open: dp
  \小型实验室门禁系统  \u_小型实验室门禁系统_1  (
    .\报警 (out_4), .a1(\小型实验室门禁系统_1_a1 ), .b1(\小型实验室门禁系统_1_b1 ), .c1(\小型实验室门禁系统_1_c1 ), .d1(\小型实验室门禁系统_1_d1 ),
    .e1(\小型实验室门禁系统_1_e1 ), .f1(\小型实验室门禁系统_1_f1 ), .g1(\小型实验室门禁系统_1_g1 ), .a(\小型实验室门禁系统_1_a ),
    .b(\小型实验室门禁系统_1_b ), .c(\小型实验室门禁系统_1_c ), .d(\小型实验室门禁系统_1_d ), .e(\小型实验室门禁系统_1_e ), .f(\小型实验室门禁系统_1_f ),
    .g(\小型实验室门禁系统_1_g ), .CPu(in_1), .CPd(in_2), .CLR(in_3));
  LED #(.active("true")) led_1 (.in(out_4));
endmodule
