// Logisim project 实验五-ACM1901-U201915035-邹雅.circ as structural Verilog: 14 circuits, main circuit 四位二进制可逆计数器
module \四位二进制可逆计数器  (
  input  A,
  input  B,
  input  C,
  input  D,
  input  nLD,
  input  CLR,
  input  CPu,
  input  CPd,
  output QA,
  output QB,
  output QC,
  output QD
);

  wire and_1_out, and_2_out, and_3_out, and_4_out, and_5_out, and_6_out, and_7_out, and_8_out, and_9_out,
       and_10_out, and_11_out, and_12_out, and_13_out, and_14_out, d_ff_1_qn, d_ff_2_qn, d_ff_3_qn,
       d_ff_4_qn, not_1_out, not_2_out, not_3_out, not_4_out, not_5_out, or_1_out, or_2_out, or_3_out,
       or_4_out, or_5_out, or_6_out, or_7_out, or_8_out;

  not not_1 (not_1_out, A);
  and and_1 (and_1_out, not_1_out, not_5_out);
  or or_1 (or_1_out, CPu, CPd);
  and and_2 (and_2_out, A, not_5_out);
  D_Flip_Flop #(.trigger("falling"), .Pre_Clr_Positions("ABOVE_BELOW"), .NegatePresetClear("false"), .enable("false"), .NewFFLayout("true")) d_ff_1 (
    .clk(or_1_out), .D(d_ff_1_qn), .Q(QA), .Qn(d_ff_1_qn), .preset(and_2_out), .reset(or_2_out));
  or or_2 (or_2_out, and_1_out, CLR);
  not not_2 (not_2_out, B);
  or or_3 (or_3_out, and_3_out, and_6_out);
  and and_3 (and_3_out, QA, CPu);
  and and_4 (and_4_out, B, not_5_out);
  D_Flip_Flop #(.trigger("falling"), .Pre_Clr_Positions("ABOVE_BELOW"), .NegatePresetClear("false"), .enable("false"), .NewFFLayout("true")) d_ff_2 (
    .clk(or_3_out), .D(d_ff_2_qn), .Q(QB), .Qn(d_ff_2_qn), .preset(and_4_out), .reset(or_4_out));
  or or_4 (or_4_out, and_5_out, CLR);
  and and_5 (and_5_out, not_2_out, not_5_out);
  and and_6 (and_6_out, d_ff_1_qn, CPd);
  or or_5 (or_5_out, and_7_out, and_10_out);
  and and_7 (and_7_out, CPu, QA, QB);
  not not_3 (not_3_out, C);
  and and_8 (and_8_out, C, not_5_out);
  or or_6 (or_6_out, and_9_out, CLR);
  and and_9 (and_9_out, not_3_out, not_5_out);
  and and_10 (and_10_out, CPd, d_ff_1_qn, d_ff_2_qn);
  D_Flip_Flop #(.trigger("falling"), .Pre_Clr_Positions("ABOVE_BELOW"), .NegatePresetClear("false"), .enable("false"), .NewFFLayout("true")) d_ff_3 (
    .clk(or_5_out), .D(d_ff_3_qn), .Q(QC), .Qn(d_ff_3_qn), .preset(and_8_out), .reset(or_6_out));
  not not_4 (not_4_out, D);
  and and_11 (and_11_out, not_4_out, not_5_out);
  or or_7 (or_7_out, and_12_out, and_14_out);
  and and_12 (and_12_out, CPu, QA, QB, QC);
  and and_13 (and_13_out, D, not_5_out);
  D_Flip_Flop #(.trigger("falling"), .Pre_Clr_Positions("ABOVE_BELOW"), .NegatePresetClear("false"), .enable("false"), .NewFFLayout("true")) d_ff_4 (
    .clk(or_7_out), .D(d_ff_4_qn), .Q(QD), .Qn(d_ff_4_qn), .preset(and_13_out), .reset(or_8_out));
  or or_8 (or_8_out, and_11_out, CLR);
  and and_14 (and_14_out, CPd, d_ff_1_qn, d_ff_2_qn, d_ff_3_qn);
  not not_5 (not_5_out, nLD);
endmodule

module \六十进制计数器  (
  input  CPu,
  input  CPd,
  input  Adj,
  input  CLR,
  output Q1D,
  output out_6,
  output Q1B,
  output Q1A,
  output Q0D,
  output Q0C,
  output Q0B,
  output Q0A,
  output nQcc
);

  wire and_2_out, and_3_out, and_4_out, and_5_out, and_6_out, and_7_out, and_8_out, and_9_out, and_10_out,
       and_11_out, buffer_1_out, buffer_2_out, not_1_out, not_2_out, not_3_out, not_4_out, or_1_out,
       or_2_out, or_3_out, or_4_out, or_5_out, or_6_out, or_7_out, or_8_out, or_9_out, or_10_out;

  or or_1 (or_1_out, Q0D, Q0C);
  or or_2 (or_2_out, Q0B, Q0A);
  not not_1 (not_1_out, Adj);
  and and_1 (nQcc, not_1_out, and_11_out);
  or or_3 (or_3_out, or_1_out, or_2_out);
  or or_4 (or_4_out, or_3_out, or_9_out);
  and and_2 (and_2_out, CPd, Adj);
  or or_5 (or_5_out, and_9_out, and_11_out);
  or or_6 (or_6_out, or_5_out, CLR);
  and and_3 (and_3_out, or_4_out, and_2_out);
  \四位二进制可逆计数器  \u_四位二进制可逆计数器_1  (
    .A(1'b1), .B(1'b0), .C(1'b0), .D(1'b1), .nLD(not_4_out), .QA(Q0A), .QB(Q0B), .QC(Q0C), .QD(Q0D),
    .CLR(or_6_out), .CPu(CPu), .CPd(and_3_out));
  and and_4 (and_4_out, Q0A, Q0C);
  and and_5 (and_5_out, Q0B, Q0D);
  buf buffer_1 (buffer_1_out, Q0B);
  and and_6 (and_6_out, buffer_1_out, buffer_2_out);
  buf buffer_2 (buffer_2_out, Q0D);
  not not_2 (not_2_out, Q0A);
  and and_7 (and_7_out, not_2_out, not_3_out);
  not not_3 (not_3_out, Q0C);
  not not_4 (not_4_out, and_8_out);
  and and_8 (and_8_out, and_4_out, and_5_out);
  and and_9 (and_9_out, and_6_out, and_7_out);
  or or_7 (or_7_out, Q1A, Q1B);
  or or_8 (or_8_out, out_6, Q1D);
  or or_9 (or_9_out, or_7_out, or_8_out);
  or or_10 (or_10_out, and_11_out, CLR);
  and and_10 (and_10_out, or_9_out, and_8_out);
  and and_11 (and_11_out, out_6, Q1B);
  \四位二进制可逆计数器  \u_四位二进制可逆计数器_2  (
    .A(1'b1), .B(1'b1), .C(1'b1), .D(1'b1), .nLD(1'b1), .QA(Q1A), .QB(Q1B), .QC(out_6), .QD(Q1D),
    .CLR(or_10_out), .CPu(and_9_out), .CPd(and_10_out));
endmodule

module \六十进制计数器测试电路  (
  input  in_1,
  input  in_2,
  input  in_3,
  input  in_4
);

  wire button_1_out, button_2_out, \六十进制计数器_1_nqcc ;
  wire [3:0] \六十进制计数器_1_q0a , \六十进制计数器_1_q1a , \六十进制计数器_2_q0a , \六十进制计数器_2_q1a ;

  Hex_Digit_Display hex_digit_display_1 (.value(\六十进制计数器_1_q1a ));  // open: dp
  Button button_1 (.out(button_1_out));
  Button button_2 (.out(button_2_out));
  Hex_Digit_Display hex_digit_display_2 (.value(\六十进制计数器_1_q0a ));  // open: dp
  \六十进制计数器  \u_六十进制计数器_1  (
    .Q1D(\六十进制计数器_1_q1a [3]), .out_6(\六十进制计数器_1_q1a [2]), .Q1B(\六十进制计数器_1_q1a [1]), .Q1A(\六十进制计数器_1_q1a [0]),
    .Q0D(\六十进制计数器_1_q0a [3]), .Q0C(\六十进制计数器_1_q0a [2]), .Q0B(\六十进制计数器_1_q0a [1]), .Q0A(\六十进制计数器_1_q0a [0]),
    .CPu(button_1_out), .CPd(button_2_out), .Adj(in_1), .CLR(in_2), .nQcc(\六十进制计数器_1_nqcc ));
  Hex_Digit_Display hex_digit_display_3 (.value(\六十进制计数器_2_q0a ));  // open: dp
  Hex_Digit_Display hex_digit_display_4 (.value(\六十进制计数器_2_q1a ));  // open: dp
  \六十进制计数器  \u_六十进制计数器_2  (
    .Q1D(\六十进制计数器_2_q1a [3]), .out_6(\六十进制计数器_2_q1a [2]), .Q1B(\六十进制计数器_2_q1a [1]), .Q1A(\六十进制计数器_2_q1a [0]),
    .Q0D(\六十进制计数器_2_q0a [3]), .Q0C(\六十进制计数器_2_q0a [2]), .Q0B(\六十进制计数器_2_q0a [1]), .Q0A(\六十进制计数器_2_q0a [0]),
    .CPu(\六十进制计数器_1_nqcc ), .CPd(in_4), .Adj(in_3), .CLR(1'b0));  // open: nQcc
endmodule

module \十二进制计数器或二十四进制的计数器电路  (
  input  Set,
  input  CPu,
  input  Adj,
  input  Clr,
  input  CPd,
  output QD1,
  output QC1,
  output QB1,
  output QA1,
  output QD0,
  output QC0,
  output QB0,
  output QA0,
  output led
);

  wire _12_out, _24_out, and_1_out, and_2_out, and_3_out, and_4_out, and_5_out, and_6_out, not_1_out,
       not_2_out, or_1_out, or_2_out;

  not not_1 (not_1_out, Adj);
  or or_1 (or_1_out, and_2_out, and_3_out, Clr);
  \六十进制计数器  \u_六十进制计数器_1  (
    .Q1D(QD1), .out_6(QC1), .Q1B(QB1), .Q1A(QA1), .Q0D(QD0), .Q0C(QC0), .Q0B(QB0), .Q0A(QA0), .CPu(CPu),
    .CPd(CPd), .Adj(Adj), .CLR(or_1_out));  // open: nQcc
  and _24 (_24_out, QB1, QC0);
  and _12 (_12_out, QA1, QB0);
  and and_1 (and_1_out, QB1, QB0, QA0);
  and and_2 (and_2_out, _24_out, Set);
  not not_2 (not_2_out, Set);
  and and_3 (and_3_out, not_2_out, _12_out);
  and and_4 (and_4_out, QA1, QA0);
  and and_5 (and_5_out, and_1_out, Set);
  and and_6 (and_6_out, not_2_out, and_4_out);
  or or_2 (or_2_out, and_5_out, and_6_out);
  and and_7 (led, not_1_out, or_2_out);
endmodule

module \十二进制计数器或二十四进制的计数器测试电路  (
  input  in_1,
  input  in_2,
  input  in_3,
  input  in_4,
  input  in_5
);

  wire button_1_out, button_2_out, \十二进制计数器或二十四进制的计数器电路_1_led ;
  wire [3:0] \十二进制计数器或二十四进制的计数器电路_1_qa0 , \十二进制计数器或二十四进制的计数器电路_1_qa1 , \十二进制计数器或二十四进制的计数器电路_2_qa0 ,
       \十二进制计数器或二十四进制的计数器电路_2_qa1 ;

  Hex_Digit_Display hex_digit_display_1 (.value(\十二进制计数器或二十四进制的计数器电路_1_qa1 ));  // open: dp
  Button button_1 (.out(button_1_out));
  Button button_2 (.out(button_2_out));
  Hex_Digit_Display hex_digit_display_2 (.value(\十二进制计数器或二十四进制的计数器电路_1_qa0 ));  // open: dp
  \十二进制计数器或二十四进制的计数器电路  \u_十二进制计数器或二十四进制的计数器电路_1  (
    .Set(in_2), .CPu(button_1_out), .Adj(in_1), .CPd(button_2_out), .led(\十二进制计数器或二十四进制的计数器电路_1_led ),
    .Clr(in_4), .QD1(\十二进制计数器或二十四进制的计数器电路_1_qa1 [3]), .QC1(\十二进制计数器或二十四进制的计数器电路_1_qa1 [2]),
    .QB1(\十二进制计数器或二十四进制的计数器电路_1_qa1 [1]), .QA1(\十二进制计数器或二十四进制的计数器电路_1_qa1 [0]),
    .QD0(\十二进制计数器或二十四进制的计数器电路_1_qa0 [3]), .QC0(\十二进制计数器或二十四进制的计数器电路_1_qa0 [2]),
    .QB0(\十二进制计数器或二十四进制的计数器电路_1_qa0 [1]), .QA0(\十二进制计数器或二十四进制的计数器电路_1_qa0 [0]));
  Hex_Digit_Display hex_digit_display_3 (.value(\十二进制计数器或二十四进制的计数器电路_2_qa1 ));  // open: dp
  Hex_Digit_Display hex_digit_display_4 (.value(\十二进制计数器或二十四进制的计数器电路_2_qa0 ));  // open: dp
  \十二进制计数器或二十四进制的计数器电路  \u_十二进制计数器或二十四进制的计数器电路_2  (
    .Set(in_3), .CPu(\十二进制计数器或二十四进制的计数器电路_1_led ), .Adj(1'b0), .CPd(1'b0), .Clr(in_5),
    .QD1(\十二进制计数器或二十四进制的计数器电路_2_qa1 [3]), .QC1(\十二进制计数器或二十四进制的计数器电路_2_qa1 [2]),
    .QB1(\十二进制计数器或二十四进制的计数器电路_2_qa1 [1]), .QA1(\十二进制计数器或二十四进制的计数器电路_2_qa1 [0]),
    .QD0(\十二进制计数器或二十四进制的计数器电路_2_qa0 [3]), .QC0(\十二进制计数器或二十四进制的计数器电路_2_qa0 [2]),
    .QB0(\十二进制计数器或二十四进制的计数器电路_2_qa0 [1]), .QA0(\十二进制计数器或二十四进制的计数器电路_2_qa0 [0]));  // open: led
endmodule

module \上下午文字显示的电路  (
  input  TT,
  input  AM_FM,
  output [4:0] out_3,
  output [4:0] out_4,
  output [4:0] out_5,
  output [4:0] out_6
);

  wire [4:0] multiplexer_3_out, multiplexer_5_out, multiplexer_6_out, multiplexer_8_out;

  Multiplexer #(.select(1), .width(5), .disabled("Z"), .enable("false")) multiplexer_1 (
    .in0({5{1'b0}}), .in1(multiplexer_3_out), .out(out_3), .sel(TT));
  Multiplexer #(.select(1), .width(5), .disabled("Z"), .enable("false")) multiplexer_2 (
    .in0({5{1'b0}}), .in1(multiplexer_6_out), .out(out_4), .sel(TT));
  Multiplexer #(.select(1), .width(5), .disabled("Z"), .enable("false")) multiplexer_3 (
    .in0(5'b00001), .in1(5'b10000), .out(multiplexer_3_out), .sel(AM_FM));
  Multiplexer #(.select(1), .width(5), .disabled("Z"), .enable("false")) multiplexer_4 (
    .in0({5{1'b0}}), .in1(multiplexer_5_out), .out(out_5), .sel(TT));
  Multiplexer #(.select(1), .width(5), .disabled("Z"), .enable("false")) multiplexer_5 (
    .in0(5'b00101), .in1(5'b10100), .out(multiplexer_5_out), .sel(AM_FM));
  Multiplexer #(.select(1), .width(5), .disabled("Z"), .enable("false")) multiplexer_6 (
    .in0({5{1'b1}}), .in1({5{1'b1}}), .out(multiplexer_6_out), .sel(AM_FM));
  Multiplexer #(.select(1), .width(5), .disabled("Z"), .enable("false")) multiplexer_7 (
    .in0({5{1'b0}}), .in1(multiplexer_8_out), .out(out_6), .sel(TT));
  Multiplexer #(.select(1), .width(5), .disabled("Z"), .enable("false")) multiplexer_8 (
    .in0(5'b00001), .in1(5'b10000), .out(multiplexer_8_out), .sel(AM_FM));
endmodule

module \上下午文字显示测试电路  (
  input  in_1,
  input  in_2
);

  wire [4:0] \上下午文字显示的电路_1_out_3 , \上下午文字显示的电路_1_out_4 , \上下午文字显示的电路_1_out_5 , \上下午文字显示的电路_1_out_6 ;

  DotMatrix #(.inputtype("column"), .matrixcols(4), .matrixrows(5), .persist(0), .dotshape("square")) dotmatrix_1 (
    .col0(\上下午文字显示的电路_1_out_3 ), .col1(\上下午文字显示的电路_1_out_4 ), .col2(\上下午文字显示的电路_1_out_5 ),
    .col3(\上下午文字显示的电路_1_out_6 ));
  \上下午文字显示的电路  \u_上下午文字显示的电路_1  (
    .TT(in_2), .AM_FM(in_1), .out_3(\上下午文字显示的电路_1_out_3 ), .out_4(\上下午文字显示的电路_1_out_4 ),
    .out_5(\上下午文字显示的电路_1_out_5 ), .out_6(\上下午文字显示的电路_1_out_6 ));
endmodule

module \电子钟整点报时电路  (
  input  Adj,
  input  m13,
  input  m12,
  input  m11,
  input  m10,
  input  m03,
  input  m02,
  input  m01,
  input  m00,
  input  s3,
  input  s2,
  input  s1,
  input  s0,
  input  s30,
  input  s20,
  input  s10,
  input  in_17,
  output LED
);

  wire not_1_out, not_2_out, not_3_out, not_4_out, not_5_out, not_6_out;

  not not_1 (not_1_out, m02);
  not not_2 (not_2_out, m01);
  not not_3 (not_3_out, s3);
  not not_4 (not_4_out, s1);
  not not_5 (not_5_out, m13);
  not not_6 (not_6_out, m11);
  and and_1 (LED, not_5_out, m12, not_6_out, m10, m03, not_1_out, Adj, not_2_out, m00, not_3_out, s2, not_4_out, s0);

  assign s10 = in_17;
  assign s20 = in_17;
  assign s30 = in_17;
  // also tied to GND on the sheet: in_17

  // Notes on the sheet:
  //   分
  //   秒
endmodule

module \电子钟整点报时电路测试电路  (
  input  in_1,
  input  in_2,
  input  in_3,
  input  in_4,
  input  in_5,
  input  in_6,
  input  in_7,
  input  in_8,
  input  in_9,
  input  in_10,
  input  in_11,
  input  in_12,
  input  in_13,
  input  in_14,
  input  in_15,
  input  in_16,
  input  in_17
);

  wire \电子钟整点报时电路_1_led ;

  \电子钟整点报时电路  \u_电子钟整点报时电路_1  (
    .Adj(in_1), .m13(in_10), .m12(in_11), .m11(in_12), .m10(in_13), .m03(in_14), .m02(in_15), .m01(in_16),
    .LED(\电子钟整点报时电路_1_led ), .m00(in_17), .s3(in_2), .s2(in_3), .s1(in_4), .s0(in_5), .s30(in_6), .s20(in_7),
    .s10(in_8), .in_17(in_9));
  LED #(.active("true")) led_1 (.in(\电子钟整点报时电路_1_led ));
endmodule

module \秒脉冲产生电路  (
  input  in_1,
  output out_2
);

  wire \四位二进制可逆计数器_1_qa , \四位二进制可逆计数器_1_qb , \四位二进制可逆计数器_1_qc ;

  \四位二进制可逆计数器  \u_四位二进制可逆计数器_1  (
    .A(1'b0), .B(1'b0), .C(1'b0), .D(1'b0), .nLD(1'b1), .QA(\四位二进制可逆计数器_1_qa ), .QB(\四位二进制可逆计数器_1_qb ),
    .QC(\四位二进制可逆计数器_1_qc ), .CLR(out_2), .CPu(in_1), .CPd(1'b0));  // open: QD
  and and_1 (out_2, \四位二进制可逆计数器_1_qc , \四位二进制可逆计数器_1_qb , \四位二进制可逆计数器_1_qa );
endmodule

module \多功能数字钟  (
  input  CPu,
  input  CPd,
  input  Clr,
  input  Set,
  input  CP,
  input  Adj0,
  input  Adj1,
  output LED,
  output [3:0] H1,
  output [3:0] H0,
  output [3:0] M1,
  output [3:0] M0,
  output [3:0] S1,
  output [3:0] S0,
  output [4:0] _1,
  output [4:0] _2,
  output [4:0] _3,
  output [4:0] _4
);

  wire and_1_out, and_2_out, and_3_out, and_4_out, and_5_out, and_6_out, and_7_out, comparator_1_eq,
       comparator_1_gt, comparator_2_eq, not_1_out, not_2_out, not_3_out, not_4_out, or_1_out, or_2_out,
       or_3_out, \六十进制计数器_1_nqcc , \六十进制计数器_2_nqcc , \秒脉冲产生电路_1_out_2 ;
  wire [7:0] multiplexer_1_out, multiplexer_2_out, multiplexer_4_out, subtractor_1_out,
       \十二进制计数器或二十四进制的计数器电路_1_qa0 ;

  and and_1 (and_1_out, CP, not_1_out);
  \六十进制计数器  \u_六十进制计数器_1  (
    .Q1D(S1[3]), .out_6(S1[2]), .Q1B(S1[1]), .Q1A(S1[0]), .Q0D(S0[3]), .Q0C(S0[2]), .Q0B(S0[1]), .Q0A(S0[0]),
    .CPu(\秒脉冲产生电路_1_out_2 ), .CPd(1'b0), .Adj(1'b0), .CLR(Clr), .nQcc(\六十进制计数器_1_nqcc ));
  \秒脉冲产生电路  \u_秒脉冲产生电路_1  (.in_1(and_1_out), .out_2(\秒脉冲产生电路_1_out_2 ));
  and and_2 (and_2_out, CPu, and_3_out);
  or or_1 (or_1_out, and_2_out, \六十进制计数器_1_nqcc );
  \电子钟整点报时电路  \u_电子钟整点报时电路_1  (
    .Adj(not_1_out), .m13(M1[3]), .m12(M1[2]), .m11(M1[1]), .m10(M1[0]), .m03(M0[3]), .m02(M0[2]),
    .m01(M0[1]), .LED(LED), .m00(M0[0]), .s3(S1[3]), .s2(S1[2]), .s1(S1[1]), .s0(S1[0]), .s30(S0[3]),
    .s20(S0[2]), .s10(S0[1]), .in_17(S0[0]));
  and and_3 (and_3_out, Adj0, Adj1);
  not not_1 (not_1_out, Adj0);
  \六十进制计数器  \u_六十进制计数器_2  (
    .Q1D(M1[3]), .out_6(M1[2]), .Q1B(M1[1]), .Q1A(M1[0]), .Q0D(M0[3]), .Q0C(M0[2]), .Q0B(M0[1]), .Q0A(M0[0]),
    .CPu(or_1_out), .CPd(CPd), .Adj(and_3_out), .CLR(Clr), .nQcc(\六十进制计数器_2_nqcc ));
  and and_4 (and_4_out, not_1_out, \六十进制计数器_2_nqcc );
  not not_2 (not_2_out, Adj1);
  and and_5 (and_5_out, CPu, and_6_out);
  or or_2 (or_2_out, and_5_out, and_4_out);
  and and_6 (and_6_out, not_2_out, Adj0);
  and and_7 (and_7_out, \十二进制计数器或二十四进制的计数器电路_1_qa0 [5], not_3_out);
  not not_3 (not_3_out, \十二进制计数器或二十四进制的计数器电路_1_qa0 [1]);
  Multiplexer #(.select(1), .width(8), .disabled("Z"), .enable("true")) multiplexer_1 (
    .in0(8'h12), .in1(8'h18), .out(multiplexer_1_out), .sel(and_7_out));  // open: en
  Comparator #(.width(8), .mode("twosComplement")) comparator_1 (
    .a(\十二进制计数器或二十四进制的计数器电路_1_qa0 ), .b(8'h12), .gt(comparator_1_gt), .eq(comparator_1_eq));  // open: lt
  \十二进制计数器或二十四进制的计数器电路  \u_十二进制计数器或二十四进制的计数器电路_1  (
    .Set(1'b1), .CPu(or_2_out), .Adj(and_6_out), .CPd(CPd), .Clr(Clr), .QD1(\十二进制计数器或二十四进制的计数器电路_1_qa0 [7]),
    .QC1(\十二进制计数器或二十四进制的计数器电路_1_qa0 [6]), .QB1(\十二进制计数器或二十四进制的计数器电路_1_qa0 [5]),
    .QA1(\十二进制计数器或二十四进制的计数器电路_1_qa0 [4]), .QD0(\十二进制计数器或二十四进制的计数器电路_1_qa0 [3]),
    .QC0(\十二进制计数器或二十四进制的计数器电路_1_qa0 [2]), .QB0(\十二进制计数器或二十四进制的计数器电路_1_qa0 [1]),
    .QA0(\十二进制计数器或二十四进制的计数器电路_1_qa0 [0]));  // open: led
  Subtractor #(.width(8)) subtractor_1 (
    .a(\十二进制计数器或二十四进制的计数器电路_1_qa0 ), .b(multiplexer_1_out), .out(subtractor_1_out));  // open: bin, bout
  or or_3 (or_3_out, comparator_1_gt, comparator_1_eq);
  Multiplexer #(.select(1), .width(8), .disabled("Z"), .enable("true")) multiplexer_2 (
    .in0(\十二进制计数器或二十四进制的计数器电路_1_qa0 ), .in1(subtractor_1_out), .out(multiplexer_2_out), .sel(or_3_out));  // open: en
  Comparator #(.width(8), .mode("twosComplement")) comparator_2 (
    .a(multiplexer_2_out), .b({8{1'b0}}), .eq(comparator_2_eq));  // open: gt, lt
  Multiplexer #(.select(1), .width(8), .disabled("Z"), .enable("true")) multiplexer_3 (
    .in0(multiplexer_4_out), .in1(\十二进制计数器或二十四进制的计数器电路_1_qa0 ), .out({H1, H0}), .sel(Set));  // open: en
  Multiplexer #(.select(1), .width(8), .disabled("Z"), .enable("true")) multiplexer_4 (
    .in0(multiplexer_2_out), .in1(8'h12), .out(multiplexer_4_out), .sel(comparator_2_eq));  // open: en
  not not_4 (not_4_out, Set);
  \上下午文字显示的电路  \u_上下午文字显示的电路_1  (.TT(not_4_out), .AM_FM(or_3_out), .out_3(_1), .out_4(_2), .out_5(_3), .out_6(_4));
endmodule

module \多功能数字钟测试电路  (
  input  in_1,
  input  in_2,
  input  in_3,
  input  in_4
);

  wire button_1_out, button_2_out, clock_1_out, \多功能数字钟_1_led ;
  wire [3:0] \多功能数字钟_1_h0 , \多功能数字钟_1_h1 , \多功能数字钟_1_m0 , \多功能数字钟_1_m1 , \多功能数字钟_1_s0 , \多功能数字钟_1_s1 ;
  wire [4:0] \多功能数字钟_1__1 , \多功能数字钟_1__2 , \多功能数字钟_1__3 , \多功能数字钟_1__4 ;

  DotMatrix #(.inputtype("column"), .matrixcols(4), .matrixrows(5), .persist(0), .dotshape("square")) dotmatrix_1 (
    .col0(\多功能数字钟_1__1 ), .col1(\多功能数字钟_1__2 ), .col2(\多功能数字钟_1__3 ), .col3(\多功能数字钟_1__4 ));
  Clock #(.highDuration(1), .lowDuration(1)) clock_1 (.out(clock_1_out));
  Hex_Digit_Display hex_digit_display_1 (.value(\多功能数字钟_1_h1 ));  // open: dp
  Button button_1 (.out(button_1_out));
  Button button_2 (.out(button_2_out));
  Hex_Digit_Display hex_digit_display_2 (.value(\多功能数字钟_1_h0 ));  // open: dp
  Hex_Digit_Display hex_digit_display_3 (.value(\多功能数字钟_1_m1 ));  // open: dp
  \多功能数字钟  \u_多功能数字钟_1  (
    .LED(\多功能数字钟_1_led ), .H1(\多功能数字钟_1_h1 ), .H0(\多功能数字钟_1_h0 ), ._1(\多功能数字钟_1__1 ), ._2(\多功能数字钟_1__2 ),
    ._3(\多功能数字钟_1__3 ), ._4(\多功能数字钟_1__4 ), .S1(\多功能数字钟_1_s1 ), .S0(\多功能数字钟_1_s0 ), .CPu(button_2_out),
    .M1(\多功能数字钟_1_m1 ), .M0(\多功能数字钟_1_m0 ), .CP(clock_1_out), .CPd(button_1_out), .Adj0(in_1), .Adj1(in_2),
    .Clr(in_4), .Set(in_3));
  Hex_Digit_Display hex_digit_display_4 (.value(\多功能数字钟_1_m0 ));  // open: dp
  LED #(.active("true")) led_1 (.in(\多功能数字钟_1_led ));
  Hex_Digit_Display hex_digit_display_5 (.value(\多功能数字钟_1_s1 ));  // open: dp
  Hex_Digit_Display hex_digit_display_6 (.value(\多功能数字钟_1_s0 ));  // open: dp
endmodule

module \闹钟  (
  input  in_1,
  input  Adj0,
  input  Adj1,
  input  CP,
  input  CPu,
  input  CPd,
  input  set,
  input  Clr,
  input  Clockadj,
  output [3:0] h1,
  output [3:0] h0,
  output [3:0] m1,
  output [3:0] m0,
  output [3:0] s1,
  output [3:0] out_15,
  output [4:0] _1,
  output [4:0] _2,
  output [4:0] _3,
  output [4:0] _4,
  output \定点报时 ,
  output out_21
);

  wire and_1_out, and_2_out, and_3_out, and_4_out, and_5_out, and_7_out, comparator_1_eq, comparator_2_eq,
       multiplexer_5_out, nand_1_out, \四位二进制可逆计数器_1_qb , \四位二进制可逆计数器_1_qd , \多功能数字钟_2_led , \秒脉冲产生电路_1_out_2 ;
  wire [3:0] \多功能数字钟_2_m0 , \多功能数字钟_2_m1 , \多功能数字钟_2_s1 ;
  wire [4:0] \多功能数字钟_1__1 , \多功能数字钟_1__2 , \多功能数字钟_1__3 , \多功能数字钟_1__4 ;
  wire [7:0] \多功能数字钟_1_s0 , \多功能数字钟_2_h0 ;
  wire [15:0] \多功能数字钟_1_m0 ;
  wire [19:0] \多功能数字钟_2__4 ;
  wire [23:8] multiplexer_4_out;

  Multiplexer #(.select(1), .width(24), .disabled("Z"), .enable("true")) multiplexer_1 (
    .in0({\多功能数字钟_1_m0 , \多功能数字钟_1_s0 }), .in1({multiplexer_4_out, {8{1'b0}}}),
    .out({h1, h0, m1, m0, s1, out_15}), .sel(and_1_out));  // open: en
  and and_1 (and_1_out, Clockadj, in_1);
  \多功能数字钟  \u_多功能数字钟_1  (
    .LED(\定点报时 ), .H1(\多功能数字钟_1_m0 [15:12]), .H0(\多功能数字钟_1_m0 [11:8]), ._1(\多功能数字钟_1__1 ),
    ._2(\多功能数字钟_1__2 ), ._3(\多功能数字钟_1__3 ), ._4(\多功能数字钟_1__4 ), .S1(\多功能数字钟_1_s0 [7:4]),
    .S0(\多功能数字钟_1_s0 [3:0]), .CPu(CPu), .M1(\多功能数字钟_1_m0 [7:4]), .M0(\多功能数字钟_1_m0 [3:0]), .CP(CP), .CPd(CPd),
    .Adj0(Adj0), .Adj1(Adj1), .Clr(Clr), .Set(set));
  Comparator #(.width(20), .mode("twosComplement")) comparator_1 (
    .a({\多功能数字钟_1__1 , \多功能数字钟_1__2 , \多功能数字钟_1__3 , \多功能数字钟_1__4 }), .b(\多功能数字钟_2__4 ), .eq(comparator_1_eq));  // open: gt, lt
  and and_2 (and_2_out, in_1, Clockadj);
  Multiplexer #(.select(1), .width(20), .disabled("Z"), .enable("true")) multiplexer_2 (
    .in0({\多功能数字钟_1__1 , \多功能数字钟_1__2 , \多功能数字钟_1__3 , \多功能数字钟_1__4 }), .in1(\多功能数字钟_2__4 ),
    .out({_1, _2, _3, _4}), .sel(and_2_out));  // open: en
  and and_3 (and_3_out, Clockadj, Adj1);
  Multiplexer #(.select(1), .width(8), .disabled("Z"), .enable("true")) multiplexer_3 (
    .in0({8{1'b0}}), .in1(\多功能数字钟_2_h0 ), .out(multiplexer_4_out[23:16]), .sel(in_1));  // open: en
  \多功能数字钟  \u_多功能数字钟_2  (
    .LED(\多功能数字钟_2_led ), .H1(\多功能数字钟_2_h0 [7:4]), .H0(\多功能数字钟_2_h0 [3:0]), ._1(\多功能数字钟_2__4 [19:15]),
    ._2(\多功能数字钟_2__4 [14:10]), ._3(\多功能数字钟_2__4 [9:5]), ._4(\多功能数字钟_2__4 [4:0]), .S1(\多功能数字钟_2_s1 ),
    .S0(\多功能数字钟_2_s1 ), .CPu(and_4_out), .M1(\多功能数字钟_2_m1 ), .M0(\多功能数字钟_2_m0 ), .CP(1'b0), .CPd(and_5_out),
    .Adj0(in_1), .Adj1(and_3_out), .Clr(1'b0), .Set(set));
  and and_4 (and_4_out, Clockadj, CPu, in_1);
  and and_5 (and_5_out, Clockadj, CPd, in_1);
  Multiplexer #(.select(1), .width(8), .disabled("Z"), .enable("true")) multiplexer_4 (
    .in0({8{1'b0}}), .in1({\多功能数字钟_2_m1 , \多功能数字钟_2_m0 }), .out(multiplexer_4_out[15:8]), .sel(in_1));  // open: en
  and and_6 (out_21, in_1, CP, nand_1_out, and_7_out);
  nand nand_1 (nand_1_out, \四位二进制可逆计数器_1_qb , \四位二进制可逆计数器_1_qd );
  \秒脉冲产生电路  \u_秒脉冲产生电路_1  (.in_1(CP), .out_2(\秒脉冲产生电路_1_out_2 ));
  Comparator #(.width(16), .mode("twosComplement")) comparator_2 (
    .a(\多功能数字钟_1_m0 ), .b({\多功能数字钟_2_h0 , \多功能数字钟_2_m1 , \多功能数字钟_2_m0 }), .eq(comparator_2_eq));  // open: gt, lt
  \四位二进制可逆计数器  \u_四位二进制可逆计数器_1  (
    .A(1'b0), .B(1'b0), .C(1'b0), .D(1'b0), .nLD(1'b1), .QB(\四位二进制可逆计数器_1_qb ), .QD(\四位二进制可逆计数器_1_qd ),
    .CLR(1'b0), .CPu(multiplexer_5_out), .CPd(1'b0));  // open: QA, QC
  and and_7 (and_7_out, comparator_2_eq, comparator_1_eq, nand_1_out);
  Multiplexer #(.select(1), .width(1), .disabled("Z"), .enable("true")) multiplexer_5 (
    .in0(1'b0), .in1(\秒脉冲产生电路_1_out_2 ), .out(multiplexer_5_out), .sel(and_7_out));  // open: en
  // also tied to GND on the sheet: {\多功能数字钟_2_s1 [0], \多功能数字钟_2_s1 [1], \多功能数字钟_2_s1 [2], \多功能数字钟_2_s1 [3], \多功能数字钟_2_led }
endmodule

module \闹钟测试  (
  input  in_1,
  input  in_2,
  input  in_3,
  input  in_4,
  input  in_5,
  input  in_6
);

  wire button_1_out, button_2_out, clock_1_out, \闹钟_1_out_21 , \闹钟_1_定点报时 ;
  wire [3:0] \闹钟_1_h0 , \闹钟_1_h1 , \闹钟_1_m0 , \闹钟_1_m1 , \闹钟_1_out_15 , \闹钟_1_s1 ;
  wire [4:0] \闹钟_1__1 , \闹钟_1__2 , \闹钟_1__3 , \闹钟_1__4 ;

  Hex_Digit_Display hex_digit_display_1 (.value(\闹钟_1_h1 ));  // open: dp
  Hex_Digit_Display hex_digit_display_2 (.value(\闹钟_1_h0 ));  // open: dp
  Hex_Digit_Display hex_digit_display_3 (.value(\闹钟_1_m1 ));  // open: dp
  Hex_Digit_Display hex_digit_display_4 (.value(\闹钟_1_m0 ));  // open: dp
  Clock #(.highDuration(1), .lowDuration(1)) clock_1 (.out(clock_1_out));
  Button button_1 (.out(button_1_out));
  Hex_Digit_Display hex_digit_display_5 (.value(\闹钟_1_s1 ));  // open: dp
  Button button_2 (.out(button_2_out));
  Hex_Digit_Display hex_digit_display_6 (.value(\闹钟_1_out_15 ));  // open: dp
  DotMatrix #(.inputtype("column"), .matrixcols(4), .matrixrows(5), .persist(0), .dotshape("square")) dotmatrix_1 (
    .col0(\闹钟_1__1 ), .col1(\闹钟_1__2 ), .col2(\闹钟_1__3 ), .col3(\闹钟_1__4 ));
  \闹钟  \u_闹钟_1  (
    .h1(\闹钟_1_h1 ), .h0(\闹钟_1_h0 ), .m1(\闹钟_1_m1 ), .m0(\闹钟_1_m0 ), .s1(\闹钟_1_s1 ), .out_15(\闹钟_1_out_15 ),
    ._1(\闹钟_1__1 ), ._2(\闹钟_1__2 ), ._3(\闹钟_1__3 ), ._4(\闹钟_1__4 ), .in_1(in_5), .Adj0(in_1),
    .\定点报时 (\闹钟_1_定点报时 ), .Adj1(in_2), .CP(clock_1_out), .CPu(button_1_out), .CPd(button_2_out), .set(in_3),
    .Clr(in_4), .out_21(\闹钟_1_out_21 ), .Clockadj(in_6));
  LED #(.active("true")) led_1 (.in(\闹钟_1_定点报时 ));
  LED #(.active("true")) led_2 (.in(\闹钟_1_out_21 ));
endmodule
