// Logisim project 实验4-ACM1901-U201915035-邹雅.circ as structural Verilog: 5 circuits, main circuit 四位除法器
module \四位除法器  (
  input  [3:0] n2,
  input  [3:0] d,
  output [3:0] quot,
  output [3:0] rem
);

  wire comparator_1_lt, comparator_2_lt, comparator_3_lt, comparator_4_lt;
  wire [3:0] multiplexer_1_out, multiplexer_2_out, multiplexer_3_out, multiplexer_4_out, multiplexer_5_out,
       multiplexer_6_out, or_1_out, or_2_out, or_3_out, or_4_out, shifter_3_out, shifter_3_out_2,
       subtractor_1_out, subtractor_2_out, subtractor_3_out, subtractor_4_out;
  wire [7:0] shifter_1_out, shifter_2_out, shifter_4_out;

  Shifter #(.width(8), .shift("ll")) shifter_1 (.in({4'b0000, n2}), .\dist (3'b001), .out(shifter_1_out));
  assign or_1_out = 4'b0001 | shifter_1_out[3:0];  // OR_Gate or_1, 4 bits wide
  Multiplexer #(.select(1), .width(4), .disabled("Z"), .enable("false")) multiplexer_1 (
    .in0(or_1_out), .in1(shifter_1_out[3:0]), .out(multiplexer_1_out), .sel(comparator_1_lt));
  Comparator #(.width(4), .mode("unsigned")) comparator_1 (
    .a(shifter_1_out[7:4]), .b(d), .lt(comparator_1_lt));  // open: gt, eq
  Subtractor #(.width(4)) subtractor_1 (.a(shifter_1_out[7:4]), .b(d), .out(subtractor_1_out));  // open: bin, bout
  Multiplexer #(.select(1), .width(4), .disabled("Z"), .enable("false")) multiplexer_2 (
    .in0(subtractor_1_out), .in1(shifter_1_out[7:4]), .out(multiplexer_2_out), .sel(comparator_1_lt));
  Shifter #(.width(8), .shift("ll")) shifter_2 (
    .in({multiplexer_2_out, multiplexer_1_out}), .\dist (3'b001), .out(shifter_2_out));
  assign or_2_out = 4'b0001 | shifter_2_out[3:0];  // OR_Gate or_2, 4 bits wide
  Multiplexer #(.select(1), .width(4), .disabled("Z"), .enable("false")) multiplexer_3 (
    .in0(or_2_out), .in1(shifter_2_out[3:0]), .out(multiplexer_3_out), .sel(comparator_2_lt));
  Comparator #(.width(4), .mode("unsigned")) comparator_2 (
    .a(shifter_2_out[7:4]), .b(d), .lt(comparator_2_lt));  // open: gt, eq
  Subtractor #(.width(4)) subtractor_2 (.a(shifter_2_out[7:4]), .b(d), .out(subtractor_2_out));  // open: bin, bout
  Multiplexer #(.select(1), .width(4), .disabled("Z"), .enable("false")) multiplexer_4 (
    .in0(subtractor_2_out), .in1(shifter_2_out[7:4]), .out(multiplexer_4_out), .sel(comparator_2_lt));
  Shifter #(.width(8), .shift("ll")) shifter_3 (
    .in({multiplexer_4_out, multiplexer_3_out}), .\dist (3'b001), .out({shifter_3_out_2, shifter_3_out}));
  assign or_3_out = 4'b0001 | shifter_3_out;  // OR_Gate or_3, 4 bits wide
  Multiplexer #(.select(1), .width(4), .disabled("Z"), .enable("false")) multiplexer_5 (
    .in0(or_3_out), .in1(shifter_3_out), .out(multiplexer_5_out), .sel(comparator_3_lt));
  Comparator #(.width(4), .mode("unsigned")) comparator_3 (
    .a(shifter_3_out_2), .b(d), .lt(comparator_3_lt));  // open: gt, eq
  Subtractor #(.width(4)) subtractor_3 (.a(shifter_3_out_2), .b(d), .out(subtractor_3_out));  // open: bin, bout
  Multiplexer #(.select(1), .width(4), .disabled("Z"), .enable("false")) multiplexer_6 (
    .in0(subtractor_3_out), .in1(shifter_3_out_2), .out(multiplexer_6_out), .sel(comparator_3_lt));
  Shifter #(.width(8), .shift("ll")) shifter_4 (
    .in({multiplexer_6_out, multiplexer_5_out}), .\dist (3'b001), .out(shifter_4_out));
  assign or_4_out = 4'b0001 | shifter_4_out[3:0];  // OR_Gate or_4, 4 bits wide
  Multiplexer #(.select(1), .width(4), .disabled("Z"), .enable("false")) multiplexer_7 (
    .in0(or_4_out), .in1(shifter_4_out[3:0]), .out(quot), .sel(comparator_4_lt));
  Comparator #(.width(4), .mode("unsigned")) comparator_4 (
    .a(shifter_4_out[7:4]), .b(d), .lt(comparator_4_lt));  // open: gt, eq
  Subtractor #(.width(4)) subtractor_4 (.a(shifter_4_out[7:4]), .b(d), .out(subtractor_4_out));  // open: bin, bout
  Multiplexer #(.select(1), .width(4), .disabled("Z"), .enable("false")) multiplexer_8 (
    .in0(subtractor_4_out), .in1(shifter_4_out[7:4]), .out(rem), .sel(comparator_4_lt));

  // Notes on the sheet:
  //   n1
endmodule

module \四位除法器测试电路  (
  input  [3:0] n2,
  input  [3:0] d,
  output [3:0] \测试商 ,
  output [3:0] \测试余数 ,
  output [3:0] quot,
  output [3:0] rem
);

  Divider #(.width(4)) divider_1 (.a(n2), .b(d), .out(\测试商 ), .upper(4'b0000), .rem(\测试余数 ));
  \四位除法器  \u_四位除法器_1  (.n2(n2), .d(d), .quot(quot), .rem(rem));
endmodule

module \_32位除法器  (
  input  [31:0] d,
  input  [31:0] n,
  output [31:0] rem,
  output [31:0] quot
);

  wire [31:0] n32div1_1_next_quot, n32div1_1_next_rem, n32div1_3_next_quot, n32div1_3_next_rem,
       n32div1_4_next_quot, n32div1_4_next_rem, n32div1_5_next_quot, n32div1_5_next_rem, n32div1_6_next_quot,
       n32div1_6_next_rem, n32div1_7_next_quot, n32div1_7_next_rem, n32div1_8_next_quot, n32div1_8_next_rem,
       n32div1_9_next_quot, n32div1_9_next_rem, n32div1_10_next_quot, n32div1_10_next_rem,
       n32div1_11_next_quot, n32div1_11_next_rem, n32div1_12_next_quot, n32div1_12_next_rem,
       n32div1_13_next_quot, n32div1_13_next_rem, n32div1_14_next_quot, n32div1_14_next_rem,
       n32div1_15_next_quot, n32div1_15_next_rem, n32div1_16_next_quot, n32div1_16_next_rem,
       n32div1_17_next_quot, n32div1_17_next_rem, n32div1_18_next_quot, n32div1_18_next_rem,
       n32div1_19_next_quot, n32div1_19_next_rem, n32div1_20_next_quot, n32div1_20_next_rem,
       n32div1_21_next_quot, n32div1_21_next_rem, n32div1_22_next_quot, n32div1_22_next_rem,
       n32div1_23_next_quot, n32div1_23_next_rem, n32div1_24_next_quot, n32div1_24_next_rem,
       n32div1_25_next_quot, n32div1_25_next_rem, n32div1_26_next_quot, n32div1_26_next_rem,
       n32div1_27_next_quot, n32div1_27_next_rem, n32div1_28_next_quot, n32div1_28_next_rem,
       n32div1_29_next_quot, n32div1_29_next_rem, n32div1_30_next_quot, n32div1_30_next_rem,
       n32div1_31_next_quot, n32div1_31_next_rem, n32div1_32_next_quot, n32div1_32_next_rem;

  _32div1 u_32div1_1 (
    .d(d), .cur_rem(n32div1_5_next_rem), .cur_quot(n32div1_5_next_quot), .next_rem(n32div1_1_next_rem),
    .next_quot(n32div1_1_next_quot));
  _32div1 u_32div1_2 (
    .d(d), .cur_rem(n32div1_6_next_rem), .cur_quot(n32div1_6_next_quot), .next_rem(rem), .next_quot(quot));
  _32div1 u_32div1_3 (
    .d(d), .cur_rem({32{1'b0}}), .cur_quot(n), .next_rem(n32div1_3_next_rem), .next_quot(n32div1_3_next_quot));
  _32div1 u_32div1_4 (
    .d(d), .cur_rem(n32div1_1_next_rem), .cur_quot(n32div1_1_next_quot), .next_rem(n32div1_4_next_rem),
    .next_quot(n32div1_4_next_quot));
  _32div1 u_32div1_5 (
    .d(d), .cur_rem(n32div1_8_next_rem), .cur_quot(n32div1_8_next_quot), .next_rem(n32div1_5_next_rem),
    .next_quot(n32div1_5_next_quot));
  _32div1 u_32div1_6 (
    .d(d), .cur_rem(n32div1_10_next_rem), .cur_quot(n32div1_10_next_quot), .next_rem(n32div1_6_next_rem),
    .next_quot(n32div1_6_next_quot));
  _32div1 u_32div1_7 (
    .d(d), .cur_rem(n32div1_3_next_rem), .cur_quot(n32div1_3_next_quot), .next_rem(n32div1_7_next_rem),
    .next_quot(n32div1_7_next_quot));
  _32div1 u_32div1_8 (
    .d(d), .cur_rem(n32div1_13_next_rem), .cur_quot(n32div1_13_next_quot), .next_rem(n32div1_8_next_rem),
    .next_quot(n32div1_8_next_quot));
  _32div1 u_32div1_9 (
    .d(d), .cur_rem(n32div1_4_next_rem), .cur_quot(n32div1_4_next_quot), .next_rem(n32div1_9_next_rem),
    .next_quot(n32div1_9_next_quot));
  _32div1 u_32div1_10 (
    .d(d), .cur_rem(n32div1_14_next_rem), .cur_quot(n32div1_14_next_quot), .next_rem(n32div1_10_next_rem),
    .next_quot(n32div1_10_next_quot));
  _32div1 u_32div1_11 (
    .d(d), .cur_rem(n32div1_7_next_rem), .cur_quot(n32div1_7_next_quot), .next_rem(n32div1_11_next_rem),
    .next_quot(n32div1_11_next_quot));
  _32div1 u_32div1_12 (
    .d(d), .cur_rem(n32div1_9_next_rem), .cur_quot(n32div1_9_next_quot), .next_rem(n32div1_12_next_rem),
    .next_quot(n32div1_12_next_quot));
  _32div1 u_32div1_13 (
    .d(d), .cur_rem(n32div1_17_next_rem), .cur_quot(n32div1_17_next_quot), .next_rem(n32div1_13_next_rem),
    .next_quot(n32div1_13_next_quot));
  _32div1 u_32div1_14 (
    .d(d), .cur_rem(n32div1_18_next_rem), .cur_quot(n32div1_18_next_quot), .next_rem(n32div1_14_next_rem),
    .next_quot(n32div1_14_next_quot));
  _32div1 u_32div1_15 (
    .d(d), .cur_rem(n32div1_11_next_rem), .cur_quot(n32div1_11_next_quot), .next_rem(n32div1_15_next_rem),
    .next_quot(n32div1_15_next_quot));
  _32div1 u_32div1_16 (
    .d(d), .cur_rem(n32div1_12_next_rem), .cur_quot(n32div1_12_next_quot), .next_rem(n32div1_16_next_rem),
    .next_quot(n32div1_16_next_quot));
  _32div1 u_32div1_17 (
    .d(d), .cur_rem(n32div1_20_next_rem), .cur_quot(n32div1_20_next_quot), .next_rem(n32div1_17_next_rem),
    .next_quot(n32div1_17_next_quot));
  _32div1 u_32div1_18 (
    .d(d), .cur_rem(n32div1_22_next_rem), .cur_quot(n32div1_22_next_quot), .next_rem(n32div1_18_next_rem),
    .next_quot(n32div1_18_next_quot));
  _32div1 u_32div1_19 (
    .d(d), .cur_rem(n32div1_15_next_rem), .cur_quot(n32div1_15_next_quot), .next_rem(n32div1_19_next_rem),
    .next_quot(n32div1_19_next_quot));
  _32div1 u_32div1_20 (
    .d(d), .cur_rem(n32div1_25_next_rem), .cur_quot(n32div1_25_next_quot), .next_rem(n32div1_20_next_rem),
    .next_quot(n32div1_20_next_quot));
  _32div1 u_32div1_21 (
    .d(d), .cur_rem(n32div1_16_next_rem), .cur_quot(n32div1_16_next_quot), .next_rem(n32div1_21_next_rem),
    .next_quot(n32div1_21_next_quot));
  _32div1 u_32div1_22 (
    .d(d), .cur_rem(n32div1_26_next_rem), .cur_quot(n32div1_26_next_quot), .next_rem(n32div1_22_next_rem),
    .next_quot(n32div1_22_next_quot));
  _32div1 u_32div1_23 (
    .d(d), .cur_rem(n32div1_19_next_rem), .cur_quot(n32div1_19_next_quot), .next_rem(n32div1_23_next_rem),
    .next_quot(n32div1_23_next_quot));
  _32div1 u_32div1_24 (
    .d(d), .cur_rem(n32div1_21_next_rem), .cur_quot(n32div1_21_next_quot), .next_rem(n32div1_24_next_rem),
    .next_quot(n32div1_24_next_quot));
  _32div1 u_32div1_25 (
    .d(d), .cur_rem(n32div1_29_next_rem), .cur_quot(n32div1_29_next_quot), .next_rem(n32div1_25_next_rem),
    .next_quot(n32div1_25_next_quot));
  _32div1 u_32div1_26 (
    .d(d), .cur_rem(n32div1_30_next_rem), .cur_quot(n32div1_30_next_quot), .next_rem(n32div1_26_next_rem),
    .next_quot(n32div1_26_next_quot));
  _32div1 u_32div1_27 (
    .d(d), .cur_rem(n32div1_23_next_rem), .cur_quot(n32div1_23_next_quot), .next_rem(n32div1_27_next_rem),
    .next_quot(n32div1_27_next_quot));
  _32div1 u_32div1_28 (
    .d(d), .cur_rem(n32div1_24_next_rem), .cur_quot(n32div1_24_next_quot), .next_rem(n32div1_28_next_rem),
    .next_quot(n32div1_28_next_quot));
  _32div1 u_32div1_29 (
    .d(d), .cur_rem(n32div1_31_next_rem), .cur_quot(n32div1_31_next_quot), .next_rem(n32div1_29_next_rem),
    .next_quot(n32div1_29_next_quot));
  _32div1 u_32div1_30 (
    .d(d), .cur_rem(n32div1_32_next_rem), .cur_quot(n32div1_32_next_quot), .next_rem(n32div1_30_next_rem),
    .next_quot(n32div1_30_next_quot));
  _32div1 u_32div1_31 (
    .d(d), .cur_rem(n32div1_27_next_rem), .cur_quot(n32div1_27_next_quot), .next_rem(n32div1_31_next_rem),
    .next_quot(n32div1_31_next_quot));
  _32div1 u_32div1_32 (
    .d(d), .cur_rem(n32div1_28_next_rem), .cur_quot(n32div1_28_next_quot), .next_rem(n32div1_32_next_rem),
    .next_quot(n32div1_32_next_quot));
endmodule

module \_32位除法器测试电路  (
  input  [31:0] n,
  input  [31:0] d,
  output [31:0] \测试quot ,
  output [31:0] \测试rem ,
  output [31:0] quot,
  output [31:0] rem
);

  // Probe on n
  // Probe on d
  Divider #(.width(32)) divider_1 (.a(n), .b(d), .out(\测试quot ), .rem(\测试rem ));  // open: upper
  \_32位除法器  \u_32位除法器_1  (.n(n), .rem(rem), .quot(quot), .d(d));
  // Probe on rem
  // Probe on quot
endmodule

module _32div1 (
  input  [31:0] d,
  input  [31:0] cur_rem,
  input  [31:0] cur_quot,
  output [31:0] next_rem,
  output [31:0] next_quot
);

  wire comparator_1_gt;
  wire [31:0] or_1_out, or_2_out, shifter_1_out, shifter_2_out, shifter_3_out, subtractor_1_out;

  Shifter #(.width(32), .shift("ll")) shifter_1 (.in(cur_rem), .\dist (5'b00001), .out(shifter_1_out));
  Shifter #(.width(32), .shift("lr")) shifter_2 (.in(cur_quot), .\dist ({5{1'b1}}), .out(shifter_2_out));
  Shifter #(.width(32), .shift("ll")) shifter_3 (.in(cur_quot), .\dist (5'b00001), .out(shifter_3_out));
  assign or_1_out = shifter_1_out | shifter_2_out;  // OR_Gate or_1, 32 bits wide
  Comparator #(.width(32), .mode("unsigned")) comparator_1 (.a(d), .b(or_1_out), .gt(comparator_1_gt));  // open: eq, lt
  Subtractor #(.width(32)) subtractor_1 (.a(or_1_out), .b(d), .out(subtractor_1_out));  // open: bin, bout
  Multiplexer #(.select(1), .width(32), .disabled("Z"), .enable("false")) multiplexer_1 (
    .in0(or_2_out), .in1(shifter_3_out), .out(next_quot), .sel(comparator_1_gt));
  assign or_2_out = shifter_3_out | 32'h1;  // OR_Gate or_2, 32 bits wide
  Multiplexer #(.select(1), .width(32), .disabled("Z"), .enable("false")) multiplexer_2 (
    .in0(subtractor_1_out), .in1(or_1_out), .out(next_rem), .sel(comparator_1_gt));
endmodule
