// Logisim project cpu24.circ as structural Verilog: 25 circuits, main circuit ◇单周期MIPS
module \单周期MIPS  (
  input  IR1,
  input  IR2,
  input  IR3,
  output RegWrite,
  output MemWrite,
  output [31:0] PC,
  output [31:0] IR,
  output [31:0] RDin,
  output [31:0] MDin,
  output [31:0] LedData
);

  wire AluSrcB, and_1_out, and_2_out, and_3_out, and_4_out, and_5_out, and_6_out, BEqual, BGTZ, CLK,
       clock_2_out, comparator_1_eq, comparator_2_eq, comparator_2_lt, comparator_3_gt, comparator_4_eq,
       d_ff_1_q, equal, Go, Halt, IR1_t, IR2_t, IR3_t, IRA, IRB, IRC, JAL, JMP, JR, LBU, LUI, MemToReg,
       nand_1_out, not_1_out, not_2_out, RegDst, SignedExt, Syscall, W1, W2, W3, \单周期硬布线控制器_1_beq ,
       \单周期硬布线控制器_1_bne ;
  wire [3:0] AluOP;
  wire [4:0] multiplexer_4_out, multiplexer_5_out, multiplexer_6_out, multiplexer_7_out, multiplexer_10_out;
  wire [7:0] multiplexer_13_out, multiplexer_13_out_2, multiplexer_13_out_3, multiplexer_13_out_4,
       multiplexer_14_out;
  wire [12:0] CNT_num;
  wire [15:0] \总周期数 ;
  wire [27:0] PC_4;
  wire [31:0] adder_3_out, bit_extender_1_out, bit_extender_2_out, bit_extender_3_out, Din, imme,
       mips_alu_1_result, multiplexer_1_out, multiplexer_2_out, multiplexer_3_out, multiplexer_9_out,
       multiplexer_11_out, multiplexer_16_out, PCBranch, ram_1_data, rs, shifter_1_out;
  wire [31:28] JMPAddr;

  Clock #(.highDuration(1), .lowDuration(1)) clock_1 ();  // open: out
  Button _1 (.out(IRA));
  Button _2 (.out(IRB));
  Button _3 (.out(IRC));
  Counter #(.width(16), .max('hffff), .ongoal("wrap"), .trigger("rising"), .behavior("old")) counter_1 (
    .Q(\总周期数 ), .clk(and_1_out));  // open: load, D, count, carry, clr, preset
  and and_1 (and_1_out, ~Halt, CLK);  // AND_Gate
  Button \u_继续运行  (.out(Go));
  LED #(.active("true")) led_1 (.in(W1));
  LED #(.active("true")) led_2 (.in(W2));
  LED #(.active("true")) led_3 (.in(W3));
  Comparator #(.width(32), .mode("twosComplement")) comparator_1 (
    .a(rs), .b(32'h22), .eq(comparator_1_eq));  // open: gt, lt
  and and_2 (and_2_out, JMP, ~JR);  // AND_Gate
  not not_1 (not_1_out, Halt);
  Multiplexer #(.select(1), .width(32), .disabled("Z"), .enable("false")) multiplexer_1 (
    .in0(multiplexer_2_out), .in1({JMPAddr, IR[25:0], 2'b00}), .out(multiplexer_1_out), .sel(and_2_out));
  Multiplexer #(.select(1), .width(32), .disabled("Z"), .enable("false")) multiplexer_2 (
    .in0(multiplexer_3_out), .in1(rs), .out(multiplexer_2_out), .sel(JR));
  Multiplexer #(.select(1), .width(32), .disabled("Z"), .enable("false")) multiplexer_3 (
    .in0({JMPAddr, PC_4}), .in1(PCBranch), .out(multiplexer_3_out), .sel(BEqual));
  Hex_Digit_Display hex_digit_display_1 (.value(LedData[31:28]));  // open: dp
  Register #(.width(32), .trigger("rising"), .Select("low")) register_1 (
    .D(MDin), .en(comparator_1_eq), .Q(LedData), .clk(CLK));  // open: clr
  and and_3 (and_3_out, ~comparator_1_eq, Syscall);  // AND_Gate
  Register #(.width(32), .trigger("rising"), .Select("low")) u_PC (
    .D(multiplexer_1_out), .en(not_1_out), .Q(PC), .clk(CLK));  // open: clr
  D_Flip_Flop #(.trigger("high"), .Pre_Clr_Positions("LEGACY"), .NegatePresetClear("false"), .enable("true"), .NewFFLayout("false")) d_ff_1 (.Q(d_ff_1_q));  // open: clk, D, Qn, preset, en, reset
  // Probe on 13'hc
  Hex_Digit_Display hex_digit_display_2 (.value(LedData[27:24]));  // open: dp
  Hex_Digit_Display hex_digit_display_3 (.value(LedData[23:20]));  // open: dp
  Register #(.width(1), .trigger("rising"), .Select("low")) register_2 (
    .D(and_3_out), .en(and_3_out), .Q(Halt), .clk(CLK), .clr(Go));
  Comparator #(.width(13), .mode("twosComplement")) comparator_2 (
    .a(CNT_num), .b(13'hc), .eq(comparator_2_eq), .lt(comparator_2_lt));  // open: gt
  Clock #(.highDuration(1), .lowDuration(1)) clock_2 (.out(clock_2_out));
  Hex_Digit_Display hex_digit_display_4 (.value(LedData[15:12]));  // open: dp
  Hex_Digit_Display hex_digit_display_5 (.value(LedData[19:16]));  // open: dp
  Adder #(.width(32)) adder_1 (.a(PC), .b(32'h4), .out({JMPAddr, PC_4}));  // open: cin, cout
  \单周期硬布线控制器  \u_单周期硬布线控制器_1  (
    .Func(IR[5:0]), .OP(IR[31:26]), .ALU_OP(AluOP), .MemToReg(MemToReg), .MemWrite(MemWrite),
    .ALU_SRC(AluSrcB), .RegWrite(RegWrite), .SysCALL(Syscall), .SignedExt(SignedExt), .RegDst(RegDst),
    .JR(JR), .JMP(JMP), .Beq(\单周期硬布线控制器_1_beq ), .JAL(JAL), .Bne(\单周期硬布线控制器_1_bne ), .LUI(LUI), .LBU(LBU),
    .BGTZ(BGTZ));  // open: ERET, MF, MFC0, MTC0
  nand nand_1 (nand_1_out, d_ff_1_q, comparator_2_eq);
  Counter #(.width(13), .max('h1fff), .ongoal("stay"), .trigger("rising"), .behavior("old")) counter_2 (
    .count(comparator_2_lt), .Q(CNT_num), .clk(clock_2_out));  // open: load, D, carry, clr, preset
  Hex_Digit_Display hex_digit_display_6 (.value(LedData[11:8]));  // open: dp
  Hex_Digit_Display hex_digit_display_7 (.value(LedData[7:4]));  // open: dp
  // Probe on \总周期数 
  // Mips_Probe mips_probe_1: pin names not known; wires that end beside it: IR
  ROM #(.addrWidth(10), .dataWidth(32), .Select("high")) rom_1 (.addr(PC[11:2]), .data(IR));
  Hex_Digit_Display hex_digit_display_8 (.value(LedData[3:0]));  // open: dp
  assign CLK = nand_1_out ? clock_2_out : 1'bz;  // Controlled_Buffer controlled_buffer_1
  Pull_Resistor #(.pull(1)) pull_resistor_1 (.node(CLK));
  Multiplexer #(.select(1), .width(5), .disabled("Z"), .enable("false")) multiplexer_4 (
    .in0(IR[25:21]), .in1(5'b00010), .out(multiplexer_4_out), .sel(Syscall));
  Multiplexer #(.select(1), .width(5), .disabled("Z"), .enable("false")) multiplexer_5 (
    .in0(IR[20:16]), .in1(5'b00100), .out(multiplexer_5_out), .sel(Syscall));
  Multiplexer #(.select(1), .width(5), .disabled("Z"), .enable("false")) multiplexer_6 (
    .in0(IR[20:16]), .in1(IR[15:11]), .out(multiplexer_6_out), .sel(RegDst));
  and and_4 (and_4_out, equal, \单周期硬布线控制器_1_beq );
  and and_5 (and_5_out, ~equal, \单周期硬布线控制器_1_bne );  // AND_Gate
  or or_1 (IR1_t, IR1, IRA);
  Multiplexer #(.select(1), .width(5), .disabled("Z"), .enable("false")) multiplexer_7 (
    .in0(multiplexer_6_out), .in1({5{1'b1}}), .out(multiplexer_7_out), .sel(JAL));
  assign bit_extender_1_out = {{16{1'b0}}, IR[15:0]};  // Bit_Extender bit_extender_1
  assign bit_extender_2_out = {{16{IR[15]}}, IR[15:0]};  // Bit_Extender bit_extender_2
  and and_6 (and_6_out, BGTZ, comparator_3_gt);
  Comparator #(.width(32), .mode("twosComplement")) comparator_3 (
    .a(rs), .b({32{1'b0}}), .gt(comparator_3_gt));  // open: eq, lt
  or or_2 (IR2_t, IR2, IRB);
  Multiplexer #(.select(1), .width(32), .disabled("Z"), .enable("false")) multiplexer_8 (
    .in0(bit_extender_1_out), .in1(bit_extender_2_out), .out(imme), .sel(SignedExt));
  MIPS_Regifile mips_regifile_1 (
    .Din(Din), .Clk(CLK), .R1(rs), .R2(MDin), .WE(RegWrite), .W_num(multiplexer_7_out),
    .R1_num(multiplexer_4_out), .R2_num(multiplexer_5_out));
  or or_3 (BEqual, and_4_out, and_6_out, and_5_out);
  or or_4 (IR3_t, IR3, IRC);
  Multiplexer #(.select(1), .width(32), .disabled("Z"), .enable("false")) multiplexer_9 (
    .in0(MDin), .in1(imme), .out(multiplexer_9_out), .sel(AluSrcB));
  Shifter #(.width(32), .shift("ll")) shifter_1 (.in(imme), .\dist (5'b00010), .out(shifter_1_out));
  MIPS_ALU mips_alu_1 (
    .X(rs), .Y(multiplexer_9_out), .AluOP(AluOP), .Equal(equal), .Result(mips_alu_1_result),
    .shamt(multiplexer_10_out));  // open: Result_2
  Adder #(.width(32)) adder_2 (.a(shifter_1_out), .b({JMPAddr, PC_4}), .out(PCBranch));  // open: cin, cout
  Multiplexer #(.select(1), .width(5), .disabled("Z"), .enable("false")) multiplexer_10 (
    .in0(IR[10:6]), .in1(rs[4:0]), .out(multiplexer_10_out), .sel(comparator_4_eq));
  Comparator #(.width(6), .mode("twosComplement")) comparator_4 (
    .a(IR[5:0]), .b(6'b000111), .eq(comparator_4_eq));  // open: gt, lt
  Multiplexer #(.select(1), .width(32), .disabled("Z"), .enable("false")) multiplexer_11 (
    .in0(mips_alu_1_result), .in1(adder_3_out), .out(multiplexer_11_out), .sel(LBU));
  Adder #(.width(32)) adder_3 (.a(rs), .b(imme), .out(adder_3_out));  // open: cin, cout
  not not_2 (not_2_out, Halt);
  RAM #(.addrWidth(10), .dataWidth(32), .bus("separate"), .Select("high")) ram_1 (
    .addr(multiplexer_11_out[11:2]), .din(MDin), .data(ram_1_data), .str(MemWrite), .sel(not_2_out), .clk(CLK));  // open: ld, clr
  Multiplexer #(.select(1), .width(32), .disabled("Z"), .enable("false")) multiplexer_12 (
    .in0(RDin), .in1({IR[15:0], {16{1'b0}}}), .out(Din), .sel(LUI));
  Multiplexer #(.select(1), .width(32), .disabled("Z"), .enable("false")) multiplexer_13 (
    .in0(mips_alu_1_result), .in1(ram_1_data),
    .out({multiplexer_13_out_4, multiplexer_13_out_3, multiplexer_13_out_2, multiplexer_13_out}),
    .sel(MemToReg));
  Multiplexer #(.select(2), .width(8), .disabled("Z"), .enable("false")) multiplexer_14 (
    .in0(multiplexer_13_out), .in1(multiplexer_13_out_2), .in2(multiplexer_13_out_3),
    .in3(multiplexer_13_out_4), .out(multiplexer_14_out), .sel(multiplexer_11_out[1:0]));
  assign bit_extender_3_out = {{24{1'b0}}, multiplexer_14_out};  // Bit_Extender bit_extender_3
  Multiplexer #(.select(1), .width(32), .disabled("Z"), .enable("false")) multiplexer_15 (
    .in0(multiplexer_16_out), .in1({JMPAddr, PC_4}), .out(RDin), .sel(JAL));
  Multiplexer #(.select(1), .width(32), .disabled("Z"), .enable("false")) multiplexer_16 (
    .in0({multiplexer_13_out_4, multiplexer_13_out_3, multiplexer_13_out_2, multiplexer_13_out}),
    .in1(bit_extender_3_out), .out(multiplexer_16_out), .sel(LBU));

  // Other names for the same wires on the sheet: _0_15[15:0] = IR[15:0]; Func[5:0] = IR[5:0];
  //   JMPAddr[27:2] = IR[25:0]; shamt[4:0] = IR[10:6]; OP[5:0] = IR[31:26]; PC_4[31:28] = JMPAddr; rt[31:0] = MDin

  // Notes on the sheet:
  //   中断源
  //   中断等待指示
  //   总复位信号应将除ROM以外所有存储组件全部清零
  //   控制位
  //   暂停节拍，不能为0
  //   JMP
  //   JR
  //   OP
  //   Func
  //   戳工具置1进入计数暂停模式，ctrl+k时钟自动运行到对应节拍暂停
  //   ctrl+k关闭时钟连续运行，将控制位置零，进入单步调试模式调试
  //   用这个时钟源需要去掉电路中的其他时钟源
  //   数码管输出
  //   指令存储器
  //   Beq
  //   Bne
  //   MemToReg
  //   MemWrite
  //   AluOP
  //   AluSrcB
  //   RegWrite
  //   JAL
  //   RegDst
  //   Syscall
  //   数码管输出应该用寄存器锁存，否则显示数据只能一闪而过
  //   指令字
  //   contents of rom_1 (hex, n*v repeats v):
  //   2011000f 112020 20020022 c 2231ffff 1e20fffb 2002000a c
  //   可计数暂停的时钟源
  //   OP
  //   Func
  //   rs
  //   rt
  //   rd
  //   SRAV指令
  //   为方便自动评测，需要输出PC，IR，寄存器堆写如数据RDin
  //   RAM写使能MemWrite、RAM写入数据MDin等信号
endmodule

// 单周期硬布线控制器
module \单周期硬布线控制器  (
  input  [5:0] OP,
  input  [5:0] Func,
  input  [4:0] MF,
  output [3:0] ALU_OP,
  output MemToReg,
  output MemWrite,
  output ALU_SRC,
  output RegWrite,
  output SysCALL,
  output SignedExt,
  output RegDst,
  output Beq,
  output Bne,
  output JR,
  output JMP,
  output JAL,
  output LUI,
  output LBU,
  output BGTZ,
  output ERET,
  output MFC0,
  output MTC0
);

  \运算控制器自动生成  \u_运算控制器自动生成_1  (
    .OP0(OP[0]), .OP1(OP[1]), .OP2(OP[2]), .OP3(OP[3]), .OP4(OP[4]), .OP5(OP[5]), .F0(Func[0]), .F1(Func[1]),
    .F2(Func[2]), .F3(Func[3]), .F4(Func[4]), .F5(Func[5]), .S0(ALU_OP[0]), .S1(ALU_OP[1]), .S2(ALU_OP[2]),
    .S3(ALU_OP[3]));
  \控制信号自动生成  \u_控制信号自动生成_1  (
    .OP0(OP[0]), .OP1(OP[1]), .OP2(OP[2]), .MemToReg(MemToReg), .OP3(OP[3]), .OP4(OP[4]), .OP5(OP[5]),
    .MemWrite(MemWrite), .F0(Func[0]), .F1(Func[1]), .F2(Func[2]), .F3(Func[3]), .F4(Func[4]), .F5(Func[5]),
    .MF0(MF[0]), .ALU_SRC(ALU_SRC), .MF1(MF[1]), .MF2(MF[2]), .MF3(MF[3]), .MF4(MF[4]), .RegWrite(RegWrite),
    .SysCALL(SysCALL), .SignedExt(SignedExt), .RegDst(RegDst), .BEQ(Beq), .BNE(Bne), .JR(JR), .JUMP(JMP),
    .JAL(JAL), .LUI(LUI), .LBU(LBU), .BGTZ(BGTZ), .ERET(ERET), .MFC0(MFC0), .MTC0(MTC0));

  // Other names for the same wires on the sheet: OP_CODE[5:0] = OP

  // Notes on the sheet:
  //   运算器控制器，根据指令生成运算器功能选择信号
  //   控制信号生成，产生数据通路需要的其他控制信号
endmodule

// 运算器控制器
module \运算控制器自动生成  (
  input  OP0,
  input  OP1,
  input  OP2,
  input  OP3,
  input  OP4,
  input  OP5,
  input  F0,
  input  F1,
  input  F2,
  input  F3,
  input  F4,
  input  F5,
  output S0,
  output S1,
  output S2,
  output S3
);

  wire and_1_out, and_2_out, and_3_out, and_4_out, and_5_out, and_6_out, and_7_out, and_8_out, and_9_out,
       and_10_out, and_11_out, and_12_out, and_13_out, and_14_out, and_15_out, and_16_out, and_17_out,
       and_18_out, and_19_out, and_20_out, and_21_out, and_22_out, and_23_out, and_24_out, and_25_out,
       and_26_out, and_27_out, and_28_out, and_29_out, and_30_out, and_31_out, and_32_out, and_33_out,
       and_34_out, and_35_out, and_36_out, and_37_out, and_38_out, and_39_out, and_40_out, and_41_out,
       not_1_out, not_2_out, not_3_out, not_4_out, not_5_out, not_6_out, not_7_out, not_8_out, not_9_out,
       not_10_out, not_11_out, not_12_out, not_13_out, not_14_out, not_15_out, not_16_out, not_17_out,
       not_18_out, not_19_out, not_20_out, not_21_out, not_22_out, not_23_out, not_24_out, not_25_out,
       not_26_out, not_27_out, not_28_out, not_29_out, not_30_out, not_31_out, not_32_out, not_33_out,
       not_34_out, not_35_out, not_36_out, not_37_out, not_38_out, not_39_out, not_40_out, not_41_out,
       not_42_out, not_43_out, not_44_out, not_45_out, not_46_out, not_47_out, not_48_out, not_49_out,
       not_50_out, not_51_out, not_52_out, not_53_out, not_54_out, not_55_out, not_56_out, not_57_out,
       not_58_out, not_59_out, not_60_out, not_61_out, not_62_out, not_63_out, not_64_out, not_65_out,
       not_66_out, not_67_out, not_68_out, not_69_out, not_70_out, not_71_out, not_72_out, not_73_out,
       not_74_out, not_75_out, not_76_out, not_77_out, not_78_out, not_79_out, not_80_out, not_81_out,
       not_82_out, not_83_out, not_84_out, not_85_out, not_86_out, not_87_out, not_88_out, not_89_out,
       not_90_out, not_91_out, not_92_out, not_93_out, not_94_out, not_95_out, not_96_out, not_97_out,
       not_98_out, not_99_out, not_100_out, not_101_out, not_102_out, not_103_out, not_104_out, not_105_out,
       not_106_out, not_107_out, not_108_out, not_109_out, not_110_out, not_111_out, not_112_out,
       not_113_out, not_114_out, not_115_out, not_116_out, not_117_out, not_118_out, not_119_out,
       not_120_out, not_121_out, not_122_out, not_123_out, not_124_out, not_125_out, not_126_out,
       not_127_out, not_128_out, not_129_out, not_130_out, not_131_out, not_132_out, not_133_out,
       not_134_out, not_135_out, not_136_out, not_137_out, not_138_out, not_139_out, not_140_out,
       not_141_out, not_142_out, not_143_out, not_144_out, not_145_out, not_146_out, not_147_out,
       not_148_out, not_149_out, not_150_out, not_151_out, not_152_out, not_153_out, not_154_out,
       not_155_out, not_156_out, not_157_out, not_158_out, not_159_out, not_160_out, not_161_out,
       not_162_out, not_163_out, not_164_out, not_165_out, not_166_out, not_167_out, not_168_out,
       not_169_out, not_170_out, not_171_out, not_172_out, not_173_out, not_174_out, not_175_out,
       not_176_out, not_177_out, not_178_out, not_179_out, not_180_out, not_181_out, not_182_out,
       not_183_out, not_184_out, not_185_out, not_186_out, not_187_out, not_188_out, not_189_out,
       not_190_out, not_191_out, not_192_out, not_193_out, not_194_out, not_195_out, not_196_out,
       not_197_out, not_198_out, not_199_out, not_200_out, not_201_out, not_202_out, not_203_out,
       not_204_out, not_205_out, not_206_out, not_207_out, not_208_out, not_209_out, not_210_out,
       not_211_out, not_212_out, not_213_out, not_214_out, not_215_out, not_216_out, not_217_out,
       not_218_out, not_219_out, not_220_out, not_221_out, not_222_out, not_223_out, not_224_out,
       not_225_out, not_226_out, not_227_out, not_228_out, not_229_out, not_230_out, not_231_out,
       not_232_out, not_233_out, not_234_out, not_235_out, not_236_out, not_237_out, not_238_out,
       not_239_out, not_240_out, not_241_out, not_242_out, not_243_out, not_244_out, not_245_out,
       not_246_out, not_247_out, not_248_out, not_249_out, not_250_out, not_251_out, not_252_out,
       not_253_out, not_254_out, not_255_out, not_256_out, not_257_out, not_258_out, not_259_out,
       not_260_out, not_261_out, not_262_out, not_263_out;

  not not_1 (not_1_out, OP5);
  not not_2 (not_2_out, OP4);
  not not_3 (not_3_out, OP3);
  not not_4 (not_4_out, OP2);
  not not_5 (not_5_out, OP1);
  not not_6 (not_6_out, OP0);
  not not_7 (not_7_out, F5);
  not not_8 (not_8_out, F4);
  not not_9 (not_9_out, F3);
  not not_10 (not_10_out, F2);
  not not_11 (not_11_out, OP5);
  not not_12 (not_12_out, OP4);
  not not_13 (not_13_out, OP3);
  not not_14 (not_14_out, OP2);
  not not_15 (not_15_out, OP1);
  not not_16 (not_16_out, OP0);
  not not_17 (not_17_out, F4);
  not not_18 (not_18_out, F3);
  not not_19 (not_19_out, F2);
  not not_20 (not_20_out, F1);
  not not_21 (not_21_out, F0);
  not not_22 (not_22_out, OP5);
  not not_23 (not_23_out, OP4);
  not not_24 (not_24_out, OP3);
  not not_25 (not_25_out, OP2);
  not not_26 (not_26_out, OP1);
  not not_27 (not_27_out, OP0);
  not not_28 (not_28_out, F4);
  not not_29 (not_29_out, F3);
  not not_30 (not_30_out, F2);
  not not_31 (not_31_out, F1);
  not not_32 (not_32_out, OP5);
  not not_33 (not_33_out, OP4);
  not not_34 (not_34_out, OP3);
  not not_35 (not_35_out, OP2);
  not not_36 (not_36_out, OP1);
  not not_37 (not_37_out, OP0);
  not not_38 (not_38_out, F4);
  not not_39 (not_39_out, F3);
  not not_40 (not_40_out, F1);
  not not_41 (not_41_out, F0);
  not not_42 (not_42_out, OP5);
  not not_43 (not_43_out, OP4);
  not not_44 (not_44_out, OP3);
  not not_45 (not_45_out, OP2);
  not not_46 (not_46_out, OP1);
  not not_47 (not_47_out, OP0);
  not not_48 (not_48_out, F4);
  not not_49 (not_49_out, F2);
  not not_50 (not_50_out, F0);
  not not_51 (not_51_out, OP5);
  not not_52 (not_52_out, OP4);
  not not_53 (not_53_out, OP2);
  not not_54 (not_54_out, OP1);
  not not_55 (not_55_out, OP0);
  not not_56 (not_56_out, OP5);
  not not_57 (not_57_out, OP4);
  not not_58 (not_58_out, OP1);
  not not_59 (not_59_out, OP0);
  not not_60 (not_60_out, OP5);
  not not_61 (not_61_out, OP4);
  not not_62 (not_62_out, OP2);
  not not_63 (not_63_out, OP1);
  not not_64 (not_64_out, OP5);
  not not_65 (not_65_out, OP4);
  not not_66 (not_66_out, OP2);
  not not_67 (not_67_out, OP0);
  not not_68 (not_68_out, OP4);
  not not_69 (not_69_out, OP3);
  not not_70 (not_70_out, OP2);
  not not_71 (not_71_out, OP4);
  not not_72 (not_72_out, OP2);
  not not_73 (not_73_out, OP5);
  not not_74 (not_74_out, OP4);
  not not_75 (not_75_out, OP3);
  not not_76 (not_76_out, OP2);
  not not_77 (not_77_out, OP1);
  not not_78 (not_78_out, OP0);
  not not_79 (not_79_out, F5);
  not not_80 (not_80_out, F4);
  not not_81 (not_81_out, F3);
  not not_82 (not_82_out, OP5);
  not not_83 (not_83_out, OP4);
  not not_84 (not_84_out, OP4);
  not not_85 (not_85_out, OP3);
  not not_86 (not_86_out, OP1);
  not not_87 (not_87_out, OP0);
  not not_88 (not_88_out, OP5);
  not not_89 (not_89_out, OP4);
  not not_90 (not_90_out, OP3);
  not not_91 (not_91_out, OP5);
  not not_92 (not_92_out, OP4);
  not not_93 (not_93_out, OP3);
  not not_94 (not_94_out, OP2);
  not not_95 (not_95_out, OP1);
  not not_96 (not_96_out, OP0);
  not not_97 (not_97_out, F5);
  not not_98 (not_98_out, F4);
  not not_99 (not_99_out, F3);
  not not_100 (not_100_out, F2);
  not not_101 (not_101_out, F0);
  not not_102 (not_102_out, OP5);
  not not_103 (not_103_out, OP4);
  not not_104 (not_104_out, OP3);
  not not_105 (not_105_out, OP2);
  not not_106 (not_106_out, OP1);
  not not_107 (not_107_out, OP0);
  not not_108 (not_108_out, F4);
  not not_109 (not_109_out, F3);
  not not_110 (not_110_out, F2);
  not not_111 (not_111_out, F0);
  not not_112 (not_112_out, OP5);
  not not_113 (not_113_out, OP4);
  not not_114 (not_114_out, OP3);
  not not_115 (not_115_out, OP2);
  not not_116 (not_116_out, OP1);
  not not_117 (not_117_out, OP0);
  not not_118 (not_118_out, F4);
  not not_119 (not_119_out, F3);
  not not_120 (not_120_out, F1);
  not not_121 (not_121_out, F0);
  not not_122 (not_122_out, OP5);
  not not_123 (not_123_out, OP4);
  not not_124 (not_124_out, OP3);
  not not_125 (not_125_out, OP2);
  not not_126 (not_126_out, OP1);
  not not_127 (not_127_out, OP0);
  not not_128 (not_128_out, F4);
  not not_129 (not_129_out, F3);
  not not_130 (not_130_out, OP5);
  not not_131 (not_131_out, OP4);
  not not_132 (not_132_out, OP3);
  not not_133 (not_133_out, OP2);
  not not_134 (not_134_out, OP1);
  not not_135 (not_135_out, OP0);
  not not_136 (not_136_out, F4);
  not not_137 (not_137_out, F2);
  not not_138 (not_138_out, F0);
  not not_139 (not_139_out, OP5);
  not not_140 (not_140_out, OP4);
  not not_141 (not_141_out, OP1);
  not not_142 (not_142_out, OP0);
  not not_143 (not_143_out, OP5);
  not not_144 (not_144_out, OP4);
  not not_145 (not_145_out, OP2);
  not not_146 (not_146_out, OP0);
  not not_147 (not_147_out, OP5);
  not not_148 (not_148_out, OP4);
  not not_149 (not_149_out, OP3);
  not not_150 (not_150_out, OP2);
  not not_151 (not_151_out, OP1);
  not not_152 (not_152_out, OP0);
  not not_153 (not_153_out, F4);
  not not_154 (not_154_out, F3);
  not not_155 (not_155_out, F2);
  not not_156 (not_156_out, F1);
  not not_157 (not_157_out, F0);
  not not_158 (not_158_out, OP5);
  not not_159 (not_159_out, OP4);
  not not_160 (not_160_out, OP3);
  not not_161 (not_161_out, OP2);
  not not_162 (not_162_out, OP1);
  not not_163 (not_163_out, OP0);
  not not_164 (not_164_out, F4);
  not not_165 (not_165_out, F3);
  not not_166 (not_166_out, F2);
  not not_167 (not_167_out, F1);
  not not_168 (not_168_out, OP5);
  not not_169 (not_169_out, OP4);
  not not_170 (not_170_out, OP3);
  not not_171 (not_171_out, OP2);
  not not_172 (not_172_out, OP1);
  not not_173 (not_173_out, OP0);
  not not_174 (not_174_out, F4);
  not not_175 (not_175_out, F3);
  not not_176 (not_176_out, F2);
  not not_177 (not_177_out, F0);
  not not_178 (not_178_out, OP5);
  not not_179 (not_179_out, OP4);
  not not_180 (not_180_out, OP3);
  not not_181 (not_181_out, OP2);
  not not_182 (not_182_out, OP1);
  not not_183 (not_183_out, OP0);
  not not_184 (not_184_out, F4);
  not not_185 (not_185_out, F3);
  not not_186 (not_186_out, F1);
  not not_187 (not_187_out, F0);
  not not_188 (not_188_out, OP5);
  not not_189 (not_189_out, OP4);
  not not_190 (not_190_out, OP3);
  not not_191 (not_191_out, OP2);
  not not_192 (not_192_out, OP1);
  not not_193 (not_193_out, OP0);
  not not_194 (not_194_out, F4);
  not not_195 (not_195_out, F2);
  not not_196 (not_196_out, OP5);
  not not_197 (not_197_out, OP4);
  not not_198 (not_198_out, OP2);
  not not_199 (not_199_out, OP1);
  not not_200 (not_200_out, OP0);
  not not_201 (not_201_out, OP5);
  not not_202 (not_202_out, OP4);
  not not_203 (not_203_out, OP1);
  not not_204 (not_204_out, OP0);
  not not_205 (not_205_out, OP5);
  not not_206 (not_206_out, OP4);
  not not_207 (not_207_out, OP2);
  not not_208 (not_208_out, OP1);
  not not_209 (not_209_out, OP4);
  not not_210 (not_210_out, OP3);
  not not_211 (not_211_out, OP2);
  not not_212 (not_212_out, OP4);
  not not_213 (not_213_out, OP2);
  not not_214 (not_214_out, OP5);
  not not_215 (not_215_out, OP4);
  not not_216 (not_216_out, OP4);
  not not_217 (not_217_out, OP3);
  not not_218 (not_218_out, OP1);
  not not_219 (not_219_out, OP0);
  not not_220 (not_220_out, OP5);
  not not_221 (not_221_out, OP4);
  not not_222 (not_222_out, OP3);
  not not_223 (not_223_out, OP5);
  not not_224 (not_224_out, OP4);
  not not_225 (not_225_out, OP3);
  not not_226 (not_226_out, OP2);
  not not_227 (not_227_out, OP1);
  not not_228 (not_228_out, OP0);
  not not_229 (not_229_out, F4);
  not not_230 (not_230_out, F3);
  not not_231 (not_231_out, F1);
  not not_232 (not_232_out, OP5);
  not not_233 (not_233_out, OP4);
  not not_234 (not_234_out, OP3);
  not not_235 (not_235_out, OP2);
  not not_236 (not_236_out, OP1);
  not not_237 (not_237_out, OP0);
  not not_238 (not_238_out, F4);
  not not_239 (not_239_out, F3);
  not not_240 (not_240_out, OP5);
  not not_241 (not_241_out, OP4);
  not not_242 (not_242_out, OP3);
  not not_243 (not_243_out, OP2);
  not not_244 (not_244_out, OP1);
  not not_245 (not_245_out, OP0);
  not not_246 (not_246_out, F4);
  not not_247 (not_247_out, F2);
  not not_248 (not_248_out, F0);
  not not_249 (not_249_out, OP5);
  not not_250 (not_250_out, OP4);
  not not_251 (not_251_out, OP3);
  not not_252 (not_252_out, OP2);
  not not_253 (not_253_out, OP1);
  not not_254 (not_254_out, OP0);
  not not_255 (not_255_out, F4);
  not not_256 (not_256_out, F2);
  not not_257 (not_257_out, OP5);
  not not_258 (not_258_out, OP4);
  not not_259 (not_259_out, OP2);
  not not_260 (not_260_out, OP0);
  not not_261 (not_261_out, OP5);
  not not_262 (not_262_out, OP4);
  not not_263 (not_263_out, OP1);
  and and_1 (and_1_out, not_1_out, not_2_out, not_3_out, not_4_out, not_5_out, not_6_out, not_7_out, not_8_out, not_9_out, not_10_out, F1, F0);
  and and_2 (and_2_out, not_11_out, not_12_out, not_13_out, not_14_out, not_15_out, not_16_out, F5, not_17_out, not_18_out, not_19_out, not_20_out, not_21_out);
  and and_3 (and_3_out, not_22_out, not_23_out, not_24_out, not_25_out, not_26_out, not_27_out, F5, not_28_out, not_29_out, not_30_out, not_31_out, F0);
  and and_4 (and_4_out, not_32_out, not_33_out, not_34_out, not_35_out, not_36_out, not_37_out, F5, not_38_out, not_39_out, F2, not_40_out, not_41_out);
  and and_5 (and_5_out, not_42_out, not_43_out, not_44_out, not_45_out, not_46_out, not_47_out, F5, not_48_out, F3, not_49_out, F1, not_50_out);
  and and_6 (and_6_out, not_51_out, not_52_out, OP3, not_53_out, not_54_out, not_55_out);
  and and_7 (and_7_out, not_56_out, not_57_out, OP3, OP2, not_58_out, not_59_out);
  and and_8 (and_8_out, not_60_out, not_61_out, OP3, not_62_out, not_63_out, OP0);
  and and_9 (and_9_out, not_64_out, not_65_out, OP3, not_66_out, OP1, not_67_out);
  and and_10 (and_10_out, OP5, not_68_out, not_69_out, not_70_out, OP1, OP0);
  and and_11 (and_11_out, OP5, not_71_out, OP3, not_72_out, OP1, OP0);
  and and_12 (and_12_out, not_73_out, not_74_out, not_75_out, not_76_out, not_77_out, not_78_out, not_79_out, not_80_out, not_81_out, F2, F1, F0);
  and and_13 (and_13_out, not_82_out, not_83_out, OP3, OP2, OP1, OP0);
  and and_14 (and_14_out, OP5, not_84_out, not_85_out, OP2, not_86_out, not_87_out);
  and and_15 (and_15_out, not_88_out, not_89_out, not_90_out, OP2, OP1, OP0);
  and and_16 (and_16_out, not_91_out, not_92_out, not_93_out, not_94_out, not_95_out, not_96_out, not_97_out, not_98_out, not_99_out, not_100_out, F1, not_101_out);
  and and_17 (and_17_out, not_102_out, not_103_out, not_104_out, not_105_out, not_106_out, not_107_out, F5, not_108_out, not_109_out, not_110_out, F1, not_111_out);
  and and_18 (and_18_out, not_112_out, not_113_out, not_114_out, not_115_out, not_116_out, not_117_out, F5, not_118_out, not_119_out, F2, not_120_out, not_121_out);
  and and_19 (and_19_out, not_122_out, not_123_out, not_124_out, not_125_out, not_126_out, not_127_out, F5, not_128_out, not_129_out, F2, F1, F0);
  and and_20 (and_20_out, not_130_out, not_131_out, not_132_out, not_133_out, not_134_out, not_135_out, F5, not_136_out, F3, not_137_out, F1, not_138_out);
  and and_21 (and_21_out, not_139_out, not_140_out, OP3, OP2, not_141_out, not_142_out);
  and and_22 (and_22_out, not_143_out, not_144_out, OP3, not_145_out, OP1, not_146_out);
  and and_23 (and_23_out, not_147_out, not_148_out, not_149_out, not_150_out, not_151_out, not_152_out, F5, not_153_out, not_154_out, not_155_out, not_156_out, not_157_out);
  and and_24 (and_24_out, not_158_out, not_159_out, not_160_out, not_161_out, not_162_out, not_163_out, F5, not_164_out, not_165_out, not_166_out, not_167_out, F0);
  and and_25 (and_25_out, not_168_out, not_169_out, not_170_out, not_171_out, not_172_out, not_173_out, F5, not_174_out, not_175_out, not_176_out, F1, not_177_out);
  and and_26 (and_26_out, not_178_out, not_179_out, not_180_out, not_181_out, not_182_out, not_183_out, F5, not_184_out, not_185_out, F2, not_186_out, not_187_out);
  and and_27 (and_27_out, not_188_out, not_189_out, not_190_out, not_191_out, not_192_out, not_193_out, F5, not_194_out, F3, not_195_out, F1, F0);
  and and_28 (and_28_out, not_196_out, not_197_out, OP3, not_198_out, not_199_out, not_200_out);
  and and_29 (and_29_out, not_201_out, not_202_out, OP3, OP2, not_203_out, not_204_out);
  and and_30 (and_30_out, not_205_out, not_206_out, OP3, not_207_out, not_208_out, OP0);
  and and_31 (and_31_out, OP5, not_209_out, not_210_out, not_211_out, OP1, OP0);
  and and_32 (and_32_out, OP5, not_212_out, OP3, not_213_out, OP1, OP0);
  and and_33 (and_33_out, not_214_out, not_215_out, OP3, OP2, OP1, OP0);
  and and_34 (and_34_out, OP5, not_216_out, not_217_out, OP2, not_218_out, not_219_out);
  and and_35 (and_35_out, not_220_out, not_221_out, not_222_out, OP2, OP1, OP0);
  and and_36 (and_36_out, not_223_out, not_224_out, not_225_out, not_226_out, not_227_out, not_228_out, F5, not_229_out, not_230_out, F2, not_231_out, F0);
  and and_37 (and_37_out, not_232_out, not_233_out, not_234_out, not_235_out, not_236_out, not_237_out, F5, not_238_out, not_239_out, F2, F1, F0);
  and and_38 (and_38_out, not_240_out, not_241_out, not_242_out, not_243_out, not_244_out, not_245_out, F5, not_246_out, F3, not_247_out, F1, not_248_out);
  and and_39 (and_39_out, not_249_out, not_250_out, not_251_out, not_252_out, not_253_out, not_254_out, F5, not_255_out, F3, not_256_out, F1, F0);
  and and_40 (and_40_out, not_257_out, not_258_out, OP3, not_259_out, OP1, not_260_out);
  and and_41 (and_41_out, not_261_out, not_262_out, OP3, OP2, not_263_out, OP0);
  or or_1 (S1, and_16_out, and_17_out, and_18_out, and_19_out, and_20_out, and_21_out, and_22_out);
  or or_2 (S3, and_36_out, and_37_out, and_38_out, and_39_out, and_40_out, and_41_out);
  or or_3 (S0, and_1_out, and_2_out, and_3_out, and_4_out, and_5_out, and_6_out, and_7_out, and_8_out, and_9_out, and_10_out, and_11_out, and_12_out, and_13_out, and_14_out, and_15_out);
  or or_4 (S2, and_23_out, and_24_out, and_25_out, and_26_out, and_27_out, and_28_out, and_29_out, and_30_out, and_31_out, and_32_out, and_33_out, and_34_out, and_35_out);
endmodule

// 控制信号生成
module \控制信号自动生成  (
  input  OP0,
  input  OP1,
  input  OP2,
  input  OP3,
  input  OP4,
  input  OP5,
  input  F0,
  input  F1,
  input  F2,
  input  F3,
  input  F4,
  input  F5,
  input  MF0,
  input  MF1,
  input  MF2,
  input  MF3,
  input  MF4,
  output MemToReg,
  output MemWrite,
  output ALU_SRC,
  output RegWrite,
  output SysCALL,
  output SignedExt,
  output RegDst,
  output BEQ,
  output BNE,
  output JR,
  output JUMP,
  output JAL,
  output LUI,
  output LBU,
  output BGTZ,
  output ERET,
  output MFC0,
  output MTC0
);

  wire and_1_out, and_2_out, and_4_out, and_5_out, and_6_out, and_7_out, and_8_out, and_9_out, and_10_out,
       and_11_out, and_12_out, and_13_out, and_14_out, and_15_out, and_16_out, and_17_out, and_18_out,
       and_19_out, and_21_out, and_22_out, and_23_out, and_24_out, and_25_out, and_26_out, and_27_out,
       and_28_out, and_29_out, and_30_out, and_34_out, and_35_out, not_1_out, not_2_out, not_3_out,
       not_4_out, not_5_out, not_6_out, not_7_out, not_8_out, not_9_out, not_10_out, not_11_out, not_12_out,
       not_13_out, not_14_out, not_15_out, not_16_out, not_17_out, not_18_out, not_19_out, not_20_out,
       not_21_out, not_22_out, not_23_out, not_24_out, not_25_out, not_26_out, not_27_out, not_28_out,
       not_29_out, not_30_out, not_31_out, not_32_out, not_33_out, not_34_out, not_35_out, not_36_out,
       not_37_out, not_38_out, not_39_out, not_40_out, not_41_out, not_42_out, not_43_out, not_44_out,
       not_45_out, not_46_out, not_47_out, not_48_out, not_49_out, not_50_out, not_51_out, not_52_out,
       not_53_out, not_54_out, not_55_out, not_56_out, not_57_out, not_58_out, not_59_out, not_60_out,
       not_61_out, not_62_out, not_63_out, not_64_out, not_65_out, not_66_out, not_67_out, not_68_out,
       not_69_out, not_70_out, not_71_out, not_72_out, not_73_out, not_74_out, not_75_out, not_76_out,
       not_77_out, not_78_out, not_79_out, not_80_out, not_81_out, not_82_out, not_83_out, not_84_out,
       not_85_out, not_86_out, not_87_out, not_88_out, not_89_out, not_90_out, not_91_out, not_92_out,
       not_93_out, not_94_out, not_95_out, not_96_out, not_97_out, not_98_out, not_99_out, not_100_out,
       not_101_out, not_102_out, not_103_out, not_104_out, not_105_out, not_106_out, not_107_out,
       not_108_out, not_109_out, not_110_out, not_111_out, not_112_out, not_113_out, not_114_out,
       not_115_out, not_116_out, not_117_out, not_118_out, not_119_out, not_120_out, not_121_out,
       not_122_out, not_123_out, not_124_out, not_125_out, not_126_out, not_127_out, not_128_out,
       not_129_out, not_130_out, not_131_out, not_132_out, not_133_out, not_134_out, not_135_out,
       not_136_out, not_137_out, not_138_out, not_139_out, not_140_out, not_141_out, not_142_out,
       not_143_out, not_144_out, not_145_out, not_146_out, not_147_out, not_148_out, not_149_out,
       not_150_out, not_151_out, not_152_out, not_153_out, not_154_out, not_155_out, not_156_out,
       not_157_out, not_158_out, not_159_out, not_160_out, not_161_out, not_162_out, not_163_out,
       not_164_out, not_165_out, not_166_out, not_167_out, not_168_out, not_169_out, not_170_out,
       not_171_out, not_172_out, not_173_out, not_174_out, not_175_out, not_176_out, not_177_out,
       not_178_out, not_179_out, not_180_out, not_181_out, not_182_out, not_183_out, not_184_out,
       not_185_out, not_186_out, not_187_out, not_188_out, not_189_out, not_190_out, not_191_out,
       not_192_out, not_193_out, not_194_out, not_195_out, not_196_out, not_197_out, not_198_out,
       not_199_out, not_200_out, not_201_out, not_202_out, not_203_out, not_204_out, not_205_out,
       not_206_out, not_207_out, not_208_out, not_209_out, not_210_out, not_211_out, not_212_out,
       not_213_out, not_214_out, not_215_out, not_216_out, not_217_out, not_218_out, not_219_out,
       not_220_out, not_221_out, not_222_out, not_223_out, not_224_out, not_225_out, not_226_out,
       not_227_out, not_228_out, not_229_out, not_230_out, not_231_out;

  not not_1 (not_1_out, OP0);
  not not_2 (not_2_out, OP1);
  not not_3 (not_3_out, OP3);
  not not_4 (not_4_out, OP4);
  not not_5 (not_5_out, OP2);
  not not_6 (not_6_out, OP3);
  not not_7 (not_7_out, OP4);
  not not_8 (not_8_out, OP2);
  not not_9 (not_9_out, OP4);
  not not_10 (not_10_out, OP0);
  not not_11 (not_11_out, OP2);
  not not_12 (not_12_out, OP4);
  not not_13 (not_13_out, OP5);
  not not_14 (not_14_out, OP1);
  not not_15 (not_15_out, OP4);
  not not_16 (not_16_out, OP5);
  not not_17 (not_17_out, OP0);
  not not_18 (not_18_out, OP1);
  not not_19 (not_19_out, OP3);
  not not_20 (not_20_out, OP4);
  not not_21 (not_21_out, OP2);
  not not_22 (not_22_out, OP4);
  not not_23 (not_23_out, OP5);
  not not_24 (not_24_out, OP4);
  not not_25 (not_25_out, OP0);
  not not_26 (not_26_out, OP1);
  not not_27 (not_27_out, OP2);
  not not_28 (not_28_out, OP4);
  not not_29 (not_29_out, OP5);
  not not_30 (not_30_out, F0);
  not not_31 (not_31_out, F2);
  not not_32 (not_32_out, F3);
  not not_33 (not_33_out, F4);
  not not_34 (not_34_out, OP0);
  not not_35 (not_35_out, OP1);
  not not_36 (not_36_out, OP2);
  not not_37 (not_37_out, OP4);
  not not_38 (not_38_out, OP5);
  not not_39 (not_39_out, F1);
  not not_40 (not_40_out, F3);
  not not_41 (not_41_out, F4);
  not not_42 (not_42_out, OP0);
  not not_43 (not_43_out, OP1);
  not not_44 (not_44_out, OP2);
  not not_45 (not_45_out, OP4);
  not not_46 (not_46_out, OP5);
  not not_47 (not_47_out, F0);
  not not_48 (not_48_out, F2);
  not not_49 (not_49_out, F4);
  not not_50 (not_50_out, OP0);
  not not_51 (not_51_out, OP1);
  not not_52 (not_52_out, OP2);
  not not_53 (not_53_out, OP4);
  not not_54 (not_54_out, OP5);
  not not_55 (not_55_out, F3);
  not not_56 (not_56_out, F4);
  not not_57 (not_57_out, OP0);
  not not_58 (not_58_out, OP1);
  not not_59 (not_59_out, OP2);
  not not_60 (not_60_out, OP3);
  not not_61 (not_61_out, OP5);
  not not_62 (not_62_out, MF0);
  not not_63 (not_63_out, MF1);
  not not_64 (not_64_out, MF2);
  not not_65 (not_65_out, MF3);
  not not_66 (not_66_out, MF4);
  not not_67 (not_67_out, OP0);
  not not_68 (not_68_out, OP2);
  not not_69 (not_69_out, OP4);
  not not_70 (not_70_out, OP5);
  not not_71 (not_71_out, OP1);
  not not_72 (not_72_out, OP4);
  not not_73 (not_73_out, OP5);
  not not_74 (not_74_out, OP0);
  not not_75 (not_75_out, OP1);
  not not_76 (not_76_out, OP3);
  not not_77 (not_77_out, OP4);
  not not_78 (not_78_out, OP2);
  not not_79 (not_79_out, OP3);
  not not_80 (not_80_out, OP4);
  not not_81 (not_81_out, OP4);
  not not_82 (not_82_out, OP5);
  not not_83 (not_83_out, OP2);
  not not_84 (not_84_out, OP3);
  not not_85 (not_85_out, OP4);
  not not_86 (not_86_out, OP0);
  not not_87 (not_87_out, OP1);
  not not_88 (not_88_out, OP2);
  not not_89 (not_89_out, OP3);
  not not_90 (not_90_out, OP4);
  not not_91 (not_91_out, OP5);
  not not_92 (not_92_out, F0);
  not not_93 (not_93_out, F1);
  not not_94 (not_94_out, F4);
  not not_95 (not_95_out, F5);
  not not_96 (not_96_out, OP0);
  not not_97 (not_97_out, OP2);
  not not_98 (not_98_out, OP4);
  not not_99 (not_99_out, OP5);
  not not_100 (not_100_out, OP1);
  not not_101 (not_101_out, OP2);
  not not_102 (not_102_out, OP4);
  not not_103 (not_103_out, OP5);
  not not_104 (not_104_out, OP0);
  not not_105 (not_105_out, OP1);
  not not_106 (not_106_out, OP3);
  not not_107 (not_107_out, OP4);
  not not_108 (not_108_out, OP3);
  not not_109 (not_109_out, OP4);
  not not_110 (not_110_out, OP5);
  not not_111 (not_111_out, OP2);
  not not_112 (not_112_out, OP4);
  not not_113 (not_113_out, OP0);
  not not_114 (not_114_out, OP1);
  not not_115 (not_115_out, OP2);
  not not_116 (not_116_out, OP3);
  not not_117 (not_117_out, OP4);
  not not_118 (not_118_out, OP5);
  not not_119 (not_119_out, F0);
  not not_120 (not_120_out, F2);
  not not_121 (not_121_out, F3);
  not not_122 (not_122_out, F4);
  not not_123 (not_123_out, OP0);
  not not_124 (not_124_out, OP1);
  not not_125 (not_125_out, OP2);
  not not_126 (not_126_out, OP3);
  not not_127 (not_127_out, OP4);
  not not_128 (not_128_out, OP5);
  not not_129 (not_129_out, F1);
  not not_130 (not_130_out, F3);
  not not_131 (not_131_out, F4);
  not not_132 (not_132_out, OP0);
  not not_133 (not_133_out, OP1);
  not not_134 (not_134_out, OP2);
  not not_135 (not_135_out, OP3);
  not not_136 (not_136_out, OP4);
  not not_137 (not_137_out, OP5);
  not not_138 (not_138_out, F2);
  not not_139 (not_139_out, F4);
  not not_140 (not_140_out, OP0);
  not not_141 (not_141_out, OP1);
  not not_142 (not_142_out, OP2);
  not not_143 (not_143_out, OP3);
  not not_144 (not_144_out, OP4);
  not not_145 (not_145_out, OP5);
  not not_146 (not_146_out, F3);
  not not_147 (not_147_out, F4);
  not not_148 (not_148_out, OP0);
  not not_149 (not_149_out, OP1);
  not not_150 (not_150_out, OP2);
  not not_151 (not_151_out, OP3);
  not not_152 (not_152_out, OP4);
  not not_153 (not_153_out, OP5);
  not not_154 (not_154_out, F3);
  not not_155 (not_155_out, F4);
  not not_156 (not_156_out, F5);
  not not_157 (not_157_out, OP0);
  not not_158 (not_158_out, OP1);
  not not_159 (not_159_out, OP3);
  not not_160 (not_160_out, OP4);
  not not_161 (not_161_out, OP5);
  not not_162 (not_162_out, OP1);
  not not_163 (not_163_out, OP3);
  not not_164 (not_164_out, OP4);
  not not_165 (not_165_out, OP5);
  not not_166 (not_166_out, OP0);
  not not_167 (not_167_out, OP1);
  not not_168 (not_168_out, OP2);
  not not_169 (not_169_out, OP3);
  not not_170 (not_170_out, OP4);
  not not_171 (not_171_out, OP5);
  not not_172 (not_172_out, F0);
  not not_173 (not_173_out, F1);
  not not_174 (not_174_out, F2);
  not not_175 (not_175_out, F4);
  not not_176 (not_176_out, F5);
  not not_177 (not_177_out, OP0);
  not not_178 (not_178_out, OP2);
  not not_179 (not_179_out, OP3);
  not not_180 (not_180_out, OP4);
  not not_181 (not_181_out, OP5);
  not not_182 (not_182_out, F0);
  not not_183 (not_183_out, F1);
  not not_184 (not_184_out, F2);
  not not_185 (not_185_out, F4);
  not not_186 (not_186_out, F5);
  not not_187 (not_187_out, OP2);
  not not_188 (not_188_out, OP3);
  not not_189 (not_189_out, OP4);
  not not_190 (not_190_out, OP5);
  not not_191 (not_191_out, OP2);
  not not_192 (not_192_out, OP3);
  not not_193 (not_193_out, OP4);
  not not_194 (not_194_out, OP5);
  not not_195 (not_195_out, OP4);
  not not_196 (not_196_out, OP5);
  not not_197 (not_197_out, OP0);
  not not_198 (not_198_out, OP1);
  not not_199 (not_199_out, OP3);
  not not_200 (not_200_out, OP4);
  not not_201 (not_201_out, OP3);
  not not_202 (not_202_out, OP4);
  not not_203 (not_203_out, OP5);
  not not_204 (not_204_out, OP0);
  not not_205 (not_205_out, OP1);
  not not_206 (not_206_out, OP2);
  not not_207 (not_207_out, OP3);
  not not_208 (not_208_out, OP5);
  not not_209 (not_209_out, F0);
  not not_210 (not_210_out, F1);
  not not_211 (not_211_out, F2);
  not not_212 (not_212_out, F5);
  not not_213 (not_213_out, OP0);
  not not_214 (not_214_out, OP1);
  not not_215 (not_215_out, OP2);
  not not_216 (not_216_out, OP3);
  not not_217 (not_217_out, OP5);
  not not_218 (not_218_out, MF0);
  not not_219 (not_219_out, MF1);
  not not_220 (not_220_out, MF2);
  not not_221 (not_221_out, MF3);
  not not_222 (not_222_out, MF4);
  not not_223 (not_223_out, OP0);
  not not_224 (not_224_out, OP1);
  not not_225 (not_225_out, OP2);
  not not_226 (not_226_out, OP3);
  not not_227 (not_227_out, OP5);
  not not_228 (not_228_out, MF0);
  not not_229 (not_229_out, MF1);
  not not_230 (not_230_out, MF3);
  not not_231 (not_231_out, MF4);
  and and_1 (and_1_out, not_1_out, not_2_out, OP2, not_3_out, not_4_out, OP5);
  and and_2 (and_2_out, OP0, OP1, not_5_out, not_6_out, not_7_out, OP5);
  and and_3 (MemWrite, OP0, OP1, not_8_out, OP3, not_9_out, OP5);
  and and_4 (and_4_out, not_10_out, not_11_out, OP3, not_12_out, not_13_out);
  and and_5 (and_5_out, not_14_out, OP3, not_15_out, not_16_out);
  and and_6 (and_6_out, not_17_out, not_18_out, OP2, not_19_out, not_20_out, OP5);
  and and_7 (and_7_out, OP0, OP1, not_21_out, not_22_out, OP5);
  and and_8 (and_8_out, not_23_out, not_24_out, OP3, OP2, OP1, OP0);
  and and_9 (and_9_out, not_25_out, not_26_out, not_27_out, not_28_out, not_29_out, not_30_out, not_31_out, not_32_out, not_33_out);
  and and_10 (and_10_out, not_34_out, not_35_out, not_36_out, not_37_out, not_38_out, not_39_out, not_40_out, not_41_out, F5);
  and and_11 (and_11_out, not_42_out, not_43_out, not_44_out, not_45_out, not_46_out, not_47_out, F1, not_48_out, not_49_out, F5);
  and and_12 (and_12_out, not_50_out, not_51_out, not_52_out, not_53_out, not_54_out, F0, F1, not_55_out, not_56_out);
  and and_13 (and_13_out, not_57_out, not_58_out, not_59_out, not_60_out, OP4, not_61_out, not_62_out, not_63_out, not_64_out, not_65_out, not_66_out);
  and and_14 (and_14_out, not_67_out, not_68_out, OP3, not_69_out, not_70_out);
  and and_15 (and_15_out, not_71_out, OP3, not_72_out, not_73_out);
  and and_16 (and_16_out, not_74_out, not_75_out, OP2, not_76_out, not_77_out, OP5);
  and and_17 (and_17_out, OP0, not_78_out, not_79_out, not_80_out, OP5);
  and and_18 (and_18_out, OP0, OP2, OP3, not_81_out, not_82_out);
  and and_19 (and_19_out, OP0, OP1, not_83_out, not_84_out, not_85_out);
  and and_20 (SysCALL, not_86_out, not_87_out, not_88_out, not_89_out, not_90_out, not_91_out, not_92_out, not_93_out, F2, F3, not_94_out, not_95_out);
  and and_21 (and_21_out, not_96_out, not_97_out, OP3, not_98_out, not_99_out);
  and and_22 (and_22_out, not_100_out, not_101_out, OP3, not_102_out, not_103_out);
  and and_23 (and_23_out, not_104_out, not_105_out, OP2, not_106_out, not_107_out);
  and and_24 (and_24_out, OP0, OP2, not_108_out, not_109_out, not_110_out);
  and and_25 (and_25_out, OP0, OP1, not_111_out, not_112_out, OP5);
  and and_26 (and_26_out, not_113_out, not_114_out, not_115_out, not_116_out, not_117_out, not_118_out, not_119_out, not_120_out, not_121_out, not_122_out);
  and and_27 (and_27_out, not_123_out, not_124_out, not_125_out, not_126_out, not_127_out, not_128_out, not_129_out, not_130_out, not_131_out, F5);
  and and_28 (and_28_out, not_132_out, not_133_out, not_134_out, not_135_out, not_136_out, not_137_out, F1, not_138_out, F3, not_139_out, F5);
  and and_29 (and_29_out, not_140_out, not_141_out, not_142_out, not_143_out, not_144_out, not_145_out, F0, F2, not_146_out, not_147_out, F5);
  and and_30 (and_30_out, not_148_out, not_149_out, not_150_out, not_151_out, not_152_out, not_153_out, F0, F1, not_154_out, not_155_out, not_156_out);
  and and_31 (BEQ, not_157_out, not_158_out, OP2, not_159_out, not_160_out, not_161_out);
  and and_32 (BNE, OP0, not_162_out, OP2, not_163_out, not_164_out, not_165_out);
  and and_33 (JR, not_166_out, not_167_out, not_168_out, not_169_out, not_170_out, not_171_out, not_172_out, not_173_out, not_174_out, F3, not_175_out, not_176_out);
  and and_34 (and_34_out, not_177_out, not_178_out, not_179_out, not_180_out, not_181_out, not_182_out, not_183_out, not_184_out, F3, not_185_out, not_186_out);
  and and_35 (and_35_out, OP1, not_187_out, not_188_out, not_189_out, not_190_out);
  and and_36 (JAL, OP0, OP1, not_191_out, not_192_out, not_193_out, not_194_out);
  and and_37 (LUI, OP0, OP1, OP2, OP3, not_195_out, not_196_out);
  and and_38 (LBU, not_197_out, not_198_out, OP2, not_199_out, not_200_out, OP5);
  and and_39 (BGTZ, OP0, OP1, OP2, not_201_out, not_202_out, not_203_out);
  and and_40 (ERET, not_204_out, not_205_out, not_206_out, not_207_out, OP4, not_208_out, not_209_out, not_210_out, not_211_out, F3, F4, not_212_out, MF4);
  and and_41 (MFC0, not_213_out, not_214_out, not_215_out, not_216_out, OP4, not_217_out, not_218_out, not_219_out, not_220_out, not_221_out, not_222_out);
  and and_42 (MTC0, not_223_out, not_224_out, not_225_out, not_226_out, OP4, not_227_out, not_228_out, not_229_out, MF2, not_230_out, not_231_out);
  or or_1 (MemToReg, and_1_out, and_2_out);
  or or_2 (ALU_SRC, and_4_out, and_5_out, and_6_out, and_7_out, and_8_out);
  or or_3 (SignedExt, and_21_out, and_22_out, and_23_out, and_24_out, and_25_out);
  or or_4 (RegDst, and_26_out, and_27_out, and_28_out, and_29_out, and_30_out);
  or or_5 (JUMP, and_34_out, and_35_out);
  or or_6 (RegWrite, and_9_out, and_10_out, and_11_out, and_12_out, and_13_out, and_14_out, and_15_out, and_16_out, and_17_out, and_18_out, and_19_out);
endmodule

// ALU
module MIPS_ALU (
  input  [4:0] shamt,
  input  [31:0] X,
  input  [31:0] Y,
  input  [3:0] AluOP,
  output Equal,
  output [31:0] Result,
  output [31:0] Result_2
);

  wire [0:0] comparator_1_lt, comparator_2_lt;
  wire [31:0] adder_1_out, AND_out, divider_1_out, divider_1_rem, multiplier_1_cout, multiplier_1_out,
       NOR_out, OR_out, shifter_1_out, shifter_2_out, shifter_3_out, subtractor_1_out, XOR_out;

  assign AND_out = X & Y;  // AND_Gate AND, 32 bits wide
  assign OR_out = X | Y;  // OR_Gate OR, 32 bits wide
  Shifter #(.width(32), .shift("ll")) shifter_1 (.in(Y), .\dist (shamt), .out(shifter_1_out));
  Shifter #(.width(32), .shift("ar")) shifter_2 (.in(Y), .\dist (shamt), .out(shifter_2_out));
  Shifter #(.width(32), .shift("lr")) shifter_3 (.in(Y), .\dist (shamt), .out(shifter_3_out));
  Multiplier #(.width(32)) multiplier_1 (.a(X), .b(Y), .out(multiplier_1_out), .cout(multiplier_1_cout));  // open: cin
  Divider #(.width(32)) divider_1 (.a(X), .b(Y), .out(divider_1_out), .rem(divider_1_rem));  // open: upper
  Adder #(.width(32)) adder_1 (.a(X), .b(Y), .out(adder_1_out));  // open: cin, cout
  Subtractor #(.width(32)) subtractor_1 (.a(X), .b(Y), .out(subtractor_1_out));  // open: bin, bout
  assign XOR_out = X ^ Y;  // XOR_Gate XOR, 32 bits wide
  assign NOR_out = ~(X | Y);  // NOR_Gate NOR, 32 bits wide
  Comparator #(.width(32), .mode("twosComplement")) comparator_1 (
    .a(X), .b(Y), .eq(Equal), .lt(comparator_1_lt[0]));  // open: gt
  Comparator #(.width(32), .mode("unsigned")) comparator_2 (.a(X), .b(Y), .lt(comparator_2_lt[0]));  // open: gt, eq
  Multiplexer #(.select(4), .width(32), .disabled("Z"), .enable("false")) multiplexer_1 (
    .in0(shifter_1_out), .in1(shifter_2_out), .in2(shifter_3_out), .in3(multiplier_1_out),
    .in4(divider_1_out), .in5(adder_1_out), .in6(subtractor_1_out), .in7(AND_out), .in8(OR_out),
    .in9(XOR_out), .in10(NOR_out), .in11({{31{1'b0}}, comparator_1_lt[0]}),
    .in12({{31{1'b0}}, comparator_2_lt[0]}), .in13({32{1'b0}}), .in14({32{1'b0}}), .in15({32{1'b0}}),
    .out(Result), .sel(AluOP));
  Multiplexer #(.select(4), .width(32), .disabled("Z"), .enable("false")) multiplexer_2 (
    .in0({32{1'b0}}), .in1({32{1'b0}}), .in2({32{1'b0}}), .in3(multiplier_1_cout), .in4(divider_1_rem),
    .in5({32{1'b0}}), .in6({32{1'b0}}), .in7({32{1'b0}}), .in8({32{1'b0}}), .in9({32{1'b0}}),
    .in10({32{1'b0}}), .in11({32{1'b0}}), .in12({32{1'b0}}), .in13({32{1'b0}}), .in14({32{1'b0}}),
    .in15({32{1'b0}}), .out(Result_2), .sel(AluOP));

  // Other names for the same wires on the sheet: Result2[31:0] = Result_2; S[3:0] = AluOP

  // Notes on the sheet:
  //   不要改变此引脚区域内容，也不要改变ALU封装形式
  //   输入引脚
  //   输出引脚
endmodule

module MIPS_Regifile (
  input  [31:0] Din,
  input  Clk,
  input  WE,
  input  [4:0] R1_num,
  input  [4:0] W_num,
  input  [4:0] R2_num,
  output [31:0] R1,
  output [31:0] R2
);

  // RegisterFile registerfile_1: pin names not known; wires that end beside it: Din, Clk, WE, W_num, R1_num, R2_num, R1, R2
endmodule

module \理想流水线  (
  output RegWrite,
  output MemWrite,
  output [31:0] IF_PC,
  output [31:0] ID_PC,
  output [31:0] EX_PC,
  output [31:0] M_PC,
  output [31:0] WB_PC,
  output [31:0] RDin,
  output [31:0] MDin,
  output [31:0] LedData
);

  wire and_1_out, and_2_out, and_3_out, and_4_out, and_5_out, and_6_out, BEqual, CLK, clock_1_out,
       clock_2_out, comparator_1_eq, comparator_2_eq, comparator_2_lt, comparator_3_gt, comparator_4_eq,
       d_ff_1_q, equal, EX_Halt, ex_mem_1_halt_2, ex_mem_1_lbu_2, ex_mem_1_lui_2, ex_mem_1_memtoreg_2,
       ex_mem_1_regwrite_2, Go, Halt, id_ex_1_alusrcb_2, id_ex_1_beq_2, id_ex_1_bgtz_2, id_ex_1_bne_2,
       id_ex_1_lbu_2, id_ex_1_lui_2, id_ex_1_memtoreg_2, id_ex_1_memwrite_2, id_ex_1_regwrite_2, IR1, IR2,
       IR3, JAL, JMP, JR, mem_wb_1_lbu_2, mem_wb_1_lui_2, mem_wb_1_memtoreg_2, nand_1_out, not_1_out,
       not_2_out, RegDst, RST, SignedExt, Syscall, W1, W2, W3, \单周期硬布线控制器_1_alu_src , \单周期硬布线控制器_1_beq ,
       \单周期硬布线控制器_1_bgtz , \单周期硬布线控制器_1_bne , \单周期硬布线控制器_1_lbu , \单周期硬布线控制器_1_lui , \单周期硬布线控制器_1_memtoreg ,
       \单周期硬布线控制器_1_memwrite , \单周期硬布线控制器_1_regwrite ;
  wire [3:0] id_ex_1_aluop_2, \单周期硬布线控制器_1_alu_op ;
  wire [4:0] ex_mem_1_w_num_2, id_ex_1_shamt_2, id_ex_1_w_num_2, multiplexer_4_out, multiplexer_5_out,
       multiplexer_6_out, multiplexer_7_out, multiplexer_10_out, W_num;
  wire [7:0] multiplexer_14_out;
  wire [12:0] CNT_num;
  wire [15:0] \LoadUse次数 , \总周期数 , \插入气泡数 , \无条件分支数 , \条件分支成功数 ;
  wire [27:2] JMPAddr;
  wire [31:0] adder_1_out, adder_2_out, adder_4_out, bit_extender_1_out, bit_extender_2_out,
       bit_extender_3_out, Din, EX_IR, ex_mem_1_alu_2, ex_mem_1_data_2, id_ex_1_imm_2, ID_IR, IF_IR, MEM_IR,
       mem_wb_1_addr_2, mem_wb_1_alu_2, mem_wb_1_md_2, mips_alu_1_result, mips_regifile_1_r1,
       mips_regifile_1_r2, multiplexer_1_out, multiplexer_2_out, multiplexer_3_out, multiplexer_8_out,
       multiplexer_9_out, multiplexer_11_out, multiplexer_12_out, multiplexer_16_out, PCBranch, ram_1_data,
       rs, rt, shifter_1_out, WB_IR;

  Button \u_总复位  (.out(RST));
  Button _1 (.out(IR1));
  Button _2 (.out(IR2));
  Button _3 (.out(IR3));
  // Probe on \总周期数 
  // Probe on \总周期数 
  Button \u_继续运行  (.out(Go));
  LED #(.active("true")) led_1 (.in(W1));
  LED #(.active("true")) led_2 (.in(W2));
  LED #(.active("true")) led_3 (.in(W3));
  Multiplexer #(.select(1), .width(32), .disabled("Z"), .enable("false")) multiplexer_1 (
    .in0(adder_2_out), .in1(adder_1_out), .out(multiplexer_1_out), .sel(BEqual));
  Adder #(.width(32)) adder_1 (.a(PCBranch), .b(32'h4), .out(adder_1_out));  // open: cin, cout
  Hex_Digit_Display hex_digit_display_1 (.value(LedData[31:28]));  // open: dp
  // Probe on IF_PC[19:0]
  // Mips_Probe mips_probe_1: pin names not known; wires that end beside it: IF_IR
  Comparator #(.width(32), .mode("twosComplement")) comparator_1 (
    .a(rs), .b(32'h22), .eq(comparator_1_eq));  // open: gt, lt
  and and_1 (and_1_out, JMP, ~JR);  // AND_Gate
  not not_1 (not_1_out, Halt);
  Multiplexer #(.select(1), .width(32), .disabled("Z"), .enable("false")) multiplexer_2 (
    .in0(multiplexer_3_out), .in1({EX_PC[31:28], JMPAddr, 2'b00}), .out(multiplexer_2_out), .sel(and_1_out));
  Multiplexer #(.select(1), .width(32), .disabled("Z"), .enable("false")) multiplexer_3 (
    .in0(multiplexer_1_out), .in1(rs), .out(multiplexer_3_out), .sel(JR));
  Hex_Digit_Display hex_digit_display_2 (.value(LedData[23:20]));  // open: dp
  Hex_Digit_Display hex_digit_display_3 (.value(LedData[27:24]));  // open: dp
  // Probe on ID_PC[19:0]
  // Mips_Probe mips_probe_2: pin names not known; wires that end beside it: ID_IR
  Register #(.width(32), .trigger("rising"), .Select("low")) register_1 (
    .D(rt), .en(comparator_1_eq), .Q(LedData), .clk(CLK));  // open: clr
  Register #(.width(1), .trigger("rising"), .Select("low")) register_2 (
    .D(and_2_out), .en(and_2_out), .Q(EX_Halt), .clk(CLK), .clr(Go));
  and and_2 (and_2_out, ~comparator_1_eq, Syscall);  // AND_Gate
  Register #(.width(32), .trigger("rising"), .Select("low")) PC (
    .D(multiplexer_2_out), .en(not_1_out), .Q(IF_PC), .clk(CLK));  // open: clr
  Hex_Digit_Display hex_digit_display_4 (.value(LedData[15:12]));  // open: dp
  Hex_Digit_Display hex_digit_display_5 (.value(LedData[19:16]));  // open: dp
  Hex_Digit_Display hex_digit_display_6 (.value(LedData[7:4]));  // open: dp
  Hex_Digit_Display hex_digit_display_7 (.value(LedData[11:8]));  // open: dp
  Clock #(.highDuration(1), .lowDuration(1)) clock_1 (.out(clock_1_out));
  // Probe on EX_PC[19:0]
  // Mips_Probe mips_probe_3: pin names not known; wires that end beside it: clock_1_out, EX_IR, CLK
  Adder #(.width(32)) adder_2 (.a(IF_PC), .b(32'h4), .out(adder_2_out));  // open: cin, cout
  Hex_Digit_Display hex_digit_display_8 (.value(LedData[3:0]));  // open: dp
  and and_3 (and_3_out, ~Halt, CLK);  // AND_Gate
  ROM #(.addrWidth(10), .dataWidth(32), .Select("high")) rom_1 (.addr(IF_PC[11:2]), .data(IF_IR));
  // Probe on \总周期数 
  // Probe on M_PC[19:0]
  // Mips_Probe mips_probe_4: pin names not known; wires that end beside it: MEM_IR
  Counter #(.width(16), .max('hffff), .ongoal("wrap"), .trigger("rising"), .behavior("old")) counter_1 (
    .Q(\总周期数 ), .clk(and_3_out));  // open: load, D, count, carry, clr, preset
  // Mips_Probe mips_probe_5: pin names not known; wires that end beside it: ID_IR
  IF_ID if_id_1 (.IR(IF_IR), .PC_4(IF_PC), .CLK(CLK), .IR_2(ID_IR), .PC_4_2(ID_PC));  // open: 同步清零_高电平有效, 使能端_低电平有效
  // Probe on \总周期数 
  // Probe on \无条件分支数 
  // Probe on \条件分支成功数 
  // Probe on \插入气泡数 
  // Probe on \LoadUse次数 
  // Probe on IF_PC[11:0]
  // Probe on WB_PC[19:0]
  // Mips_Probe mips_probe_6: pin names not known; wires that end beside it: WB_IR
  Multiplexer #(.select(1), .width(5), .disabled("Z"), .enable("false")) multiplexer_4 (
    .in0(ID_IR[25:21]), .in1(5'b00010), .out(multiplexer_4_out), .sel(Syscall));
  Multiplexer #(.select(1), .width(5), .disabled("Z"), .enable("false")) multiplexer_5 (
    .in0(ID_IR[20:16]), .in1(5'b00100), .out(multiplexer_5_out), .sel(Syscall));
  Multiplexer #(.select(1), .width(5), .disabled("Z"), .enable("false")) multiplexer_6 (
    .in0(ID_IR[20:16]), .in1(ID_IR[15:11]), .out(multiplexer_6_out), .sel(RegDst));
  // Probe on ID_PC[11:0]
  // Probe on EX_PC[11:0]
  Multiplexer #(.select(1), .width(5), .disabled("Z"), .enable("false")) multiplexer_7 (
    .in0(multiplexer_6_out), .in1({5{1'b1}}), .out(multiplexer_7_out), .sel(JAL));
  assign bit_extender_1_out = {{16{1'b0}}, ID_IR[15:0]};  // Bit_Extender bit_extender_1
  assign bit_extender_2_out = {{16{ID_IR[15]}}, ID_IR[15:0]};  // Bit_Extender bit_extender_2
  // Probe on M_PC[11:0]
  D_Flip_Flop #(.trigger("high"), .Pre_Clr_Positions("LEGACY"), .NegatePresetClear("false"), .enable("true"), .NewFFLayout("false")) d_ff_1 (.Q(d_ff_1_q));  // open: clk, D, Qn, preset, en, reset
  // Probe on 13'hc
  \单周期硬布线控制器  \u_单周期硬布线控制器_1  (
    .Func(ID_IR[5:0]), .OP(ID_IR[31:26]), .ALU_OP(\单周期硬布线控制器_1_alu_op ), .MemToReg(\单周期硬布线控制器_1_memtoreg ),
    .MemWrite(\单周期硬布线控制器_1_memwrite ), .ALU_SRC(\单周期硬布线控制器_1_alu_src ), .RegWrite(\单周期硬布线控制器_1_regwrite ),
    .SysCALL(Syscall), .SignedExt(SignedExt), .RegDst(RegDst), .JR(JR), .JMP(JMP), .Beq(\单周期硬布线控制器_1_beq ),
    .JAL(JAL), .Bne(\单周期硬布线控制器_1_bne ), .LUI(\单周期硬布线控制器_1_lui ), .LBU(\单周期硬布线控制器_1_lbu ),
    .BGTZ(\单周期硬布线控制器_1_bgtz ));  // open: ERET, MF, MFC0, MTC0
  Multiplexer #(.select(1), .width(32), .disabled("Z"), .enable("false")) multiplexer_8 (
    .in0(bit_extender_1_out), .in1(bit_extender_2_out), .out(multiplexer_8_out), .sel(SignedExt));
  // Probe on WB_PC[11:0]
  Comparator #(.width(13), .mode("twosComplement")) comparator_2 (
    .a(CNT_num), .b(13'hc), .eq(comparator_2_eq), .lt(comparator_2_lt));  // open: gt
  Clock #(.highDuration(1), .lowDuration(1)) clock_2 (.out(clock_2_out));
  MIPS_Regifile mips_regifile_1 (
    .Din(Din), .Clk(CLK), .R1(mips_regifile_1_r1), .R2(mips_regifile_1_r2), .WE(RegWrite), .W_num(W_num),
    .R1_num(multiplexer_4_out), .R2_num(multiplexer_5_out));
  nand nand_1 (nand_1_out, d_ff_1_q, comparator_2_eq);
  Counter #(.width(13), .max('h1fff), .ongoal("stay"), .trigger("rising"), .behavior("old")) counter_2 (
    .count(comparator_2_lt), .Q(CNT_num), .clk(clock_2_out));  // open: load, D, carry, clr, preset
  ID_EX id_ex_1 (
    .BGTZ(\单周期硬布线控制器_1_bgtz ), .LBU(\单周期硬布线控制器_1_lbu ), .RegWrite(\单周期硬布线控制器_1_regwrite ),
    .W_num(multiplexer_7_out), .MemToReg(\单周期硬布线控制器_1_memtoreg ), .Beq(\单周期硬布线控制器_1_beq ),
    .Bne(\单周期硬布线控制器_1_bne ), .Shamt(ID_IR[10:6]), .MemWrite(\单周期硬布线控制器_1_memwrite ),
    .AluOP(\单周期硬布线控制器_1_alu_op ), .AluSrcB(\单周期硬布线控制器_1_alu_src ), .R1(mips_regifile_1_r1),
    .R2(mips_regifile_1_r2), .Imm(multiplexer_8_out), .PC_4(ID_PC), .IR(ID_IR), ._26(ID_IR[25:0]), .CLK(CLK),
    .BGTZ_2(id_ex_1_bgtz_2), .LBU_2(id_ex_1_lbu_2), .RegWrite_2(id_ex_1_regwrite_2),
    .W_num_2(id_ex_1_w_num_2), .MemToReg_2(id_ex_1_memtoreg_2), .Beq_2(id_ex_1_beq_2), .Bne_2(id_ex_1_bne_2),
    .Shamt_2(id_ex_1_shamt_2), .MemWrite_2(id_ex_1_memwrite_2), .AluOP_2(id_ex_1_aluop_2),
    .AluSrcB_2(id_ex_1_alusrcb_2), .R1_2(rs), .R2_2(rt), .Imm_2(id_ex_1_imm_2), .PC_4_2(EX_PC), .IR_2(EX_IR),
    ._26_2(JMPAddr), .LUI(\单周期硬布线控制器_1_lui ), .LUI_2(id_ex_1_lui_2));  // open: JAL, JR, JMP, Sys, eret, eret_2, f1, f2, JAL_2, JR_2, JMP_2, Sys_2, eret_3, eret_4, f1_2, f2_2, 同步清零_高电平有效, 使能端_低电平有效, OP, OP_2
  assign CLK = nand_1_out ? clock_2_out : 1'bz;  // Controlled_Buffer controlled_buffer_1
  Pull_Resistor #(.pull(1)) pull_resistor_1 (.node(CLK));
  Comparator #(.width(32), .mode("twosComplement")) comparator_3 (
    .a(rs), .b({32{1'b0}}), .gt(comparator_3_gt));  // open: eq, lt
  and and_4 (and_4_out, equal, id_ex_1_beq_2);
  and and_5 (and_5_out, ~equal, id_ex_1_bne_2);  // AND_Gate
  Shifter #(.width(32), .shift("ll")) shifter_1 (.in(id_ex_1_imm_2), .\dist (5'b00010), .out(shifter_1_out));
  Comparator #(.width(6), .mode("twosComplement")) comparator_4 (
    .a(JMPAddr[7:2]), .b(6'b000111), .eq(comparator_4_eq));  // open: gt, lt
  and and_6 (and_6_out, id_ex_1_bgtz_2, comparator_3_gt);
  Multiplexer #(.select(1), .width(32), .disabled("Z"), .enable("false")) multiplexer_9 (
    .in0(rt), .in1(id_ex_1_imm_2), .out(multiplexer_9_out), .sel(id_ex_1_alusrcb_2));
  Adder #(.width(32)) adder_3 (.a(shifter_1_out), .b(EX_PC), .out(PCBranch));  // open: cin, cout
  Multiplexer #(.select(1), .width(5), .disabled("Z"), .enable("false")) multiplexer_10 (
    .in0(id_ex_1_shamt_2), .in1(rs[4:0]), .out(multiplexer_10_out), .sel(comparator_4_eq));
  or or_1 (BEqual, and_6_out, and_4_out, and_5_out);
  MIPS_ALU mips_alu_1 (
    .X(rs), .Y(multiplexer_9_out), .AluOP(id_ex_1_aluop_2), .Equal(equal), .Result(mips_alu_1_result),
    .shamt(multiplexer_10_out));  // open: Result_2
  Adder #(.width(32)) adder_4 (.a(rs), .b(id_ex_1_imm_2), .out(adder_4_out));  // open: cin, cout
  EX_MEM ex_mem_1 (
    .LBU(id_ex_1_lbu_2), .RegWrite(id_ex_1_regwrite_2), .W_num(id_ex_1_w_num_2),
    .MemToReg(id_ex_1_memtoreg_2), .MemWrite(id_ex_1_memwrite_2), .Halt(EX_Halt), .data(adder_4_out),
    .Alu(mips_alu_1_result), .R2(rt), .PC_4(EX_PC), .IR(EX_IR), .CLK(CLK), .LBU_2(ex_mem_1_lbu_2),
    .RegWrite_2(ex_mem_1_regwrite_2), .W_num_2(ex_mem_1_w_num_2), .MemToReg_2(ex_mem_1_memtoreg_2),
    .MemWrite_2(MemWrite), .Halt_2(ex_mem_1_halt_2), .data_2(ex_mem_1_data_2), .Alu_2(ex_mem_1_alu_2),
    .R2_2(MDin), .PC_4_2(M_PC), .IR_2(MEM_IR), .LUI(id_ex_1_lui_2), .LUI_2(ex_mem_1_lui_2));  // open: JAL, JAL_2, 同步清零_高电平有效, 使能端_低电平有效, OP, OP_2, imm26, imm26_2, sys, sys_2
  Multiplexer #(.select(1), .width(32), .disabled("Z"), .enable("false")) multiplexer_11 (
    .in0(ex_mem_1_alu_2), .in1(ex_mem_1_data_2), .out(multiplexer_11_out), .sel(ex_mem_1_lbu_2));
  not not_2 (not_2_out, Halt);
  RAM #(.addrWidth(10), .dataWidth(32), .bus("separate"), .Select("high")) ram_1 (
    .addr(multiplexer_11_out[11:2]), .din(MDin), .data(ram_1_data), .str(ex_mem_1_memtoreg_2),
    .sel(not_2_out), .clk(CLK));  // open: ld, clr
  MEM_WB mem_wb_1 (
    .LBU(ex_mem_1_lbu_2), .RegWrite(ex_mem_1_regwrite_2), .W_num(ex_mem_1_w_num_2),
    .MemToReg(ex_mem_1_memtoreg_2), .Addr(multiplexer_11_out), .Halt(ex_mem_1_halt_2), .Alu(ex_mem_1_alu_2),
    .MD(ram_1_data), .PC_4(M_PC), .IR(MEM_IR), .CLK(CLK), .LBU_2(mem_wb_1_lbu_2), .RegWrite_2(RegWrite),
    .W_num_2(W_num), .MemToReg_2(mem_wb_1_memtoreg_2), .Addr_2(mem_wb_1_addr_2), .Halt_2(Halt),
    .Alu_2(mem_wb_1_alu_2), .MD_2(mem_wb_1_md_2), .PC_4_2(WB_PC), .IR_2(WB_IR), .LUI(ex_mem_1_lui_2),
    .LUI_2(mem_wb_1_lui_2));  // open: JAL, JAL_2, 同步清零_高电平有效, 使能端_低电平有效, OP, OP_2, data, data_2, imm26, imm26_2, sys, sys_2, rs, rs_2
  Multiplexer #(.select(1), .width(32), .disabled("Z"), .enable("false")) multiplexer_12 (
    .in0(mem_wb_1_alu_2), .in1(mem_wb_1_md_2), .out(multiplexer_12_out), .sel(mem_wb_1_memtoreg_2));
  Multiplexer #(.select(1), .width(32), .disabled("Z"), .enable("false")) multiplexer_13 (
    .in0(RDin), .in1({JMPAddr[17:2], {16{1'b0}}}), .out(Din), .sel(mem_wb_1_lui_2));
  Multiplexer #(.select(2), .width(8), .disabled("Z"), .enable("false")) multiplexer_14 (
    .in0(multiplexer_12_out[7:0]), .in1(multiplexer_12_out[15:8]), .in2(multiplexer_12_out[23:16]),
    .in3(multiplexer_12_out[31:24]), .out(multiplexer_14_out), .sel(mem_wb_1_addr_2[1:0]));
  assign bit_extender_3_out = {{24{1'b0}}, multiplexer_14_out};  // Bit_Extender bit_extender_3
  Multiplexer #(.select(1), .width(32), .disabled("Z"), .enable("false")) multiplexer_15 (
    .in0(multiplexer_16_out), .in1(WB_PC), .out(RDin), .sel(JAL));
  Multiplexer #(.select(1), .width(32), .disabled("Z"), .enable("false")) multiplexer_16 (
    .in0(multiplexer_12_out), .in1(bit_extender_3_out), .out(multiplexer_16_out), .sel(mem_wb_1_lbu_2));

  // Other names for the same wires on the sheet: JMPAddr[31:28] = EX_PC[31:28]; MEM_PC[31:0] = M_PC

  // Notes on the sheet:
  //   中断源
  //   时空图监测，可删除
  //   中断等待指示
  //   数码管输出
  //   指令存储器
  //   contents of rom_1 (hex, n*v repeats v):
  //   20100000 20110000 20120000 20130000 36100000 36310001 36520002 36730003 ae100000 ae110004 ae120008
  //   ae13000c 2002000a 20110000 20120000 20130000 c
  //   指令字
  //   OP
  //   Func
  //   rs
  //   rt
  //   rd
  //   控制位
  //   流水调试日志用
  //   暂停节拍，不能为0
  //   JMP
  //   JR
  //   OP
  //   Func
  //   Syscall
  //   戳工具置1进入计数暂停模式，ctrl+k时钟自动运行到对应节拍暂停
  //   ctrl+k关闭时钟连续运行，将控制位置零，进入单步调试模式调试
  //   用这个时钟源需要去掉电路中的其他时钟源
  //   Beq
  //   Bne
  //   MemToReg
  //   MemWrite
  //   AluOP
  //   AluSrcB
  //   RegWrite
  //   JAL
  //   RegDst
  //   可计数暂停的时钟源
  //   SRAV指令
  //   为方便自动评测，需要输出流水线各段保存的PC值，注意是PC不是PC+4，另外ID段寄存器写入信息，Mem段内存写入信息也要输出
endmodule

module \重定向流水线  (
  output RegWrite,
  output MemWrite,
  output [31:0] IF_PC,
  output [31:0] ID_PC,
  output [31:0] EX_PC,
  output [31:0] M_PC,
  output [31:0] WB_PC,
  output [31:0] RDin,
  output [31:0] MDin,
  output [31:0] LedData
);

  wire and_1_out, and_2_out, and_3_out, and_4_out, and_5_out, and_6_out, and_7_out, and_8_out, BEqual, clear,
       CLK, clock_1_out, clock_2_out, comparator_1_eq, comparator_1_lt, comparator_2_gt, comparator_3_eq,
       d_ff_1_q, enable, equal, ex_mem_1_halt_2, ex_mem_1_jal_2, ex_mem_1_lbu_2, ex_mem_1_lui_2,
       ex_mem_1_sys_2, EX_MTR, EX_RW, EX_sys, Go, id_ex_1_alusrcb_2, id_ex_1_beq_2, id_ex_1_bgtz_2,
       id_ex_1_bne_2, id_ex_1_jal_2, id_ex_1_lbu_2, id_ex_1_lui_2, id_ex_1_memwrite_2, ID_JMP, ID_JR, ID_LUI,
       IR1, IR2, IR3, JAL, JMP, JR, judge, Led, MEM_MTR, MEM_RW, mem_wb_1_lbu_2, mem_wb_1_memtoreg_2,
       nand_1_out, not_1_out, not_2_out, not_3_out, or_1_out, or_2_out, or_3_out, RegDst, RST, SignedExt,
       Syscall, W1, W2, W3, \单周期硬布线控制器_1_alu_src , \单周期硬布线控制器_1_beq , \单周期硬布线控制器_1_bgtz , \单周期硬布线控制器_1_bne ,
       \单周期硬布线控制器_1_jal , \单周期硬布线控制器_1_lbu , \单周期硬布线控制器_1_memtoreg , \单周期硬布线控制器_1_memwrite ,
       \单周期硬布线控制器_1_regwrite , \单周期硬布线控制器_1_syscall , \数据相关 ;
  wire [1:0] EX_F1, EX_F2, forwardR1, forwardR2;
  wire [3:0] id_ex_1_aluop_2, \单周期硬布线控制器_1_alu_op ;
  wire [4:0] ex_mem_1_w_num_2, id_ex_1_shamt_2, id_ex_1_w_num_2, multiplexer_4_out, multiplexer_5_out,
       multiplexer_6_out, multiplexer_7_out, multiplexer_12_out, W_num;
  wire [7:0] multiplexer_15_out;
  wire [12:0] CNT_num;
  wire [15:0] \LoadUse次数 , \总周期数 , \无条件分支数 , \条件分支成功数 ;
  wire [25:0] ex_mem_1_imm26_2, mem_wb_1_imm26_2;
  wire [27:2] JMPAddr;
  wire [31:0] adder_1_out, adder_2_out, adder_4_out, ALURes, bit_extender_1_out, bit_extender_2_out,
       bit_extender_3_out, EX_Data, EX_IR, ex_mem_1_data_2, EX_R1, EX_R2, EXALU, id_ex_1_imm_2, ID_IR, IF_IR,
       MEM_IR, mem_wb_1_addr_2, mem_wb_1_md_2, mips_alu_1_result, multiplexer_1_out, multiplexer_2_out,
       multiplexer_3_out, multiplexer_8_out, multiplexer_9_out, multiplexer_11_out, multiplexer_14_out,
       PCBranch, R1, R2, ram_1_data, RD, shifter_1_out, WB_IR, \下降沿regifile_1_r1 , \下降沿regifile_1_r2 ;

  Button \u_总复位  (.out(RST));
  Button _1 ();  // open: out
  Button _2 ();  // open: out
  Button _3 ();  // open: out
  // Probe on \总周期数 
  // Probe on \总周期数 
  not not_1 (not_1_out, judge);
  Button \u_继续运行  (.out(Go));
  LED #(.active("true")) led_1 (.in(W1));
  LED #(.active("true")) led_2 (.in(W2));
  LED #(.active("true")) led_3 (.in(W3));
  Multiplexer #(.select(1), .width(32), .disabled("Z"), .enable("false")) multiplexer_1 (
    .in0(adder_2_out), .in1(adder_1_out), .out(multiplexer_1_out), .sel(BEqual));
  Adder #(.width(32)) adder_1 (.a(PCBranch), .b(32'h4), .out(adder_1_out));  // open: cin, cout
  not not_2 (not_2_out, \数据相关 );
  and and_1 (and_1_out, not_1_out, Syscall);
  Hex_Digit_Display hex_digit_display_1 (.value(LedData[31:28]));  // open: dp
  // Probe on IF_PC[19:0]
  // Mips_Probe mips_probe_1: pin names not known; wires that end beside it: IR1, IR2, IR3, IF_IR
  and and_2 (and_2_out, JMP, ~JR);  // AND_Gate
  Multiplexer #(.select(1), .width(32), .disabled("Z"), .enable("false")) multiplexer_2 (
    .in0(multiplexer_3_out), .in1({EX_PC[31:28], JMPAddr, 2'b00}), .out(multiplexer_2_out), .sel(and_2_out));
  Multiplexer #(.select(1), .width(32), .disabled("Z"), .enable("false")) multiplexer_3 (
    .in0(multiplexer_1_out), .in1(R1), .out(multiplexer_3_out), .sel(JR));
  and and_3 (and_3_out, not_2_out, not_3_out);
  Counter #(.width(16), .max('hffff), .ongoal("wrap"), .trigger("rising"), .behavior("old")) counter_1 (
    .count(not_3_out), .Q(\总周期数 ), .clk(CLK), .clr(RST));  // open: load, D, carry, preset
  Register #(.width(1), .trigger("rising"), .Select("low")) register_1 (
    .D(Syscall), .en(and_1_out), .Q(enable), .clk(CLK), .clr(or_1_out));
  or or_1 (or_1_out, Go, RST);
  Hex_Digit_Display hex_digit_display_2 (.value(LedData[23:20]));  // open: dp
  Hex_Digit_Display hex_digit_display_3 (.value(LedData[27:24]));  // open: dp
  // Probe on ID_PC[19:0]
  // Mips_Probe mips_probe_2: pin names not known; wires that end beside it: ID_IR
  Register #(.width(32), .trigger("rising"), .Select("low")) PC (
    .D(multiplexer_2_out), .en(and_3_out), .Q(IF_PC), .clk(CLK), .clr(RST));
  not not_3 (not_3_out, enable);
  Hex_Digit_Display hex_digit_display_4 (.value(LedData[15:12]));  // open: dp
  Hex_Digit_Display hex_digit_display_5 (.value(LedData[19:16]));  // open: dp
  and and_4 (and_4_out, \数据相关 , not_3_out);
  Hex_Digit_Display hex_digit_display_6 (.value(LedData[11:8]));  // open: dp
  Hex_Digit_Display hex_digit_display_7 (.value(LedData[7:4]));  // open: dp
  Clock #(.highDuration(1), .lowDuration(1)) clock_1 (.out(clock_1_out));
  // Probe on EX_PC[19:0]
  // Mips_Probe mips_probe_3: pin names not known; wires that end beside it: clock_1_out, EX_IR, CLK
  Adder #(.width(32)) adder_2 (.a(IF_PC), .b(32'h4), .out(adder_2_out));  // open: cin, cout
  Counter #(.width(16), .max('hffff), .ongoal("wrap"), .trigger("rising"), .behavior("old")) counter_2 (
    .count(and_4_out), .Q(\LoadUse次数 ), .clk(CLK), .clr(RST));  // open: load, D, carry, preset
  Hex_Digit_Display hex_digit_display_8 (.value(LedData[3:0]));  // open: dp
  ROM #(.addrWidth(10), .dataWidth(32), .Select("high")) rom_1 (.addr(IF_PC[11:2]), .data(IF_IR));
  or or_2 (or_2_out, \数据相关 , enable);
  // Probe on \总周期数 
  // Probe on M_PC[19:0]
  // Mips_Probe mips_probe_4: pin names not known; wires that end beside it: MEM_IR
  // Mips_Probe mips_probe_5: pin names not known; wires that end beside it: ID_IR
  IF_ID if_id_1 (
    .IR(IF_IR), .PC_4(IF_PC), .CLK(CLK), .IR_2(ID_IR), .PC_4_2(ID_PC), .\同步清零_高电平有效 (clear),
    .\使能端_低电平有效 (or_2_out));
  // Probe on \总周期数 
  // Probe on \无条件分支数 
  // Probe on \条件分支成功数 
  // Probe on \LoadUse次数 
  // Probe on \LoadUse次数 
  // Probe on IF_PC[11:0]
  // Probe on WB_PC[19:0]
  // Mips_Probe mips_probe_6: pin names not known; wires that end beside it: WB_IR
  \重定向检测  \u_重定向检测_1  (
    .MEM_MemToReg(MEM_MTR), .ID_R1(multiplexer_4_out), .EX_WriteReg(id_ex_1_w_num_2), .EX_RegWrite(EX_RW),
    .MEM_WriteReg(ex_mem_1_w_num_2), .MEM_RegWrite(MEM_RW), .OP(ID_IR[31:26]), .Func(ID_IR[5:0]),
    .ID_R2(multiplexer_5_out), .ForwardToR1(forwardR1), .EX_MemToReg(EX_MTR), .Load_Use(\数据相关 ),
    .ForwardToR2(forwardR2));
  Multiplexer #(.select(1), .width(5), .disabled("Z"), .enable("false")) multiplexer_4 (
    .in0(ID_IR[25:21]), .in1(5'b00100), .out(multiplexer_4_out), .sel(\单周期硬布线控制器_1_syscall ));
  Multiplexer #(.select(1), .width(5), .disabled("Z"), .enable("false")) multiplexer_5 (
    .in0(ID_IR[20:16]), .in1(5'b00010), .out(multiplexer_5_out), .sel(\单周期硬布线控制器_1_syscall ));
  Multiplexer #(.select(1), .width(5), .disabled("Z"), .enable("false")) multiplexer_6 (
    .in0(ID_IR[20:16]), .in1(ID_IR[15:11]), .out(multiplexer_6_out), .sel(RegDst));
  assign bit_extender_1_out = {{16{1'b0}}, ID_IR[15:0]};  // Bit_Extender bit_extender_1
  assign bit_extender_2_out = {{16{ID_IR[15]}}, ID_IR[15:0]};  // Bit_Extender bit_extender_2
  // Probe on ID_PC[11:0]
  // Probe on EX_PC[11:0]
  Multiplexer #(.select(1), .width(5), .disabled("Z"), .enable("false")) multiplexer_7 (
    .in0(multiplexer_6_out), .in1({5{1'b1}}), .out(multiplexer_7_out), .sel(\单周期硬布线控制器_1_jal ));
  Multiplexer #(.select(1), .width(32), .disabled("Z"), .enable("false")) multiplexer_8 (
    .in0(bit_extender_1_out), .in1(bit_extender_2_out), .out(multiplexer_8_out), .sel(SignedExt));
  // Probe on M_PC[11:0]
  D_Flip_Flop #(.trigger("high"), .Pre_Clr_Positions("LEGACY"), .NegatePresetClear("false"), .enable("true"), .NewFFLayout("false")) d_ff_1 (.Q(d_ff_1_q));  // open: clk, D, Qn, preset, en, reset
  // Probe on 13'hc
  \单周期硬布线控制器  \u_单周期硬布线控制器_1  (
    .Func(ID_IR[5:0]), .OP(ID_IR[31:26]), .ALU_OP(\单周期硬布线控制器_1_alu_op ), .MemToReg(\单周期硬布线控制器_1_memtoreg ),
    .MemWrite(\单周期硬布线控制器_1_memwrite ), .ALU_SRC(\单周期硬布线控制器_1_alu_src ), .RegWrite(\单周期硬布线控制器_1_regwrite ),
    .SysCALL(\单周期硬布线控制器_1_syscall ), .SignedExt(SignedExt), .RegDst(RegDst), .JR(ID_JR), .JMP(ID_JMP),
    .Beq(\单周期硬布线控制器_1_beq ), .JAL(\单周期硬布线控制器_1_jal ), .Bne(\单周期硬布线控制器_1_bne ), .LUI(ID_LUI),
    .LBU(\单周期硬布线控制器_1_lbu ), .BGTZ(\单周期硬布线控制器_1_bgtz ));  // open: ERET, MF, MFC0, MTC0
  Multiplexer #(.select(1), .width(32), .disabled("Z"), .enable("false")) multiplexer_9 (
    .in0(multiplexer_8_out), .in1({ID_IR[15:0], {16{1'b0}}}), .out(multiplexer_9_out), .sel(ID_LUI));
  // Probe on WB_PC[11:0]
  Comparator #(.width(13), .mode("twosComplement")) comparator_1 (
    .a(CNT_num), .b(13'hc), .eq(comparator_1_eq), .lt(comparator_1_lt));  // open: gt
  Clock #(.highDuration(1), .lowDuration(1)) clock_2 (.out(clock_2_out));
  \下降沿Regifile  \u_下降沿regifile_1  (
    .Din(RDin), .Clk(CLK), .R1(\下降沿regifile_1_r1 ), .R2(\下降沿regifile_1_r2 ), .WE(RegWrite), .W_num(W_num),
    .R1_num(multiplexer_4_out), .R2_num(multiplexer_5_out));
  or or_3 (or_3_out, clear, \数据相关 );
  nand nand_1 (nand_1_out, d_ff_1_q, comparator_1_eq);
  Counter #(.width(13), .max('h1fff), .ongoal("stay"), .trigger("rising"), .behavior("old")) counter_3 (
    .count(comparator_1_lt), .Q(CNT_num), .clk(clock_2_out));  // open: load, D, carry, clr, preset
  ID_EX id_ex_1 (
    .BGTZ(\单周期硬布线控制器_1_bgtz ), .LBU(\单周期硬布线控制器_1_lbu ), .RegWrite(\单周期硬布线控制器_1_regwrite ),
    .W_num(multiplexer_7_out), .MemToReg(\单周期硬布线控制器_1_memtoreg ), .Beq(\单周期硬布线控制器_1_beq ),
    .Bne(\单周期硬布线控制器_1_bne ), .JAL(\单周期硬布线控制器_1_jal ), .Shamt(ID_IR[10:6]), .JR(ID_JR), .JMP(ID_JMP),
    .MemWrite(\单周期硬布线控制器_1_memwrite ), .AluOP(\单周期硬布线控制器_1_alu_op ), .AluSrcB(\单周期硬布线控制器_1_alu_src ),
    .Sys(\单周期硬布线控制器_1_syscall ), .f1(forwardR1), .f2(forwardR2), .R1(\下降沿regifile_1_r1 ),
    .R2(\下降沿regifile_1_r2 ), .Imm(multiplexer_9_out), .PC_4(ID_PC), .IR(ID_IR), ._26(ID_IR[25:0]), .CLK(CLK),
    .BGTZ_2(id_ex_1_bgtz_2), .LBU_2(id_ex_1_lbu_2), .RegWrite_2(EX_RW), .W_num_2(id_ex_1_w_num_2),
    .MemToReg_2(EX_MTR), .Beq_2(id_ex_1_beq_2), .Bne_2(id_ex_1_bne_2), .JAL_2(id_ex_1_jal_2),
    .Shamt_2(id_ex_1_shamt_2), .JR_2(JR), .JMP_2(JMP), .MemWrite_2(id_ex_1_memwrite_2),
    .AluOP_2(id_ex_1_aluop_2), .AluSrcB_2(id_ex_1_alusrcb_2), .Sys_2(EX_sys), .f1_2(EX_F1), .f2_2(EX_F2),
    .R1_2(EX_R1), .R2_2(EX_R2), .Imm_2(id_ex_1_imm_2), .PC_4_2(EX_PC), .IR_2(EX_IR), ._26_2(JMPAddr),
    .\同步清零_高电平有效 (or_3_out), .\使能端_低电平有效 (enable), .LUI(ID_LUI), .LUI_2(id_ex_1_lui_2));  // open: eret, eret_2, eret_3, eret_4, OP, OP_2
  Multiplexer #(.select(2), .width(32), .disabled("Z"), .enable("false")) multiplexer_10 (
    .in0(EX_R1), .in1(ALURes), .in2(RD), .in3(EXALU), .out(R1), .sel(EX_F1));
  assign CLK = nand_1_out ? clock_2_out : 1'bz;  // Controlled_Buffer controlled_buffer_1
  Pull_Resistor #(.pull(1)) pull_resistor_1 (.node(CLK));
  Comparator #(.width(32), .mode("twosComplement")) comparator_2 (
    .a(R1), .b(32'h1), .gt(comparator_2_gt));  // open: eq, lt
  and and_5 (and_5_out, equal, id_ex_1_beq_2);
  and and_6 (and_6_out, ~equal, id_ex_1_bne_2);  // AND_Gate
  Shifter #(.width(32), .shift("ll")) shifter_1 (.in(id_ex_1_imm_2), .\dist (5'b00010), .out(shifter_1_out));
  Comparator #(.width(6), .mode("twosComplement")) comparator_3 (
    .a(JMPAddr[7:2]), .b(6'b000111), .eq(comparator_3_eq));  // open: gt, lt
  and and_7 (and_7_out, id_ex_1_bgtz_2, comparator_2_gt);
  Multiplexer #(.select(1), .width(32), .disabled("Z"), .enable("false")) multiplexer_11 (
    .in0(R2), .in1(id_ex_1_imm_2), .out(multiplexer_11_out), .sel(id_ex_1_alusrcb_2));
  Adder #(.width(32)) adder_3 (.a(shifter_1_out), .b(EX_PC), .out(PCBranch));  // open: cin, cout
  Multiplexer #(.select(1), .width(5), .disabled("Z"), .enable("false")) multiplexer_12 (
    .in0(id_ex_1_shamt_2), .in1(R1[4:0]), .out(multiplexer_12_out), .sel(comparator_3_eq));
  Multiplexer #(.select(2), .width(32), .disabled("Z"), .enable("false")) multiplexer_13 (
    .in0(EX_R2), .in1(ALURes), .in2(RD), .in3(EXALU), .out(R2), .sel(EX_F2));
  or or_4 (clear, JMP, and_5_out, and_6_out, and_7_out);
  or or_5 (BEqual, and_7_out, and_5_out, and_6_out);
  MIPS_ALU mips_alu_1 (
    .X(R1), .Y(multiplexer_11_out), .AluOP(id_ex_1_aluop_2), .Equal(equal), .Result(mips_alu_1_result),
    .shamt(multiplexer_12_out));  // open: Result_2
  Comparator #(.width(32), .mode("twosComplement")) comparator_4 (.a(R2), .b(32'h22), .eq(Led));  // open: gt, lt
  // Probe on nothing
  EX_MEM ex_mem_1 (
    .LBU(id_ex_1_lbu_2), .RegWrite(EX_RW), .W_num(id_ex_1_w_num_2), .MemToReg(EX_MTR),
    .MemWrite(id_ex_1_memwrite_2), .Halt(Led), .JAL(id_ex_1_jal_2), .data(EX_Data), .Alu(mips_alu_1_result),
    .R2(R2), .PC_4(EX_PC), .IR(EX_IR), .CLK(CLK), .LBU_2(ex_mem_1_lbu_2), .RegWrite_2(MEM_RW),
    .W_num_2(ex_mem_1_w_num_2), .MemToReg_2(MEM_MTR), .MemWrite_2(MemWrite), .Halt_2(ex_mem_1_halt_2),
    .JAL_2(ex_mem_1_jal_2), .data_2(ex_mem_1_data_2), .Alu_2(EXALU), .R2_2(MDin), .PC_4_2(M_PC),
    .IR_2(MEM_IR), .\使能端_低电平有效 (enable), .LUI(id_ex_1_lui_2), .LUI_2(ex_mem_1_lui_2), .imm26(JMPAddr),
    .imm26_2(ex_mem_1_imm26_2), .sys(EX_sys), .sys_2(ex_mem_1_sys_2));  // open: 同步清零_高电平有效, OP, OP_2
  and and_8 (and_8_out, EX_sys, Led);
  Register #(.width(32), .trigger("rising"), .Select("low")) register_2 (
    .D(R1), .en(and_8_out), .Q(EX_Data), .clk(CLK));  // open: clr
  RAM #(.addrWidth(10), .dataWidth(32), .bus("separate"), .Select("high")) ram_1 (
    .addr(EXALU[11:2]), .din(MDin), .data(ram_1_data), .str(MemWrite), .clk(CLK));  // open: sel, ld, clr
  MEM_WB mem_wb_1 (
    .LBU(ex_mem_1_lbu_2), .RegWrite(MEM_RW), .W_num(ex_mem_1_w_num_2), .MemToReg(MEM_MTR), .Addr(EXALU),
    .Halt(ex_mem_1_halt_2), .JAL(ex_mem_1_jal_2), .Alu(EXALU), .MD(ram_1_data), .PC_4(M_PC), .IR(MEM_IR),
    .CLK(CLK), .LBU_2(mem_wb_1_lbu_2), .RegWrite_2(RegWrite), .W_num_2(W_num),
    .MemToReg_2(mem_wb_1_memtoreg_2), .Addr_2(mem_wb_1_addr_2), .Halt_2(judge), .JAL_2(JAL), .Alu_2(ALURes),
    .MD_2(mem_wb_1_md_2), .PC_4_2(WB_PC), .IR_2(WB_IR), .\使能端_低电平有效 (enable), .LUI(ex_mem_1_lui_2),
    .data(ex_mem_1_data_2), .data_2(LedData), .imm26(ex_mem_1_imm26_2), .imm26_2(mem_wb_1_imm26_2),
    .sys(ex_mem_1_sys_2), .sys_2(Syscall));  // open: 同步清零_高电平有效, LUI_2, OP, OP_2, rs, rs_2
  Multiplexer #(.select(1), .width(32), .disabled("Z"), .enable("false")) multiplexer_14 (
    .in0(ALURes), .in1(mem_wb_1_md_2), .out(multiplexer_14_out), .sel(mem_wb_1_memtoreg_2));
  Multiplexer #(.select(2), .width(8), .disabled("Z"), .enable("false")) multiplexer_15 (
    .in0(multiplexer_14_out[7:0]), .in1(multiplexer_14_out[15:8]), .in2(multiplexer_14_out[23:16]),
    .in3(multiplexer_14_out[31:24]), .out(multiplexer_15_out), .sel(mem_wb_1_addr_2[1:0]));
  assign bit_extender_3_out = {{24{1'b0}}, multiplexer_15_out};  // Bit_Extender bit_extender_3
  Multiplexer #(.select(1), .width(32), .disabled("Z"), .enable("false")) multiplexer_16 (
    .in0(RD), .in1(adder_4_out), .out(RDin), .sel(JAL));
  Multiplexer #(.select(1), .width(32), .disabled("Z"), .enable("false")) multiplexer_17 (
    .in0(multiplexer_14_out), .in1(bit_extender_3_out), .out(RD), .sel(mem_wb_1_lbu_2));
  Adder #(.width(32)) adder_4 (.a(32'h4), .b(WB_PC), .out(adder_4_out));  // open: cin, cout

  // Other names for the same wires on the sheet: Din[31:0] = RDin; JMPAddr[31:28] = EX_PC[31:28]; MEM_PC[31:0] = M_PC;
  //   插入气泡数[15:0] = \LoadUse次数 

  // Notes on the sheet:
  //   中断源
  //   时空图监测，可删除
  //   中断等待指示
  //   数码管输出
  //   指令存储器
  //   contents of rom_1 (hex, n*v repeats v):
  //   200b0008 3c11fedc 3631ffff 112020 20020022 c 3c11ba98 112020 c 3c117654 112020 c 3c113210 112020 c
  //   216bffff 1560fff0 2002000a c
  //   指令字
  //   OP
  //   Func
  //   rs
  //   rt
  //   rd
  //   控制位
  //   流水调试日志用
  //   暂停节拍，不能为0
  //   JMP
  //   JR
  //   OP
  //   Func
  //   Syscall
  //   戳工具置1进入计数暂停模式，ctrl+k时钟自动运行到对应节拍暂停
  //   ctrl+k关闭时钟连续运行，将控制位置零，进入单步调试模式调试
  //   Beq
  //   Bne
  //   MemToReg
  //   MemWrite
  //   AluOP
  //   AluSrcB
  //   RegWrite
  //   JAL
  //   可计数暂停的时钟源
  //   SRAV指令
  //   为方便自动评测，需要输出流水线各段保存的PC值，注意是PC不是PC+4，另外ID段寄存器写入信息，Mem段内存写入信息也要输出
endmodule

module \气泡流水线  (
  output RegWrite,
  output MemWrite,
  output [31:0] IF_PC,
  output [31:0] ID_PC,
  output [31:0] EX_PC,
  output [31:0] M_PC,
  output [31:0] WB_PC,
  output [31:0] RDin,
  output [31:0] MDin,
  output [31:0] LedData
);

  wire and_1_out, and_2_out, and_3_out, and_4_out, and_5_out, and_6_out, BEqual, clear, CLK, clock_1_out,
       clock_2_out, comparator_1_eq, comparator_2_eq, comparator_2_lt, comparator_3_gt, comparator_4_eq,
       d_ff_1_q, equal, EX_Halt, ex_mem_1_halt_2, ex_mem_1_jal_2, ex_mem_1_lbu_2, ex_mem_1_lui_2,
       ex_mem_1_memtoreg_2, EX_RW, Go, Halt, id_ex_1_alusrcb_2, id_ex_1_beq_2, id_ex_1_bgtz_2, id_ex_1_bne_2,
       id_ex_1_jal_2, id_ex_1_lbu_2, id_ex_1_lui_2, id_ex_1_memtoreg_2, id_ex_1_memwrite_2, ID_JMP, ID_JR,
       IR1, IR2, IR3, JAL, JMP, JR, MEM_RW, mem_wb_1_lbu_2, mem_wb_1_lui_2, mem_wb_1_memtoreg_2, nand_1_out,
       not_1_out, not_2_out, or_1_out, or_2_out, pause, RegDst, RST, SignedExt, Syscall, W1, W2, W3,
       \单周期硬布线控制器_1_alu_src , \单周期硬布线控制器_1_beq , \单周期硬布线控制器_1_bgtz , \单周期硬布线控制器_1_bne , \单周期硬布线控制器_1_jal ,
       \单周期硬布线控制器_1_lbu , \单周期硬布线控制器_1_lui , \单周期硬布线控制器_1_memtoreg , \单周期硬布线控制器_1_memwrite ,
       \单周期硬布线控制器_1_regwrite , \单周期硬布线控制器_1_syscall , \数据检测逻辑_1_pause , \数据检测逻辑_2_pause ;
  wire [3:0] id_ex_1_aluop_2, \单周期硬布线控制器_1_alu_op ;
  wire [4:0] ex_mem_1_w_num_2, id_ex_1_shamt_2, id_ex_1_w_num_2, multiplexer_4_out, multiplexer_5_out,
       multiplexer_6_out, multiplexer_7_out, multiplexer_10_out, W_num;
  wire [7:0] multiplexer_13_out;
  wire [12:0] CNT_num;
  wire [15:0] \LoadUse次数 , \总周期数 , \插入气泡数 , \无条件分支数 , \条件分支成功数 ;
  wire [25:0] ex_mem_1_imm26_2;
  wire [25:16] mem_wb_1_imm26_2_2;
  wire [27:2] JMPAddr;
  wire [31:0] adder_1_out, adder_2_out, adder_4_out, bit_extender_1_out, bit_extender_2_out,
       bit_extender_3_out, Din, EX_IR, ex_mem_1_alu_2, id_ex_1_imm_2, ID_IR, IF_IR, MEM_IR, mem_wb_1_addr_2,
       mem_wb_1_alu_2, mem_wb_1_md_2, mips_alu_1_result, multiplexer_1_out, multiplexer_2_out,
       multiplexer_3_out, multiplexer_8_out, multiplexer_9_out, multiplexer_11_out, multiplexer_15_out,
       PCBranch, ram_1_data, rs, rt, shifter_1_out, WB_IR, \下降沿regifile_1_r1 , \下降沿regifile_1_r2 ;
  wire [31:16] mem_wb_1_imm26_2;

  Button \u_总复位  (.out(RST));
  Button _1 ();  // open: out
  Button _2 ();  // open: out
  Button _3 ();  // open: out
  // Probe on \总周期数 
  // Probe on \总周期数 
  Button \u_继续运行  (.out(Go));
  LED #(.active("true")) led_1 (.in(W1));
  LED #(.active("true")) led_2 (.in(W2));
  LED #(.active("true")) led_3 (.in(W3));
  Multiplexer #(.select(1), .width(32), .disabled("Z"), .enable("false")) multiplexer_1 (
    .in0(adder_2_out), .in1(adder_1_out), .out(multiplexer_1_out), .sel(BEqual));
  Adder #(.width(32)) adder_1 (.a(PCBranch), .b(32'h4), .out(adder_1_out));  // open: cin, cout
  Hex_Digit_Display hex_digit_display_1 (.value(LedData[31:28]));  // open: dp
  // Probe on IF_PC[19:0]
  // Mips_Probe mips_probe_1: pin names not known; wires that end beside it: IR1, IR2, IR3, IF_IR
  Comparator #(.width(32), .mode("twosComplement")) comparator_1 (
    .a(rs), .b(32'h22), .eq(comparator_1_eq));  // open: gt, lt
  or or_1 (or_1_out, Halt, pause);
  and and_1 (and_1_out, JMP, ~JR);  // AND_Gate
  not not_1 (not_1_out, or_1_out);
  Multiplexer #(.select(1), .width(32), .disabled("Z"), .enable("false")) multiplexer_2 (
    .in0(multiplexer_3_out), .in1({EX_PC[31:28], JMPAddr, 2'b00}), .out(multiplexer_2_out), .sel(and_1_out));
  Multiplexer #(.select(1), .width(32), .disabled("Z"), .enable("false")) multiplexer_3 (
    .in0(multiplexer_1_out), .in1(rs), .out(multiplexer_3_out), .sel(JR));
  Hex_Digit_Display hex_digit_display_2 (.value(LedData[27:24]));  // open: dp
  Hex_Digit_Display hex_digit_display_3 (.value(LedData[23:20]));  // open: dp
  // Probe on ID_PC[19:0]
  // Mips_Probe mips_probe_2: pin names not known; wires that end beside it: ID_IR
  Register #(.width(32), .trigger("rising"), .Select("low")) register_1 (
    .D(rt), .en(comparator_1_eq), .Q(LedData), .clk(CLK));  // open: clr
  Register #(.width(1), .trigger("rising"), .Select("low")) register_2 (
    .D(and_2_out), .en(and_2_out), .Q(EX_Halt), .clk(CLK), .clr(Go));
  and and_2 (and_2_out, ~comparator_1_eq, Syscall);  // AND_Gate
  Register #(.width(32), .trigger("rising"), .Select("low")) PC (
    .D(multiplexer_2_out), .en(not_1_out), .Q(IF_PC), .clk(CLK));  // open: clr
  Hex_Digit_Display hex_digit_display_4 (.value(LedData[19:16]));  // open: dp
  Hex_Digit_Display hex_digit_display_5 (.value(LedData[15:12]));  // open: dp
  Hex_Digit_Display hex_digit_display_6 (.value(LedData[7:4]));  // open: dp
  Hex_Digit_Display hex_digit_display_7 (.value(LedData[11:8]));  // open: dp
  Clock #(.highDuration(1), .lowDuration(1)) clock_1 (.out(clock_1_out));
  // Probe on EX_PC[19:0]
  // Mips_Probe mips_probe_3: pin names not known; wires that end beside it: clock_1_out, EX_IR, CLK
  Adder #(.width(32)) adder_2 (.a(IF_PC), .b(32'h4), .out(adder_2_out));  // open: cin, cout
  Hex_Digit_Display hex_digit_display_8 (.value(LedData[3:0]));  // open: dp
  and and_3 (and_3_out, ~Halt, CLK);  // AND_Gate
  ROM #(.addrWidth(10), .dataWidth(32), .Select("high")) rom_1 (.addr(IF_PC[11:2]), .data(IF_IR));
  // Probe on \总周期数 
  // Probe on M_PC[19:0]
  // Mips_Probe mips_probe_4: pin names not known; wires that end beside it: MEM_IR
  Counter #(.width(16), .max('hffff), .ongoal("wrap"), .trigger("rising"), .behavior("old")) counter_1 (
    .Q(\总周期数 ), .clk(and_3_out));  // open: load, D, count, carry, clr, preset
  // Mips_Probe mips_probe_5: pin names not known; wires that end beside it: ID_IR
  IF_ID if_id_1 (
    .IR(IF_IR), .PC_4(IF_PC), .CLK(CLK), .IR_2(ID_IR), .PC_4_2(ID_PC), .\同步清零_高电平有效 (clear),
    .\使能端_低电平有效 (pause));
  // Probe on \总周期数 
  // Probe on \无条件分支数 
  // Probe on \条件分支成功数 
  // Probe on \插入气泡数 
  // Probe on \LoadUse次数 
  // Probe on IF_PC[11:0]
  // Probe on WB_PC[19:0]
  // Mips_Probe mips_probe_6: pin names not known; wires that end beside it: WB_IR
  Multiplexer #(.select(1), .width(5), .disabled("Z"), .enable("false")) multiplexer_4 (
    .in0(ID_IR[25:21]), .in1(5'b00010), .out(multiplexer_4_out), .sel(\单周期硬布线控制器_1_syscall ));
  Multiplexer #(.select(1), .width(5), .disabled("Z"), .enable("false")) multiplexer_5 (
    .in0(ID_IR[20:16]), .in1(5'b00100), .out(multiplexer_5_out), .sel(\单周期硬布线控制器_1_syscall ));
  Multiplexer #(.select(1), .width(5), .disabled("Z"), .enable("false")) multiplexer_6 (
    .in0(ID_IR[20:16]), .in1(ID_IR[15:11]), .out(multiplexer_6_out), .sel(RegDst));
  // Probe on EX_PC[11:0]
  // Probe on ID_PC[11:0]
  Multiplexer #(.select(1), .width(5), .disabled("Z"), .enable("false")) multiplexer_7 (
    .in0(multiplexer_6_out), .in1({5{1'b1}}), .out(multiplexer_7_out), .sel(\单周期硬布线控制器_1_jal ));
  assign bit_extender_1_out = {{16{1'b0}}, ID_IR[15:0]};  // Bit_Extender bit_extender_1
  assign bit_extender_2_out = {{16{ID_IR[15]}}, ID_IR[15:0]};  // Bit_Extender bit_extender_2
  // Probe on M_PC[11:0]
  D_Flip_Flop #(.trigger("high"), .Pre_Clr_Positions("LEGACY"), .NegatePresetClear("false"), .enable("true"), .NewFFLayout("false")) d_ff_1 (.Q(d_ff_1_q));  // open: clk, D, Qn, preset, en, reset
  // Probe on 13'hc
  \单周期硬布线控制器  \u_单周期硬布线控制器_1  (
    .Func(ID_IR[5:0]), .OP(ID_IR[31:26]), .ALU_OP(\单周期硬布线控制器_1_alu_op ), .MemToReg(\单周期硬布线控制器_1_memtoreg ),
    .MemWrite(\单周期硬布线控制器_1_memwrite ), .ALU_SRC(\单周期硬布线控制器_1_alu_src ), .RegWrite(\单周期硬布线控制器_1_regwrite ),
    .SysCALL(\单周期硬布线控制器_1_syscall ), .SignedExt(SignedExt), .RegDst(RegDst), .JR(ID_JR), .JMP(ID_JMP),
    .Beq(\单周期硬布线控制器_1_beq ), .JAL(\单周期硬布线控制器_1_jal ), .Bne(\单周期硬布线控制器_1_bne ), .LUI(\单周期硬布线控制器_1_lui ),
    .LBU(\单周期硬布线控制器_1_lbu ), .BGTZ(\单周期硬布线控制器_1_bgtz ));  // open: ERET, MF, MFC0, MTC0
  Multiplexer #(.select(1), .width(32), .disabled("Z"), .enable("false")) multiplexer_8 (
    .in0(bit_extender_1_out), .in1(bit_extender_2_out), .out(multiplexer_8_out), .sel(SignedExt));
  // Probe on WB_PC[11:0]
  Comparator #(.width(13), .mode("twosComplement")) comparator_2 (
    .a(CNT_num), .b(13'hc), .eq(comparator_2_eq), .lt(comparator_2_lt));  // open: gt
  Clock #(.highDuration(1), .lowDuration(1)) clock_2 (.out(clock_2_out));
  \下降沿Regifile  \u_下降沿regifile_1  (
    .Din(Din), .Clk(CLK), .R1(\下降沿regifile_1_r1 ), .R2(\下降沿regifile_1_r2 ), .WE(RegWrite), .W_num(W_num),
    .R1_num(multiplexer_4_out), .R2_num(multiplexer_5_out));
  or or_2 (or_2_out, clear, pause);
  nand nand_1 (nand_1_out, d_ff_1_q, comparator_2_eq);
  Counter #(.width(13), .max('h1fff), .ongoal("stay"), .trigger("rising"), .behavior("old")) counter_2 (
    .count(comparator_2_lt), .Q(CNT_num), .clk(clock_2_out));  // open: load, D, carry, clr, preset
  ID_EX id_ex_1 (
    .BGTZ(\单周期硬布线控制器_1_bgtz ), .LBU(\单周期硬布线控制器_1_lbu ), .RegWrite(\单周期硬布线控制器_1_regwrite ),
    .W_num(multiplexer_7_out), .MemToReg(\单周期硬布线控制器_1_memtoreg ), .Beq(\单周期硬布线控制器_1_beq ),
    .Bne(\单周期硬布线控制器_1_bne ), .JAL(\单周期硬布线控制器_1_jal ), .Shamt(ID_IR[10:6]), .JR(ID_JR), .JMP(ID_JMP),
    .MemWrite(\单周期硬布线控制器_1_memwrite ), .AluOP(\单周期硬布线控制器_1_alu_op ), .AluSrcB(\单周期硬布线控制器_1_alu_src ),
    .Sys(\单周期硬布线控制器_1_syscall ), .R1(\下降沿regifile_1_r1 ), .R2(\下降沿regifile_1_r2 ), .Imm(multiplexer_8_out),
    .PC_4(ID_PC), .IR(ID_IR), ._26(ID_IR[25:0]), .CLK(CLK), .BGTZ_2(id_ex_1_bgtz_2), .LBU_2(id_ex_1_lbu_2),
    .RegWrite_2(EX_RW), .W_num_2(id_ex_1_w_num_2), .MemToReg_2(id_ex_1_memtoreg_2), .Beq_2(id_ex_1_beq_2),
    .Bne_2(id_ex_1_bne_2), .JAL_2(id_ex_1_jal_2), .Shamt_2(id_ex_1_shamt_2), .JR_2(JR), .JMP_2(JMP),
    .MemWrite_2(id_ex_1_memwrite_2), .AluOP_2(id_ex_1_aluop_2), .AluSrcB_2(id_ex_1_alusrcb_2),
    .Sys_2(Syscall), .R1_2(rs), .R2_2(rt), .Imm_2(id_ex_1_imm_2), .PC_4_2(EX_PC), .IR_2(EX_IR),
    ._26_2(JMPAddr), .\同步清零_高电平有效 (or_2_out), .LUI(\单周期硬布线控制器_1_lui ), .LUI_2(id_ex_1_lui_2));  // open: eret, eret_2, f1, f2, eret_3, eret_4, f1_2, f2_2, 使能端_低电平有效, OP, OP_2
  assign CLK = nand_1_out ? clock_2_out : 1'bz;  // Controlled_Buffer controlled_buffer_1
  Pull_Resistor #(.pull(1)) pull_resistor_1 (.node(CLK));
  Comparator #(.width(32), .mode("twosComplement")) comparator_3 (
    .a(rs), .b({32{1'b0}}), .gt(comparator_3_gt));  // open: eq, lt
  and and_4 (and_4_out, equal, id_ex_1_beq_2);
  and and_5 (and_5_out, ~equal, id_ex_1_bne_2);  // AND_Gate
  Shifter #(.width(32), .shift("ll")) shifter_1 (.in(id_ex_1_imm_2), .\dist (5'b00010), .out(shifter_1_out));
  Comparator #(.width(6), .mode("twosComplement")) comparator_4 (
    .a(JMPAddr[7:2]), .b(6'b000111), .eq(comparator_4_eq));  // open: gt, lt
  and and_6 (and_6_out, id_ex_1_bgtz_2, comparator_3_gt);
  Multiplexer #(.select(1), .width(32), .disabled("Z"), .enable("false")) multiplexer_9 (
    .in0(rt), .in1(id_ex_1_imm_2), .out(multiplexer_9_out), .sel(id_ex_1_alusrcb_2));
  Adder #(.width(32)) adder_3 (.a(shifter_1_out), .b(EX_PC), .out(PCBranch));  // open: cin, cout
  Multiplexer #(.select(1), .width(5), .disabled("Z"), .enable("false")) multiplexer_10 (
    .in0(id_ex_1_shamt_2), .in1(rs[4:0]), .out(multiplexer_10_out), .sel(comparator_4_eq));
  or or_3 (clear, JMP, JR, and_6_out, and_4_out, and_5_out, id_ex_1_jal_2);
  or or_4 (BEqual, and_6_out, and_4_out, and_5_out);
  MIPS_ALU mips_alu_1 (
    .X(rs), .Y(multiplexer_9_out), .AluOP(id_ex_1_aluop_2), .Equal(equal), .Result(mips_alu_1_result),
    .shamt(multiplexer_10_out));  // open: Result_2
  \数据检测逻辑  \u_数据检测逻辑_1  (.ID_IR(ID_IR), .EX_RW(EX_RW), .EX_IR(EX_IR), .pause(\数据检测逻辑_1_pause ));
  EX_MEM ex_mem_1 (
    .LBU(id_ex_1_lbu_2), .RegWrite(EX_RW), .W_num(id_ex_1_w_num_2), .MemToReg(id_ex_1_memtoreg_2),
    .MemWrite(id_ex_1_memwrite_2), .Halt(EX_Halt), .JAL(id_ex_1_jal_2), .Alu(mips_alu_1_result), .R2(rt),
    .PC_4(EX_PC), .IR(EX_IR), .CLK(CLK), .LBU_2(ex_mem_1_lbu_2), .RegWrite_2(MEM_RW),
    .W_num_2(ex_mem_1_w_num_2), .MemToReg_2(ex_mem_1_memtoreg_2), .MemWrite_2(MemWrite),
    .Halt_2(ex_mem_1_halt_2), .JAL_2(ex_mem_1_jal_2), .Alu_2(ex_mem_1_alu_2), .R2_2(MDin), .PC_4_2(M_PC),
    .IR_2(MEM_IR), .LUI(id_ex_1_lui_2), .LUI_2(ex_mem_1_lui_2), .imm26(JMPAddr), .imm26_2(ex_mem_1_imm26_2));  // open: data, data_2, 同步清零_高电平有效, 使能端_低电平有效, OP, OP_2, sys, sys_2
  \数据检测逻辑  \u_数据检测逻辑_2  (.ID_IR(ID_IR), .EX_RW(MEM_RW), .EX_IR(MEM_IR), .pause(\数据检测逻辑_2_pause ));
  or or_5 (pause, \数据检测逻辑_2_pause , \数据检测逻辑_1_pause );
  not not_2 (not_2_out, Halt);
  RAM #(.addrWidth(10), .dataWidth(32), .bus("separate"), .Select("high")) ram_1 (
    .addr(ex_mem_1_alu_2[11:2]), .din(MDin), .data(ram_1_data), .str(MemWrite), .sel(not_2_out), .clk(CLK));  // open: ld, clr
  MEM_WB mem_wb_1 (
    .LBU(ex_mem_1_lbu_2), .RegWrite(MEM_RW), .W_num(ex_mem_1_w_num_2), .MemToReg(ex_mem_1_memtoreg_2),
    .Addr(ex_mem_1_alu_2), .Halt(ex_mem_1_halt_2), .JAL(ex_mem_1_jal_2), .Alu(ex_mem_1_alu_2),
    .MD(ram_1_data), .PC_4(M_PC), .IR(MEM_IR), .CLK(CLK), .LBU_2(mem_wb_1_lbu_2), .RegWrite_2(RegWrite),
    .W_num_2(W_num), .MemToReg_2(mem_wb_1_memtoreg_2), .Addr_2(mem_wb_1_addr_2), .Halt_2(Halt), .JAL_2(JAL),
    .Alu_2(mem_wb_1_alu_2), .MD_2(mem_wb_1_md_2), .PC_4_2(WB_PC), .IR_2(WB_IR), .LUI(ex_mem_1_lui_2),
    .LUI_2(mem_wb_1_lui_2), .imm26(ex_mem_1_imm26_2), .imm26_2({mem_wb_1_imm26_2_2, mem_wb_1_imm26_2}));  // open: 同步清零_高电平有效, 使能端_低电平有效, OP, OP_2, data, data_2, sys, sys_2, rs, rs_2
  Multiplexer #(.select(1), .width(32), .disabled("Z"), .enable("false")) multiplexer_11 (
    .in0(mem_wb_1_alu_2), .in1(mem_wb_1_md_2), .out(multiplexer_11_out), .sel(mem_wb_1_memtoreg_2));
  Multiplexer #(.select(1), .width(32), .disabled("Z"), .enable("false")) multiplexer_12 (
    .in0(RDin), .in1({mem_wb_1_imm26_2, {16{1'b0}}}), .out(Din), .sel(mem_wb_1_lui_2));
  Multiplexer #(.select(2), .width(8), .disabled("Z"), .enable("false")) multiplexer_13 (
    .in0(multiplexer_11_out[7:0]), .in1(multiplexer_11_out[15:8]), .in2(multiplexer_11_out[23:16]),
    .in3(multiplexer_11_out[31:24]), .out(multiplexer_13_out), .sel(mem_wb_1_addr_2[1:0]));
  assign bit_extender_3_out = {{24{1'b0}}, multiplexer_13_out};  // Bit_Extender bit_extender_3
  Multiplexer #(.select(1), .width(32), .disabled("Z"), .enable("false")) multiplexer_14 (
    .in0(multiplexer_15_out), .in1(adder_4_out), .out(RDin), .sel(JAL));
  Multiplexer #(.select(1), .width(32), .disabled("Z"), .enable("false")) multiplexer_15 (
    .in0(multiplexer_11_out), .in1(bit_extender_3_out), .out(multiplexer_15_out), .sel(mem_wb_1_lbu_2));
  Adder #(.width(32)) adder_4 (.a(32'h4), .b(WB_PC), .out(adder_4_out));  // open: cin, cout

  // Other names for the same wires on the sheet: JMPAddr[31:28] = EX_PC[31:28]; MEM_PC[31:0] = M_PC

  // Notes on the sheet:
  //   中断源
  //   时空图监测，可删除
  //   中断等待指示
  //   数码管输出
  //   指令存储器
  //   contents of rom_1 (hex, n*v repeats v):
  //   20110001 8000c05 20110001 20120002 20130003 8000c09 20110001 20120002 20130003 8000c0d 20110001
  //   20120002 20130003 8000c11 20110001 20120002 20130003 c000cb8 20100001 20110001 118fc0 112020
  //   20020022 c 118882 12200001 8000c15 112020 20020022 c 20110001 118880 112020 20020022 c 12200001
  //   8000c1f 20110001 118fc0 112020 20020022 c 1188c3 112020 20020022 c 118903 112020 20020022 c 118903
  //   112020 20020022 c 118903 112020 20020022 c 118903 112020 20020022 c 118903 112020 20020022 c 118903
  //   112020 20020022 c 118903 112020 20020022 c 20100001 109fc0 139fc3 8021 2012000c 24160003 26100001
  //   3210000f 20080008 20090001 139900 2709825 132020 20020022 c 1094022 1500fff9 22100001 2018000f
  //   2188024 108700 20080008 20090001 139902 2709825 132021 20020022 c 1094022 1500fff9 108702 2c9b022
  //   12c00001 8000c50 4020 1084027 84400 3508ffff 82021 20020022 c 2010ffff 20110000 ae300000 22100001
  //   22310004 ae300000 22100001 22310004 ae300000 22100001 22310004 ae300000 22100001 22310004 ae300000
  //   22100001 22310004 ae300000 22100001 22310004 ae300000 22100001 22310004 ae300000 22100001 22310004
  //   ae300000 22100001 22310004 ae300000 22100001 22310004 ae300000 22100001 22310004 ae300000 22100001
  //   22310004 ae300000 22100001 22310004 ae300000 22100001 22310004 ae300000 22100001 22310004 ae300000
  //   22100001 22310004 22100001 8020 2011003c 8e130000 8e340000 274402a 11000002 ae330000 ae140000
  //   2231fffc 1611fff8 102020 20020022 c 22100004 2011003c 1611fff2 20020032 c 20100000 22100001 102020
  //   20020022 c 22100002 102020 20020022 c 22100003 102020 20020022 c 22100004 102020 20020022 c 22100005
  //   102020 20020022 c 22100006 102020 20020022 c 22100007 102020 20020022 c 22100008 102020 20020022
  //   20020022 c 3e00008
  //   指令字
  //   OP
  //   Func
  //   rs
  //   rt
  //   rd
  //   控制位
  //   流水调试日志用
  //   暂停节拍，不能为0
  //   JMP
  //   JR
  //   OP
  //   Func
  //   Syscall
  //   戳工具置1进入计数暂停模式，ctrl+k时钟自动运行到对应节拍暂停
  //   ctrl+k关闭时钟连续运行，将控制位置零，进入单步调试模式调试
  //   Beq
  //   Bne
  //   MemToReg
  //   MemWrite
  //   AluOP
  //   AluSrcB
  //   RegWrite
  //   JAL
  //   可计数暂停的时钟源
  //   SRAV指令
  //   为方便自动评测，需要输出流水线各段保存的PC值，注意是PC不是PC+4，另外ID段寄存器写入信息，Mem段内存写入信息也要输出
endmodule

module \中断按键参考电路  (
  input  \同步清零信号 ,
  output \与中断屏蔽位与 
);

  wire \_1号中断_out , and_1_out, clock_1_out, d_ff_1_q, or_1_out, or_2_out;

  Clock #(.highDuration(1), .lowDuration(1)) clock_1 (.out(clock_1_out));
  Button \_1号中断  (.out(\_1号中断_out ));
  or or_1 (or_1_out, \与中断屏蔽位与 , d_ff_1_q);
  LED #(.active("true")) \_1号中断等待指示灯  (.in(or_1_out));
  D_Flip_Flop #(.trigger("rising"), .Pre_Clr_Positions("LEGACY"), .NegatePresetClear("false"), .enable("true"), .NewFFLayout("false")) d_ff_1 (
    .clk(\_1号中断_out ), .D(1'b1), .Q(d_ff_1_q), .reset(\与中断屏蔽位与 ));  // open: Qn, preset, en
  or or_2 (or_2_out, d_ff_1_q, \与中断屏蔽位与 );
  and and_1 (and_1_out, or_2_out, ~\同步清零信号 );  // AND_Gate
  D_Flip_Flop #(.trigger("rising"), .Pre_Clr_Positions("LEGACY"), .NegatePresetClear("false"), .enable("true"), .NewFFLayout("false")) IR1 (
    .clk(clock_1_out), .D(and_1_out), .Q(\与中断屏蔽位与 ));  // open: Qn, preset, en, reset
  \单周期硬布线控制器  \u_单周期硬布线控制器_1  ();  // open: Func, OP, ALU_OP, MemToReg, MemWrite, ALU_SRC, RegWrite, SysCALL, SignedExt, RegDst, JR, JMP, Beq, JAL, Bne, LUI, LBU, BGTZ, ERET, MF, MFC0, MTC0

  // Notes on the sheet:
  //   中断信号采样参考电路
  //   Reset 
endmodule
module \单周期MIPS_单级中断  (
  input  IR1,
  input  IR2,
  input  IR3,
  output RegWrite,
  output MemWrite,
  output [31:0] PC,
  output [31:0] IR,
  output [31:0] RDin,
  output [31:0] MDin,
  output [31:0] LedData
);

  wire AluSrcB, and_1_out, and_2_out, and_3_out, and_4_out, and_5_out, and_6_out, and_7_out, and_8_out,
       and_9_out, and_10_out, and_11_out, and_12_out, BEqual, BGTZ, CLK, comparator_1_eq, comparator_2_eq,
       comparator_3_eq, comparator_4_eq, comparator_5_eq, comparator_6_gt, comparator_7_eq, d_ff_1_q,
       d_ff_2_q, d_ff_3_q, decoder_1_out1, decoder_1_out2, decoder_1_out3, equal, ERET, Go, Halt, IE,
       IR1_2_q, IR1_3_q, IR1_q, IR1_t, IR2_t, IR3_t, IRA, IRB, IRC, JAL, JMP, JR, LBU, LUI, MemToReg,
       not_1_out, not_2_out, not_3_out, not_4_out, or_1_out, or_9_out, or_10_out, or_11_out, or_12_out,
       RegDst, sig, SignedExt, Syscall, W1, W2, W3, \单周期硬布线控制器_1_beq , \单周期硬布线控制器_1_bne ;
  wire [1:0] priority_encoder_1_out, register_3_q;
  wire [3:0] AluOP;
  wire [4:0] multiplexer_6_out, multiplexer_7_out, multiplexer_8_out, multiplexer_9_out, multiplexer_12_out;
  wire [7:0] multiplexer_16_out;
  wire [15:0] \总周期数 ;
  wire [27:0] PC_4;
  wire [31:0] adder_3_out, bit_extender_1_out, bit_extender_2_out, bit_extender_3_out, Din, EPC_q, imme,
       \int , mips_alu_1_result, multiplexer_1_out, multiplexer_2_out, multiplexer_3_out, multiplexer_4_out,
       multiplexer_5_out, multiplexer_11_out, multiplexer_13_out, multiplexer_15_out, multiplexer_19_out,
       PCBranch, ram_1_data, rs, shifter_1_out;
  wire [31:28] JMPAddr;

  Clock #(.highDuration(1), .lowDuration(1)) clock_1 (.out(CLK));
  Button _1 (.out(IRA));
  Button _2 (.out(IRB));
  Button _3 (.out(IRC));
  Button \u_继续运行  (.out(Go));
  LED #(.active("true")) led_1 (.in(W1));
  LED #(.active("true")) led_2 (.in(W2));
  LED #(.active("true")) led_3 (.in(W3));
  Hex_Digit_Display hex_digit_display_1 (.value(LedData[31:28]));  // open: dp
  Comparator #(.width(16), .mode("twosComplement")) comparator_1 (
    .a(16'h23b), .b(\总周期数 ), .eq(comparator_1_eq));  // open: gt, lt
  Comparator #(.width(16), .mode("twosComplement")) comparator_2 (
    .a(\总周期数 ), .b(16'h1), .eq(comparator_2_eq));  // open: gt, lt
  Comparator #(.width(16), .mode("twosComplement")) comparator_3 (
    .a(\总周期数 ), .b(16'h4), .eq(comparator_3_eq));  // open: gt, lt
  Comparator #(.width(16), .mode("twosComplement")) comparator_4 (
    .a(\总周期数 ), .b(16'h7), .eq(comparator_4_eq));  // open: gt, lt
  and and_1 (and_1_out, JMP, ~JR);  // AND_Gate
  Hex_Digit_Display hex_digit_display_2 (.value(LedData[23:20]));  // open: dp
  Hex_Digit_Display hex_digit_display_3 (.value(LedData[27:24]));  // open: dp
  or or_1 (or_1_out, comparator_1_eq, comparator_2_eq);
  assign IRA = or_1_out ? ~CLK : 1'bz;  // Controlled_Inverter controlled_inverter_1
  assign IRB = comparator_3_eq ? ~CLK : 1'bz;  // Controlled_Inverter controlled_inverter_2
  assign IRC = comparator_4_eq ? ~CLK : 1'bz;  // Controlled_Inverter controlled_inverter_3
  Multiplexer #(.select(1), .width(32), .disabled("Z"), .enable("false")) multiplexer_1 (
    .in0(multiplexer_2_out), .in1({JMPAddr, IR[25:0], 2'b00}), .out(multiplexer_1_out), .sel(and_1_out));
  Multiplexer #(.select(1), .width(32), .disabled("Z"), .enable("false")) multiplexer_2 (
    .in0(multiplexer_3_out), .in1(rs), .out(multiplexer_2_out), .sel(JR));
  Multiplexer #(.select(1), .width(32), .disabled("Z"), .enable("false")) multiplexer_3 (
    .in0({JMPAddr, PC_4}), .in1(PCBranch), .out(multiplexer_3_out), .sel(BEqual));
  and and_2 (and_2_out, ~Halt, CLK);  // AND_Gate
  Hex_Digit_Display hex_digit_display_4 (.value(LedData[19:16]));  // open: dp
  Hex_Digit_Display hex_digit_display_5 (.value(LedData[15:12]));  // open: dp
  Pull_Resistor #(.pull(0)) pull_resistor_1 (.node(IRA));
  Pull_Resistor #(.pull(0)) pull_resistor_2 (.node(IRB));
  Pull_Resistor #(.pull(0)) pull_resistor_3 (.node(IRC));
  Comparator #(.width(32), .mode("twosComplement")) comparator_5 (
    .a(rs), .b(32'h22), .eq(comparator_5_eq));  // open: gt, lt
  Register #(.width(32), .trigger("rising"), .Select("low")) EPC (
    .D(multiplexer_1_out), .en(sig), .Q(EPC_q), .clk(CLK));  // open: clr
  Multiplexer #(.select(1), .width(32), .disabled("Z"), .enable("false")) multiplexer_4 (
    .in0(multiplexer_1_out), .in1(\int ), .out(multiplexer_4_out), .sel(sig));
  Multiplexer #(.select(1), .width(32), .disabled("Z"), .enable("false")) multiplexer_5 (
    .in0(multiplexer_4_out), .in1(EPC_q), .out(multiplexer_5_out), .sel(ERET));
  Counter #(.width(16), .max('hffff), .ongoal("wrap"), .trigger("rising"), .behavior("old")) counter_1 (
    .Q(\总周期数 ), .clk(and_2_out));  // open: load, D, count, carry, clr, preset
  Hex_Digit_Display hex_digit_display_6 (.value(LedData[11:8]));  // open: dp
  Hex_Digit_Display hex_digit_display_7 (.value(LedData[7:4]));  // open: dp
  // Probe on \总周期数 
  and and_3 (and_3_out, ~comparator_5_eq, Syscall);  // AND_Gate
  Register #(.width(32), .trigger("rising"), .Select("low")) u_PC (
    .D(multiplexer_5_out), .en(not_1_out), .Q(PC), .clk(CLK));  // open: clr
  not not_1 (not_1_out, Halt);
  Hex_Digit_Display hex_digit_display_8 (.value(LedData[3:0]));  // open: dp
  Register #(.width(32), .trigger("rising"), .Select("low")) register_1 (
    .D(MDin), .en(comparator_5_eq), .Q(LedData), .clk(CLK));  // open: clr
  Register #(.width(1), .trigger("rising"), .Select("low")) register_2 (
    .D(and_3_out), .en(and_3_out), .Q(Halt), .clk(CLK), .clr(Go));
  Adder #(.width(32)) adder_1 (.a(PC), .b(32'h4), .out({JMPAddr, PC_4}));  // open: cin, cout
  \单周期硬布线控制器  \u_单周期硬布线控制器_1  (
    .Func(IR[5:0]), .OP(IR[31:26]), .ALU_OP(AluOP), .MemToReg(MemToReg), .MemWrite(MemWrite),
    .ALU_SRC(AluSrcB), .RegWrite(RegWrite), .SysCALL(Syscall), .SignedExt(SignedExt), .RegDst(RegDst),
    .JR(JR), .JMP(JMP), .Beq(\单周期硬布线控制器_1_beq ), .JAL(JAL), .Bne(\单周期硬布线控制器_1_bne ), .LUI(LUI), .LBU(LBU),
    .BGTZ(BGTZ), .ERET(ERET), .MF(IR[25:21]));  // open: MFC0, MTC0
  or or_2 (IR1_t, IR1, IRA);
  ROM #(.addrWidth(10), .dataWidth(32), .Select("high")) rom_1 (.addr(PC[11:2]), .data(IR));
  or or_3 (IR2_t, IR2, IRB);
  // Mips_Probe mips_probe_1: pin names not known; wires that end beside it: IR
  Multiplexer #(.select(1), .width(5), .disabled("Z"), .enable("false")) multiplexer_6 (
    .in0(IR[25:21]), .in1(5'b00010), .out(multiplexer_6_out), .sel(Syscall));
  Multiplexer #(.select(1), .width(5), .disabled("Z"), .enable("false")) multiplexer_7 (
    .in0(IR[20:16]), .in1(5'b00100), .out(multiplexer_7_out), .sel(Syscall));
  Multiplexer #(.select(1), .width(5), .disabled("Z"), .enable("false")) multiplexer_8 (
    .in0(IR[20:16]), .in1(IR[15:11]), .out(multiplexer_8_out), .sel(RegDst));
  and and_4 (and_4_out, equal, \单周期硬布线控制器_1_beq );
  and and_5 (and_5_out, ~equal, \单周期硬布线控制器_1_bne );  // AND_Gate
  or or_4 (IR3_t, IR3, IRC);
  Multiplexer #(.select(1), .width(5), .disabled("Z"), .enable("false")) multiplexer_9 (
    .in0(multiplexer_8_out), .in1({5{1'b1}}), .out(multiplexer_9_out), .sel(JAL));
  assign bit_extender_1_out = {{16{1'b0}}, IR[15:0]};  // Bit_Extender bit_extender_1
  assign bit_extender_2_out = {{16{IR[15]}}, IR[15:0]};  // Bit_Extender bit_extender_2
  Comparator #(.width(32), .mode("twosComplement")) comparator_6 (
    .a(rs), .b({32{1'b0}}), .gt(comparator_6_gt));  // open: eq, lt
  and and_6 (and_6_out, BGTZ, comparator_6_gt);
  MIPS_Regifile mips_regifile_1 (
    .Din(Din), .Clk(CLK), .R1(rs), .R2(MDin), .WE(RegWrite), .W_num(multiplexer_9_out),
    .R1_num(multiplexer_6_out), .R2_num(multiplexer_7_out));
  Multiplexer #(.select(1), .width(32), .disabled("Z"), .enable("false")) multiplexer_10 (
    .in0(bit_extender_1_out), .in1(bit_extender_2_out), .out(imme), .sel(SignedExt));
  or or_5 (BEqual, and_4_out, and_6_out, and_5_out);
  Multiplexer #(.select(1), .width(32), .disabled("Z"), .enable("false")) multiplexer_11 (
    .in0(MDin), .in1(imme), .out(multiplexer_11_out), .sel(AluSrcB));
  Shifter #(.width(32), .shift("ll")) shifter_1 (.in(imme), .\dist (5'b00010), .out(shifter_1_out));
  MIPS_ALU mips_alu_1 (
    .X(rs), .Y(multiplexer_11_out), .AluOP(AluOP), .Equal(equal), .Result(mips_alu_1_result),
    .shamt(multiplexer_12_out));  // open: Result_2
  Adder #(.width(32)) adder_2 (.a(shifter_1_out), .b({JMPAddr, PC_4}), .out(PCBranch));  // open: cin, cout
  Multiplexer #(.select(1), .width(5), .disabled("Z"), .enable("false")) multiplexer_12 (
    .in0(IR[10:6]), .in1(rs[4:0]), .out(multiplexer_12_out), .sel(comparator_7_eq));
  Comparator #(.width(6), .mode("twosComplement")) comparator_7 (
    .a(IR[5:0]), .b(6'b000111), .eq(comparator_7_eq));  // open: gt, lt
  Adder #(.width(32)) adder_3 (.a(rs), .b(imme), .out(adder_3_out));  // open: cin, cout
  Multiplexer #(.select(1), .width(32), .disabled("Z"), .enable("false")) multiplexer_13 (
    .in0(mips_alu_1_result), .in1(adder_3_out), .out(multiplexer_13_out), .sel(LBU));
  or or_6 (W1, IR1_q, d_ff_1_q);
  or or_7 (W2, IR1_2_q, d_ff_2_q);
  or or_8 (W3, IR1_3_q, d_ff_3_q);
  not not_2 (not_2_out, Halt);
  D_Flip_Flop #(.trigger("rising"), .Pre_Clr_Positions("LEGACY"), .NegatePresetClear("false"), .enable("true"), .NewFFLayout("false")) d_ff_1 (
    .clk(IR1_t), .D(1'b1), .Q(d_ff_1_q), .reset(IR1_q));  // open: Qn, preset, en
  D_Flip_Flop #(.trigger("rising"), .Pre_Clr_Positions("LEGACY"), .NegatePresetClear("false"), .enable("true"), .NewFFLayout("false")) d_ff_2 (
    .clk(IR2_t), .D(1'b1), .Q(d_ff_2_q), .reset(IR1_2_q));  // open: Qn, preset, en
  D_Flip_Flop #(.trigger("rising"), .Pre_Clr_Positions("LEGACY"), .NegatePresetClear("false"), .enable("true"), .NewFFLayout("false")) d_ff_3 (
    .clk(IR3_t), .D(1'b1), .Q(d_ff_3_q), .reset(IR1_3_q));  // open: Qn, preset, en
  RAM #(.addrWidth(10), .dataWidth(32), .bus("separate"), .Select("high")) ram_1 (
    .addr(multiplexer_13_out[11:2]), .din(MDin), .data(ram_1_data), .str(MemWrite), .sel(not_2_out), .clk(CLK));  // open: ld, clr
  Multiplexer #(.select(1), .width(32), .disabled("Z"), .enable("false")) multiplexer_14 (
    .in0(RDin), .in1({IR[15:0], {16{1'b0}}}), .out(Din), .sel(LUI));
  or or_9 (or_9_out, d_ff_1_q, IR1_q);
  or or_10 (or_10_out, d_ff_2_q, IR1_2_q);
  or or_11 (or_11_out, d_ff_3_q, IR1_3_q);
  Multiplexer #(.select(1), .width(32), .disabled("Z"), .enable("false")) multiplexer_15 (
    .in0(mips_alu_1_result), .in1(ram_1_data), .out(multiplexer_15_out), .sel(MemToReg));
  and and_7 (and_7_out, or_9_out, ~and_8_out);  // AND_Gate
  and and_8 (and_8_out, decoder_1_out1, ERET);
  and and_9 (and_9_out, or_10_out, ~and_10_out);  // AND_Gate
  and and_10 (and_10_out, decoder_1_out2, ERET);
  and and_11 (and_11_out, or_11_out, ~and_12_out);  // AND_Gate
  and and_12 (and_12_out, ERET, decoder_1_out3);
  D_Flip_Flop #(.trigger("rising"), .Pre_Clr_Positions("LEGACY"), .NegatePresetClear("false"), .enable("true"), .NewFFLayout("false")) u_IR1 (
    .clk(CLK), .D(and_7_out), .Q(IR1_q));  // open: Qn, preset, en, reset
  D_Flip_Flop #(.trigger("rising"), .Pre_Clr_Positions("LEGACY"), .NegatePresetClear("false"), .enable("true"), .NewFFLayout("false")) IR1_2 (
    .clk(CLK), .D(and_9_out), .Q(IR1_2_q));  // open: Qn, preset, en, reset
  D_Flip_Flop #(.trigger("rising"), .Pre_Clr_Positions("LEGACY"), .NegatePresetClear("false"), .enable("true"), .NewFFLayout("false")) IR1_3 (
    .clk(CLK), .D(and_11_out), .Q(IR1_3_q));  // open: Qn, preset, en, reset
  not not_3 (not_3_out, IE);
  Multiplexer #(.select(2), .width(8), .disabled("Z"), .enable("false")) multiplexer_16 (
    .in0(multiplexer_15_out[7:0]), .in1(multiplexer_15_out[15:8]), .in2(multiplexer_15_out[23:16]),
    .in3(multiplexer_15_out[31:24]), .out(multiplexer_16_out), .sel(multiplexer_13_out[1:0]));
  or or_12 (or_12_out, IR1_q, IR1_2_q, IR1_3_q);
  Register #(.width(1), .trigger("rising"), .Select("low")) u_IE (
    .D(or_12_out), .en(not_3_out), .Q(IE), .clk(CLK), .clr(ERET));
  assign bit_extender_3_out = {{24{1'b0}}, multiplexer_16_out};  // Bit_Extender bit_extender_3
  Multiplexer #(.select(1), .width(32), .disabled("Z"), .enable("false")) multiplexer_17 (
    .in0(multiplexer_19_out), .in1({JMPAddr, PC_4}), .out(RDin), .sel(JAL));
  not not_4 (not_4_out, IE);
  Priority_Encoder #(.select(2), .disabled("Z")) priority_encoder_1 (
    .in0(1'b1), .in1(IR1_q), .in2(IR1_2_q), .in3(IR1_3_q), .out(priority_encoder_1_out));  // open: gs, en_out, en_in
  Multiplexer #(.select(2), .width(32), .disabled("Z"), .enable("false")) multiplexer_18 (
    .in1(32'h30ac), .in2(32'h3150), .in3(32'h31f4), .out(\int ), .sel(priority_encoder_1_out));  // open: in0
  and and_13 (sig, or_12_out, ~IE);  // AND_Gate
  Multiplexer #(.select(1), .width(32), .disabled("Z"), .enable("false")) multiplexer_19 (
    .in0(multiplexer_15_out), .in1(bit_extender_3_out), .out(multiplexer_19_out), .sel(LBU));
  Register #(.width(2), .trigger("rising"), .Select("low")) register_3 (
    .D(priority_encoder_1_out), .en(not_4_out), .Q(register_3_q), .clk(CLK));  // open: clr
  Decoder #(.select(2), .tristate("false"), .disabled("Z"), .enable("false")) decoder_1 (
    .out1(decoder_1_out1), .out2(decoder_1_out2), .out3(decoder_1_out3), .sel(register_3_q));  // open: out0
  // Probe on priority_encoder_1_out

  // Other names for the same wires on the sheet: _0_15[15:0] = IR[15:0]; Func[5:0] = IR[5:0];
  //   JMPAddr[27:2] = IR[25:0]; shamt[4:0] = IR[10:6]; OP[5:0] = IR[31:26]; MF[4:0] = IR[25:21];
  //   PC_4[31:28] = JMPAddr; rt[31:0] = MDin

  // Notes on the sheet:
  //   中断源
  //   中断等待指示
  //   总复位信号应将除ROM以外所有存储组件全部清零
  //   单级中断测试信号模拟器
  //   数码管输出
  //   数码管输出应该用寄存器锁存，否则显示数据只能一闪而过
  //   指令存储器
  //   Beq
  //   JMP
  //   JR
  //   Bne
  //   OP
  //   JAL
  //   Func
  //   Syscall
  //   contents of rom_1 (hex, n*v repeats v):
  //   201d07d0 20100001 109fc0 139fc3 8021 2012000c 24160008 26100001 3210000f 20080008 20090001 139900
  //   2709825 132020 20020022 c 1094022 1500fff9 22100001 2018000f 2188024 108700 20080008 20090001 139902
  //   2709825 132021 20020022 c 1094022 1500fff9 108702 2c9b022 12c00001 8100007 4020 1084027 84400
  //   3508ffff 82021 20020022 c 8100001 afa20000 23bd0004 afa40000 23bd0004 afb00000 23bd0004 afb30000
  //   23bd0004 afb40000 23bd0004 afb50000 23bd0004 afb60000 23bd0004 20160001 20140003 20150001 168020
  //   108100 2149825 132020 20020022 c 1600fffa 295a022 1680fff7 23bdfffc 8fb60000 23bdfffc 8fb50000
  //   23bdfffc 8fb40000 23bdfffc 8fb30000 23bdfffc 8fb00000 23bdfffc 8fa40000 23bdfffc 8fa20000 42000018
  //   afa20000 23bd0004 afa40000 23bd0004 afb00000 23bd0004 afb30000 23bd0004 afb40000 23bd0004 afb50000
  //   23bd0004 afb60000 23bd0004 20160002 20140003 20150001 168020 108100 2149825 132020 20020022 c
  //   1600fffa 295a022 1680fff7 23bdfffc 8fb60000 23bdfffc 8fb50000 23bdfffc 8fb40000 23bdfffc 8fb30000
  //   23bdfffc 8fb00000 23bdfffc 8fa40000 23bdfffc 8fa20000 42000018 afa20000 23bd0004 afa40000 23bd0004
  //   afb00000 23bd0004 afb30000 23bd0004 afb40000 23bd0004 afb50000 23bd0004 afb60000 23bd0004 20160003
  //   20140003 20150001 168020 108100 2149825 132020 20020022 c 1600fffa 295a022 1680fff7 23bdfffc
  //   8fb60000 23bdfffc 8fb50000 23bdfffc 8fb40000 23bdfffc 8fb30000 23bdfffc 8fb00000 23bdfffc 8fa40000
  //   23bdfffc 8fa20000 42000018
  //   MemToReg
  //   MemWrite
  //   AluOP
  //   AluSrcB
  //   RegWrite
  //   RegDst
  //   OP
  //   Func
  //   rs
  //   指令字
  //   rt
  //   rd
  //   为方便自动评测，需要输出PC，IR，寄存器堆写如数据RDin
  //   SRAV指令
  //   RAM写使能MemWrite、RAM写入数据MDin等信号
  //   中断策略
  //   Reset 
  //   Reset 
  //   Reset 
  //   0是开
endmodule

module \单周期MIPS_多级中断  (
  input  IR1,
  input  IR2,
  input  IR3,
  output RegWrite,
  output MemWrite,
  output [31:0] PC,
  output [31:0] IR,
  output [31:0] RDin,
  output [31:0] MDin,
  output [31:0] LedData
);

  wire AluSrcB, and_1_out, and_2_out, and_3_out, and_4_out, and_5_out, and_6_out, and_7_out, and_8_out,
       and_9_out, and_10_out, and_11_out, and_12_out, BEqual, BGTZ, CLK, comparator_1_eq, comparator_2_eq,
       comparator_3_eq, comparator_4_eq, comparator_5_eq, comparator_6_eq, comparator_9_gt, comparator_10_eq,
       comparator_11_lt, d_ff_1_q, d_ff_2_q, d_ff_3_q, demultiplexer_1_out1, demultiplexer_1_out2,
       demultiplexer_1_out3, epc_t, equal, ERET, Go, Halt, IE, ie_t, IR1_2_q, IR1_3_q, IR1_q, IR1_t, IR2_t,
       IR3_t, IRA, IRB, IRC, JAL, JMP, JR, LBU, LUI, MemToReg, MFC0, MTC0, multiplexer_17_out, nand_1_out,
       not_1_out, not_2_out, not_3_out, or_1_out, or_2_out, or_3_out, or_11_out, or_12_out, or_13_out,
       or_14_out, RegDst, sig, SignedExt, Syscall, W1, W2, W3, \单周期硬布线控制器_1_beq , \单周期硬布线控制器_1_bne ;
  wire [1:0] multiplexer_21_out, priority_encoder_1_out, \中断栈_1_peak , \当前中断号_q ;
  wire [3:0] AluOP;
  wire [4:0] multiplexer_7_out, multiplexer_8_out, multiplexer_9_out, multiplexer_10_out, multiplexer_13_out;
  wire [7:0] multiplexer_18_out;
  wire [15:0] \总周期数 ;
  wire [27:0] PC_4;
  wire [31:0] adder_3_out, bit_extender_1_out, bit_extender_2_out, bit_extender_3_out, bit_extender_4_out,
       Din, EPC, imme, \int , mips_alu_1_result, multiplexer_1_out, multiplexer_2_out, multiplexer_3_out,
       multiplexer_4_out, multiplexer_5_out, multiplexer_6_out, multiplexer_12_out, multiplexer_14_out,
       multiplexer_16_out, multiplexer_20_out, multiplexer_23_out, PCBranch, ram_1_data, rs, shifter_1_out;
  wire [31:28] JMPAddr;

  Clock #(.highDuration(1), .lowDuration(1)) clock_1 (.out(CLK));
  Button _1 (.out(IRA));
  Button _2 (.out(IRB));
  Button _3 (.out(IRC));
  Button \u_继续运行  (.out(Go));
  LED #(.active("true")) led_1 (.in(W1));
  LED #(.active("true")) led_2 (.in(W2));
  LED #(.active("true")) led_3 (.in(W3));
  Hex_Digit_Display hex_digit_display_1 (.value(LedData[31:28]));  // open: dp
  Comparator #(.width(16), .mode("twosComplement")) comparator_1 (
    .a(16'h258), .b(\总周期数 ), .eq(comparator_1_eq));  // open: gt, lt
  Comparator #(.width(16), .mode("twosComplement")) comparator_2 (
    .a(\总周期数 ), .b(16'h1), .eq(comparator_2_eq));  // open: gt, lt
  Comparator #(.width(16), .mode("twosComplement")) comparator_3 (
    .a(\总周期数 ), .b(16'h4), .eq(comparator_3_eq));  // open: gt, lt
  Comparator #(.width(16), .mode("twosComplement")) comparator_4 (
    .a(\总周期数 ), .b(16'h7), .eq(comparator_4_eq));  // open: gt, lt
  Comparator #(.width(16), .mode("twosComplement")) comparator_5 (
    .a(\总周期数 ), .b(16'h241), .eq(comparator_5_eq));  // open: gt, lt
  and and_1 (and_1_out, JMP, ~JR);  // AND_Gate
  Hex_Digit_Display hex_digit_display_2 (.value(LedData[27:24]));  // open: dp
  Hex_Digit_Display hex_digit_display_3 (.value(LedData[23:20]));  // open: dp
  or or_1 (or_1_out, comparator_1_eq, comparator_2_eq);
  assign IRA = or_1_out ? ~CLK : 1'bz;  // Controlled_Inverter controlled_inverter_1
  assign IRB = comparator_3_eq ? ~CLK : 1'bz;  // Controlled_Inverter controlled_inverter_2
  or or_2 (or_2_out, comparator_4_eq, comparator_5_eq);
  assign IRC = or_2_out ? ~CLK : 1'bz;  // Controlled_Inverter controlled_inverter_3
  and and_2 (and_2_out, MTC0, epc_t);
  Multiplexer #(.select(1), .width(32), .disabled("Z"), .enable("false")) multiplexer_1 (
    .in0(multiplexer_2_out), .in1({JMPAddr, IR[25:0], 2'b00}), .out(multiplexer_1_out), .sel(and_1_out));
  Multiplexer #(.select(1), .width(32), .disabled("Z"), .enable("false")) multiplexer_2 (
    .in0(multiplexer_3_out), .in1(rs), .out(multiplexer_2_out), .sel(JR));
  Multiplexer #(.select(1), .width(32), .disabled("Z"), .enable("false")) multiplexer_3 (
    .in0({JMPAddr, PC_4}), .in1(PCBranch), .out(multiplexer_3_out), .sel(BEqual));
  and and_3 (and_3_out, ~Halt, CLK);  // AND_Gate
  Hex_Digit_Display hex_digit_display_4 (.value(LedData[19:16]));  // open: dp
  Hex_Digit_Display hex_digit_display_5 (.value(LedData[15:12]));  // open: dp
  Pull_Resistor #(.pull(0)) pull_resistor_1 (.node(IRA));
  Pull_Resistor #(.pull(0)) pull_resistor_2 (.node(IRB));
  Pull_Resistor #(.pull(0)) pull_resistor_3 (.node(IRC));
  Comparator #(.width(32), .mode("twosComplement")) comparator_6 (
    .a(rs), .b(32'h22), .eq(comparator_6_eq));  // open: gt, lt
  Multiplexer #(.select(1), .width(32), .disabled("Z"), .enable("false")) multiplexer_4 (
    .in0(multiplexer_1_out), .in1(MDin), .out(multiplexer_4_out), .sel(and_2_out));
  Multiplexer #(.select(1), .width(32), .disabled("Z"), .enable("false")) multiplexer_5 (
    .in0(multiplexer_1_out), .in1(\int ), .out(multiplexer_5_out), .sel(sig));
  Multiplexer #(.select(1), .width(32), .disabled("Z"), .enable("false")) multiplexer_6 (
    .in0(multiplexer_5_out), .in1(EPC), .out(multiplexer_6_out), .sel(ERET));
  Counter #(.width(16), .max('hffff), .ongoal("wrap"), .trigger("rising"), .behavior("old")) counter_1 (
    .Q(\总周期数 ), .clk(and_3_out));  // open: load, D, count, carry, clr, preset
  Hex_Digit_Display hex_digit_display_6 (.value(LedData[11:8]));  // open: dp
  Hex_Digit_Display hex_digit_display_7 (.value(LedData[7:4]));  // open: dp
  // Probe on \总周期数 
  Register #(.width(32), .trigger("rising"), .Select("low")) register_1 (
    .D(MDin), .en(comparator_6_eq), .Q(LedData), .clk(CLK));  // open: clr
  and and_4 (and_4_out, ~comparator_6_eq, Syscall);  // AND_Gate
  Register #(.width(32), .trigger("rising"), .Select("low")) u_EPC (
    .D(multiplexer_4_out), .en(or_3_out), .Q(EPC), .clk(CLK));  // open: clr
  or or_3 (or_3_out, and_2_out, sig);
  Register #(.width(32), .trigger("rising"), .Select("low")) u_PC (
    .D(multiplexer_6_out), .en(not_1_out), .Q(PC), .clk(CLK));  // open: clr
  not not_1 (not_1_out, Halt);
  Hex_Digit_Display hex_digit_display_8 (.value(LedData[3:0]));  // open: dp
  Register #(.width(1), .trigger("rising"), .Select("low")) register_2 (
    .D(and_4_out), .en(and_4_out), .Q(Halt), .clk(CLK), .clr(Go));
  Adder #(.width(32)) adder_1 (.a(PC), .b(32'h4), .out({JMPAddr, PC_4}));  // open: cin, cout
  or or_4 (IR1_t, IR1, IRA);
  ROM #(.addrWidth(10), .dataWidth(32), .Select("high")) rom_1 (.addr(PC[11:2]), .data(IR));
  Comparator #(.width(5), .mode("twosComplement")) comparator_7 (
    .a(IR[15:11]), .b(5'b01100), .eq(ie_t));  // open: gt, lt
  Comparator #(.width(5), .mode("twosComplement")) comparator_8 (
    .a(IR[15:11]), .b(5'b01110), .eq(epc_t));  // open: gt, lt
  \单周期硬布线控制器  \u_单周期硬布线控制器_1  (
    .Func(IR[5:0]), .OP(IR[31:26]), .ALU_OP(AluOP), .MemToReg(MemToReg), .MemWrite(MemWrite),
    .ALU_SRC(AluSrcB), .RegWrite(RegWrite), .SysCALL(Syscall), .SignedExt(SignedExt), .RegDst(RegDst),
    .JR(JR), .JMP(JMP), .Beq(\单周期硬布线控制器_1_beq ), .JAL(JAL), .Bne(\单周期硬布线控制器_1_bne ), .LUI(LUI), .LBU(LBU),
    .BGTZ(BGTZ), .ERET(ERET), .MF(IR[25:21]), .MFC0(MFC0), .MTC0(MTC0));
  or or_5 (IR2_t, IR2, IRB);
  // Mips_Probe mips_probe_1: pin names not known; wires that end beside it: IR
  Multiplexer #(.select(1), .width(5), .disabled("Z"), .enable("false")) multiplexer_7 (
    .in0(IR[25:21]), .in1(5'b00010), .out(multiplexer_7_out), .sel(Syscall));
  Multiplexer #(.select(1), .width(5), .disabled("Z"), .enable("false")) multiplexer_8 (
    .in0(IR[20:16]), .in1(5'b00100), .out(multiplexer_8_out), .sel(Syscall));
  Multiplexer #(.select(1), .width(5), .disabled("Z"), .enable("false")) multiplexer_9 (
    .in0(IR[20:16]), .in1(IR[15:11]), .out(multiplexer_9_out), .sel(RegDst));
  and and_5 (and_5_out, equal, \单周期硬布线控制器_1_beq );
  and and_6 (and_6_out, ~equal, \单周期硬布线控制器_1_bne );  // AND_Gate
  or or_6 (IR3_t, IR3, IRC);
  Multiplexer #(.select(1), .width(5), .disabled("Z"), .enable("false")) multiplexer_10 (
    .in0(multiplexer_9_out), .in1({5{1'b1}}), .out(multiplexer_10_out), .sel(JAL));
  assign bit_extender_1_out = {{16{1'b0}}, IR[15:0]};  // Bit_Extender bit_extender_1
  assign bit_extender_2_out = {{16{IR[15]}}, IR[15:0]};  // Bit_Extender bit_extender_2
  Comparator #(.width(32), .mode("twosComplement")) comparator_9 (
    .a(rs), .b({32{1'b0}}), .gt(comparator_9_gt));  // open: eq, lt
  // Probe on nothing
  and and_7 (and_7_out, BGTZ, comparator_9_gt);
  MIPS_Regifile mips_regifile_1 (
    .Din(Din), .Clk(CLK), .R1(rs), .R2(MDin), .WE(RegWrite), .W_num(multiplexer_10_out),
    .R1_num(multiplexer_7_out), .R2_num(multiplexer_8_out));
  Multiplexer #(.select(1), .width(32), .disabled("Z"), .enable("false")) multiplexer_11 (
    .in0(bit_extender_1_out), .in1(bit_extender_2_out), .out(imme), .sel(SignedExt));
  or or_7 (BEqual, and_5_out, and_7_out, and_6_out);
  // Probe on nothing
  Multiplexer #(.select(1), .width(32), .disabled("Z"), .enable("false")) multiplexer_12 (
    .in0(MDin), .in1(imme), .out(multiplexer_12_out), .sel(AluSrcB));
  Shifter #(.width(32), .shift("ll")) shifter_1 (.in(imme), .\dist (5'b00010), .out(shifter_1_out));
  MIPS_ALU mips_alu_1 (
    .X(rs), .Y(multiplexer_12_out), .AluOP(AluOP), .Equal(equal), .Result(mips_alu_1_result),
    .shamt(multiplexer_13_out));  // open: Result_2
  Adder #(.width(32)) adder_2 (.a(shifter_1_out), .b({JMPAddr, PC_4}), .out(PCBranch));  // open: cin, cout
  Multiplexer #(.select(1), .width(5), .disabled("Z"), .enable("false")) multiplexer_13 (
    .in0(IR[10:6]), .in1(rs[4:0]), .out(multiplexer_13_out), .sel(comparator_10_eq));
  Comparator #(.width(6), .mode("twosComplement")) comparator_10 (
    .a(IR[5:0]), .b(6'b000111), .eq(comparator_10_eq));  // open: gt, lt
  Adder #(.width(32)) adder_3 (.a(rs), .b(imme), .out(adder_3_out));  // open: cin, cout
  Multiplexer #(.select(1), .width(32), .disabled("Z"), .enable("false")) multiplexer_14 (
    .in0(mips_alu_1_result), .in1(adder_3_out), .out(multiplexer_14_out), .sel(LBU));
  D_Flip_Flop #(.trigger("rising"), .Pre_Clr_Positions("LEGACY"), .NegatePresetClear("false"), .enable("true"), .NewFFLayout("false")) d_ff_1 (
    .clk(IR1_t), .D(1'b1), .Q(d_ff_1_q), .reset(IR1_q));  // open: Qn, preset, en
  or or_8 (W1, IR1_q, d_ff_1_q);
  D_Flip_Flop #(.trigger("rising"), .Pre_Clr_Positions("LEGACY"), .NegatePresetClear("false"), .enable("true"), .NewFFLayout("false")) d_ff_2 (
    .clk(IR2_t), .D(1'b1), .Q(d_ff_2_q), .reset(IR1_2_q));  // open: Qn, preset, en
  or or_9 (W2, IR1_2_q, d_ff_2_q);
  D_Flip_Flop #(.trigger("rising"), .Pre_Clr_Positions("LEGACY"), .NegatePresetClear("false"), .enable("true"), .NewFFLayout("false")) d_ff_3 (
    .clk(IR3_t), .D(1'b1), .Q(d_ff_3_q), .reset(IR1_3_q));  // open: Qn, preset, en
  or or_10 (W3, IR1_3_q, d_ff_3_q);
  not not_2 (not_2_out, Halt);
  Multiplexer #(.select(1), .width(32), .disabled("Z"), .enable("false")) multiplexer_15 (
    .in0(RDin), .in1({IR[15:0], {16{1'b0}}}), .out(Din), .sel(LUI));
  RAM #(.addrWidth(10), .dataWidth(32), .bus("separate"), .Select("high")) ram_1 (
    .addr(multiplexer_14_out[11:2]), .din(MDin), .data(ram_1_data), .str(MemWrite), .sel(not_2_out), .clk(CLK));  // open: ld, clr
  or or_11 (or_11_out, d_ff_1_q, IR1_q);
  and and_8 (and_8_out, or_11_out, ~demultiplexer_1_out1);  // AND_Gate
  or or_12 (or_12_out, d_ff_2_q, IR1_2_q);
  and and_9 (and_9_out, or_12_out, ~demultiplexer_1_out2);  // AND_Gate
  or or_13 (or_13_out, d_ff_3_q, IR1_3_q);
  and and_10 (and_10_out, or_13_out, ~demultiplexer_1_out3);  // AND_Gate
  and and_11 (and_11_out, MTC0, ie_t);
  Multiplexer #(.select(1), .width(32), .disabled("Z"), .enable("false")) multiplexer_16 (
    .in0(mips_alu_1_result), .in1(ram_1_data), .out(multiplexer_16_out), .sel(MemToReg));
  D_Flip_Flop #(.trigger("rising"), .Pre_Clr_Positions("LEGACY"), .NegatePresetClear("false"), .enable("true"), .NewFFLayout("false")) u_IR1 (
    .clk(CLK), .D(and_8_out), .Q(IR1_q));  // open: Qn, preset, en, reset
  D_Flip_Flop #(.trigger("rising"), .Pre_Clr_Positions("LEGACY"), .NegatePresetClear("false"), .enable("true"), .NewFFLayout("false")) IR1_2 (
    .clk(CLK), .D(and_9_out), .Q(IR1_2_q));  // open: Qn, preset, en, reset
  D_Flip_Flop #(.trigger("rising"), .Pre_Clr_Positions("LEGACY"), .NegatePresetClear("false"), .enable("true"), .NewFFLayout("false")) IR1_3 (
    .clk(CLK), .D(and_10_out), .Q(IR1_3_q));  // open: Qn, preset, en, reset
  Multiplexer #(.select(1), .width(1), .disabled("Z"), .enable("false")) multiplexer_17 (
    .in0(comparator_11_lt), .in1(MDin[0]), .out(multiplexer_17_out), .sel(and_11_out));
  not not_3 (not_3_out, IE);
  nand nand_1 (nand_1_out, ~and_11_out, IE);  // NAND_Gate
  Multiplexer #(.select(2), .width(8), .disabled("Z"), .enable("false")) multiplexer_18 (
    .in0(multiplexer_16_out[7:0]), .in1(multiplexer_16_out[15:8]), .in2(multiplexer_16_out[23:16]),
    .in3(multiplexer_16_out[31:24]), .out(multiplexer_18_out), .sel(multiplexer_14_out[1:0]));
  Multiplexer #(.select(2), .width(32), .disabled("Z"), .enable("false")) multiplexer_19 (
    .in0(multiplexer_23_out), .in1({JMPAddr, PC_4}), .in2(multiplexer_20_out), .in3(multiplexer_20_out),
    .out(RDin), .sel({MFC0, JAL}));
  assign bit_extender_3_out = {{31{1'b0}}, IE};  // Bit_Extender bit_extender_3
  or or_14 (or_14_out, not_3_out, ERET);
  Priority_Encoder #(.select(2), .disabled("Z")) priority_encoder_1 (
    .in0(1'b1), .in1(IR1_q), .in2(IR1_2_q), .in3(IR1_3_q), .out(priority_encoder_1_out));  // open: gs, en_out, en_in
  Register #(.width(1), .trigger("rising"), .Select("low")) u_IE (
    .D(multiplexer_17_out), .en(nand_1_out), .Q(IE), .clk(CLK), .clr(ERET));
  assign bit_extender_4_out = {{24{1'b0}}, multiplexer_18_out};  // Bit_Extender bit_extender_4
  Multiplexer #(.select(1), .width(32), .disabled("Z"), .enable("false")) multiplexer_20 (
    .in0(EPC), .in1(bit_extender_3_out), .out(multiplexer_20_out), .sel(and_12_out));
  and and_12 (and_12_out, MFC0, ie_t);
  Multiplexer #(.select(1), .width(2), .disabled("Z"), .enable("false")) multiplexer_21 (
    .in0(priority_encoder_1_out), .in1(\中断栈_1_peak ), .out(multiplexer_21_out), .sel(ERET));
  Demultiplexer #(.select(2), .width(1), .tristate("false"), .disabled("Z"), .enable("false")) demultiplexer_1 (
    .out1(demultiplexer_1_out1), .out2(demultiplexer_1_out2), .out3(demultiplexer_1_out3), .in(ERET),
    .sel(\当前中断号_q ));  // open: out0
  Multiplexer #(.select(2), .width(32), .disabled("Z"), .enable("false")) multiplexer_22 (
    .in1(32'h30ac), .in2(32'h3174), .in3(32'h323c), .out(\int ), .sel(priority_encoder_1_out));  // open: in0
  Multiplexer #(.select(1), .width(32), .disabled("Z"), .enable("false")) multiplexer_23 (
    .in0(multiplexer_16_out), .in1(bit_extender_4_out), .out(multiplexer_23_out), .sel(LBU));
  Register #(.width(2), .trigger("rising"), .Select("low")) \u_当前中断号  (
    .D(multiplexer_21_out), .en(or_14_out), .Q(\当前中断号_q ), .clk(CLK));  // open: clr
  // Probe on priority_encoder_1_out
  and and_13 (sig, ~IE, comparator_11_lt);  // AND_Gate
  \中断栈  \u_中断栈_1  (.ir(\当前中断号_q ), .clk(CLK), .sig(sig), .eret(ERET), .peak(\中断栈_1_peak ));
  Comparator #(.width(2), .mode("unsigned")) comparator_11 (
    .a(\当前中断号_q ), .b(priority_encoder_1_out), .lt(comparator_11_lt));  // open: gt, eq
  // Probe on \中断栈_1_peak 

  // Other names for the same wires on the sheet: _0_15[15:0] = IR[15:0]; Func[5:0] = IR[5:0];
  //   JMPAddr[27:2] = IR[25:0]; shamt[4:0] = IR[10:6]; OP[5:0] = IR[31:26]; MF[4:0] = IR[25:21];
  //   PC_4[31:28] = JMPAddr; rt[31:0] = MDin

  // Notes on the sheet:
  //   中断源
  //   中断等待指示
  //   总复位信号应将除ROM以外所有存储组件全部清零
  //   信号模拟
  //   数码管输出
  //   数码管输出应该用寄存器锁存，否则显示数据只能一闪而过
  //   指令存储器
  //   JMP
  //   JR
  //   OP
  //   Func
  //   contents of rom_1 (hex, n*v repeats v):
  //   201d07d0 20100001 109fc0 139fc3 8021 2012000c 24160008 26100001 3210000f 20080008 20090001 139900
  //   2709825 132020 20020022 c 1094022 1500fff9 22100001 2018000f 2188024 108700 20080008 20090001 139902
  //   2709825 132021 20020022 c 1094022 1500fff9 108702 2c9b022 12c00001 8000c07 4020 1084027 84400
  //   3508ffff 82021 20020022 c 8000c01 afa20000 23bd0004 afa40000 23bd0004 afb00000 23bd0004 afb30000
  //   23bd0004 afb40000 23bd0004 afb50000 23bd0004 afb60000 23bd0004 40167000 afb60000 23bd0004 40806000
  //   20160001 20140003 20150001 168020 108100 2149825 132020 20020022 c 1600fffa 295a022 1680fff7
  //   20160001 40966000 23bdfffc 8fb60000 40967000 23bdfffc 8fb60000 23bdfffc 8fb50000 23bdfffc 8fb40000
  //   23bdfffc 8fb30000 23bdfffc 8fb00000 23bdfffc 8fa40000 23bdfffc 8fa20000 42000018 afa20000 23bd0004
  //   afa40000 23bd0004 afb00000 23bd0004 afb30000 23bd0004 afb40000 23bd0004 afb50000 23bd0004 afb60000
  //   23bd0004 40167000 afb60000 23bd0004 40806000 20160002 20140003 20150001 168020 108100 2149825 132020
  //   20020022 c 1600fffa 295a022 1680fff7 20160001 40966000 23bdfffc 8fb60000 40967000 23bdfffc 8fb60000
  //   23bdfffc 8fb50000 23bdfffc 8fb40000 23bdfffc 8fb30000 23bdfffc 8fb00000 23bdfffc 8fa40000 23bdfffc
  //   8fa20000 42000018 afa20000 23bd0004 afa40000 23bd0004 afb00000 23bd0004 afb30000 23bd0004 afb40000
  //   23bd0004 afb50000 23bd0004 afb60000 23bd0004 40167000 afb60000 23bd0004 40806000 20160003 20140003
  //   20150001 168020 108100 2149825 132020 20020022 c 1600fffa 295a022 1680fff7 20160001 40966000
  //   23bdfffc 8fb60000 40967000 23bdfffc 8fb60000 23bdfffc 8fb50000 23bdfffc 8fb40000 23bdfffc 8fb30000
  //   23bdfffc 8fb00000 23bdfffc 8fa40000 23bdfffc 8fa20000 42000018
  //   Beq
  //   Bne
  //   MemToReg
  //   MemWrite
  //   AluOP
  //   AluSrcB
  //   RegWrite
  //   JAL
  //   RegDst
  //   Syscall
  //   OP
  //   Func
  //   rs
  //   指令字
  //   rt
  //   rd
  //   为方便自动评测，需要输出PC，IR，寄存器堆写如数据RDin
  //   SRAV指令
  //   RAM写使能MemWrite、RAM写入数据MDin等信号
  //   中断策略
  //   rt
  //   Reset 
  //   Reset 
  //   Reset 
  //   0是开
endmodule

module \封装正确性测试  (
);

  wire IR1, IR2, IR3, MemW, RegW;
  wire [31:0] EX_PC, ID_PC, IF_PC, IR, LED, MDin, MDinr, MEM_PC, PC, RDin, RDinr, WB_PC;

  \单周期MIPS  \u_单周期mips_1  (
    .IR1(IR1), .IR2(IR2), .IR3(IR3), .RegWrite(RegW), .MemWrite(MemW), .PC(PC), .IR(IR), .RDin(RDin),
    .MDin(MDin), .LedData(LED));
  \气泡流水线  \u_气泡流水线_1  (
    .RegWrite(RegW), .MemWrite(MemW), .IF_PC(IF_PC), .ID_PC(ID_PC), .EX_PC(EX_PC), .M_PC(MEM_PC),
    .WB_PC(WB_PC), .RDin(RDinr), .MDin(MDinr), .LedData(LED));
  \单周期MIPS_单级中断  \u_单周期mips_单级中断_1  (
    .IR1(IR1), .IR2(IR2), .IR3(IR3), .RegWrite(RegW), .MemWrite(MemW), .PC(PC), .IR(IR), .RDin(RDin),
    .MDin(MDin), .LedData(LED));
  \理想流水线  \u_理想流水线_1  (
    .RegWrite(RegW), .MemWrite(MemW), .IF_PC(IF_PC), .ID_PC(ID_PC), .EX_PC(EX_PC), .M_PC(MEM_PC),
    .WB_PC(WB_PC), .RDin(RDinr), .MDin(MDinr), .LedData(LED));
  \重定向流水线  \u_重定向流水线_1  (
    .RegWrite(RegW), .MemWrite(MemW), .IF_PC(IF_PC), .ID_PC(ID_PC), .EX_PC(EX_PC), .M_PC(MEM_PC),
    .WB_PC(WB_PC), .RDin(RDinr), .MDin(MDinr), .LedData(LED));
  \单周期MIPS_多级中断  \u_单周期mips_多级中断_1  (
    .IR1(IR1), .IR2(IR2), .IR3(IR3), .RegWrite(RegW), .MemWrite(MemW), .PC(PC), .IR(IR), .RDin(RDin),
    .MDin(MDin), .LedData(LED));

  // Notes on the sheet:
  //   单周期封装测试
  //   气泡流水封装测试
  //   单周期+单级中断封装测试
  //   请检查上面封装有无位宽不匹配，引脚标签是否和连接的标签相对应，否则无法在educoder平台上正确测试
  //   理想流水封装测试
  //   重定向流水封装测试
  //   单周期+多级中断封装测试
endmodule

module IF_ID (
  input  [31:0] IR,
  input  [31:0] PC_4,
  input  CLK,
  input  \同步清零_高电平有效 ,
  input  \使能端_低电平有效 ,
  output [31:0] IR_2,
  output [31:0] PC_4_2
);

  wire pull_resistor_2_node;
  wire [31:0] multiplexer_1_out, multiplexer_2_out;

  Multiplexer #(.select(1), .width(32), .disabled("Z"), .enable("false")) multiplexer_1 (
    .in0(IR), .in1({32{1'b0}}), .out(multiplexer_1_out), .sel(\同步清零_高电平有效 ));
  Multiplexer #(.select(1), .width(32), .disabled("Z"), .enable("false")) multiplexer_2 (
    .in0(PC_4), .in1({32{1'b0}}), .out(multiplexer_2_out), .sel(\同步清零_高电平有效 ));
  Pull_Resistor #(.pull(0)) pull_resistor_1 (.node(\同步清零_高电平有效 ));
  Register #(.width(32), .trigger("rising"), .Select("low")) register_1 (
    .D(multiplexer_1_out), .en(pull_resistor_2_node), .Q(IR_2), .clk(CLK));  // open: clr
  Register #(.width(32), .trigger("rising"), .Select("low")) register_2 (
    .D(multiplexer_2_out), .en(pull_resistor_2_node), .Q(PC_4_2), .clk(CLK));  // open: clr
  Pull_Resistor #(.pull(0)) pull_resistor_2 (.node(pull_resistor_2_node));
  not not_1 (pull_resistor_2_node, \使能端_低电平有效 );

  // Notes on the sheet:
  //   使能端_低电平有效: pull=down
  //   同步清零_高电平有效: pull=down
endmodule

module ID_EX (
  input  [5:0] OP,
  input  LUI,
  input  BGTZ,
  input  LBU,
  input  RegWrite,
  input  [4:0] W_num,
  input  MemToReg,
  input  Beq,
  input  Bne,
  input  JAL,
  input  [4:0] Shamt,
  input  JR,
  input  JMP,
  input  MemWrite,
  input  [3:0] AluOP,
  input  AluSrcB,
  input  Sys,
  input  eret,
  input  eret_2,
  input  [1:0] f1,
  input  [1:0] f2,
  input  [31:0] R1,
  input  [31:0] R2,
  input  [31:0] Imm,
  input  [31:0] PC_4,
  input  [31:0] IR,
  input  [25:0] _26,
  input  CLK,
  input  \同步清零_高电平有效 ,
  input  \使能端_低电平有效 ,
  output [5:0] OP_2,
  output LUI_2,
  output BGTZ_2,
  output LBU_2,
  output RegWrite_2,
  output [4:0] W_num_2,
  output MemToReg_2,
  output Beq_2,
  output Bne_2,
  output JAL_2,
  output [4:0] Shamt_2,
  output JR_2,
  output JMP_2,
  output MemWrite_2,
  output [3:0] AluOP_2,
  output AluSrcB_2,
  output Sys_2,
  output eret_3,
  output eret_4,
  output [1:0] f1_2,
  output [1:0] f2_2,
  output [31:0] R1_2,
  output [31:0] R2_2,
  output [31:0] Imm_2,
  output [31:0] PC_4_2,
  output [31:0] IR_2,
  output [25:0] _26_2
);

  wire multiplexer_2_out, multiplexer_3_out, multiplexer_4_out, multiplexer_5_out, multiplexer_7_out,
       multiplexer_8_out, multiplexer_9_out, multiplexer_10_out, multiplexer_12_out, multiplexer_13_out,
       multiplexer_14_out, multiplexer_16_out, multiplexer_17_out, multiplexer_18_out, multiplexer_19_out,
       not_1_out;
  wire [1:0] multiplexer_20_out, multiplexer_21_out;
  wire [3:0] multiplexer_15_out;
  wire [4:0] multiplexer_6_out, multiplexer_11_out;
  wire [5:0] multiplexer_1_out;
  wire [25:0] multiplexer_27_out;
  wire [31:0] multiplexer_22_out, multiplexer_23_out, multiplexer_24_out, multiplexer_25_out,
       multiplexer_26_out;

  Multiplexer #(.select(1), .width(6), .disabled("Z"), .enable("false")) multiplexer_1 (
    .in0(OP), .in1({6{1'b0}}), .out(multiplexer_1_out), .sel(\同步清零_高电平有效 ));
  Multiplexer #(.select(1), .width(1), .disabled("Z"), .enable("false")) multiplexer_2 (
    .in0(LUI), .in1(1'b0), .out(multiplexer_2_out), .sel(\同步清零_高电平有效 ));
  Multiplexer #(.select(1), .width(1), .disabled("Z"), .enable("false")) multiplexer_3 (
    .in0(BGTZ), .in1(1'b0), .out(multiplexer_3_out), .sel(\同步清零_高电平有效 ));
  Multiplexer #(.select(1), .width(1), .disabled("Z"), .enable("false")) multiplexer_4 (
    .in0(LBU), .in1(1'b0), .out(multiplexer_4_out), .sel(\同步清零_高电平有效 ));
  Multiplexer #(.select(1), .width(1), .disabled("Z"), .enable("false")) multiplexer_5 (
    .in0(RegWrite), .in1(1'b0), .out(multiplexer_5_out), .sel(\同步清零_高电平有效 ));
  Multiplexer #(.select(1), .width(5), .disabled("Z"), .enable("false")) multiplexer_6 (
    .in0(W_num), .in1({5{1'b0}}), .out(multiplexer_6_out), .sel(\同步清零_高电平有效 ));
  Multiplexer #(.select(1), .width(1), .disabled("Z"), .enable("false")) multiplexer_7 (
    .in0(MemToReg), .in1(1'b0), .out(multiplexer_7_out), .sel(\同步清零_高电平有效 ));
  Multiplexer #(.select(1), .width(1), .disabled("Z"), .enable("false")) multiplexer_8 (
    .in0(Beq), .in1(1'b0), .out(multiplexer_8_out), .sel(\同步清零_高电平有效 ));
  Multiplexer #(.select(1), .width(1), .disabled("Z"), .enable("false")) multiplexer_9 (
    .in0(Bne), .in1(1'b0), .out(multiplexer_9_out), .sel(\同步清零_高电平有效 ));
  Multiplexer #(.select(1), .width(1), .disabled("Z"), .enable("false")) multiplexer_10 (
    .in0(JAL), .in1(1'b0), .out(multiplexer_10_out), .sel(\同步清零_高电平有效 ));
  Multiplexer #(.select(1), .width(5), .disabled("Z"), .enable("false")) multiplexer_11 (
    .in0(Shamt), .in1({5{1'b0}}), .out(multiplexer_11_out), .sel(\同步清零_高电平有效 ));
  Multiplexer #(.select(1), .width(1), .disabled("Z"), .enable("false")) multiplexer_12 (
    .in0(JR), .in1(1'b0), .out(multiplexer_12_out), .sel(\同步清零_高电平有效 ));
  Multiplexer #(.select(1), .width(1), .disabled("Z"), .enable("false")) multiplexer_13 (
    .in0(JMP), .in1(1'b0), .out(multiplexer_13_out), .sel(\同步清零_高电平有效 ));
  Multiplexer #(.select(1), .width(1), .disabled("Z"), .enable("false")) multiplexer_14 (
    .in0(MemWrite), .in1(1'b0), .out(multiplexer_14_out), .sel(\同步清零_高电平有效 ));
  Multiplexer #(.select(1), .width(4), .disabled("Z"), .enable("false")) multiplexer_15 (
    .in0(AluOP), .in1(4'b0000), .out(multiplexer_15_out), .sel(\同步清零_高电平有效 ));
  Multiplexer #(.select(1), .width(1), .disabled("Z"), .enable("false")) multiplexer_16 (
    .in0(AluSrcB), .in1(1'b0), .out(multiplexer_16_out), .sel(\同步清零_高电平有效 ));
  Multiplexer #(.select(1), .width(1), .disabled("Z"), .enable("false")) multiplexer_17 (
    .in0(Sys), .in1(1'b0), .out(multiplexer_17_out), .sel(\同步清零_高电平有效 ));
  Multiplexer #(.select(1), .width(1), .disabled("Z"), .enable("false")) multiplexer_18 (
    .in0(eret), .in1(1'b0), .out(multiplexer_18_out), .sel(\同步清零_高电平有效 ));
  Multiplexer #(.select(1), .width(1), .disabled("Z"), .enable("false")) multiplexer_19 (
    .in0(eret_2), .in1(1'b0), .out(multiplexer_19_out), .sel(\同步清零_高电平有效 ));
  Multiplexer #(.select(1), .width(2), .disabled("Z"), .enable("false")) multiplexer_20 (
    .in0(f1), .in1(2'b00), .out(multiplexer_20_out), .sel(\同步清零_高电平有效 ));
  Multiplexer #(.select(1), .width(2), .disabled("Z"), .enable("false")) multiplexer_21 (
    .in0(f2), .in1(2'b00), .out(multiplexer_21_out), .sel(\同步清零_高电平有效 ));
  Multiplexer #(.select(1), .width(32), .disabled("Z"), .enable("false")) multiplexer_22 (
    .in0(R1), .in1({32{1'b0}}), .out(multiplexer_22_out), .sel(\同步清零_高电平有效 ));
  Multiplexer #(.select(1), .width(32), .disabled("Z"), .enable("false")) multiplexer_23 (
    .in0(R2), .in1({32{1'b0}}), .out(multiplexer_23_out), .sel(\同步清零_高电平有效 ));
  Multiplexer #(.select(1), .width(32), .disabled("Z"), .enable("false")) multiplexer_24 (
    .in0(Imm), .in1({32{1'b0}}), .out(multiplexer_24_out), .sel(\同步清零_高电平有效 ));
  Multiplexer #(.select(1), .width(32), .disabled("Z"), .enable("false")) multiplexer_25 (
    .in0(PC_4), .in1({32{1'b0}}), .out(multiplexer_25_out), .sel(\同步清零_高电平有效 ));
  Multiplexer #(.select(1), .width(32), .disabled("Z"), .enable("false")) multiplexer_26 (
    .in0(IR), .in1({32{1'b0}}), .out(multiplexer_26_out), .sel(\同步清零_高电平有效 ));
  Multiplexer #(.select(1), .width(26), .disabled("Z"), .enable("false")) multiplexer_27 (
    .in0(_26), .in1({26{1'b0}}), .out(multiplexer_27_out), .sel(\同步清零_高电平有效 ));
  Pull_Resistor #(.pull(0)) pull_resistor_1 (.node(\同步清零_高电平有效 ));
  not not_1 (not_1_out, \使能端_低电平有效 );
  Register #(.width(6), .trigger("rising"), .Select("low")) register_1 (
    .D(multiplexer_1_out), .en(not_1_out), .Q(OP_2), .clk(CLK));  // open: clr
  Register #(.width(1), .trigger("rising"), .Select("low")) register_2 (
    .D(multiplexer_2_out), .en(not_1_out), .Q(LUI_2), .clk(CLK));  // open: clr
  Register #(.width(1), .trigger("rising"), .Select("low")) register_3 (
    .D(multiplexer_3_out), .en(not_1_out), .Q(BGTZ_2), .clk(CLK));  // open: clr
  Register #(.width(1), .trigger("rising"), .Select("low")) register_4 (
    .D(multiplexer_4_out), .en(not_1_out), .Q(LBU_2), .clk(CLK));  // open: clr
  Register #(.width(1), .trigger("rising"), .Select("low")) register_5 (
    .D(multiplexer_5_out), .en(not_1_out), .Q(RegWrite_2), .clk(CLK));  // open: clr
  Register #(.width(5), .trigger("rising"), .Select("low")) register_6 (
    .D(multiplexer_6_out), .en(not_1_out), .Q(W_num_2), .clk(CLK));  // open: clr
  Register #(.width(1), .trigger("rising"), .Select("low")) register_7 (
    .D(multiplexer_7_out), .en(not_1_out), .Q(MemToReg_2), .clk(CLK));  // open: clr
  Register #(.width(1), .trigger("rising"), .Select("low")) register_8 (
    .D(multiplexer_8_out), .en(not_1_out), .Q(Beq_2), .clk(CLK));  // open: clr
  Register #(.width(1), .trigger("rising"), .Select("low")) register_9 (
    .D(multiplexer_9_out), .en(not_1_out), .Q(Bne_2), .clk(CLK));  // open: clr
  Register #(.width(1), .trigger("rising"), .Select("low")) register_10 (
    .D(multiplexer_10_out), .en(not_1_out), .Q(JAL_2), .clk(CLK));  // open: clr
  Register #(.width(5), .trigger("rising"), .Select("low")) register_11 (
    .D(multiplexer_11_out), .en(not_1_out), .Q(Shamt_2), .clk(CLK));  // open: clr
  Register #(.width(1), .trigger("rising"), .Select("low")) register_12 (
    .D(multiplexer_12_out), .en(not_1_out), .Q(JR_2), .clk(CLK));  // open: clr
  Register #(.width(1), .trigger("rising"), .Select("low")) register_13 (
    .D(multiplexer_13_out), .en(not_1_out), .Q(JMP_2), .clk(CLK));  // open: clr
  Register #(.width(1), .trigger("rising"), .Select("low")) register_14 (
    .D(multiplexer_14_out), .en(not_1_out), .Q(MemWrite_2), .clk(CLK));  // open: clr
  Register #(.width(4), .trigger("rising"), .Select("low")) register_15 (
    .D(multiplexer_15_out), .en(not_1_out), .Q(AluOP_2), .clk(CLK));  // open: clr
  Register #(.width(1), .trigger("rising"), .Select("low")) register_16 (
    .D(multiplexer_16_out), .en(not_1_out), .Q(AluSrcB_2), .clk(CLK));  // open: clr
  Register #(.width(1), .trigger("rising"), .Select("low")) register_17 (
    .D(multiplexer_17_out), .en(not_1_out), .Q(Sys_2), .clk(CLK));  // open: clr
  Register #(.width(1), .trigger("rising"), .Select("low")) register_18 (
    .D(multiplexer_18_out), .en(not_1_out), .Q(eret_3), .clk(CLK));  // open: clr
  Register #(.width(1), .trigger("rising"), .Select("low")) register_19 (
    .D(multiplexer_19_out), .en(not_1_out), .Q(eret_4), .clk(CLK));  // open: clr
  Register #(.width(2), .trigger("rising"), .Select("low")) register_20 (
    .D(multiplexer_20_out), .en(not_1_out), .Q(f1_2), .clk(CLK));  // open: clr
  Register #(.width(2), .trigger("rising"), .Select("low")) register_21 (
    .D(multiplexer_21_out), .en(not_1_out), .Q(f2_2), .clk(CLK));  // open: clr
  Register #(.width(32), .trigger("rising"), .Select("low")) register_22 (
    .D(multiplexer_22_out), .en(not_1_out), .Q(R1_2), .clk(CLK));  // open: clr
  Register #(.width(32), .trigger("rising"), .Select("low")) register_23 (
    .D(multiplexer_23_out), .en(not_1_out), .Q(R2_2), .clk(CLK));  // open: clr
  Register #(.width(32), .trigger("rising"), .Select("low")) register_24 (
    .D(multiplexer_24_out), .en(not_1_out), .Q(Imm_2), .clk(CLK));  // open: clr
  Register #(.width(32), .trigger("rising"), .Select("low")) register_25 (
    .D(multiplexer_25_out), .en(not_1_out), .Q(PC_4_2), .clk(CLK));  // open: clr
  Register #(.width(32), .trigger("rising"), .Select("low")) register_26 (
    .D(multiplexer_26_out), .en(not_1_out), .Q(IR_2), .clk(CLK));  // open: clr
  Register #(.width(26), .trigger("rising"), .Select("low")) register_27 (
    .D(multiplexer_27_out), .en(not_1_out), .Q(_26_2), .clk(CLK));  // open: clr
  Pull_Resistor #(.pull(0)) pull_resistor_2 (.node(not_1_out));

  // Notes on the sheet:
  //   同步清零_高电平有效: pull=down
  //   使能端_低电平有效: pull=down
endmodule

module EX_MEM (
  input  sys,
  input  LUI,
  input  LBU,
  input  RegWrite,
  input  [4:0] W_num,
  input  MemToReg,
  input  MemWrite,
  input  Halt,
  input  JAL,
  input  [5:0] OP,
  input  [31:0] data,
  input  [31:0] Alu,
  input  [31:0] R2,
  input  [31:0] PC_4,
  input  [31:0] IR,
  input  [25:0] imm26,
  input  CLK,
  input  \同步清零_高电平有效 ,
  input  \使能端_低电平有效 ,
  output sys_2,
  output LUI_2,
  output LBU_2,
  output RegWrite_2,
  output [4:0] W_num_2,
  output MemToReg_2,
  output MemWrite_2,
  output Halt_2,
  output JAL_2,
  output [5:0] OP_2,
  output [31:0] data_2,
  output [31:0] Alu_2,
  output [31:0] R2_2,
  output [31:0] PC_4_2,
  output [31:0] IR_2,
  output [25:0] imm26_2
);

  wire multiplexer_1_out, multiplexer_2_out, multiplexer_3_out, multiplexer_4_out, multiplexer_6_out,
       multiplexer_7_out, multiplexer_8_out, multiplexer_9_out, pull_resistor_2_node;
  wire [4:0] multiplexer_5_out;
  wire [5:0] multiplexer_10_out;
  wire [25:0] multiplexer_16_out;
  wire [31:0] multiplexer_11_out, multiplexer_12_out, multiplexer_13_out, multiplexer_14_out,
       multiplexer_15_out;

  Multiplexer #(.select(1), .width(1), .disabled("Z"), .enable("false")) multiplexer_1 (
    .in0(sys), .in1(1'b0), .out(multiplexer_1_out), .sel(\同步清零_高电平有效 ));
  Multiplexer #(.select(1), .width(1), .disabled("Z"), .enable("false")) multiplexer_2 (
    .in0(LUI), .in1(1'b0), .out(multiplexer_2_out), .sel(\同步清零_高电平有效 ));
  Multiplexer #(.select(1), .width(1), .disabled("Z"), .enable("false")) multiplexer_3 (
    .in0(LBU), .in1(1'b0), .out(multiplexer_3_out), .sel(\同步清零_高电平有效 ));
  Multiplexer #(.select(1), .width(1), .disabled("Z"), .enable("false")) multiplexer_4 (
    .in0(RegWrite), .in1(1'b0), .out(multiplexer_4_out), .sel(\同步清零_高电平有效 ));
  Multiplexer #(.select(1), .width(5), .disabled("Z"), .enable("false")) multiplexer_5 (
    .in0(W_num), .in1({5{1'b0}}), .out(multiplexer_5_out), .sel(\同步清零_高电平有效 ));
  Multiplexer #(.select(1), .width(1), .disabled("Z"), .enable("false")) multiplexer_6 (
    .in0(MemToReg), .in1(1'b0), .out(multiplexer_6_out), .sel(\同步清零_高电平有效 ));
  Multiplexer #(.select(1), .width(1), .disabled("Z"), .enable("false")) multiplexer_7 (
    .in0(MemWrite), .in1(1'b0), .out(multiplexer_7_out), .sel(\同步清零_高电平有效 ));
  Multiplexer #(.select(1), .width(1), .disabled("Z"), .enable("false")) multiplexer_8 (
    .in0(Halt), .in1(1'b0), .out(multiplexer_8_out), .sel(\同步清零_高电平有效 ));
  Multiplexer #(.select(1), .width(1), .disabled("Z"), .enable("false")) multiplexer_9 (
    .in0(JAL), .in1(1'b0), .out(multiplexer_9_out), .sel(\同步清零_高电平有效 ));
  Multiplexer #(.select(1), .width(6), .disabled("Z"), .enable("false")) multiplexer_10 (
    .in0(OP), .in1({6{1'b0}}), .out(multiplexer_10_out), .sel(\同步清零_高电平有效 ));
  Multiplexer #(.select(1), .width(32), .disabled("Z"), .enable("false")) multiplexer_11 (
    .in0(data), .in1({32{1'b0}}), .out(multiplexer_11_out), .sel(\同步清零_高电平有效 ));
  Multiplexer #(.select(1), .width(32), .disabled("Z"), .enable("false")) multiplexer_12 (
    .in0(Alu), .in1({32{1'b0}}), .out(multiplexer_12_out), .sel(\同步清零_高电平有效 ));
  Multiplexer #(.select(1), .width(32), .disabled("Z"), .enable("false")) multiplexer_13 (
    .in0(R2), .in1({32{1'b0}}), .out(multiplexer_13_out), .sel(\同步清零_高电平有效 ));
  Multiplexer #(.select(1), .width(32), .disabled("Z"), .enable("false")) multiplexer_14 (
    .in0(PC_4), .in1({32{1'b0}}), .out(multiplexer_14_out), .sel(\同步清零_高电平有效 ));
  Multiplexer #(.select(1), .width(32), .disabled("Z"), .enable("false")) multiplexer_15 (
    .in0(IR), .in1({32{1'b0}}), .out(multiplexer_15_out), .sel(\同步清零_高电平有效 ));
  Multiplexer #(.select(1), .width(26), .disabled("Z"), .enable("false")) multiplexer_16 (
    .in0(imm26), .in1({26{1'b0}}), .out(multiplexer_16_out), .sel(\同步清零_高电平有效 ));
  Pull_Resistor #(.pull(0)) pull_resistor_1 (.node(\同步清零_高电平有效 ));
  Pull_Resistor #(.pull(0)) pull_resistor_2 (.node(pull_resistor_2_node));
  not not_1 (pull_resistor_2_node, \使能端_低电平有效 );
  Register #(.width(1), .trigger("rising"), .Select("low")) register_1 (
    .D(multiplexer_1_out), .en(pull_resistor_2_node), .Q(sys_2), .clk(CLK));  // open: clr
  Register #(.width(1), .trigger("rising"), .Select("low")) register_2 (
    .D(multiplexer_2_out), .en(pull_resistor_2_node), .Q(LUI_2), .clk(CLK));  // open: clr
  Register #(.width(1), .trigger("rising"), .Select("low")) register_3 (
    .D(multiplexer_3_out), .en(pull_resistor_2_node), .Q(LBU_2), .clk(CLK));  // open: clr
  Register #(.width(1), .trigger("rising"), .Select("low")) register_4 (
    .D(multiplexer_4_out), .en(pull_resistor_2_node), .Q(RegWrite_2), .clk(CLK));  // open: clr
  Register #(.width(5), .trigger("rising"), .Select("low")) register_5 (
    .D(multiplexer_5_out), .en(pull_resistor_2_node), .Q(W_num_2), .clk(CLK));  // open: clr
  Register #(.width(1), .trigger("rising"), .Select("low")) register_6 (
    .D(multiplexer_6_out), .en(pull_resistor_2_node), .Q(MemToReg_2), .clk(CLK));  // open: clr
  Register #(.width(1), .trigger("rising"), .Select("low")) register_7 (
    .D(multiplexer_7_out), .en(pull_resistor_2_node), .Q(MemWrite_2), .clk(CLK));  // open: clr
  Register #(.width(1), .trigger("rising"), .Select("low")) register_8 (
    .D(multiplexer_8_out), .en(pull_resistor_2_node), .Q(Halt_2), .clk(CLK));  // open: clr
  Register #(.width(1), .trigger("rising"), .Select("low")) register_9 (
    .D(multiplexer_9_out), .en(pull_resistor_2_node), .Q(JAL_2), .clk(CLK));  // open: clr
  Register #(.width(6), .trigger("rising"), .Select("low")) register_10 (
    .D(multiplexer_10_out), .en(pull_resistor_2_node), .Q(OP_2), .clk(CLK));  // open: clr
  Register #(.width(32), .trigger("rising"), .Select("low")) register_11 (
    .D(multiplexer_11_out), .en(pull_resistor_2_node), .Q(data_2), .clk(CLK));  // open: clr
  Register #(.width(32), .trigger("rising"), .Select("low")) register_12 (
    .D(multiplexer_12_out), .en(pull_resistor_2_node), .Q(Alu_2), .clk(CLK));  // open: clr
  Register #(.width(32), .trigger("rising"), .Select("low")) register_13 (
    .D(multiplexer_13_out), .en(pull_resistor_2_node), .Q(R2_2), .clk(CLK));  // open: clr
  Register #(.width(32), .trigger("rising"), .Select("low")) register_14 (
    .D(multiplexer_14_out), .en(pull_resistor_2_node), .Q(PC_4_2), .clk(CLK));  // open: clr
  Register #(.width(32), .trigger("rising"), .Select("low")) register_15 (
    .D(multiplexer_15_out), .en(pull_resistor_2_node), .Q(IR_2), .clk(CLK));  // open: clr
  Register #(.width(26), .trigger("rising"), .Select("low")) register_16 (
    .D(multiplexer_16_out), .en(pull_resistor_2_node), .Q(imm26_2), .clk(CLK));  // open: clr

  // Notes on the sheet:
  //   使能端_低电平有效: pull=down
  //   同步清零_高电平有效: pull=down
endmodule

module MEM_WB (
  input  sys,
  input  LUI,
  input  LBU,
  input  RegWrite,
  input  [4:0] W_num,
  input  MemToReg,
  input  [31:0] Addr,
  input  Halt,
  input  JAL,
  input  [5:0] OP,
  input  [31:0] Alu,
  input  [31:0] MD,
  input  [31:0] PC_4,
  input  [31:0] IR,
  input  [31:0] data,
  input  [25:0] imm26,
  input  [31:0] rs,
  input  CLK,
  input  \同步清零_高电平有效 ,
  input  \使能端_低电平有效 ,
  output sys_2,
  output LUI_2,
  output LBU_2,
  output RegWrite_2,
  output [4:0] W_num_2,
  output MemToReg_2,
  output [31:0] Addr_2,
  output Halt_2,
  output JAL_2,
  output [5:0] OP_2,
  output [31:0] Alu_2,
  output [31:0] MD_2,
  output [31:0] PC_4_2,
  output [31:0] IR_2,
  output [31:0] data_2,
  output [25:0] imm26_2,
  output [31:0] rs_2
);

  wire multiplexer_1_out, multiplexer_2_out, multiplexer_3_out, multiplexer_4_out, multiplexer_6_out,
       multiplexer_8_out, multiplexer_9_out, not_1_out;
  wire [4:0] multiplexer_5_out;
  wire [5:0] multiplexer_10_out;
  wire [25:0] multiplexer_16_out;
  wire [31:0] multiplexer_7_out, multiplexer_11_out, multiplexer_12_out, multiplexer_13_out,
       multiplexer_14_out, multiplexer_15_out, multiplexer_17_out;

  Multiplexer #(.select(1), .width(1), .disabled("Z"), .enable("false")) multiplexer_1 (
    .in0(sys), .in1(1'b0), .out(multiplexer_1_out), .sel(\同步清零_高电平有效 ));
  Multiplexer #(.select(1), .width(1), .disabled("Z"), .enable("false")) multiplexer_2 (
    .in0(LUI), .in1(1'b0), .out(multiplexer_2_out), .sel(\同步清零_高电平有效 ));
  Multiplexer #(.select(1), .width(1), .disabled("Z"), .enable("false")) multiplexer_3 (
    .in0(LBU), .in1(1'b0), .out(multiplexer_3_out), .sel(\同步清零_高电平有效 ));
  Multiplexer #(.select(1), .width(1), .disabled("Z"), .enable("false")) multiplexer_4 (
    .in0(RegWrite), .in1(1'b0), .out(multiplexer_4_out), .sel(\同步清零_高电平有效 ));
  Multiplexer #(.select(1), .width(5), .disabled("Z"), .enable("false")) multiplexer_5 (
    .in0(W_num), .in1({5{1'b0}}), .out(multiplexer_5_out), .sel(\同步清零_高电平有效 ));
  Multiplexer #(.select(1), .width(1), .disabled("Z"), .enable("false")) multiplexer_6 (
    .in0(MemToReg), .in1(1'b0), .out(multiplexer_6_out), .sel(\同步清零_高电平有效 ));
  Multiplexer #(.select(1), .width(32), .disabled("Z"), .enable("false")) multiplexer_7 (
    .in0(Addr), .in1({32{1'b0}}), .out(multiplexer_7_out), .sel(\同步清零_高电平有效 ));
  Multiplexer #(.select(1), .width(1), .disabled("Z"), .enable("false")) multiplexer_8 (
    .in0(Halt), .in1(1'b0), .out(multiplexer_8_out), .sel(\同步清零_高电平有效 ));
  Multiplexer #(.select(1), .width(1), .disabled("Z"), .enable("false")) multiplexer_9 (
    .in0(JAL), .in1(1'b0), .out(multiplexer_9_out), .sel(\同步清零_高电平有效 ));
  Multiplexer #(.select(1), .width(6), .disabled("Z"), .enable("false")) multiplexer_10 (
    .in0(OP), .in1({6{1'b0}}), .out(multiplexer_10_out), .sel(\同步清零_高电平有效 ));
  Multiplexer #(.select(1), .width(32), .disabled("Z"), .enable("false")) multiplexer_11 (
    .in0(Alu), .in1({32{1'b0}}), .out(multiplexer_11_out), .sel(\同步清零_高电平有效 ));
  Multiplexer #(.select(1), .width(32), .disabled("Z"), .enable("false")) multiplexer_12 (
    .in0(MD), .in1({32{1'b0}}), .out(multiplexer_12_out), .sel(\同步清零_高电平有效 ));
  Multiplexer #(.select(1), .width(32), .disabled("Z"), .enable("false")) multiplexer_13 (
    .in0(PC_4), .in1({32{1'b0}}), .out(multiplexer_13_out), .sel(\同步清零_高电平有效 ));
  Multiplexer #(.select(1), .width(32), .disabled("Z"), .enable("false")) multiplexer_14 (
    .in0(IR), .in1({32{1'b0}}), .out(multiplexer_14_out), .sel(\同步清零_高电平有效 ));
  Multiplexer #(.select(1), .width(32), .disabled("Z"), .enable("false")) multiplexer_15 (
    .in0(data), .in1({32{1'b0}}), .out(multiplexer_15_out), .sel(\同步清零_高电平有效 ));
  Multiplexer #(.select(1), .width(26), .disabled("Z"), .enable("false")) multiplexer_16 (
    .in0(imm26), .in1({26{1'b0}}), .out(multiplexer_16_out), .sel(\同步清零_高电平有效 ));
  Multiplexer #(.select(1), .width(32), .disabled("Z"), .enable("false")) multiplexer_17 (
    .in0(rs), .in1({32{1'b0}}), .out(multiplexer_17_out), .sel(\同步清零_高电平有效 ));
  Pull_Resistor #(.pull(0)) pull_resistor_1 (.node(\同步清零_高电平有效 ));
  not not_1 (not_1_out, \使能端_低电平有效 );
  Register #(.width(1), .trigger("rising"), .Select("low")) register_1 (
    .D(multiplexer_1_out), .en(not_1_out), .Q(sys_2), .clk(CLK));  // open: clr
  Register #(.width(1), .trigger("rising"), .Select("low")) register_2 (
    .D(multiplexer_2_out), .en(not_1_out), .Q(LUI_2), .clk(CLK));  // open: clr
  Register #(.width(1), .trigger("rising"), .Select("low")) register_3 (
    .D(multiplexer_3_out), .en(not_1_out), .Q(LBU_2), .clk(CLK));  // open: clr
  Register #(.width(1), .trigger("rising"), .Select("low")) register_4 (
    .D(multiplexer_4_out), .en(not_1_out), .Q(RegWrite_2), .clk(CLK));  // open: clr
  Register #(.width(5), .trigger("rising"), .Select("low")) register_5 (
    .D(multiplexer_5_out), .en(not_1_out), .Q(W_num_2), .clk(CLK));  // open: clr
  Register #(.width(1), .trigger("rising"), .Select("low")) register_6 (
    .D(multiplexer_6_out), .en(not_1_out), .Q(MemToReg_2), .clk(CLK));  // open: clr
  Register #(.width(32), .trigger("rising"), .Select("low")) register_7 (
    .D(multiplexer_7_out), .en(not_1_out), .Q(Addr_2), .clk(CLK));  // open: clr
  Register #(.width(1), .trigger("rising"), .Select("low")) register_8 (
    .D(multiplexer_8_out), .en(not_1_out), .Q(Halt_2), .clk(CLK));  // open: clr
  Register #(.width(1), .trigger("rising"), .Select("low")) register_9 (
    .D(multiplexer_9_out), .en(not_1_out), .Q(JAL_2), .clk(CLK));  // open: clr
  Register #(.width(6), .trigger("rising"), .Select("low")) register_10 (
    .D(multiplexer_10_out), .en(not_1_out), .Q(OP_2), .clk(CLK));  // open: clr
  Register #(.width(32), .trigger("rising"), .Select("low")) register_11 (
    .D(multiplexer_11_out), .en(not_1_out), .Q(Alu_2), .clk(CLK));  // open: clr
  Register #(.width(32), .trigger("rising"), .Select("low")) register_12 (
    .D(multiplexer_12_out), .en(not_1_out), .Q(MD_2), .clk(CLK));  // open: clr
  Register #(.width(32), .trigger("rising"), .Select("low")) register_13 (
    .D(multiplexer_13_out), .en(not_1_out), .Q(PC_4_2), .clk(CLK));  // open: clr
  Register #(.width(32), .trigger("rising"), .Select("low")) register_14 (
    .D(multiplexer_14_out), .en(not_1_out), .Q(IR_2), .clk(CLK));  // open: clr
  Register #(.width(32), .trigger("rising"), .Select("low")) register_15 (
    .D(multiplexer_15_out), .en(not_1_out), .Q(data_2), .clk(CLK));  // open: clr
  Register #(.width(26), .trigger("rising"), .Select("low")) register_16 (
    .D(multiplexer_16_out), .en(not_1_out), .Q(imm26_2), .clk(CLK));  // open: clr
  Register #(.width(32), .trigger("rising"), .Select("low")) register_17 (
    .D(multiplexer_17_out), .en(not_1_out), .Q(rs_2), .clk(CLK));  // open: clr
  Pull_Resistor #(.pull(0)) pull_resistor_2 (.node(not_1_out));

  // Notes on the sheet:
  //   使能端_低电平有效: pull=down
  //   同步清零_高电平有效: pull=down
endmodule

module \数据检测逻辑  (
  input  [31:0] ID_IR,
  input  EX_RW,
  input  [31:0] EX_IR,
  output pause
);

  wire and_7_out, and_8_out, and_9_out, and_10_out, and_11_out, and_12_out, and_13_out, and_14_out,
       and_15_out, and_16_out, and_17_out, and_18_out, comparator_2_eq, comparator_7_eq, comparator_8_eq,
       comparator_9_eq, comparator_10_eq, comparator_15_eq, comparator_16_eq, comparator_17_eq,
       comparator_18_eq, comparator_19_eq, comparator_20_eq, comparator_21_eq, comparator_22_eq,
       comparator_23_eq, comparator_24_eq, comparator_25_eq, comparator_26_eq, comparator_27_eq,
       comparator_28_eq, ex_beq, ex_bne, ex_I, ex_jal, ex_jr, ex_R, ex_rd, ex_rt, ex_sw, ex_sys, id_beq,
       id_bne, id_I, id_jr, id_R, id_rs, id_rt, id_sw, id_sys, nor_1_out, nor_2_out, or_1_out, or_3_out;

  // Mips_Probe mips_probe_1: pin names not known; wires that end beside it: EX_IR
  // Mips_Probe mips_probe_2: pin names not known; wires that end beside it: ID_IR
  Comparator #(.width(6), .mode("twosComplement")) comparator_1 (
    .a(6'b000011), .b(EX_IR[31:26]), .eq(ex_jal));  // open: gt, lt
  Comparator #(.width(6), .mode("twosComplement")) comparator_2 (
    .a(6'b000010), .b(EX_IR[31:26]), .eq(comparator_2_eq));  // open: gt, lt
  Comparator #(.width(6), .mode("twosComplement")) comparator_3 (
    .a(6'b101011), .b(EX_IR[31:26]), .eq(ex_sw));  // open: gt, lt
  Comparator #(.width(6), .mode("twosComplement")) comparator_4 (
    .a(6'b000100), .b(EX_IR[31:26]), .eq(ex_beq));  // open: gt, lt
  Comparator #(.width(6), .mode("twosComplement")) comparator_5 (
    .a(6'b000101), .b(EX_IR[31:26]), .eq(ex_bne));  // open: gt, lt
  Comparator #(.width(6), .mode("twosComplement")) comparator_6 (
    .a({6{1'b0}}), .b(EX_IR[31:26]), .eq(ex_R));  // open: gt, lt
  Comparator #(.width(6), .mode("twosComplement")) comparator_7 (
    .a(6'b001000), .b(EX_IR[5:0]), .eq(comparator_7_eq));  // open: gt, lt
  Comparator #(.width(6), .mode("twosComplement")) comparator_8 (
    .a(EX_IR[5:0]), .b(6'b001100), .eq(comparator_8_eq));  // open: gt, lt
  // Probe on EX_IR[20:16]
  Comparator #(.width(6), .mode("twosComplement")) comparator_9 (
    .a(6'b000011), .b(ID_IR[31:26]), .eq(comparator_9_eq));  // open: gt, lt
  Comparator #(.width(6), .mode("twosComplement")) comparator_10 (
    .a(6'b000010), .b(ID_IR[31:26]), .eq(comparator_10_eq));  // open: gt, lt
  Comparator #(.width(6), .mode("twosComplement")) comparator_11 (
    .a(6'b101011), .b(ID_IR[31:26]), .eq(id_sw));  // open: gt, lt
  Comparator #(.width(6), .mode("twosComplement")) comparator_12 (
    .a(6'b000100), .b(ID_IR[31:26]), .eq(id_beq));  // open: gt, lt
  Comparator #(.width(6), .mode("twosComplement")) comparator_13 (
    .a(6'b000101), .b(ID_IR[31:26]), .eq(id_bne));  // open: gt, lt
  Comparator #(.width(6), .mode("twosComplement")) comparator_14 (
    .a({6{1'b0}}), .b(ID_IR[31:26]), .eq(id_R));  // open: gt, lt
  Comparator #(.width(6), .mode("twosComplement")) comparator_15 (
    .a(6'b001100), .b(ID_IR[5:0]), .eq(comparator_15_eq));  // open: gt, lt
  Comparator #(.width(6), .mode("twosComplement")) comparator_16 (
    .a(ID_IR[5:0]), .b(6'b001000), .eq(comparator_16_eq));  // open: gt, lt
  nor nor_1 (nor_1_out, ex_jal, comparator_2_eq);
  and and_1 (ex_jr, ex_R, comparator_7_eq);
  and and_2 (ex_sys, ex_R, comparator_8_eq);
  nor nor_2 (nor_2_out, comparator_9_eq, comparator_10_eq);
  and and_3 (id_sys, id_R, comparator_15_eq);
  and and_4 (id_jr, id_R, comparator_16_eq);
  and and_5 (id_I, nor_2_out, ~id_R);  // AND_Gate
  Comparator #(.width(5), .mode("twosComplement")) comparator_17 (
    .a({5{1'b0}}), .b(ID_IR[20:16]), .eq(comparator_17_eq));  // open: gt, lt
  Comparator #(.width(5), .mode("twosComplement")) comparator_18 (
    .a(5'b00010), .b(EX_IR[20:16]), .eq(comparator_18_eq));  // open: gt, lt
  Comparator #(.width(5), .mode("twosComplement")) comparator_19 (
    .a(5'b00010), .b(EX_IR[15:11]), .eq(comparator_19_eq));  // open: gt, lt
  Comparator #(.width(5), .mode("twosComplement")) comparator_20 (
    .a(5'b00100), .b(EX_IR[20:16]), .eq(comparator_20_eq));  // open: gt, lt
  Comparator #(.width(5), .mode("twosComplement")) comparator_21 (
    .a(5'b00100), .b(EX_IR[15:11]), .eq(comparator_21_eq));  // open: gt, lt
  and and_6 (ex_I, nor_1_out, ~ex_R);  // AND_Gate
  or or_1 (or_1_out, id_sw, id_beq, id_bne);
  Comparator #(.width(5), .mode("twosComplement")) comparator_22 (
    .a(ID_IR[20:16]), .b(EX_IR[20:16]), .eq(comparator_22_eq));  // open: gt, lt
  Comparator #(.width(5), .mode("twosComplement")) comparator_23 (
    .a(ID_IR[20:16]), .b(EX_IR[15:11]), .eq(comparator_23_eq));  // open: gt, lt
  Comparator #(.width(5), .mode("twosComplement")) comparator_24 (
    .a(ID_IR[25:21]), .b(EX_IR[20:16]), .eq(comparator_24_eq));  // open: gt, lt
  Comparator #(.width(5), .mode("twosComplement")) comparator_25 (
    .a(ID_IR[25:21]), .b(EX_IR[15:11]), .eq(comparator_25_eq));  // open: gt, lt
  and and_7 (and_7_out, id_I, or_1_out);
  and and_8 (and_8_out, ~id_sys, id_R, ~id_jr, ~comparator_17_eq);  // AND_Gate
  Comparator #(.width(5), .mode("twosComplement")) comparator_26 (
    .a({5{1'b0}}), .b(ID_IR[25:21]), .eq(comparator_26_eq));  // open: gt, lt
  and and_9 (and_9_out, ex_rt, id_sys, comparator_18_eq);
  and and_10 (and_10_out, ex_rd, id_sys, comparator_19_eq);
  and and_11 (and_11_out, ex_rt, id_sys, comparator_20_eq);
  and and_12 (and_12_out, ex_rd, id_sys, comparator_21_eq);
  Comparator #(.width(5), .mode("twosComplement")) comparator_27 (
    .a(ID_IR[25:21]), .b({5{1'b1}}), .eq(comparator_27_eq));  // open: gt, lt
  Comparator #(.width(5), .mode("twosComplement")) comparator_28 (
    .a({5{1'b1}}), .b(ID_IR[20:16]), .eq(comparator_28_eq));  // open: gt, lt
  nor nor_3 (ex_rt, ~nor_1_out, ex_sw, ex_beq, ex_bne, ex_R);  // NOR_Gate
  nor nor_4 (ex_rd, ~nor_1_out, ex_I, ex_jr, ex_sys);  // NOR_Gate
  or or_2 (id_rt, and_7_out, and_8_out);
  nor nor_5 (id_rs, ~nor_2_out, id_sys, comparator_26_eq);  // NOR_Gate
  and and_13 (and_13_out, id_rs, comparator_27_eq, ex_jal);
  and and_14 (and_14_out, id_rt, comparator_28_eq, ex_jal);
  and and_15 (and_15_out, ex_rt, comparator_22_eq, id_rt);
  and and_16 (and_16_out, ex_rd, comparator_23_eq, id_rt);
  and and_17 (and_17_out, ex_rt, comparator_24_eq, id_rs);
  and and_18 (and_18_out, ex_rd, comparator_25_eq, id_rs);
  or or_3 (or_3_out, and_9_out, and_10_out, and_11_out, and_12_out, and_13_out, and_14_out, and_15_out, and_16_out, and_17_out, and_18_out);
  and and_19 (pause, EX_RW, or_3_out);

  // Notes on the sheet:
  //   OP
  //   Func
  //   rt
  //   rd
  //   OP
  //   Func
  //   rs
  //   rt
  //   JAL
  //   非J
  //   非J
  //   02 = ex.rt
  //   02 = ex.rd
  //   04 = ex.rt
  //   04 = ex.rd
  //   I型
  //   id.rt = ex.rt
  //   id.rt = ex.rd
  //   id.rs = ex.rt
  //   id.rs = ex.rd
  //   JAL
endmodule

module \中断栈  (
  input  [1:0] ir,
  input  clk,
  input  sig,
  input  eret,
  output [1:0] peak
);

  wire and_1_out, and_2_out, and_3_out, decoder_1_out0, decoder_1_out1, decoder_1_out2, or_1_out;
  wire [1:0] counter_1_q, \栈1_q , \栈2_q , \栈3_q ;

  or or_1 (or_1_out, eret, sig);
  Decoder #(.select(2), .tristate("false"), .disabled("Z"), .enable("false")) decoder_1 (
    .out0(decoder_1_out0), .out1(decoder_1_out1), .out2(decoder_1_out2), .sel(counter_1_q));  // open: out3
  Counter #(.width(2), .max('h3), .ongoal("wrap"), .trigger("rising"), .behavior("old")) counter_1 (
    .load(eret), .count(or_1_out), .Q(counter_1_q), .clk(clk));  // open: D, carry, clr, preset
  and and_1 (and_1_out, sig, decoder_1_out0);
  Register #(.width(2), .trigger("rising"), .Select("low")) \u_栈1  (
    .D(ir), .en(and_1_out), .Q(\栈1_q ), .clk(clk));  // open: clr
  and and_2 (and_2_out, sig, decoder_1_out1);
  Register #(.width(2), .trigger("rising"), .Select("low")) \u_栈2  (
    .D(ir), .en(and_2_out), .Q(\栈2_q ), .clk(clk));  // open: clr
  and and_3 (and_3_out, sig, decoder_1_out2);
  Register #(.width(2), .trigger("rising"), .Select("low")) \u_栈3  (
    .D(ir), .en(and_3_out), .Q(\栈3_q ), .clk(clk));  // open: clr
  Multiplexer #(.select(2), .width(2), .disabled("Z"), .enable("false")) multiplexer_1 (
    .in0(2'b00), .in1(\栈1_q ), .in2(\栈2_q ), .in3(\栈3_q ), .out(peak), .sel(counter_1_q));
  // Probe on counter_1_q
endmodule

module \下降沿Regifile  (
  input  [31:0] Din,
  input  Clk,
  input  WE,
  input  [4:0] R1_num,
  input  [4:0] W_num,
  input  [4:0] R2_num,
  output [31:0] R1,
  output [31:0] R2
);

  // RegisterFile registerfile_1: pin names not known; wires that end beside it: Din, Clk, WE, W_num, R1_num, R2_num, R1, R2
endmodule

module \重定向检测  (
  input  MEM_MemToReg,
  input  [4:0] ID_R1,
  input  [4:0] EX_WriteReg,
  input  EX_RegWrite,
  input  EX_MemToReg,
  input  [4:0] MEM_WriteReg,
  input  MEM_RegWrite,
  input  [5:0] OP,
  input  [5:0] Func,
  input  [4:0] ID_R2,
  output [1:0] ForwardToR1,
  output Load_Use,
  output [1:0] ForwardToR2
);

  wire and_1_out, and_2_out, and_3_out, and_4_out, and_5_out, and_6_out, and_7_out, and_8_out,
       comparator_1_eq, comparator_2_eq, comparator_3_eq, comparator_4_eq, comparator_5_eq, comparator_6_eq,
       not_1_out, not_2_out, or_1_out, or_2_out, or_3_out, \源寄存器使用情况_1_r1_used , \源寄存器使用情况_1_r2_used ;
  wire [1:0] multiplexer_1_out, multiplexer_2_out, multiplexer_4_out, multiplexer_6_out;

  Multiplexer #(.select(1), .width(2), .disabled("Z"), .enable("false")) multiplexer_1 (
    .in0(2'b01), .in1(2'b10), .out(multiplexer_1_out), .sel(MEM_MemToReg));
  Comparator #(.width(5), .mode("twosComplement")) comparator_1 (
    .a(ID_R1), .b(EX_WriteReg), .eq(comparator_1_eq));  // open: gt, lt
  Comparator #(.width(5), .mode("twosComplement")) comparator_2 (
    .a(ID_R1), .b(MEM_WriteReg), .eq(comparator_2_eq));  // open: gt, lt
  \源寄存器使用情况  \u_源寄存器使用情况_1  (
    .OP0(OP[0]), .OP1(OP[1]), .OP2(OP[2]), .OP3(OP[3]), .OP4(OP[4]), .OP5(OP[5]), .F0(Func[0]), .F1(Func[1]),
    .F2(Func[2]), .F3(Func[3]), .F4(Func[4]), .F5(Func[5]), .R1_used(\源寄存器使用情况_1_r1_used ),
    .R2_used(\源寄存器使用情况_1_r2_used ));
  Comparator #(.width(5), .mode("twosComplement")) comparator_3 (
    .a(ID_R2), .b(EX_WriteReg), .eq(comparator_3_eq));  // open: gt, lt
  Comparator #(.width(5), .mode("twosComplement")) comparator_4 (
    .a(ID_R2), .b(MEM_WriteReg), .eq(comparator_4_eq));  // open: gt, lt
  Multiplexer #(.select(1), .width(2), .disabled("Z"), .enable("false")) multiplexer_2 (
    .in0(2'b01), .in1(2'b10), .out(multiplexer_2_out), .sel(MEM_MemToReg));
  Multiplexer #(.select(1), .width(2), .disabled("Z"), .enable("false")) multiplexer_3 (
    .in0(2'b00), .in1(multiplexer_4_out), .out(ForwardToR1), .sel(and_5_out));
  Multiplexer #(.select(1), .width(2), .disabled("Z"), .enable("false")) multiplexer_4 (
    .in0(multiplexer_1_out), .in1(2'b11), .out(multiplexer_4_out), .sel(comparator_1_eq));
  Multiplexer #(.select(1), .width(2), .disabled("Z"), .enable("false")) multiplexer_5 (
    .in0(2'b00), .in1(multiplexer_6_out), .out(ForwardToR2), .sel(and_6_out));
  Multiplexer #(.select(1), .width(2), .disabled("Z"), .enable("false")) multiplexer_6 (
    .in0(multiplexer_2_out), .in1(2'b11), .out(multiplexer_6_out), .sel(comparator_3_eq));
  Comparator #(.width(5), .mode("twosComplement")) comparator_5 (
    .a(ID_R1), .b({5{1'b0}}), .eq(comparator_5_eq));  // open: gt, lt
  not not_1 (not_1_out, comparator_5_eq);
  and and_1 (and_1_out, comparator_1_eq, EX_RegWrite);
  and and_2 (and_2_out, comparator_2_eq, MEM_RegWrite);
  and and_3 (and_3_out, comparator_3_eq, EX_RegWrite);
  and and_4 (and_4_out, comparator_4_eq, MEM_RegWrite);
  not not_2 (not_2_out, comparator_6_eq);
  Comparator #(.width(5), .mode("twosComplement")) comparator_6 (
    .a(ID_R2), .b({5{1'b0}}), .eq(comparator_6_eq));  // open: gt, lt
  or or_1 (or_1_out, and_1_out, and_2_out);
  or or_2 (or_2_out, and_3_out, and_4_out);
  and and_5 (and_5_out, not_1_out, or_1_out, \源寄存器使用情况_1_r1_used );
  and and_6 (and_6_out, \源寄存器使用情况_1_r2_used , or_2_out, not_2_out);
  and and_7 (and_7_out, not_1_out, and_1_out, \源寄存器使用情况_1_r1_used );
  and and_8 (and_8_out, \源寄存器使用情况_1_r2_used , and_3_out, not_2_out);
  or or_3 (or_3_out, and_7_out, and_8_out);
  and and_9 (Load_Use, EX_MemToReg, or_3_out);
endmodule

module \源寄存器使用情况  (
  input  OP0,
  input  OP1,
  input  OP2,
  input  OP3,
  input  OP4,
  input  OP5,
  input  F0,
  input  F1,
  input  F2,
  input  F3,
  input  F4,
  input  F5,
  output R1_used,
  output R2_used
);

  wire and_1_out, and_2_out, and_3_out, and_4_out, and_5_out, and_6_out, and_7_out, and_8_out, and_9_out,
       and_10_out, and_11_out, and_12_out, and_13_out, and_14_out, and_15_out, and_16_out, and_17_out,
       and_18_out, and_19_out, and_20_out, and_21_out, and_22_out, and_23_out, and_24_out, not_1_out,
       not_2_out, not_3_out, not_4_out, not_5_out, not_6_out, not_7_out, not_8_out, not_9_out, not_10_out,
       not_11_out, not_12_out, not_13_out, not_14_out, not_15_out, not_16_out, not_17_out, not_18_out,
       not_19_out, not_20_out, not_21_out, not_22_out, not_23_out, not_24_out, not_25_out, not_26_out,
       not_27_out, not_28_out, not_29_out, not_30_out, not_31_out, not_32_out, not_33_out, not_34_out,
       not_35_out, not_36_out, not_37_out, not_38_out, not_39_out, not_40_out, not_41_out, not_42_out,
       not_43_out, not_44_out, not_45_out, not_46_out, not_47_out, not_48_out, not_49_out, not_50_out,
       not_51_out, not_52_out, not_53_out, not_54_out, not_55_out, not_56_out, not_57_out, not_58_out,
       not_59_out, not_60_out, not_61_out, not_62_out, not_63_out, not_64_out, not_65_out, not_66_out,
       not_67_out, not_68_out, not_69_out, not_70_out, not_71_out, not_72_out, not_73_out, not_74_out,
       not_75_out, not_76_out, not_77_out, not_78_out, not_79_out, not_80_out, not_81_out, not_82_out,
       not_83_out, not_84_out, not_85_out, not_86_out, not_87_out, not_88_out, not_89_out, not_90_out,
       not_91_out, not_92_out, not_93_out, not_94_out, not_95_out, not_96_out, not_97_out, not_98_out,
       not_99_out, not_100_out, not_101_out, not_102_out, not_103_out, not_104_out, not_105_out, not_106_out,
       not_107_out, not_108_out, not_109_out, not_110_out, not_111_out, not_112_out, not_113_out,
       not_114_out, not_115_out, not_116_out, not_117_out, not_118_out, not_119_out, not_120_out,
       not_121_out, not_122_out;

  not not_1 (not_1_out, OP1);
  not not_2 (not_2_out, OP4);
  not not_3 (not_3_out, OP5);
  not not_4 (not_4_out, F0);
  not not_5 (not_5_out, F2);
  not not_6 (not_6_out, F3);
  not not_7 (not_7_out, F4);
  not not_8 (not_8_out, OP1);
  not not_9 (not_9_out, OP4);
  not not_10 (not_10_out, OP5);
  not not_11 (not_11_out, F1);
  not not_12 (not_12_out, F3);
  not not_13 (not_13_out, F4);
  not not_14 (not_14_out, OP1);
  not not_15 (not_15_out, OP4);
  not not_16 (not_16_out, OP5);
  not not_17 (not_17_out, F0);
  not not_18 (not_18_out, F1);
  not not_19 (not_19_out, F4);
  not not_20 (not_20_out, F5);
  not not_21 (not_21_out, OP1);
  not not_22 (not_22_out, OP4);
  not not_23 (not_23_out, OP5);
  not not_24 (not_24_out, F2);
  not not_25 (not_25_out, F4);
  not not_26 (not_26_out, OP1);
  not not_27 (not_27_out, OP4);
  not not_28 (not_28_out, OP5);
  not not_29 (not_29_out, F1);
  not not_30 (not_30_out, F2);
  not not_31 (not_31_out, F5);
  not not_32 (not_32_out, OP1);
  not not_33 (not_33_out, OP4);
  not not_34 (not_34_out, OP5);
  not not_35 (not_35_out, F3);
  not not_36 (not_36_out, F4);
  not not_37 (not_37_out, F5);
  not not_38 (not_38_out, OP1);
  not not_39 (not_39_out, OP4);
  not not_40 (not_40_out, OP5);
  not not_41 (not_41_out, F3);
  not not_42 (not_42_out, F4);
  not not_43 (not_43_out, OP0);
  not not_44 (not_44_out, OP1);
  not not_45 (not_45_out, OP3);
  not not_46 (not_46_out, OP4);
  not not_47 (not_47_out, OP0);
  not not_48 (not_48_out, OP2);
  not not_49 (not_49_out, OP4);
  not not_50 (not_50_out, OP5);
  not not_51 (not_51_out, OP1);
  not not_52 (not_52_out, OP4);
  not not_53 (not_53_out, OP5);
  not not_54 (not_54_out, OP1);
  not not_55 (not_55_out, OP4);
  not not_56 (not_56_out, OP5);
  not not_57 (not_57_out, OP1);
  not not_58 (not_58_out, OP4);
  not not_59 (not_59_out, OP5);
  not not_60 (not_60_out, OP2);
  not not_61 (not_61_out, OP4);
  not not_62 (not_62_out, OP0);
  not not_63 (not_63_out, OP1);
  not not_64 (not_64_out, OP3);
  not not_65 (not_65_out, OP4);
  not not_66 (not_66_out, F0);
  not not_67 (not_67_out, F2);
  not not_68 (not_68_out, F3);
  not not_69 (not_69_out, F4);
  not not_70 (not_70_out, OP0);
  not not_71 (not_71_out, OP1);
  not not_72 (not_72_out, OP3);
  not not_73 (not_73_out, OP4);
  not not_74 (not_74_out, F1);
  not not_75 (not_75_out, F3);
  not not_76 (not_76_out, F4);
  not not_77 (not_77_out, OP0);
  not not_78 (not_78_out, OP1);
  not not_79 (not_79_out, OP3);
  not not_80 (not_80_out, OP4);
  not not_81 (not_81_out, F0);
  not not_82 (not_82_out, F1);
  not not_83 (not_83_out, F4);
  not not_84 (not_84_out, F5);
  not not_85 (not_85_out, OP0);
  not not_86 (not_86_out, OP1);
  not not_87 (not_87_out, OP3);
  not not_88 (not_88_out, OP4);
  not not_89 (not_89_out, F2);
  not not_90 (not_90_out, F4);
  not not_91 (not_91_out, OP0);
  not not_92 (not_92_out, OP1);
  not not_93 (not_93_out, OP3);
  not not_94 (not_94_out, OP4);
  not not_95 (not_95_out, F1);
  not not_96 (not_96_out, F2);
  not not_97 (not_97_out, F5);
  not not_98 (not_98_out, OP0);
  not not_99 (not_99_out, OP1);
  not not_100 (not_100_out, OP3);
  not not_101 (not_101_out, OP4);
  not not_102 (not_102_out, F3);
  not not_103 (not_103_out, F4);
  not not_104 (not_104_out, F5);
  not not_105 (not_105_out, OP0);
  not not_106 (not_106_out, OP1);
  not not_107 (not_107_out, OP3);
  not not_108 (not_108_out, OP4);
  not not_109 (not_109_out, F3);
  not not_110 (not_110_out, F4);
  not not_111 (not_111_out, OP0);
  not not_112 (not_112_out, OP1);
  not not_113 (not_113_out, OP3);
  not not_114 (not_114_out, OP4);
  not not_115 (not_115_out, OP1);
  not not_116 (not_116_out, OP3);
  not not_117 (not_117_out, OP4);
  not not_118 (not_118_out, OP5);
  not not_119 (not_119_out, OP2);
  not not_120 (not_120_out, OP4);
  not not_121 (not_121_out, OP4);
  not not_122 (not_122_out, OP5);
  and and_1 (and_1_out, not_1_out, not_2_out, not_3_out, not_4_out, not_5_out, not_6_out, not_7_out);
  and and_2 (and_2_out, not_8_out, not_9_out, not_10_out, not_11_out, not_12_out, not_13_out, F5);
  and and_3 (and_3_out, not_14_out, not_15_out, not_16_out, not_17_out, not_18_out, F3, not_19_out, not_20_out);
  and and_4 (and_4_out, not_21_out, not_22_out, not_23_out, F1, not_24_out, F3, not_25_out, F5);
  and and_5 (and_5_out, not_26_out, not_27_out, not_28_out, F0, not_29_out, not_30_out, F3, F4, not_31_out);
  and and_6 (and_6_out, not_32_out, not_33_out, not_34_out, F0, F1, not_35_out, not_36_out, not_37_out);
  and and_7 (and_7_out, not_38_out, not_39_out, not_40_out, F0, F1, F2, not_41_out, not_42_out);
  and and_8 (and_8_out, not_43_out, not_44_out, not_45_out, not_46_out, OP5);
  and and_9 (and_9_out, not_47_out, not_48_out, OP3, not_49_out, not_50_out);
  and and_10 (and_10_out, not_51_out, OP2, not_52_out, not_53_out);
  and and_11 (and_11_out, OP0, not_54_out, not_55_out, not_56_out);
  and and_12 (and_12_out, OP0, not_57_out, OP2, OP3, not_58_out, not_59_out);
  and and_13 (and_13_out, OP0, OP1, not_60_out, not_61_out, OP5);
  and and_14 (and_14_out, not_62_out, not_63_out, not_64_out, not_65_out, not_66_out, not_67_out, not_68_out, not_69_out);
  and and_15 (and_15_out, not_70_out, not_71_out, not_72_out, not_73_out, not_74_out, not_75_out, not_76_out, F5);
  and and_16 (and_16_out, not_77_out, not_78_out, not_79_out, not_80_out, not_81_out, not_82_out, F2, F3, not_83_out, not_84_out);
  and and_17 (and_17_out, not_85_out, not_86_out, not_87_out, not_88_out, F1, not_89_out, F3, not_90_out, F5);
  and and_18 (and_18_out, not_91_out, not_92_out, not_93_out, not_94_out, F0, not_95_out, not_96_out, F3, F4, not_97_out);
  and and_19 (and_19_out, not_98_out, not_99_out, not_100_out, not_101_out, F0, F1, not_102_out, not_103_out, not_104_out);
  and and_20 (and_20_out, not_105_out, not_106_out, not_107_out, not_108_out, F0, F1, F2, not_109_out, not_110_out);
  and and_21 (and_21_out, not_111_out, not_112_out, not_113_out, not_114_out, OP5);
  and and_22 (and_22_out, not_115_out, OP2, not_116_out, not_117_out, not_118_out);
  and and_23 (and_23_out, OP0, OP1, not_119_out, not_120_out, OP5);
  and and_24 (and_24_out, OP0, OP1, OP2, OP3, not_121_out, not_122_out);
  or or_1 (R1_used, and_1_out, and_2_out, and_3_out, and_4_out, and_5_out, and_6_out, and_7_out, and_8_out, and_9_out, and_10_out, and_11_out, and_12_out, and_13_out);
  or or_2 (R2_used, and_14_out, and_15_out, and_16_out, and_17_out, and_18_out, and_19_out, and_20_out, and_21_out, and_22_out, and_23_out, and_24_out);
endmodule

module \图片显示  (
);

  wire [31:0] \图片显示模块_1_out_6 , \图片显示模块_1_out_7 , \图片显示模块_1_out_8 , \图片显示模块_1_out_9 , \图片显示模块_1_out_10 ,
       \图片显示模块_1_out_11 , \图片显示模块_1_out_12 , \图片显示模块_1_out_13 , \图片显示模块_1_out_14 , \图片显示模块_1_out_15 ,
       \图片显示模块_1_out_16 , \图片显示模块_1_out_17 , \图片显示模块_1_out_18 , \图片显示模块_1_out_19 , \图片显示模块_1_out_20 ,
       \图片显示模块_1_out_21 , \图片显示模块_1_out_22 , \图片显示模块_1_out_23 , \图片显示模块_1_out_24 , \图片显示模块_1_out_25 ;

  \图片显示模块  \u_图片显示模块_1  (
    .out_6(\图片显示模块_1_out_6 ), .out_16(\图片显示模块_1_out_16 ), .out_7(\图片显示模块_1_out_7 ),
    .out_17(\图片显示模块_1_out_17 ), .out_8(\图片显示模块_1_out_8 ), .out_18(\图片显示模块_1_out_18 ),
    .out_9(\图片显示模块_1_out_9 ), .out_19(\图片显示模块_1_out_19 ), .out_10(\图片显示模块_1_out_10 ),
    .out_20(\图片显示模块_1_out_20 ), .out_11(\图片显示模块_1_out_11 ), .out_21(\图片显示模块_1_out_21 ),
    .out_12(\图片显示模块_1_out_12 ), .out_22(\图片显示模块_1_out_22 ), .out_13(\图片显示模块_1_out_13 ),
    .out_23(\图片显示模块_1_out_23 ), .out_14(\图片显示模块_1_out_14 ), .out_24(\图片显示模块_1_out_24 ),
    .out_15(\图片显示模块_1_out_15 ), .out_25(\图片显示模块_1_out_25 ));  // open: Data, column, WriteEnable, OutEnable, CLK
  DotMatrix #(.inputtype("column"), .matrixcols(20), .matrixrows(32), .persist(0), .dotshape("circle")) dotmatrix_1 (
    .col0(\图片显示模块_1_out_6 ), .col1(\图片显示模块_1_out_7 ), .col2(\图片显示模块_1_out_8 ), .col3(\图片显示模块_1_out_9 ),
    .col4(\图片显示模块_1_out_10 ), .col5(\图片显示模块_1_out_11 ), .col6(\图片显示模块_1_out_12 ), .col7(\图片显示模块_1_out_13 ),
    .col8(\图片显示模块_1_out_14 ), .col9(\图片显示模块_1_out_15 ), .col10(\图片显示模块_1_out_16 ), .col11(\图片显示模块_1_out_17 ),
    .col12(\图片显示模块_1_out_18 ), .col13(\图片显示模块_1_out_19 ), .col14(\图片显示模块_1_out_20 ),
    .col15(\图片显示模块_1_out_21 ), .col16(\图片显示模块_1_out_22 ), .col17(\图片显示模块_1_out_23 ),
    .col18(\图片显示模块_1_out_24 ), .col19(\图片显示模块_1_out_25 ));
endmodule

module \图片显示模块  (
  input  WriteEnable,
  input  OutEnable,
  input  CLK,
  input  [31:0] Data,
  input  [4:0] column,
  output [31:0] out_6,
  output [31:0] out_7,
  output [31:0] out_8,
  output [31:0] out_9,
  output [31:0] out_10,
  output [31:0] out_11,
  output [31:0] out_12,
  output [31:0] out_13,
  output [31:0] out_14,
  output [31:0] out_15,
  output [31:0] out_16,
  output [31:0] out_17,
  output [31:0] out_18,
  output [31:0] out_19,
  output [31:0] out_20,
  output [31:0] out_21,
  output [31:0] out_22,
  output [31:0] out_23,
  output [31:0] out_24,
  output [31:0] out_25
);

  wire and_1_out, and_2_out, and_3_out, and_4_out, and_5_out, and_6_out, and_7_out, and_8_out, and_9_out,
       and_10_out, and_11_out, and_12_out, and_13_out, and_14_out, and_15_out, and_16_out, and_17_out,
       and_18_out, and_19_out, and_20_out, En0, En1, En2, En3, En4, En5, En6, En7, En8, En9, En10, En11,
       En12, En13, En14, En15, En16, En17, En18, En19;
  wire [31:0] In0, In1, In2, In3, In4, In5, In6, In7, In8, In9, In10, In11, In12, In13, In14, In15, In16,
       In17, In18, In19, register_1_q, register_2_q, register_3_q, register_4_q, register_5_q, register_6_q,
       register_7_q, register_8_q, register_9_q, register_10_q, register_21_q, register_22_q, register_23_q,
       register_24_q, register_25_q, register_26_q, register_27_q, register_28_q, register_29_q,
       register_30_q;

  and and_1 (and_1_out, En0, WriteEnable);
  and and_2 (and_2_out, En1, WriteEnable);
  and and_3 (and_3_out, En2, WriteEnable);
  and and_4 (and_4_out, En3, WriteEnable);
  and and_5 (and_5_out, En4, WriteEnable);
  and and_6 (and_6_out, En5, WriteEnable);
  and and_7 (and_7_out, En6, WriteEnable);
  and and_8 (and_8_out, En7, WriteEnable);
  and and_9 (and_9_out, En8, WriteEnable);
  and and_10 (and_10_out, En9, WriteEnable);
  Register #(.width(32), .trigger("rising"), .Select("low")) register_1 (
    .D(In0), .en(and_1_out), .Q(register_1_q), .clk(CLK));  // open: clr
  Register #(.width(32), .trigger("rising"), .Select("low")) register_2 (
    .D(In1), .en(and_2_out), .Q(register_2_q), .clk(CLK));  // open: clr
  Register #(.width(32), .trigger("rising"), .Select("low")) register_3 (
    .D(In2), .en(and_3_out), .Q(register_3_q), .clk(CLK));  // open: clr
  Register #(.width(32), .trigger("rising"), .Select("low")) register_4 (
    .D(In3), .en(and_4_out), .Q(register_4_q), .clk(CLK));  // open: clr
  Register #(.width(32), .trigger("rising"), .Select("low")) register_5 (
    .D(In4), .en(and_5_out), .Q(register_5_q), .clk(CLK));  // open: clr
  Register #(.width(32), .trigger("rising"), .Select("low")) register_6 (
    .D(In5), .en(and_6_out), .Q(register_6_q), .clk(CLK));  // open: clr
  Register #(.width(32), .trigger("rising"), .Select("low")) register_7 (
    .D(In6), .en(and_7_out), .Q(register_7_q), .clk(CLK));  // open: clr
  Register #(.width(32), .trigger("rising"), .Select("low")) register_8 (
    .D(In7), .en(and_8_out), .Q(register_8_q), .clk(CLK));  // open: clr
  Register #(.width(32), .trigger("rising"), .Select("low")) register_9 (
    .D(In8), .en(and_9_out), .Q(register_9_q), .clk(CLK));  // open: clr
  Register #(.width(32), .trigger("rising"), .Select("low")) register_10 (
    .D(In9), .en(and_10_out), .Q(register_10_q), .clk(CLK));  // open: clr
  Register #(.width(32), .trigger("rising"), .Select("low")) register_11 (
    .D(register_1_q), .en(OutEnable), .Q(out_6), .clk(CLK));  // open: clr
  Register #(.width(32), .trigger("rising"), .Select("low")) register_12 (
    .D(register_2_q), .en(OutEnable), .Q(out_7), .clk(CLK));  // open: clr
  Register #(.width(32), .trigger("rising"), .Select("low")) register_13 (
    .D(register_3_q), .en(OutEnable), .Q(out_8), .clk(CLK));  // open: clr
  Register #(.width(32), .trigger("rising"), .Select("low")) register_14 (
    .D(register_4_q), .en(OutEnable), .Q(out_9), .clk(CLK));  // open: clr
  Register #(.width(32), .trigger("rising"), .Select("low")) register_15 (
    .D(register_5_q), .en(OutEnable), .Q(out_10), .clk(CLK));  // open: clr
  Register #(.width(32), .trigger("rising"), .Select("low")) register_16 (
    .D(register_6_q), .en(OutEnable), .Q(out_11), .clk(CLK));  // open: clr
  Register #(.width(32), .trigger("rising"), .Select("low")) register_17 (
    .D(register_7_q), .en(OutEnable), .Q(out_12), .clk(CLK));  // open: clr
  Register #(.width(32), .trigger("rising"), .Select("low")) register_18 (
    .D(register_8_q), .en(OutEnable), .Q(out_13), .clk(CLK));  // open: clr
  Register #(.width(32), .trigger("rising"), .Select("low")) register_19 (
    .D(register_9_q), .en(OutEnable), .Q(out_14), .clk(CLK));  // open: clr
  Register #(.width(32), .trigger("rising"), .Select("low")) register_20 (
    .D(register_10_q), .en(OutEnable), .Q(out_15), .clk(CLK));  // open: clr
  and and_11 (and_11_out, En10, WriteEnable);
  and and_12 (and_12_out, En11, WriteEnable);
  and and_13 (and_13_out, En12, WriteEnable);
  and and_14 (and_14_out, En13, WriteEnable);
  and and_15 (and_15_out, En14, WriteEnable);
  and and_16 (and_16_out, En15, WriteEnable);
  and and_17 (and_17_out, En16, WriteEnable);
  and and_18 (and_18_out, En17, WriteEnable);
  and and_19 (and_19_out, En18, WriteEnable);
  and and_20 (and_20_out, En19, WriteEnable);
  Register #(.width(32), .trigger("rising"), .Select("low")) register_21 (
    .D(In10), .en(and_11_out), .Q(register_21_q), .clk(CLK));  // open: clr
  Register #(.width(32), .trigger("rising"), .Select("low")) register_22 (
    .D(In11), .en(and_12_out), .Q(register_22_q), .clk(CLK));  // open: clr
  Register #(.width(32), .trigger("rising"), .Select("low")) register_23 (
    .D(In12), .en(and_13_out), .Q(register_23_q), .clk(CLK));  // open: clr
  Register #(.width(32), .trigger("rising"), .Select("low")) register_24 (
    .D(In13), .en(and_14_out), .Q(register_24_q), .clk(CLK));  // open: clr
  Register #(.width(32), .trigger("rising"), .Select("low")) register_25 (
    .D(In14), .en(and_15_out), .Q(register_25_q), .clk(CLK));  // open: clr
  Register #(.width(32), .trigger("rising"), .Select("low")) register_26 (
    .D(In15), .en(and_16_out), .Q(register_26_q), .clk(CLK));  // open: clr
  Register #(.width(32), .trigger("rising"), .Select("low")) register_27 (
    .D(In16), .en(and_17_out), .Q(register_27_q), .clk(CLK));  // open: clr
  Register #(.width(32), .trigger("rising"), .Select("low")) register_28 (
    .D(In17), .en(and_18_out), .Q(register_28_q), .clk(CLK));  // open: clr
  Register #(.width(32), .trigger("rising"), .Select("low")) register_29 (
    .D(In18), .en(and_19_out), .Q(register_29_q), .clk(CLK));  // open: clr
  Register #(.width(32), .trigger("rising"), .Select("low")) register_30 (
    .D(In19), .en(and_20_out), .Q(register_30_q), .clk(CLK));  // open: clr
  Register #(.width(32), .trigger("rising"), .Select("low")) register_31 (
    .D(register_21_q), .en(OutEnable), .Q(out_16), .clk(CLK));  // open: clr
  Register #(.width(32), .trigger("rising"), .Select("low")) register_32 (
    .D(register_22_q), .en(OutEnable), .Q(out_17), .clk(CLK));  // open: clr
  Register #(.width(32), .trigger("rising"), .Select("low")) register_33 (
    .D(register_23_q), .en(OutEnable), .Q(out_18), .clk(CLK));  // open: clr
  Register #(.width(32), .trigger("rising"), .Select("low")) register_34 (
    .D(register_24_q), .en(OutEnable), .Q(out_19), .clk(CLK));  // open: clr
  Register #(.width(32), .trigger("rising"), .Select("low")) register_35 (
    .D(register_25_q), .en(OutEnable), .Q(out_20), .clk(CLK));  // open: clr
  Register #(.width(32), .trigger("rising"), .Select("low")) register_36 (
    .D(register_26_q), .en(OutEnable), .Q(out_21), .clk(CLK));  // open: clr
  Register #(.width(32), .trigger("rising"), .Select("low")) register_37 (
    .D(register_27_q), .en(OutEnable), .Q(out_22), .clk(CLK));  // open: clr
  Register #(.width(32), .trigger("rising"), .Select("low")) register_38 (
    .D(register_28_q), .en(OutEnable), .Q(out_23), .clk(CLK));  // open: clr
  Register #(.width(32), .trigger("rising"), .Select("low")) register_39 (
    .D(register_29_q), .en(OutEnable), .Q(out_24), .clk(CLK));  // open: clr
  Register #(.width(32), .trigger("rising"), .Select("low")) register_40 (
    .D(register_30_q), .en(OutEnable), .Q(out_25), .clk(CLK));  // open: clr
  Demultiplexer #(.select(5), .width(32), .tristate("false"), .disabled("Z"), .enable("false")) demultiplexer_1 (
    .out0(In0), .out1(In1), .out2(In2), .out3(In3), .out4(In4), .out5(In5), .out6(In6), .out7(In7),
    .out8(In8), .out9(In9), .out10(In10), .out11(In11), .out12(In12), .out13(In13), .out14(In14),
    .out15(In15), .out16(In16), .out17(In17), .out18(In18), .out19(In19), .in(Data), .sel(column));  // open: out20, out21, out22, out23, out24, out25, out26, out27, out28, out29, out30, out31
  Demultiplexer #(.select(5), .width(1), .tristate("false"), .disabled("Z"), .enable("false")) demultiplexer_2 (
    .out0(En0), .out1(En1), .out2(En2), .out3(En3), .out4(En4), .out5(En5), .out6(En6), .out7(En7),
    .out8(En8), .out9(En9), .out10(En10), .out11(En11), .out12(En12), .out13(En13), .out14(En14),
    .out15(En15), .out16(En16), .out17(En17), .out18(En18), .out19(En19), .in(1'b1), .sel(column));  // open: out20, out21, out22, out23, out24, out25, out26, out27, out28, out29, out30, out31

  // Other names for the same wires on the sheet: D0[31:0] = out_6; D1[31:0] = out_7; D2[31:0] = out_8;
  //   D3[31:0] = out_9; D4[31:0] = out_10; D5[31:0] = out_11; D6[31:0] = out_12; D7[31:0] = out_13; D8[31:0] = out_14;
  //   D9[31:0] = out_15; D10[31:0] = out_16; D11[31:0] = out_17; D12[31:0] = out_18; D13[31:0] = out_19;
  //   D14[31:0] = out_20; D15[31:0] = out_21; D16[31:0] = out_22; D17[31:0] = out_23; D18[31:0] = out_24;
  //   D19[31:0] = out_25
endmodule
module \单周期MIPS_单级中断teamwork  (
  input  IR1,
  input  IR2,
  input  IR3,
  output RegWrite,
  output MemWrite,
  output [31:0] PC,
  output [31:0] IR,
  output [31:0] RDin,
  output [31:0] MDin,
  output [31:0] LedData
);

  wire AluSrcB, and_1_out, and_2_out, and_3_out, and_4_out, and_5_out, and_6_out, and_7_out, and_8_out,
       and_9_out, and_10_out, and_11_out, and_12_out, BEqual, BGTZ, CLK, comparator_1_eq, comparator_2_eq,
       comparator_3_eq, comparator_4_eq, comparator_5_eq, comparator_6_gt, comparator_7_eq, d_ff_1_q,
       d_ff_2_q, d_ff_3_q, decoder_1_out1, decoder_1_out2, decoder_1_out3, equal, ERET, Go, Halt, IE,
       IR1_2_q, IR1_3_q, IR1_q, IR1_t, IR2_t, IR3_t, IRA, IRB, IRC, JAL, JMP, JR, LBU, LUI, MemToReg,
       not_1_out, not_2_out, not_3_out, not_4_out, or_1_out, or_9_out, or_10_out, or_11_out, or_12_out,
       RegDst, sig, SignedExt, Syscall, W1, W2, W3, \单周期硬布线控制器_1_beq , \单周期硬布线控制器_1_bne ;
  wire [1:0] priority_encoder_1_out, register_3_q;
  wire [3:0] AluOP;
  wire [4:0] multiplexer_6_out, multiplexer_7_out, multiplexer_8_out, multiplexer_9_out, multiplexer_12_out;
  wire [7:0] multiplexer_16_out;
  wire [15:0] \总周期数 ;
  wire [27:0] PC_4;
  wire [31:0] adder_3_out, bit_extender_1_out, bit_extender_2_out, bit_extender_3_out, Din, EPC_q, imme,
       \int , mips_alu_1_result, multiplexer_1_out, multiplexer_2_out, multiplexer_3_out, multiplexer_4_out,
       multiplexer_5_out, multiplexer_11_out, multiplexer_13_out, multiplexer_15_out, multiplexer_19_out,
       PCBranch, ram_1_data, rs, shifter_1_out;
  wire [31:28] JMPAddr;

  Clock #(.highDuration(1), .lowDuration(1)) clock_1 (.out(CLK));
  Button _1 (.out(IRA));
  Button _2 (.out(IRB));
  Button _3 (.out(IRC));
  Button \u_继续运行  (.out(Go));
  LED #(.active("true")) led_1 (.in(W1));
  LED #(.active("true")) led_2 (.in(W2));
  LED #(.active("true")) led_3 (.in(W3));
  Hex_Digit_Display hex_digit_display_1 (.value(LedData[31:28]));  // open: dp
  Comparator #(.width(16), .mode("twosComplement")) comparator_1 (
    .a(16'h23b), .b(\总周期数 ), .eq(comparator_1_eq));  // open: gt, lt
  Comparator #(.width(16), .mode("twosComplement")) comparator_2 (
    .a(\总周期数 ), .b(16'h1), .eq(comparator_2_eq));  // open: gt, lt
  Comparator #(.width(16), .mode("twosComplement")) comparator_3 (
    .a(\总周期数 ), .b(16'h4), .eq(comparator_3_eq));  // open: gt, lt
  Comparator #(.width(16), .mode("twosComplement")) comparator_4 (
    .a(\总周期数 ), .b(16'h7), .eq(comparator_4_eq));  // open: gt, lt
  and and_1 (and_1_out, JMP, ~JR);  // AND_Gate
  Hex_Digit_Display hex_digit_display_2 (.value(LedData[23:20]));  // open: dp
  Hex_Digit_Display hex_digit_display_3 (.value(LedData[27:24]));  // open: dp
  or or_1 (or_1_out, comparator_1_eq, comparator_2_eq);
  assign IRA = or_1_out ? ~CLK : 1'bz;  // Controlled_Inverter controlled_inverter_1
  assign IRB = comparator_3_eq ? ~CLK : 1'bz;  // Controlled_Inverter controlled_inverter_2
  assign IRC = comparator_4_eq ? ~CLK : 1'bz;  // Controlled_Inverter controlled_inverter_3
  Multiplexer #(.select(1), .width(32), .disabled("Z"), .enable("false")) multiplexer_1 (
    .in0(multiplexer_2_out), .in1({JMPAddr, IR[25:0], 2'b00}), .out(multiplexer_1_out), .sel(and_1_out));
  Multiplexer #(.select(1), .width(32), .disabled("Z"), .enable("false")) multiplexer_2 (
    .in0(multiplexer_3_out), .in1(rs), .out(multiplexer_2_out), .sel(JR));
  Multiplexer #(.select(1), .width(32), .disabled("Z"), .enable("false")) multiplexer_3 (
    .in0({JMPAddr, PC_4}), .in1(PCBranch), .out(multiplexer_3_out), .sel(BEqual));
  and and_2 (and_2_out, ~Halt, CLK);  // AND_Gate
  Hex_Digit_Display hex_digit_display_4 (.value(LedData[19:16]));  // open: dp
  Hex_Digit_Display hex_digit_display_5 (.value(LedData[15:12]));  // open: dp
  Pull_Resistor #(.pull(0)) pull_resistor_1 (.node(IRA));
  Pull_Resistor #(.pull(0)) pull_resistor_2 (.node(IRB));
  Pull_Resistor #(.pull(0)) pull_resistor_3 (.node(IRC));
  Comparator #(.width(32), .mode("twosComplement")) comparator_5 (
    .a(rs), .b(32'h22), .eq(comparator_5_eq));  // open: gt, lt
  Register #(.width(32), .trigger("rising"), .Select("low")) EPC (
    .D(multiplexer_1_out), .en(sig), .Q(EPC_q), .clk(CLK));  // open: clr
  Multiplexer #(.select(1), .width(32), .disabled("Z"), .enable("false")) multiplexer_4 (
    .in0(multiplexer_1_out), .in1(\int ), .out(multiplexer_4_out), .sel(sig));
  Multiplexer #(.select(1), .width(32), .disabled("Z"), .enable("false")) multiplexer_5 (
    .in0(multiplexer_4_out), .in1(EPC_q), .out(multiplexer_5_out), .sel(ERET));
  Counter #(.width(16), .max('hffff), .ongoal("wrap"), .trigger("rising"), .behavior("old")) counter_1 (
    .Q(\总周期数 ), .clk(and_2_out));  // open: load, D, count, carry, clr, preset
  Hex_Digit_Display hex_digit_display_6 (.value(LedData[11:8]));  // open: dp
  Hex_Digit_Display hex_digit_display_7 (.value(LedData[7:4]));  // open: dp
  // Probe on \总周期数 
  and and_3 (and_3_out, ~comparator_5_eq, Syscall);  // AND_Gate
  Register #(.width(32), .trigger("rising"), .Select("low")) u_PC (
    .D(multiplexer_5_out), .en(not_1_out), .Q(PC), .clk(CLK));  // open: clr
  not not_1 (not_1_out, Halt);
  Hex_Digit_Display hex_digit_display_8 (.value(LedData[3:0]));  // open: dp
  Register #(.width(32), .trigger("rising"), .Select("low")) register_1 (
    .D(MDin), .en(comparator_5_eq), .Q(LedData), .clk(CLK));  // open: clr
  Register #(.width(1), .trigger("rising"), .Select("low")) register_2 (
    .D(and_3_out), .en(and_3_out), .Q(Halt), .clk(CLK), .clr(Go));
  Adder #(.width(32)) adder_1 (.a(PC), .b(32'h4), .out({JMPAddr, PC_4}));  // open: cin, cout
  \单周期硬布线控制器  \u_单周期硬布线控制器_1  (
    .Func(IR[5:0]), .OP(IR[31:26]), .ALU_OP(AluOP), .MemToReg(MemToReg), .MemWrite(MemWrite),
    .ALU_SRC(AluSrcB), .RegWrite(RegWrite), .SysCALL(Syscall), .SignedExt(SignedExt), .RegDst(RegDst),
    .JR(JR), .JMP(JMP), .Beq(\单周期硬布线控制器_1_beq ), .JAL(JAL), .Bne(\单周期硬布线控制器_1_bne ), .LUI(LUI), .LBU(LBU),
    .BGTZ(BGTZ), .ERET(ERET), .MF(IR[25:21]));  // open: MFC0, MTC0
  or or_2 (IR1_t, IR1, IRA);
  ROM #(.addrWidth(10), .dataWidth(32), .Select("high")) rom_1 (.addr(PC[11:2]), .data(IR));
  or or_3 (IR2_t, IR2, IRB);
  // Mips_Probe mips_probe_1: pin names not known; wires that end beside it: IR
  Multiplexer #(.select(1), .width(5), .disabled("Z"), .enable("false")) multiplexer_6 (
    .in0(IR[25:21]), .in1(5'b00010), .out(multiplexer_6_out), .sel(Syscall));
  Multiplexer #(.select(1), .width(5), .disabled("Z"), .enable("false")) multiplexer_7 (
    .in0(IR[20:16]), .in1(5'b00100), .out(multiplexer_7_out), .sel(Syscall));
  Multiplexer #(.select(1), .width(5), .disabled("Z"), .enable("false")) multiplexer_8 (
    .in0(IR[20:16]), .in1(IR[15:11]), .out(multiplexer_8_out), .sel(RegDst));
  and and_4 (and_4_out, equal, \单周期硬布线控制器_1_beq );
  and and_5 (and_5_out, ~equal, \单周期硬布线控制器_1_bne );  // AND_Gate
  or or_4 (IR3_t, IR3, IRC);
  Multiplexer #(.select(1), .width(5), .disabled("Z"), .enable("false")) multiplexer_9 (
    .in0(multiplexer_8_out), .in1({5{1'b1}}), .out(multiplexer_9_out), .sel(JAL));
  assign bit_extender_1_out = {{16{1'b0}}, IR[15:0]};  // Bit_Extender bit_extender_1
  assign bit_extender_2_out = {{16{IR[15]}}, IR[15:0]};  // Bit_Extender bit_extender_2
  Comparator #(.width(32), .mode("twosComplement")) comparator_6 (
    .a(rs), .b({32{1'b0}}), .gt(comparator_6_gt));  // open: eq, lt
  and and_6 (and_6_out, BGTZ, comparator_6_gt);
  MIPS_Regifile mips_regifile_1 (
    .Din(Din), .Clk(CLK), .R1(rs), .R2(MDin), .WE(RegWrite), .W_num(multiplexer_9_out),
    .R1_num(multiplexer_6_out), .R2_num(multiplexer_7_out));
  Multiplexer #(.select(1), .width(32), .disabled("Z"), .enable("false")) multiplexer_10 (
    .in0(bit_extender_1_out), .in1(bit_extender_2_out), .out(imme), .sel(SignedExt));
  or or_5 (BEqual, and_4_out, and_6_out, and_5_out);
  Multiplexer #(.select(1), .width(32), .disabled("Z"), .enable("false")) multiplexer_11 (
    .in0(MDin), .in1(imme), .out(multiplexer_11_out), .sel(AluSrcB));
  Shifter #(.width(32), .shift("ll")) shifter_1 (.in(imme), .\dist (5'b00010), .out(shifter_1_out));
  MIPS_ALU mips_alu_1 (
    .X(rs), .Y(multiplexer_11_out), .AluOP(AluOP), .Equal(equal), .Result(mips_alu_1_result),
    .shamt(multiplexer_12_out));  // open: Result_2
  Adder #(.width(32)) adder_2 (.a(shifter_1_out), .b({JMPAddr, PC_4}), .out(PCBranch));  // open: cin, cout
  Multiplexer #(.select(1), .width(5), .disabled("Z"), .enable("false")) multiplexer_12 (
    .in0(IR[10:6]), .in1(rs[4:0]), .out(multiplexer_12_out), .sel(comparator_7_eq));
  Comparator #(.width(6), .mode("twosComplement")) comparator_7 (
    .a(IR[5:0]), .b(6'b000111), .eq(comparator_7_eq));  // open: gt, lt
  Adder #(.width(32)) adder_3 (.a(rs), .b(imme), .out(adder_3_out));  // open: cin, cout
  Multiplexer #(.select(1), .width(32), .disabled("Z"), .enable("false")) multiplexer_13 (
    .in0(mips_alu_1_result), .in1(adder_3_out), .out(multiplexer_13_out), .sel(LBU));
  or or_6 (W1, IR1_q, d_ff_1_q);
  or or_7 (W2, IR1_2_q, d_ff_2_q);
  or or_8 (W3, IR1_3_q, d_ff_3_q);
  not not_2 (not_2_out, Halt);
  D_Flip_Flop #(.trigger("rising"), .Pre_Clr_Positions("LEGACY"), .NegatePresetClear("false"), .enable("true"), .NewFFLayout("false")) d_ff_1 (
    .clk(IR1_t), .D(1'b1), .Q(d_ff_1_q), .reset(IR1_q));  // open: Qn, preset, en
  D_Flip_Flop #(.trigger("rising"), .Pre_Clr_Positions("LEGACY"), .NegatePresetClear("false"), .enable("true"), .NewFFLayout("false")) d_ff_2 (
    .clk(IR2_t), .D(1'b1), .Q(d_ff_2_q), .reset(IR1_2_q));  // open: Qn, preset, en
  D_Flip_Flop #(.trigger("rising"), .Pre_Clr_Positions("LEGACY"), .NegatePresetClear("false"), .enable("true"), .NewFFLayout("false")) d_ff_3 (
    .clk(IR3_t), .D(1'b1), .Q(d_ff_3_q), .reset(IR1_3_q));  // open: Qn, preset, en
  RAM #(.addrWidth(10), .dataWidth(32), .bus("separate"), .Select("high")) ram_1 (
    .addr(multiplexer_13_out[11:2]), .din(MDin), .data(ram_1_data), .str(MemWrite), .sel(not_2_out), .clk(CLK));  // open: ld, clr
  Multiplexer #(.select(1), .width(32), .disabled("Z"), .enable("false")) multiplexer_14 (
    .in0(RDin), .in1({IR[15:0], {16{1'b0}}}), .out(Din), .sel(LUI));
  or or_9 (or_9_out, d_ff_1_q, IR1_q);
  or or_10 (or_10_out, d_ff_2_q, IR1_2_q);
  or or_11 (or_11_out, d_ff_3_q, IR1_3_q);
  Multiplexer #(.select(1), .width(32), .disabled("Z"), .enable("false")) multiplexer_15 (
    .in0(mips_alu_1_result), .in1(ram_1_data), .out(multiplexer_15_out), .sel(MemToReg));
  and and_7 (and_7_out, or_9_out, ~and_8_out);  // AND_Gate
  and and_8 (and_8_out, decoder_1_out1, ERET);
  and and_9 (and_9_out, or_10_out, ~and_10_out);  // AND_Gate
  and and_10 (and_10_out, decoder_1_out2, ERET);
  and and_11 (and_11_out, or_11_out, ~and_12_out);  // AND_Gate
  and and_12 (and_12_out, ERET, decoder_1_out3);
  D_Flip_Flop #(.trigger("rising"), .Pre_Clr_Positions("LEGACY"), .NegatePresetClear("false"), .enable("true"), .NewFFLayout("false")) u_IR1 (
    .clk(CLK), .D(and_7_out), .Q(IR1_q));  // open: Qn, preset, en, reset
  D_Flip_Flop #(.trigger("rising"), .Pre_Clr_Positions("LEGACY"), .NegatePresetClear("false"), .enable("true"), .NewFFLayout("false")) IR1_2 (
    .clk(CLK), .D(and_9_out), .Q(IR1_2_q));  // open: Qn, preset, en, reset
  D_Flip_Flop #(.trigger("rising"), .Pre_Clr_Positions("LEGACY"), .NegatePresetClear("false"), .enable("true"), .NewFFLayout("false")) IR1_3 (
    .clk(CLK), .D(and_11_out), .Q(IR1_3_q));  // open: Qn, preset, en, reset
  not not_3 (not_3_out, IE);
  Multiplexer #(.select(2), .width(8), .disabled("Z"), .enable("false")) multiplexer_16 (
    .in0(multiplexer_15_out[7:0]), .in1(multiplexer_15_out[15:8]), .in2(multiplexer_15_out[23:16]),
    .in3(multiplexer_15_out[31:24]), .out(multiplexer_16_out), .sel(multiplexer_13_out[1:0]));
  or or_12 (or_12_out, IR1_q, IR1_2_q, IR1_3_q);
  Register #(.width(1), .trigger("rising"), .Select("low")) u_IE (
    .D(or_12_out), .en(not_3_out), .Q(IE), .clk(CLK), .clr(ERET));
  assign bit_extender_3_out = {{24{1'b0}}, multiplexer_16_out};  // Bit_Extender bit_extender_3
  Multiplexer #(.select(1), .width(32), .disabled("Z"), .enable("false")) multiplexer_17 (
    .in0(multiplexer_19_out), .in1({JMPAddr, PC_4}), .out(RDin), .sel(JAL));
  not not_4 (not_4_out, IE);
  Priority_Encoder #(.select(2), .disabled("Z")) priority_encoder_1 (
    .in0(1'b1), .in1(IR1_q), .in2(IR1_2_q), .in3(IR1_3_q), .out(priority_encoder_1_out));  // open: gs, en_out, en_in
  Multiplexer #(.select(2), .width(32), .disabled("Z"), .enable("false")) multiplexer_18 (
    .in1(32'h364c), .in2(32'h366c), .in3(32'h368c), .out(\int ), .sel(priority_encoder_1_out));  // open: in0
  and and_13 (sig, or_12_out, ~IE);  // AND_Gate
  Multiplexer #(.select(1), .width(32), .disabled("Z"), .enable("false")) multiplexer_19 (
    .in0(multiplexer_15_out), .in1(bit_extender_3_out), .out(multiplexer_19_out), .sel(LBU));
  Register #(.width(2), .trigger("rising"), .Select("low")) register_3 (
    .D(priority_encoder_1_out), .en(not_4_out), .Q(register_3_q), .clk(CLK));  // open: clr
  Decoder #(.select(2), .tristate("false"), .disabled("Z"), .enable("false")) decoder_1 (
    .out1(decoder_1_out1), .out2(decoder_1_out2), .out3(decoder_1_out3), .sel(register_3_q));  // open: out0
  // Probe on priority_encoder_1_out

  // Other names for the same wires on the sheet: _0_15[15:0] = IR[15:0]; Func[5:0] = IR[5:0];
  //   JMPAddr[27:2] = IR[25:0]; shamt[4:0] = IR[10:6]; OP[5:0] = IR[31:26]; MF[4:0] = IR[25:21];
  //   PC_4[31:28] = JMPAddr; rt[31:0] = MDin

  // Notes on the sheet:
  //   中断源
  //   中断等待指示
  //   总复位信号应将除ROM以外所有存储组件全部清零
  //   单级中断测试信号模拟器
  //   数码管输出
  //   数码管输出应该用寄存器锁存，否则显示数据只能一闪而过
  //   指令存储器
  //   Beq
  //   JMP
  //   JR
  //   Bne
  //   OP
  //   JAL
  //   Func
  //   Syscall
  //   contents of rom_1 (hex, n*v repeats v):
  //   201d07d0 20100001 109fc0 139fc3 8021 2012000c 24160008 26100001 3210000f 20080008 20090001 139900
  //   2709825 132020 20020022 c 1094022 1500fff9 22100001 2018000f 2188024 108700 20080008 20090001 139902
  //   2709825 132021 20020022 c 1094022 1500fff9 108702 2c9b022 12c00001 8100007 4020 1084027 84400
  //   3508ffff 82021 20020022 c 8100001 afa20000 23bd0004 afa40000 23bd0004 afb00000 23bd0004 afb30000
  //   23bd0004 afb40000 23bd0004 afb50000 23bd0004 afb60000 23bd0004 20160001 20140003 20150001 168020
  //   108100 2149825 132020 20020022 c 1600fffa 295a022 1680fff7 23bdfffc 8fb60000 23bdfffc 8fb50000
  //   23bdfffc 8fb40000 23bdfffc 8fb30000 23bdfffc 8fb00000 23bdfffc 8fa40000 23bdfffc 8fa20000 42000018
  //   afa20000 23bd0004 afa40000 23bd0004 afb00000 23bd0004 afb30000 23bd0004 afb40000 23bd0004 afb50000
  //   23bd0004 afb60000 23bd0004 20160002 20140003 20150001 168020 108100 2149825 132020 20020022 c
  //   1600fffa 295a022 1680fff7 23bdfffc 8fb60000 23bdfffc 8fb50000 23bdfffc 8fb40000 23bdfffc 8fb30000
  //   23bdfffc 8fb00000 23bdfffc 8fa40000 23bdfffc 8fa20000 42000018 afa20000 23bd0004 afa40000 23bd0004
  //   afb00000 23bd0004 afb30000 23bd0004 afb40000 23bd0004 afb50000 23bd0004 afb60000 23bd0004 20160003
  //   20140003 20150001 168020 108100 2149825 132020 20020022 c 1600fffa 295a022 1680fff7 23bdfffc
  //   8fb60000 23bdfffc 8fb50000 23bdfffc 8fb40000 23bdfffc 8fb30000 23bdfffc 8fb00000 23bdfffc 8fa40000
  //   23bdfffc 8fa20000 42000018
  //   MemToReg
  //   MemWrite
  //   AluOP
  //   AluSrcB
  //   RegWrite
  //   RegDst
  //   OP
  //   Func
  //   rs
  //   指令字
  //   rt
  //   rd
  //   为方便自动评测，需要输出PC，IR，寄存器堆写如数据RDin
  //   SRAV指令
  //   RAM写使能MemWrite、RAM写入数据MDin等信号
  //   中断策略
  //   Reset 
  //   Reset 
  //   Reset 
  //   0是开
endmodule
