// Logisim project 余天越_CS1704_U201714641_cpu.circ as structural Verilog: 23 circuits, main circuit ◇单周期MIPS
module \单周期MIPS  (
  input  IR1,
  input  IR2,
  input  IR3,
  output RegWrite,
  output MemWrite,
  output [31:0] PC,
  output [31:0] IR,
  output [31:0] RDin,
  output [31:0] MDin,
  output [31:0] LedData
);

  wire and_1_out, and_2_out, and_3_out, and_4_out, and_5_out, and_6_out, CLK, comparator_1_eq,
       comparator_2_gt, Go, Halt, IR1_t, IR2_t, IR3_t, IRA, IRB, IRC, mips_alu_1_equal, nor_1_out, not_1_out,
       not_2_out, not_3_out, or_4_out, SignedExt, Syscall, W1, W2, W3, \单周期硬布线控制器_1_alu_src ,
       \单周期硬布线控制器_1_beq , \单周期硬布线控制器_1_blez , \单周期硬布线控制器_1_bne , \单周期硬布线控制器_1_jal , \单周期硬布线控制器_1_jmp ,
       \单周期硬布线控制器_1_jr , \单周期硬布线控制器_1_lh , \单周期硬布线控制器_1_lui , \单周期硬布线控制器_1_memtoreg , \单周期硬布线控制器_1_regdst ;
  wire [3:0] \单周期硬布线控制器_1_alu_op ;
  wire [4:0] multiplexer_1_out, multiplexer_3_out, multiplexer_4_out, multiplexer_5_out;
  wire [15:0] multiplexer_12_out, \总周期数 ;
  wire [31:0] adder_1_out, adder_2_out, adder_3_out, adder_4_out, bit_extender_1_out, bit_extender_2_out,
       bit_extender_3_out, bit_extender_4_out, controlled_buffer_1_out, mips_alu_1_result, multiplexer_6_out,
       multiplexer_7_out, multiplexer_8_out, multiplexer_9_out, multiplexer_10_out, multiplexer_11_out,
       multiplexer_13_out, ram_1_data, shifter_1_out, v0;

  Clock #(.highDuration(1), .lowDuration(1)) clock_1 (.out(CLK));
  Button _1 (.out(IRA));
  Button _2 (.out(IRB));
  Button _3 (.out(IRC));
  Button \u_继续运行  (.out(Go));
  LED #(.active("true")) led_1 (.in(W1));
  LED #(.active("true")) led_2 (.in(W2));
  LED #(.active("true")) led_3 (.in(W3));
  nor nor_1 (nor_1_out, or_4_out, \单周期硬布线控制器_1_jmp );
  Hex_Digit_Display hex_digit_display_1 (.value(LedData[31:28]));  // open: dp
  and and_1 (and_1_out, \单周期硬布线控制器_1_jmp , ~\单周期硬布线控制器_1_jr );  // AND_Gate
  assign controlled_buffer_1_out = and_1_out ? {PC[31:28], IR[25:0], 2'b00} : 32'bz;  // Controlled_Buffer controlled_buffer_1
  assign controlled_buffer_1_out = \单周期硬布线控制器_1_jr  ? v0 : 32'bz;  // Controlled_Buffer controlled_buffer_2
  assign controlled_buffer_1_out = or_4_out ? adder_4_out : 32'bz;  // Controlled_Buffer controlled_buffer_3
  and and_2 (and_2_out, nor_1_out, ~\单周期硬布线控制器_1_blez );  // AND_Gate
  Hex_Digit_Display hex_digit_display_2 (.value(LedData[27:24]));  // open: dp
  Hex_Digit_Display hex_digit_display_3 (.value(LedData[23:20]));  // open: dp
  Register #(.width(32), .trigger("rising"), .Select("low")) u_PC (
    .D(controlled_buffer_1_out), .en(not_1_out), .Q(PC), .clk(CLK));  // open: clr
  not not_1 (not_1_out, Halt);
  assign controlled_buffer_1_out = and_2_out ? adder_1_out : 32'bz;  // Controlled_Buffer controlled_buffer_4
  assign controlled_buffer_1_out = \单周期硬布线控制器_1_blez  ? adder_2_out : 32'bz;  // Controlled_Buffer controlled_buffer_5
  Hex_Digit_Display hex_digit_display_4 (.value(LedData[15:12]));  // open: dp
  Hex_Digit_Display hex_digit_display_5 (.value(LedData[19:16]));  // open: dp
  Comparator #(.width(32), .mode("twosComplement")) comparator_1 (
    .a(v0), .b(32'h22), .eq(comparator_1_eq));  // open: gt, lt
  Hex_Digit_Display hex_digit_display_6 (.value(LedData[7:4]));  // open: dp
  Hex_Digit_Display hex_digit_display_7 (.value(LedData[11:8]));  // open: dp
  // Probe on \总周期数 
  Register #(.width(32), .trigger("rising"), .Select("low")) register_1 (
    .D(MDin), .en(comparator_1_eq), .Q(LedData), .clk(CLK));  // open: clr
  and and_3 (and_3_out, ~comparator_1_eq, Syscall);  // AND_Gate
  Hex_Digit_Display hex_digit_display_8 (.value(LedData[3:0]));  // open: dp
  Register #(.width(1), .trigger("rising"), .Select("low")) register_2 (
    .D(and_3_out), .en(and_3_out), .Q(Halt), .clk(CLK), .clr(Go));
  ROM #(.addrWidth(10), .dataWidth(32), .Select("high")) rom_1 (.addr(PC[11:2]), .data(IR));
  Adder #(.width(32)) adder_1 (.a(PC), .b(32'h4), .out(adder_1_out));  // open: cin, cout
  Multiplexer #(.select(1), .width(5), .disabled("Z"), .enable("false")) multiplexer_1 (
    .in0(IR[20:16]), .in1(IR[15:11]), .out(multiplexer_1_out), .sel(\单周期硬布线控制器_1_regdst ));
  Multiplexer #(.select(1), .width(32), .disabled("Z"), .enable("false")) multiplexer_2 (
    .in0(adder_1_out), .in1(multiplexer_13_out), .out(RDin), .sel(not_2_out));
  or or_1 (IR1_t, IR1, IRA);
  \单周期硬布线控制器  \u_单周期硬布线控制器_1  (
    .Func(IR[5:0]), .OP(IR[31:26]), .ALU_OP(\单周期硬布线控制器_1_alu_op ), .MemToReg(\单周期硬布线控制器_1_memtoreg ),
    .MemWrite(MemWrite), .ALU_SRC(\单周期硬布线控制器_1_alu_src ), .RegWrite(RegWrite), .SysCALL(Syscall),
    .SignedExt(SignedExt), .RegDst(\单周期硬布线控制器_1_regdst ), .JR(\单周期硬布线控制器_1_jr ), .JMP(\单周期硬布线控制器_1_jmp ),
    .Beq(\单周期硬布线控制器_1_beq ), .JAL(\单周期硬布线控制器_1_jal ), .Bne(\单周期硬布线控制器_1_bne ), .BLEZ(\单周期硬布线控制器_1_blez ),
    .LUI(\单周期硬布线控制器_1_lui ), .LH(\单周期硬布线控制器_1_lh ));  // open: MF, ERET, MFC0, MTC0
  Multiplexer #(.select(1), .width(5), .disabled("Z"), .enable("false")) multiplexer_3 (
    .in0(IR[25:21]), .in1(5'b00010), .out(multiplexer_3_out), .sel(Syscall));
  Multiplexer #(.select(1), .width(5), .disabled("Z"), .enable("false")) multiplexer_4 (
    .in0(IR[20:16]), .in1(5'b00100), .out(multiplexer_4_out), .sel(Syscall));
  assign bit_extender_1_out = {{16{1'b0}}, IR[15:0]};  // Bit_Extender bit_extender_1
  not not_2 (not_2_out, \单周期硬布线控制器_1_jal );
  or or_2 (IR2_t, IR2, IRB);
  // Probe on multiplexer_5_out
  Multiplexer #(.select(1), .width(5), .disabled("Z"), .enable("false")) multiplexer_5 (
    .in0(multiplexer_1_out), .in1({5{1'b1}}), .out(multiplexer_5_out), .sel(\单周期硬布线控制器_1_jal ));
  Multiplexer #(.select(1), .width(32), .disabled("Z"), .enable("false")) multiplexer_6 (
    .in0(RDin), .in1({IR[15:0], {16{1'b0}}}), .out(multiplexer_6_out), .sel(\单周期硬布线控制器_1_lui ));
  Multiplexer #(.select(1), .width(32), .disabled("Z"), .enable("false")) multiplexer_7 (
    .in0(bit_extender_3_out), .in1({32{1'b0}}), .out(multiplexer_7_out), .sel(comparator_2_gt));
  assign bit_extender_2_out = {{16{IR[15]}}, IR[15:0]};  // Bit_Extender bit_extender_2
  assign bit_extender_3_out = {{14{IR[15]}}, {IR[15:0], 2'b00}};  // Bit_Extender bit_extender_3
  Adder #(.width(32)) adder_2 (.a(multiplexer_7_out), .b(adder_1_out), .out(adder_2_out));  // open: cin, cout
  or or_3 (IR3_t, IR3, IRC);
  or or_4 (or_4_out, and_5_out, and_4_out);
  MIPS_Regifile mips_regifile_1 (
    .Din(multiplexer_6_out), .Clk(CLK), .R1(v0), .R2(MDin), .WE(RegWrite), .W_num(multiplexer_5_out),
    .R1_num(multiplexer_3_out), .R2_num(multiplexer_4_out));
  Multiplexer #(.select(1), .width(32), .disabled("Z"), .enable("false")) multiplexer_8 (
    .in0(bit_extender_1_out), .in1(bit_extender_2_out), .out(multiplexer_8_out), .sel(SignedExt));
  and and_4 (and_4_out, mips_alu_1_equal, \单周期硬布线控制器_1_beq );
  Multiplexer #(.select(1), .width(32), .disabled("Z"), .enable("false")) multiplexer_9 (
    .in0(MDin), .in1(multiplexer_8_out), .out(multiplexer_9_out), .sel(\单周期硬布线控制器_1_alu_src ));
  Shifter #(.width(32), .shift("ll")) shifter_1 (.in(multiplexer_8_out), .\dist (5'b00010), .out(shifter_1_out));
  and and_5 (and_5_out, ~mips_alu_1_equal, \单周期硬布线控制器_1_bne );  // AND_Gate
  MIPS_ALU mips_alu_1 (
    .X(v0), .Y(multiplexer_9_out), .AluOP(\单周期硬布线控制器_1_alu_op ), .Equal(mips_alu_1_equal),
    .Result(mips_alu_1_result), .shamt(IR[10:6]));  // open: Result_2
  Multiplexer #(.select(1), .width(32), .disabled("Z"), .enable("false")) multiplexer_10 (
    .in0(mips_alu_1_result), .in1(adder_3_out), .out(multiplexer_10_out), .sel(\单周期硬布线控制器_1_lh ));
  Adder #(.width(32)) adder_3 (.a(v0), .b(multiplexer_8_out), .out(adder_3_out));  // open: cin, cout
  Adder #(.width(32)) adder_4 (.a(shifter_1_out), .b(adder_1_out), .out(adder_4_out));  // open: cin, cout
  Comparator #(.width(32), .mode("twosComplement")) comparator_2 (
    .a(v0), .b({32{1'b0}}), .gt(comparator_2_gt));  // open: eq, lt
  not not_3 (not_3_out, Halt);
  Counter #(.width(16), .max('hffff), .ongoal("wrap"), .trigger("rising"), .behavior("old")) counter_1 (
    .Q(\总周期数 ), .clk(and_6_out));  // open: load, D, count, carry, clr, preset
  and and_6 (and_6_out, ~Halt, CLK);  // AND_Gate
  RAM #(.addrWidth(10), .dataWidth(32), .bus("separate"), .Select("high")) ram_1 (
    .addr(multiplexer_10_out[11:2]), .din(MDin), .data(ram_1_data), .str(MemWrite), .sel(not_3_out), .clk(CLK));  // open: ld, clr
  Multiplexer #(.select(1), .width(32), .disabled("Z"), .enable("false")) multiplexer_11 (
    .in0(mips_alu_1_result), .in1(ram_1_data), .out(multiplexer_11_out), .sel(\单周期硬布线控制器_1_memtoreg ));
  Multiplexer #(.select(1), .width(16), .disabled("Z"), .enable("false")) multiplexer_12 (
    .in0(multiplexer_11_out[15:0]), .in1(multiplexer_11_out[31:16]), .out(multiplexer_12_out),
    .sel(multiplexer_10_out[3]));
  Multiplexer #(.select(1), .width(32), .disabled("Z"), .enable("false")) multiplexer_13 (
    .in0(multiplexer_11_out), .in1(bit_extender_4_out), .out(multiplexer_13_out), .sel(\单周期硬布线控制器_1_lh ));
  assign bit_extender_4_out = {{16{multiplexer_12_out[15]}}, multiplexer_12_out};  // Bit_Extender bit_extender_4

  // Other names for the same wires on the sheet: a0[31:0] = MDin

  // Notes on the sheet:
  //   中断源
  //   中断等待指示
  //   总复位信号应将除ROM以外所有存储组件全部清零
  //   JAL/J
  //   JR
  //   Branch
  //   next
  //   blez
  //   中断策略
  //   将立即数左移两位得到28位和当前指令的高4位组成跳转地址
  //   数码管输出
  //   数码管输出应该用寄存器锁存，否则显示数据只能一闪而过
  //   指令存储器
  //   指令字
  //   contents of rom_1 (hex, n*v repeats v):
  //   20110001 8000c05 20110001 20120002 20130003 8000c09 20110001 20120002 20130003 8000c0d 20110001
  //   20120002 20130003 8000c11 20110001 20120002 20130003 c000cb8 20100001 20110001 118fc0 112020
  //   20020022 c 118882 12200001 8000c15 112020 20020022 c 20110001 118880 112020 20020022 c 12200001
  //   8000c1f 20110001 118fc0 112020 20020022 c 1188c3 112020 20020022 c 118903 112020 20020022 c 118903
  //   112020 20020022 c 118903 112020 20020022 c 118903 112020 20020022 c 118903 112020 20020022 c 118903
  //   112020 20020022 c 118903 112020 20020022 c 20100001 109fc0 139fc3 8021 2012000c 24160003 26100001
  //   3210000f 20080008 20090001 139900 2709825 132020 20020022 c 1094022 1500fff9 22100001 2018000f
  //   2188024 108700 20080008 20090001 139902 2709825 132021 20020022 c 1094022 1500fff9 108702 2c9b022
  //   12c00001 8000c50 4020 1084027 84400 3508ffff 82021 20020022 c 2010ffff 20110000 ae300000 22100001
  //   22310004 ae300000 22100001 22310004 ae300000 22100001 22310004 ae300000 22100001 22310004 ae300000
  //   22100001 22310004 ae300000 22100001 22310004 ae300000 22100001 22310004 ae300000 22100001 22310004
  //   ae300000 22100001 22310004 ae300000 22100001 22310004 ae300000 22100001 22310004 ae300000 22100001
  //   22310004 ae300000 22100001 22310004 ae300000 22100001 22310004 ae300000 22100001 22310004 ae300000
  //   22100001 22310004 22100001 8020 2011003c 8e130000 8e340000 274402a 11000002 ae330000 ae140000
  //   2231fffc 1611fff8 102020 20020022 c 22100004 2011003c 1611fff2 2002000a c 20100000 22100001 102020
  //   20020022 c 22100002 102020 20020022 c 22100003 102020 20020022 c 22100004 102020 20020022 c 22100005
  //   102020 20020022 c 22100006 102020 20020022 c 22100007 102020 20020022 c 22100008 102020 20020022
  //   20020022 c 3e00008
  //   LH
  //   BLEZ
  //   JMP
  //   JR
  //   OP
  //   Func
  //   Syscall
  //   rs
  //   rt
  //   rd
  //   立即数
  //   Beq
  //   LUI
  //   Bne
  //   MemToReg
  //   MemWrite
  //   AluOP
  //   AluSrcB
  //   RegWrite
  //   JAL
  //   RegDst
  //   PC+4
  //   为方便自动评测，需要输出PC，IR，寄存器堆写如数据RDin
  //   RAM写使能MemWrite、RAM写入数据MDin等信号
endmodule

// 单周期硬布线控制器
module \单周期硬布线控制器  (
  input  [5:0] OP,
  input  [5:0] Func,
  input  [4:0] MF,
  output [3:0] ALU_OP,
  output MemToReg,
  output MemWrite,
  output ALU_SRC,
  output RegWrite,
  output SysCALL,
  output SignedExt,
  output RegDst,
  output Beq,
  output Bne,
  output JR,
  output JMP,
  output JAL,
  output ERET,
  output MFC0,
  output MTC0,
  output LUI,
  output LH,
  output BLEZ
);

  \运算控制器自动生成  \u_运算控制器自动生成_1  (
    .OP0(OP[0]), .OP1(OP[1]), .OP2(OP[2]), .OP3(OP[3]), .OP4(OP[4]), .OP5(OP[5]), .F0(Func[0]), .F1(Func[1]),
    .F2(Func[2]), .F3(Func[3]), .F4(Func[4]), .F5(Func[5]), .S0(ALU_OP[0]), .S1(ALU_OP[1]), .S2(ALU_OP[2]),
    .S3(ALU_OP[3]));
  \控制信号自动生成  \u_控制信号自动生成_1  (
    .OP0(OP[0]), .OP1(OP[1]), .OP2(OP[2]), .OP3(OP[3]), .OP4(OP[4]), .OP5(OP[5]), .F0(Func[0]), .F1(Func[1]),
    .F2(Func[2]), .F3(Func[3]), .F4(Func[4]), .F5(Func[5]), .MemToReg(MemToReg), .MemWrite(MemWrite),
    .ALU_SRC(ALU_SRC), .RegWrite(RegWrite), .SysCALL(SysCALL), .SignedExt(SignedExt), .RegDst(RegDst),
    .BEQ(Beq), .BNE(Bne), .JR(JR), .JUMP(JMP), .JAL(JAL), .MF4(MF[4]), .MF3(MF[3]), .MF2(MF[2]), .MF1(MF[1]),
    .MF0(MF[0]), .ERET(ERET), .MFC0(MFC0), .MTC0(MTC0));
  \控制器生成_1  \u_控制器生成_1_1  (
    .OP0(OP[0]), .OP1(OP[1]), .OP2(OP[2]), .OP3(OP[3]), .OP4(OP[4]), .OP5(OP[5]), .LUI(LUI), .LH(LH),
    .BLEZ(BLEZ));

  // Other names for the same wires on the sheet: OP_CODE[5:0] = OP

  // Notes on the sheet:
  //   运算器控制器，根据指令生成运算器功能选择信号
endmodule

// 运算器控制器
module \运算控制器自动生成  (
  input  OP0,
  input  OP1,
  input  OP2,
  input  OP3,
  input  OP4,
  input  OP5,
  input  F0,
  input  F1,
  input  F2,
  input  F3,
  input  F4,
  input  F5,
  output S0,
  output S1,
  output S2,
  output S3
);

  wire and_1_out, and_2_out, and_3_out, and_4_out, and_5_out, and_6_out, and_7_out, and_8_out, and_9_out,
       and_10_out, and_11_out, and_12_out, and_13_out, and_14_out, and_15_out, and_16_out, and_17_out,
       and_18_out, and_19_out, and_20_out, and_21_out, and_22_out, and_23_out, and_24_out, and_25_out,
       and_26_out, and_27_out, and_28_out, and_29_out, and_30_out, and_31_out, and_32_out, and_33_out,
       and_34_out, and_35_out, and_36_out, not_1_out, not_2_out, not_3_out, not_4_out, not_5_out, not_6_out,
       not_7_out, not_8_out, not_9_out, not_10_out, not_11_out, not_12_out, not_13_out, not_14_out,
       not_15_out, not_16_out, not_17_out, not_18_out, not_19_out, not_20_out, not_21_out, not_22_out,
       not_23_out, not_24_out, not_25_out, not_26_out, not_27_out, not_28_out, not_29_out, not_30_out,
       not_31_out, not_32_out, not_33_out, not_34_out, not_35_out, not_36_out, not_37_out, not_38_out,
       not_39_out, not_40_out, not_41_out, not_42_out, not_43_out, not_44_out, not_45_out, not_46_out,
       not_47_out, not_48_out, not_49_out, not_50_out, not_51_out, not_52_out, not_53_out, not_54_out,
       not_55_out, not_56_out, not_57_out, not_58_out, not_59_out, not_60_out, not_61_out, not_62_out,
       not_63_out, not_64_out, not_65_out, not_66_out, not_67_out, not_68_out, not_69_out, not_70_out,
       not_71_out, not_72_out, not_73_out, not_74_out, not_75_out, not_76_out, not_77_out, not_78_out,
       not_79_out, not_80_out, not_81_out, not_82_out, not_83_out, not_84_out, not_85_out, not_86_out,
       not_87_out, not_88_out, not_89_out, not_90_out, not_91_out, not_92_out, not_93_out, not_94_out,
       not_95_out, not_96_out, not_97_out, not_98_out, not_99_out, not_100_out, not_101_out, not_102_out,
       not_103_out, not_104_out, not_105_out, not_106_out, not_107_out, not_108_out, not_109_out,
       not_110_out, not_111_out, not_112_out, not_113_out, not_114_out, not_115_out, not_116_out,
       not_117_out, not_118_out, not_119_out, not_120_out, not_121_out, not_122_out, not_123_out,
       not_124_out, not_125_out, not_126_out, not_127_out, not_128_out, not_129_out, not_130_out,
       not_131_out, not_132_out, not_133_out, not_134_out, not_135_out, not_136_out, not_137_out,
       not_138_out, not_139_out, not_140_out, not_141_out, not_142_out, not_143_out, not_144_out,
       not_145_out, not_146_out, not_147_out, not_148_out, not_149_out, not_150_out, not_151_out,
       not_152_out, not_153_out, not_154_out, not_155_out, not_156_out, not_157_out, not_158_out,
       not_159_out, not_160_out, not_161_out, not_162_out, not_163_out, not_164_out, not_165_out,
       not_166_out, not_167_out, not_168_out, not_169_out, not_170_out, not_171_out, not_172_out,
       not_173_out, not_174_out, not_175_out, not_176_out, not_177_out, not_178_out, not_179_out,
       not_180_out, not_181_out, not_182_out, not_183_out, not_184_out, not_185_out, not_186_out,
       not_187_out, not_188_out, not_189_out, not_190_out, not_191_out, not_192_out, not_193_out,
       not_194_out, not_195_out, not_196_out, not_197_out, not_198_out, not_199_out, not_200_out,
       not_201_out, not_202_out, not_203_out, not_204_out, not_205_out, not_206_out, not_207_out,
       not_208_out, not_209_out, not_210_out, not_211_out, not_212_out, not_213_out, not_214_out,
       not_215_out, not_216_out, not_217_out, not_218_out, not_219_out, not_220_out, not_221_out,
       not_222_out, not_223_out, not_224_out, not_225_out, not_226_out, not_227_out, not_228_out,
       not_229_out, not_230_out, not_231_out, not_232_out, not_233_out, not_234_out, not_235_out,
       not_236_out, not_237_out, not_238_out, not_239_out, not_240_out, not_241_out, not_242_out,
       not_243_out, not_244_out, not_245_out, not_246_out, not_247_out, not_248_out, not_249_out,
       not_250_out, not_251_out, not_252_out, not_253_out, not_254_out;

  not not_1 (not_1_out, OP5);
  not not_2 (not_2_out, OP4);
  not not_3 (not_3_out, OP3);
  not not_4 (not_4_out, OP2);
  not not_5 (not_5_out, OP1);
  not not_6 (not_6_out, OP0);
  not not_7 (not_7_out, F5);
  not not_8 (not_8_out, F4);
  not not_9 (not_9_out, F3);
  not not_10 (not_10_out, F2);
  not not_11 (not_11_out, OP5);
  not not_12 (not_12_out, OP4);
  not not_13 (not_13_out, OP3);
  not not_14 (not_14_out, OP2);
  not not_15 (not_15_out, OP1);
  not not_16 (not_16_out, OP0);
  not not_17 (not_17_out, F4);
  not not_18 (not_18_out, F3);
  not not_19 (not_19_out, F2);
  not not_20 (not_20_out, F1);
  not not_21 (not_21_out, F0);
  not not_22 (not_22_out, OP5);
  not not_23 (not_23_out, OP4);
  not not_24 (not_24_out, OP3);
  not not_25 (not_25_out, OP2);
  not not_26 (not_26_out, OP1);
  not not_27 (not_27_out, OP0);
  not not_28 (not_28_out, F4);
  not not_29 (not_29_out, F3);
  not not_30 (not_30_out, F2);
  not not_31 (not_31_out, F1);
  not not_32 (not_32_out, OP5);
  not not_33 (not_33_out, OP4);
  not not_34 (not_34_out, OP3);
  not not_35 (not_35_out, OP2);
  not not_36 (not_36_out, OP1);
  not not_37 (not_37_out, OP0);
  not not_38 (not_38_out, F4);
  not not_39 (not_39_out, F3);
  not not_40 (not_40_out, F1);
  not not_41 (not_41_out, F0);
  not not_42 (not_42_out, OP5);
  not not_43 (not_43_out, OP4);
  not not_44 (not_44_out, OP3);
  not not_45 (not_45_out, OP2);
  not not_46 (not_46_out, OP1);
  not not_47 (not_47_out, OP0);
  not not_48 (not_48_out, F4);
  not not_49 (not_49_out, F2);
  not not_50 (not_50_out, F0);
  not not_51 (not_51_out, OP5);
  not not_52 (not_52_out, OP4);
  not not_53 (not_53_out, OP2);
  not not_54 (not_54_out, OP1);
  not not_55 (not_55_out, OP0);
  not not_56 (not_56_out, OP5);
  not not_57 (not_57_out, OP4);
  not not_58 (not_58_out, OP1);
  not not_59 (not_59_out, OP0);
  not not_60 (not_60_out, OP5);
  not not_61 (not_61_out, OP4);
  not not_62 (not_62_out, OP2);
  not not_63 (not_63_out, OP1);
  not not_64 (not_64_out, OP5);
  not not_65 (not_65_out, OP4);
  not not_66 (not_66_out, OP2);
  not not_67 (not_67_out, OP0);
  not not_68 (not_68_out, OP4);
  not not_69 (not_69_out, OP3);
  not not_70 (not_70_out, OP2);
  not not_71 (not_71_out, OP4);
  not not_72 (not_72_out, OP2);
  not not_73 (not_73_out, OP5);
  not not_74 (not_74_out, OP4);
  not not_75 (not_75_out, OP3);
  not not_76 (not_76_out, OP2);
  not not_77 (not_77_out, OP1);
  not not_78 (not_78_out, OP0);
  not not_79 (not_79_out, F5);
  not not_80 (not_80_out, F4);
  not not_81 (not_81_out, F3);
  not not_82 (not_82_out, F2);
  not not_83 (not_83_out, F0);
  not not_84 (not_84_out, OP5);
  not not_85 (not_85_out, OP4);
  not not_86 (not_86_out, OP3);
  not not_87 (not_87_out, OP2);
  not not_88 (not_88_out, OP1);
  not not_89 (not_89_out, OP0);
  not not_90 (not_90_out, F4);
  not not_91 (not_91_out, F3);
  not not_92 (not_92_out, F2);
  not not_93 (not_93_out, F0);
  not not_94 (not_94_out, OP5);
  not not_95 (not_95_out, OP4);
  not not_96 (not_96_out, OP3);
  not not_97 (not_97_out, OP2);
  not not_98 (not_98_out, OP1);
  not not_99 (not_99_out, OP0);
  not not_100 (not_100_out, F4);
  not not_101 (not_101_out, F3);
  not not_102 (not_102_out, F1);
  not not_103 (not_103_out, F0);
  not not_104 (not_104_out, OP5);
  not not_105 (not_105_out, OP4);
  not not_106 (not_106_out, OP3);
  not not_107 (not_107_out, OP2);
  not not_108 (not_108_out, OP1);
  not not_109 (not_109_out, OP0);
  not not_110 (not_110_out, F4);
  not not_111 (not_111_out, F3);
  not not_112 (not_112_out, OP5);
  not not_113 (not_113_out, OP4);
  not not_114 (not_114_out, OP3);
  not not_115 (not_115_out, OP2);
  not not_116 (not_116_out, OP1);
  not not_117 (not_117_out, OP0);
  not not_118 (not_118_out, F4);
  not not_119 (not_119_out, F2);
  not not_120 (not_120_out, F0);
  not not_121 (not_121_out, OP5);
  not not_122 (not_122_out, OP4);
  not not_123 (not_123_out, OP1);
  not not_124 (not_124_out, OP0);
  not not_125 (not_125_out, OP5);
  not not_126 (not_126_out, OP4);
  not not_127 (not_127_out, OP2);
  not not_128 (not_128_out, OP0);
  not not_129 (not_129_out, OP5);
  not not_130 (not_130_out, OP4);
  not not_131 (not_131_out, OP3);
  not not_132 (not_132_out, OP2);
  not not_133 (not_133_out, OP1);
  not not_134 (not_134_out, OP0);
  not not_135 (not_135_out, F4);
  not not_136 (not_136_out, F3);
  not not_137 (not_137_out, F2);
  not not_138 (not_138_out, OP5);
  not not_139 (not_139_out, OP4);
  not not_140 (not_140_out, OP3);
  not not_141 (not_141_out, OP2);
  not not_142 (not_142_out, OP1);
  not not_143 (not_143_out, OP0);
  not not_144 (not_144_out, F4);
  not not_145 (not_145_out, F3);
  not not_146 (not_146_out, F2);
  not not_147 (not_147_out, F1);
  not not_148 (not_148_out, F0);
  not not_149 (not_149_out, OP5);
  not not_150 (not_150_out, OP4);
  not not_151 (not_151_out, OP3);
  not not_152 (not_152_out, OP2);
  not not_153 (not_153_out, OP1);
  not not_154 (not_154_out, OP0);
  not not_155 (not_155_out, F4);
  not not_156 (not_156_out, F3);
  not not_157 (not_157_out, F2);
  not not_158 (not_158_out, F1);
  not not_159 (not_159_out, OP5);
  not not_160 (not_160_out, OP4);
  not not_161 (not_161_out, OP3);
  not not_162 (not_162_out, OP2);
  not not_163 (not_163_out, OP1);
  not not_164 (not_164_out, OP0);
  not not_165 (not_165_out, F4);
  not not_166 (not_166_out, F3);
  not not_167 (not_167_out, F2);
  not not_168 (not_168_out, F0);
  not not_169 (not_169_out, OP5);
  not not_170 (not_170_out, OP4);
  not not_171 (not_171_out, OP3);
  not not_172 (not_172_out, OP2);
  not not_173 (not_173_out, OP1);
  not not_174 (not_174_out, OP0);
  not not_175 (not_175_out, F4);
  not not_176 (not_176_out, F3);
  not not_177 (not_177_out, F1);
  not not_178 (not_178_out, F0);
  not not_179 (not_179_out, OP5);
  not not_180 (not_180_out, OP4);
  not not_181 (not_181_out, OP3);
  not not_182 (not_182_out, OP2);
  not not_183 (not_183_out, OP1);
  not not_184 (not_184_out, OP0);
  not not_185 (not_185_out, F4);
  not not_186 (not_186_out, F2);
  not not_187 (not_187_out, OP5);
  not not_188 (not_188_out, OP4);
  not not_189 (not_189_out, OP2);
  not not_190 (not_190_out, OP1);
  not not_191 (not_191_out, OP0);
  not not_192 (not_192_out, OP5);
  not not_193 (not_193_out, OP4);
  not not_194 (not_194_out, OP1);
  not not_195 (not_195_out, OP0);
  not not_196 (not_196_out, OP5);
  not not_197 (not_197_out, OP4);
  not not_198 (not_198_out, OP2);
  not not_199 (not_199_out, OP1);
  not not_200 (not_200_out, OP4);
  not not_201 (not_201_out, OP3);
  not not_202 (not_202_out, OP2);
  not not_203 (not_203_out, OP4);
  not not_204 (not_204_out, OP2);
  not not_205 (not_205_out, OP5);
  not not_206 (not_206_out, OP4);
  not not_207 (not_207_out, OP3);
  not not_208 (not_208_out, OP2);
  not not_209 (not_209_out, OP1);
  not not_210 (not_210_out, OP0);
  not not_211 (not_211_out, F4);
  not not_212 (not_212_out, F3);
  not not_213 (not_213_out, F2);
  not not_214 (not_214_out, OP5);
  not not_215 (not_215_out, OP4);
  not not_216 (not_216_out, OP3);
  not not_217 (not_217_out, OP2);
  not not_218 (not_218_out, OP1);
  not not_219 (not_219_out, OP0);
  not not_220 (not_220_out, F4);
  not not_221 (not_221_out, F3);
  not not_222 (not_222_out, F1);
  not not_223 (not_223_out, OP5);
  not not_224 (not_224_out, OP4);
  not not_225 (not_225_out, OP3);
  not not_226 (not_226_out, OP2);
  not not_227 (not_227_out, OP1);
  not not_228 (not_228_out, OP0);
  not not_229 (not_229_out, F4);
  not not_230 (not_230_out, F3);
  not not_231 (not_231_out, OP5);
  not not_232 (not_232_out, OP4);
  not not_233 (not_233_out, OP3);
  not not_234 (not_234_out, OP2);
  not not_235 (not_235_out, OP1);
  not not_236 (not_236_out, OP0);
  not not_237 (not_237_out, F4);
  not not_238 (not_238_out, F2);
  not not_239 (not_239_out, F0);
  not not_240 (not_240_out, OP5);
  not not_241 (not_241_out, OP4);
  not not_242 (not_242_out, OP3);
  not not_243 (not_243_out, OP2);
  not not_244 (not_244_out, OP1);
  not not_245 (not_245_out, OP0);
  not not_246 (not_246_out, F4);
  not not_247 (not_247_out, F2);
  not not_248 (not_248_out, OP5);
  not not_249 (not_249_out, OP4);
  not not_250 (not_250_out, OP2);
  not not_251 (not_251_out, OP0);
  not not_252 (not_252_out, OP5);
  not not_253 (not_253_out, OP4);
  not not_254 (not_254_out, OP1);
  and and_1 (and_1_out, not_1_out, not_2_out, not_3_out, not_4_out, not_5_out, not_6_out, not_7_out, not_8_out, not_9_out, not_10_out, F1, F0);
  and and_2 (and_2_out, not_11_out, not_12_out, not_13_out, not_14_out, not_15_out, not_16_out, F5, not_17_out, not_18_out, not_19_out, not_20_out, not_21_out);
  and and_3 (and_3_out, not_22_out, not_23_out, not_24_out, not_25_out, not_26_out, not_27_out, F5, not_28_out, not_29_out, not_30_out, not_31_out, F0);
  and and_4 (and_4_out, not_32_out, not_33_out, not_34_out, not_35_out, not_36_out, not_37_out, F5, not_38_out, not_39_out, F2, not_40_out, not_41_out);
  and and_5 (and_5_out, not_42_out, not_43_out, not_44_out, not_45_out, not_46_out, not_47_out, F5, not_48_out, F3, not_49_out, F1, not_50_out);
  and and_6 (and_6_out, not_51_out, not_52_out, OP3, not_53_out, not_54_out, not_55_out);
  and and_7 (and_7_out, not_56_out, not_57_out, OP3, OP2, not_58_out, not_59_out);
  and and_8 (and_8_out, not_60_out, not_61_out, OP3, not_62_out, not_63_out, OP0);
  and and_9 (and_9_out, not_64_out, not_65_out, OP3, not_66_out, OP1, not_67_out);
  and and_10 (and_10_out, OP5, not_68_out, not_69_out, not_70_out, OP1, OP0);
  and and_11 (and_11_out, OP5, not_71_out, OP3, not_72_out, OP1, OP0);
  and and_12 (and_12_out, not_73_out, not_74_out, not_75_out, not_76_out, not_77_out, not_78_out, not_79_out, not_80_out, not_81_out, not_82_out, F1, not_83_out);
  and and_13 (and_13_out, not_84_out, not_85_out, not_86_out, not_87_out, not_88_out, not_89_out, F5, not_90_out, not_91_out, not_92_out, F1, not_93_out);
  and and_14 (and_14_out, not_94_out, not_95_out, not_96_out, not_97_out, not_98_out, not_99_out, F5, not_100_out, not_101_out, F2, not_102_out, not_103_out);
  and and_15 (and_15_out, not_104_out, not_105_out, not_106_out, not_107_out, not_108_out, not_109_out, F5, not_110_out, not_111_out, F2, F1, F0);
  and and_16 (and_16_out, not_112_out, not_113_out, not_114_out, not_115_out, not_116_out, not_117_out, F5, not_118_out, F3, not_119_out, F1, not_120_out);
  and and_17 (and_17_out, not_121_out, not_122_out, OP3, OP2, not_123_out, not_124_out);
  and and_18 (and_18_out, not_125_out, not_126_out, OP3, not_127_out, OP1, not_128_out);
  and and_19 (and_19_out, not_129_out, not_130_out, not_131_out, not_132_out, not_133_out, not_134_out, F5, not_135_out, not_136_out, not_137_out, F1, F0);
  and and_20 (and_20_out, not_138_out, not_139_out, not_140_out, not_141_out, not_142_out, not_143_out, F5, not_144_out, not_145_out, not_146_out, not_147_out, not_148_out);
  and and_21 (and_21_out, not_149_out, not_150_out, not_151_out, not_152_out, not_153_out, not_154_out, F5, not_155_out, not_156_out, not_157_out, not_158_out, F0);
  and and_22 (and_22_out, not_159_out, not_160_out, not_161_out, not_162_out, not_163_out, not_164_out, F5, not_165_out, not_166_out, not_167_out, F1, not_168_out);
  and and_23 (and_23_out, not_169_out, not_170_out, not_171_out, not_172_out, not_173_out, not_174_out, F5, not_175_out, not_176_out, F2, not_177_out, not_178_out);
  and and_24 (and_24_out, not_179_out, not_180_out, not_181_out, not_182_out, not_183_out, not_184_out, F5, not_185_out, F3, not_186_out, F1, F0);
  and and_25 (and_25_out, not_187_out, not_188_out, OP3, not_189_out, not_190_out, not_191_out);
  and and_26 (and_26_out, not_192_out, not_193_out, OP3, OP2, not_194_out, not_195_out);
  and and_27 (and_27_out, not_196_out, not_197_out, OP3, not_198_out, not_199_out, OP0);
  and and_28 (and_28_out, OP5, not_200_out, not_201_out, not_202_out, OP1, OP0);
  and and_29 (and_29_out, OP5, not_203_out, OP3, not_204_out, OP1, OP0);
  and and_30 (and_30_out, not_205_out, not_206_out, not_207_out, not_208_out, not_209_out, not_210_out, F5, not_211_out, not_212_out, not_213_out, F1, F0);
  and and_31 (and_31_out, not_214_out, not_215_out, not_216_out, not_217_out, not_218_out, not_219_out, F5, not_220_out, not_221_out, F2, not_222_out, F0);
  and and_32 (and_32_out, not_223_out, not_224_out, not_225_out, not_226_out, not_227_out, not_228_out, F5, not_229_out, not_230_out, F2, F1, F0);
  and and_33 (and_33_out, not_231_out, not_232_out, not_233_out, not_234_out, not_235_out, not_236_out, F5, not_237_out, F3, not_238_out, F1, not_239_out);
  and and_34 (and_34_out, not_240_out, not_241_out, not_242_out, not_243_out, not_244_out, not_245_out, F5, not_246_out, F3, not_247_out, F1, F0);
  and and_35 (and_35_out, not_248_out, not_249_out, OP3, not_250_out, OP1, not_251_out);
  and and_36 (and_36_out, not_252_out, not_253_out, OP3, OP2, not_254_out, OP0);
  or or_1 (S0, and_1_out, and_2_out, and_3_out, and_4_out, and_5_out, and_6_out, and_7_out, and_8_out, and_9_out, and_10_out, and_11_out);
  or or_2 (S1, and_12_out, and_13_out, and_14_out, and_15_out, and_16_out, and_17_out, and_18_out, and_19_out);
  or or_3 (S2, and_20_out, and_21_out, and_22_out, and_23_out, and_24_out, and_25_out, and_26_out, and_27_out, and_28_out, and_29_out, and_30_out);
  or or_4 (S3, and_31_out, and_32_out, and_33_out, and_34_out, and_35_out, and_36_out);
endmodule

// 控制信号生成
module \控制信号自动生成  (
  input  OP0,
  input  OP1,
  input  OP2,
  input  OP3,
  input  OP4,
  input  OP5,
  input  F0,
  input  F1,
  input  F2,
  input  F3,
  input  F4,
  input  F5,
  input  MF4,
  input  MF3,
  input  MF2,
  input  MF1,
  input  MF0,
  output MemToReg,
  output MemWrite,
  output ALU_SRC,
  output RegWrite,
  output SysCALL,
  output SignedExt,
  output RegDst,
  output BEQ,
  output BNE,
  output JR,
  output JUMP,
  output JAL,
  output ERET,
  output MFC0,
  output MTC0
);

  wire and_1_out, and_2_out, and_4_out, and_5_out, and_6_out, and_7_out, and_8_out, and_9_out, and_10_out,
       and_11_out, and_12_out, and_13_out, and_14_out, and_15_out, and_16_out, and_17_out, and_18_out,
       and_19_out, and_20_out, and_21_out, and_22_out, and_23_out, and_24_out, and_25_out, and_26_out,
       and_27_out, and_28_out, and_29_out, and_30_out, and_31_out, and_33_out, and_34_out, and_35_out,
       and_36_out, and_37_out, and_38_out, and_39_out, and_40_out, and_41_out, and_42_out, and_43_out,
       and_44_out, and_45_out, and_46_out, and_47_out, and_48_out, and_49_out, and_50_out, and_51_out,
       and_52_out, and_56_out, and_57_out, and_58_out, not_1_out, not_2_out, not_3_out, not_4_out, not_5_out,
       not_6_out, not_7_out, not_8_out, not_9_out, not_10_out, not_11_out, not_12_out, not_13_out,
       not_14_out, not_15_out, not_16_out, not_17_out, not_18_out, not_19_out, not_20_out, not_21_out,
       not_22_out, not_23_out, not_24_out, not_25_out, not_26_out, not_27_out, not_28_out, not_29_out,
       not_30_out, not_31_out, not_32_out, not_33_out, not_34_out, not_35_out, not_36_out, not_37_out,
       not_38_out, not_39_out, not_40_out, not_41_out, not_42_out, not_43_out, not_44_out, not_45_out,
       not_46_out, not_47_out, not_48_out, not_49_out, not_50_out, not_51_out, not_52_out, not_53_out,
       not_54_out, not_55_out, not_56_out, not_57_out, not_58_out, not_59_out, not_60_out, not_61_out,
       not_62_out, not_63_out, not_64_out, not_65_out, not_66_out, not_67_out, not_68_out, not_69_out,
       not_70_out, not_71_out, not_72_out, not_73_out, not_74_out, not_75_out, not_76_out, not_77_out,
       not_78_out, not_79_out, not_80_out, not_81_out, not_82_out, not_83_out, not_84_out, not_85_out,
       not_86_out, not_87_out, not_88_out, not_89_out, not_90_out, not_91_out, not_92_out, not_93_out,
       not_94_out, not_95_out, not_96_out, not_97_out, not_98_out, not_99_out, not_100_out, not_101_out,
       not_102_out, not_103_out, not_104_out, not_105_out, not_106_out, not_107_out, not_108_out,
       not_109_out, not_110_out, not_111_out, not_112_out, not_113_out, not_114_out, not_115_out,
       not_116_out, not_117_out, not_118_out, not_119_out, not_120_out, not_121_out, not_122_out,
       not_123_out, not_124_out, not_125_out, not_126_out, not_127_out, not_128_out, not_129_out,
       not_130_out, not_131_out, not_132_out, not_133_out, not_134_out, not_135_out, not_136_out,
       not_137_out, not_138_out, not_139_out, not_140_out, not_141_out, not_142_out, not_143_out,
       not_144_out, not_145_out, not_146_out, not_147_out, not_148_out, not_149_out, not_150_out,
       not_151_out, not_152_out, not_153_out, not_154_out, not_155_out, not_156_out, not_157_out,
       not_158_out, not_159_out, not_160_out, not_161_out, not_162_out, not_163_out, not_164_out,
       not_165_out, not_166_out, not_167_out, not_168_out, not_169_out, not_170_out, not_171_out,
       not_172_out, not_173_out, not_174_out, not_175_out, not_176_out, not_177_out, not_178_out,
       not_179_out, not_180_out, not_181_out, not_182_out, not_183_out, not_184_out, not_185_out,
       not_186_out, not_187_out, not_188_out, not_189_out, not_190_out, not_191_out, not_192_out,
       not_193_out, not_194_out, not_195_out, not_196_out, not_197_out, not_198_out, not_199_out,
       not_200_out, not_201_out, not_202_out, not_203_out, not_204_out, not_205_out, not_206_out,
       not_207_out, not_208_out, not_209_out, not_210_out, not_211_out, not_212_out, not_213_out,
       not_214_out, not_215_out, not_216_out, not_217_out, not_218_out, not_219_out, not_220_out,
       not_221_out, not_222_out, not_223_out, not_224_out, not_225_out, not_226_out, not_227_out,
       not_228_out, not_229_out, not_230_out, not_231_out, not_232_out, not_233_out, not_234_out,
       not_235_out, not_236_out, not_237_out, not_238_out, not_239_out, not_240_out, not_241_out,
       not_242_out, not_243_out, not_244_out, not_245_out, not_246_out, not_247_out, not_248_out,
       not_249_out, not_250_out, not_251_out, not_252_out, not_253_out, not_254_out, not_255_out,
       not_256_out, not_257_out, not_258_out, not_259_out, not_260_out, not_261_out, not_262_out,
       not_263_out, not_264_out, not_265_out, not_266_out, not_267_out, not_268_out, not_269_out,
       not_270_out, not_271_out, not_272_out, not_273_out, not_274_out, not_275_out, not_276_out,
       not_277_out, not_278_out, not_279_out, not_280_out, not_281_out, not_282_out, not_283_out,
       not_284_out, not_285_out, not_286_out, not_287_out, not_288_out, not_289_out, not_290_out,
       not_291_out, not_292_out, not_293_out, not_294_out, not_295_out, not_296_out, not_297_out,
       not_298_out, not_299_out, not_300_out, not_301_out, not_302_out, not_303_out, not_304_out,
       not_305_out, not_306_out, not_307_out, not_308_out, not_309_out, not_310_out, not_311_out,
       not_312_out, not_313_out, not_314_out, not_315_out, not_316_out, not_317_out, not_318_out,
       not_319_out, not_320_out, not_321_out, not_322_out, not_323_out, not_324_out, not_325_out,
       not_326_out, not_327_out, not_328_out, not_329_out, not_330_out, not_331_out, not_332_out,
       not_333_out, not_334_out, not_335_out, not_336_out, not_337_out, not_338_out, not_339_out,
       not_340_out, not_341_out, not_342_out, not_343_out, not_344_out, not_345_out, not_346_out,
       not_347_out, not_348_out, not_349_out, not_350_out, not_351_out, not_352_out, not_353_out,
       not_354_out, not_355_out, not_356_out, not_357_out, not_358_out, not_359_out, not_360_out,
       not_361_out, not_362_out, not_363_out, not_364_out, not_365_out, not_366_out, not_367_out,
       not_368_out, not_369_out, not_370_out, not_371_out, not_372_out, not_373_out, not_374_out,
       not_375_out, not_376_out, not_377_out, not_378_out, not_379_out, not_380_out, not_381_out,
       not_382_out, not_383_out, not_384_out, not_385_out, not_386_out;

  not not_1 (not_1_out, OP4);
  not not_2 (not_2_out, OP3);
  not not_3 (not_3_out, OP2);
  not not_4 (not_4_out, OP4);
  not not_5 (not_5_out, OP3);
  not not_6 (not_6_out, OP2);
  not not_7 (not_7_out, OP1);
  not not_8 (not_8_out, OP4);
  not not_9 (not_9_out, OP2);
  not not_10 (not_10_out, OP5);
  not not_11 (not_11_out, OP4);
  not not_12 (not_12_out, OP2);
  not not_13 (not_13_out, OP1);
  not not_14 (not_14_out, OP0);
  not not_15 (not_15_out, OP5);
  not not_16 (not_16_out, OP4);
  not not_17 (not_17_out, OP1);
  not not_18 (not_18_out, OP0);
  not not_19 (not_19_out, OP5);
  not not_20 (not_20_out, OP4);
  not not_21 (not_21_out, OP2);
  not not_22 (not_22_out, OP1);
  not not_23 (not_23_out, OP5);
  not not_24 (not_24_out, OP4);
  not not_25 (not_25_out, OP2);
  not not_26 (not_26_out, OP0);
  not not_27 (not_27_out, OP5);
  not not_28 (not_28_out, OP4);
  not not_29 (not_29_out, OP1);
  not not_30 (not_30_out, OP4);
  not not_31 (not_31_out, OP3);
  not not_32 (not_32_out, OP2);
  not not_33 (not_33_out, OP4);
  not not_34 (not_34_out, OP2);
  not not_35 (not_35_out, OP5);
  not not_36 (not_36_out, OP4);
  not not_37 (not_37_out, OP3);
  not not_38 (not_38_out, OP2);
  not not_39 (not_39_out, OP1);
  not not_40 (not_40_out, OP0);
  not not_41 (not_41_out, F5);
  not not_42 (not_42_out, F4);
  not not_43 (not_43_out, F3);
  not not_44 (not_44_out, F2);
  not not_45 (not_45_out, F1);
  not not_46 (not_46_out, F0);
  not not_47 (not_47_out, OP5);
  not not_48 (not_48_out, OP4);
  not not_49 (not_49_out, OP3);
  not not_50 (not_50_out, OP2);
  not not_51 (not_51_out, OP1);
  not not_52 (not_52_out, OP0);
  not not_53 (not_53_out, F5);
  not not_54 (not_54_out, F4);
  not not_55 (not_55_out, F3);
  not not_56 (not_56_out, F2);
  not not_57 (not_57_out, OP5);
  not not_58 (not_58_out, OP4);
  not not_59 (not_59_out, OP3);
  not not_60 (not_60_out, OP2);
  not not_61 (not_61_out, OP1);
  not not_62 (not_62_out, OP0);
  not not_63 (not_63_out, F5);
  not not_64 (not_64_out, F4);
  not not_65 (not_65_out, F3);
  not not_66 (not_66_out, F2);
  not not_67 (not_67_out, F0);
  not not_68 (not_68_out, OP5);
  not not_69 (not_69_out, OP4);
  not not_70 (not_70_out, OP3);
  not not_71 (not_71_out, OP2);
  not not_72 (not_72_out, OP1);
  not not_73 (not_73_out, OP0);
  not not_74 (not_74_out, F4);
  not not_75 (not_75_out, F3);
  not not_76 (not_76_out, F2);
  not not_77 (not_77_out, F1);
  not not_78 (not_78_out, F0);
  not not_79 (not_79_out, OP5);
  not not_80 (not_80_out, OP4);
  not not_81 (not_81_out, OP3);
  not not_82 (not_82_out, OP2);
  not not_83 (not_83_out, OP1);
  not not_84 (not_84_out, OP0);
  not not_85 (not_85_out, F4);
  not not_86 (not_86_out, F3);
  not not_87 (not_87_out, F2);
  not not_88 (not_88_out, F1);
  not not_89 (not_89_out, OP5);
  not not_90 (not_90_out, OP4);
  not not_91 (not_91_out, OP3);
  not not_92 (not_92_out, OP2);
  not not_93 (not_93_out, OP1);
  not not_94 (not_94_out, OP0);
  not not_95 (not_95_out, F4);
  not not_96 (not_96_out, F3);
  not not_97 (not_97_out, F2);
  not not_98 (not_98_out, F0);
  not not_99 (not_99_out, OP5);
  not not_100 (not_100_out, OP4);
  not not_101 (not_101_out, OP3);
  not not_102 (not_102_out, OP2);
  not not_103 (not_103_out, OP1);
  not not_104 (not_104_out, OP0);
  not not_105 (not_105_out, F4);
  not not_106 (not_106_out, F3);
  not not_107 (not_107_out, F1);
  not not_108 (not_108_out, F0);
  not not_109 (not_109_out, OP5);
  not not_110 (not_110_out, OP4);
  not not_111 (not_111_out, OP3);
  not not_112 (not_112_out, OP2);
  not not_113 (not_113_out, OP1);
  not not_114 (not_114_out, OP0);
  not not_115 (not_115_out, F4);
  not not_116 (not_116_out, F3);
  not not_117 (not_117_out, F1);
  not not_118 (not_118_out, OP5);
  not not_119 (not_119_out, OP4);
  not not_120 (not_120_out, OP3);
  not not_121 (not_121_out, OP2);
  not not_122 (not_122_out, OP1);
  not not_123 (not_123_out, OP0);
  not not_124 (not_124_out, F4);
  not not_125 (not_125_out, F3);
  not not_126 (not_126_out, OP5);
  not not_127 (not_127_out, OP4);
  not not_128 (not_128_out, OP3);
  not not_129 (not_129_out, OP2);
  not not_130 (not_130_out, OP1);
  not not_131 (not_131_out, OP0);
  not not_132 (not_132_out, F4);
  not not_133 (not_133_out, F2);
  not not_134 (not_134_out, F0);
  not not_135 (not_135_out, OP5);
  not not_136 (not_136_out, OP4);
  not not_137 (not_137_out, OP3);
  not not_138 (not_138_out, OP2);
  not not_139 (not_139_out, OP1);
  not not_140 (not_140_out, OP0);
  not not_141 (not_141_out, F4);
  not not_142 (not_142_out, F2);
  not not_143 (not_143_out, OP5);
  not not_144 (not_144_out, OP4);
  not not_145 (not_145_out, OP3);
  not not_146 (not_146_out, OP2);
  not not_147 (not_147_out, OP5);
  not not_148 (not_148_out, OP4);
  not not_149 (not_149_out, OP2);
  not not_150 (not_150_out, OP1);
  not not_151 (not_151_out, OP0);
  not not_152 (not_152_out, OP5);
  not not_153 (not_153_out, OP4);
  not not_154 (not_154_out, OP1);
  not not_155 (not_155_out, OP0);
  not not_156 (not_156_out, OP5);
  not not_157 (not_157_out, OP4);
  not not_158 (not_158_out, OP2);
  not not_159 (not_159_out, OP1);
  not not_160 (not_160_out, OP5);
  not not_161 (not_161_out, OP4);
  not not_162 (not_162_out, OP2);
  not not_163 (not_163_out, OP0);
  not not_164 (not_164_out, OP5);
  not not_165 (not_165_out, OP4);
  not not_166 (not_166_out, OP1);
  not not_167 (not_167_out, OP4);
  not not_168 (not_168_out, OP3);
  not not_169 (not_169_out, OP2);
  not not_170 (not_170_out, OP5);
  not not_171 (not_171_out, OP4);
  not not_172 (not_172_out, OP3);
  not not_173 (not_173_out, OP2);
  not not_174 (not_174_out, OP1);
  not not_175 (not_175_out, OP0);
  not not_176 (not_176_out, F4);
  not not_177 (not_177_out, F3);
  not not_178 (not_178_out, F2);
  not not_179 (not_179_out, OP5);
  not not_180 (not_180_out, OP4);
  not not_181 (not_181_out, OP4);
  not not_182 (not_182_out, OP3);
  not not_183 (not_183_out, OP2);
  not not_184 (not_184_out, OP1);
  not not_185 (not_185_out, OP5);
  not not_186 (not_186_out, OP4);
  not not_187 (not_187_out, OP3);
  not not_188 (not_188_out, OP2);
  not not_189 (not_189_out, OP1);
  not not_190 (not_190_out, OP0);
  not not_191 (not_191_out, F5);
  not not_192 (not_192_out, F4);
  not not_193 (not_193_out, F1);
  not not_194 (not_194_out, F0);
  not not_195 (not_195_out, OP5);
  not not_196 (not_196_out, OP4);
  not not_197 (not_197_out, OP3);
  not not_198 (not_198_out, OP1);
  not not_199 (not_199_out, OP0);
  not not_200 (not_200_out, OP5);
  not not_201 (not_201_out, OP4);
  not not_202 (not_202_out, OP3);
  not not_203 (not_203_out, OP1);
  not not_204 (not_204_out, OP5);
  not not_205 (not_205_out, OP4);
  not not_206 (not_206_out, OP2);
  not not_207 (not_207_out, OP1);
  not not_208 (not_208_out, OP0);
  not not_209 (not_209_out, OP5);
  not not_210 (not_210_out, OP4);
  not not_211 (not_211_out, OP2);
  not not_212 (not_212_out, OP1);
  not not_213 (not_213_out, OP5);
  not not_214 (not_214_out, OP4);
  not not_215 (not_215_out, OP2);
  not not_216 (not_216_out, OP0);
  not not_217 (not_217_out, OP4);
  not not_218 (not_218_out, OP3);
  not not_219 (not_219_out, OP2);
  not not_220 (not_220_out, OP4);
  not not_221 (not_221_out, OP2);
  not not_222 (not_222_out, OP4);
  not not_223 (not_223_out, OP3);
  not not_224 (not_224_out, OP2);
  not not_225 (not_225_out, OP1);
  not not_226 (not_226_out, OP5);
  not not_227 (not_227_out, OP4);
  not not_228 (not_228_out, OP3);
  not not_229 (not_229_out, OP2);
  not not_230 (not_230_out, OP1);
  not not_231 (not_231_out, OP0);
  not not_232 (not_232_out, F5);
  not not_233 (not_233_out, F4);
  not not_234 (not_234_out, F3);
  not not_235 (not_235_out, F2);
  not not_236 (not_236_out, F1);
  not not_237 (not_237_out, F0);
  not not_238 (not_238_out, OP5);
  not not_239 (not_239_out, OP4);
  not not_240 (not_240_out, OP3);
  not not_241 (not_241_out, OP2);
  not not_242 (not_242_out, OP1);
  not not_243 (not_243_out, OP0);
  not not_244 (not_244_out, F5);
  not not_245 (not_245_out, F4);
  not not_246 (not_246_out, F3);
  not not_247 (not_247_out, F2);
  not not_248 (not_248_out, OP5);
  not not_249 (not_249_out, OP4);
  not not_250 (not_250_out, OP3);
  not not_251 (not_251_out, OP2);
  not not_252 (not_252_out, OP1);
  not not_253 (not_253_out, OP0);
  not not_254 (not_254_out, F5);
  not not_255 (not_255_out, F4);
  not not_256 (not_256_out, F3);
  not not_257 (not_257_out, F2);
  not not_258 (not_258_out, F0);
  not not_259 (not_259_out, OP5);
  not not_260 (not_260_out, OP4);
  not not_261 (not_261_out, OP3);
  not not_262 (not_262_out, OP2);
  not not_263 (not_263_out, OP1);
  not not_264 (not_264_out, OP0);
  not not_265 (not_265_out, F4);
  not not_266 (not_266_out, F3);
  not not_267 (not_267_out, F2);
  not not_268 (not_268_out, F1);
  not not_269 (not_269_out, F0);
  not not_270 (not_270_out, OP5);
  not not_271 (not_271_out, OP4);
  not not_272 (not_272_out, OP3);
  not not_273 (not_273_out, OP2);
  not not_274 (not_274_out, OP1);
  not not_275 (not_275_out, OP0);
  not not_276 (not_276_out, F4);
  not not_277 (not_277_out, F3);
  not not_278 (not_278_out, F2);
  not not_279 (not_279_out, F1);
  not not_280 (not_280_out, OP5);
  not not_281 (not_281_out, OP4);
  not not_282 (not_282_out, OP3);
  not not_283 (not_283_out, OP2);
  not not_284 (not_284_out, OP1);
  not not_285 (not_285_out, OP0);
  not not_286 (not_286_out, F4);
  not not_287 (not_287_out, F3);
  not not_288 (not_288_out, F2);
  not not_289 (not_289_out, F0);
  not not_290 (not_290_out, OP5);
  not not_291 (not_291_out, OP4);
  not not_292 (not_292_out, OP3);
  not not_293 (not_293_out, OP2);
  not not_294 (not_294_out, OP1);
  not not_295 (not_295_out, OP0);
  not not_296 (not_296_out, F4);
  not not_297 (not_297_out, F3);
  not not_298 (not_298_out, F1);
  not not_299 (not_299_out, F0);
  not not_300 (not_300_out, OP5);
  not not_301 (not_301_out, OP4);
  not not_302 (not_302_out, OP3);
  not not_303 (not_303_out, OP2);
  not not_304 (not_304_out, OP1);
  not not_305 (not_305_out, OP0);
  not not_306 (not_306_out, F4);
  not not_307 (not_307_out, F3);
  not not_308 (not_308_out, F1);
  not not_309 (not_309_out, OP5);
  not not_310 (not_310_out, OP4);
  not not_311 (not_311_out, OP3);
  not not_312 (not_312_out, OP2);
  not not_313 (not_313_out, OP1);
  not not_314 (not_314_out, OP0);
  not not_315 (not_315_out, F4);
  not not_316 (not_316_out, F3);
  not not_317 (not_317_out, OP5);
  not not_318 (not_318_out, OP4);
  not not_319 (not_319_out, OP3);
  not not_320 (not_320_out, OP2);
  not not_321 (not_321_out, OP1);
  not not_322 (not_322_out, OP0);
  not not_323 (not_323_out, F4);
  not not_324 (not_324_out, F2);
  not not_325 (not_325_out, F0);
  not not_326 (not_326_out, OP5);
  not not_327 (not_327_out, OP4);
  not not_328 (not_328_out, OP3);
  not not_329 (not_329_out, OP2);
  not not_330 (not_330_out, OP1);
  not not_331 (not_331_out, OP0);
  not not_332 (not_332_out, F4);
  not not_333 (not_333_out, F2);
  not not_334 (not_334_out, OP5);
  not not_335 (not_335_out, OP4);
  not not_336 (not_336_out, OP3);
  not not_337 (not_337_out, OP2);
  not not_338 (not_338_out, OP1);
  not not_339 (not_339_out, OP0);
  not not_340 (not_340_out, F4);
  not not_341 (not_341_out, F3);
  not not_342 (not_342_out, F2);
  not not_343 (not_343_out, OP5);
  not not_344 (not_344_out, OP4);
  not not_345 (not_345_out, OP3);
  not not_346 (not_346_out, OP1);
  not not_347 (not_347_out, OP0);
  not not_348 (not_348_out, OP5);
  not not_349 (not_349_out, OP4);
  not not_350 (not_350_out, OP3);
  not not_351 (not_351_out, OP1);
  not not_352 (not_352_out, OP5);
  not not_353 (not_353_out, OP4);
  not not_354 (not_354_out, OP3);
  not not_355 (not_355_out, OP2);
  not not_356 (not_356_out, OP1);
  not not_357 (not_357_out, OP0);
  not not_358 (not_358_out, F5);
  not not_359 (not_359_out, F4);
  not not_360 (not_360_out, F2);
  not not_361 (not_361_out, F1);
  not not_362 (not_362_out, F0);
  not not_363 (not_363_out, OP5);
  not not_364 (not_364_out, OP4);
  not not_365 (not_365_out, OP3);
  not not_366 (not_366_out, OP2);
  not not_367 (not_367_out, OP1);
  not not_368 (not_368_out, OP0);
  not not_369 (not_369_out, F5);
  not not_370 (not_370_out, F4);
  not not_371 (not_371_out, F2);
  not not_372 (not_372_out, F1);
  not not_373 (not_373_out, F0);
  not not_374 (not_374_out, OP5);
  not not_375 (not_375_out, OP4);
  not not_376 (not_376_out, OP3);
  not not_377 (not_377_out, OP2);
  not not_378 (not_378_out, OP0);
  not not_379 (not_379_out, OP5);
  not not_380 (not_380_out, OP4);
  not not_381 (not_381_out, OP3);
  not not_382 (not_382_out, OP2);
  not not_383 (not_383_out, OP5);
  not not_384 (not_384_out, OP4);
  not not_385 (not_385_out, OP3);
  not not_386 (not_386_out, OP2);
  and and_1 (and_1_out, OP5, not_1_out, not_2_out, not_3_out, OP1, OP0);
  and and_2 (and_2_out, OP5, not_4_out, not_5_out, not_6_out, not_7_out, OP0);
  and and_3 (MemWrite, OP5, not_8_out, OP3, not_9_out, OP1, OP0);
  and and_4 (and_4_out, not_10_out, not_11_out, OP3, not_12_out, not_13_out, not_14_out);
  and and_5 (and_5_out, not_15_out, not_16_out, OP3, OP2, not_17_out, not_18_out);
  and and_6 (and_6_out, not_19_out, not_20_out, OP3, not_21_out, not_22_out, OP0);
  and and_7 (and_7_out, not_23_out, not_24_out, OP3, not_25_out, OP1, not_26_out);
  and and_8 (and_8_out, not_27_out, not_28_out, OP3, OP2, not_29_out, OP0);
  and and_9 (and_9_out, OP5, not_30_out, not_31_out, not_32_out, OP1, OP0);
  and and_10 (and_10_out, OP5, not_33_out, OP3, not_34_out, OP1, OP0);
  and and_11 (and_11_out, not_35_out, not_36_out, not_37_out, not_38_out, not_39_out, not_40_out, not_41_out, not_42_out, not_43_out, not_44_out, not_45_out, not_46_out);
  and and_12 (and_12_out, not_47_out, not_48_out, not_49_out, not_50_out, not_51_out, not_52_out, not_53_out, not_54_out, not_55_out, not_56_out, F1, F0);
  and and_13 (and_13_out, not_57_out, not_58_out, not_59_out, not_60_out, not_61_out, not_62_out, not_63_out, not_64_out, not_65_out, not_66_out, F1, not_67_out);
  and and_14 (and_14_out, not_68_out, not_69_out, not_70_out, not_71_out, not_72_out, not_73_out, F5, not_74_out, not_75_out, not_76_out, not_77_out, not_78_out);
  and and_15 (and_15_out, not_79_out, not_80_out, not_81_out, not_82_out, not_83_out, not_84_out, F5, not_85_out, not_86_out, not_87_out, not_88_out, F0);
  and and_16 (and_16_out, not_89_out, not_90_out, not_91_out, not_92_out, not_93_out, not_94_out, F5, not_95_out, not_96_out, not_97_out, F1, not_98_out);
  and and_17 (and_17_out, not_99_out, not_100_out, not_101_out, not_102_out, not_103_out, not_104_out, F5, not_105_out, not_106_out, F2, not_107_out, not_108_out);
  and and_18 (and_18_out, not_109_out, not_110_out, not_111_out, not_112_out, not_113_out, not_114_out, F5, not_115_out, not_116_out, F2, not_117_out, F0);
  and and_19 (and_19_out, not_118_out, not_119_out, not_120_out, not_121_out, not_122_out, not_123_out, F5, not_124_out, not_125_out, F2, F1, F0);
  and and_20 (and_20_out, not_126_out, not_127_out, not_128_out, not_129_out, not_130_out, not_131_out, F5, not_132_out, F3, not_133_out, F1, not_134_out);
  and and_21 (and_21_out, not_135_out, not_136_out, not_137_out, not_138_out, not_139_out, not_140_out, F5, not_141_out, F3, not_142_out, F1, F0);
  and and_22 (and_22_out, not_143_out, not_144_out, not_145_out, not_146_out, OP1, OP0);
  and and_23 (and_23_out, not_147_out, not_148_out, OP3, not_149_out, not_150_out, not_151_out);
  and and_24 (and_24_out, not_152_out, not_153_out, OP3, OP2, not_154_out, not_155_out);
  and and_25 (and_25_out, not_156_out, not_157_out, OP3, not_158_out, not_159_out, OP0);
  and and_26 (and_26_out, not_160_out, not_161_out, OP3, not_162_out, OP1, not_163_out);
  and and_27 (and_27_out, not_164_out, not_165_out, OP3, OP2, not_166_out, OP0);
  and and_28 (and_28_out, OP5, not_167_out, not_168_out, not_169_out, OP1, OP0);
  and and_29 (and_29_out, not_170_out, not_171_out, not_172_out, not_173_out, not_174_out, not_175_out, F5, not_176_out, not_177_out, not_178_out, F1, F0);
  and and_30 (and_30_out, not_179_out, not_180_out, OP3, OP2, OP1, OP0);
  and and_31 (and_31_out, OP5, not_181_out, not_182_out, not_183_out, not_184_out, OP0);
  and and_32 (SysCALL, not_185_out, not_186_out, not_187_out, not_188_out, not_189_out, not_190_out, not_191_out, not_192_out, F3, F2, not_193_out, not_194_out);
  and and_33 (and_33_out, not_195_out, not_196_out, not_197_out, OP2, not_198_out, not_199_out);
  and and_34 (and_34_out, not_200_out, not_201_out, not_202_out, OP2, not_203_out, OP0);
  and and_35 (and_35_out, not_204_out, not_205_out, OP3, not_206_out, not_207_out, not_208_out);
  and and_36 (and_36_out, not_209_out, not_210_out, OP3, not_211_out, not_212_out, OP0);
  and and_37 (and_37_out, not_213_out, not_214_out, OP3, not_215_out, OP1, not_216_out);
  and and_38 (and_38_out, OP5, not_217_out, not_218_out, not_219_out, OP1, OP0);
  and and_39 (and_39_out, OP5, not_220_out, OP3, not_221_out, OP1, OP0);
  and and_40 (and_40_out, OP5, not_222_out, not_223_out, not_224_out, not_225_out, OP0);
  and and_41 (and_41_out, not_226_out, not_227_out, not_228_out, not_229_out, not_230_out, not_231_out, not_232_out, not_233_out, not_234_out, not_235_out, not_236_out, not_237_out);
  and and_42 (and_42_out, not_238_out, not_239_out, not_240_out, not_241_out, not_242_out, not_243_out, not_244_out, not_245_out, not_246_out, not_247_out, F1, F0);
  and and_43 (and_43_out, not_248_out, not_249_out, not_250_out, not_251_out, not_252_out, not_253_out, not_254_out, not_255_out, not_256_out, not_257_out, F1, not_258_out);
  and and_44 (and_44_out, not_259_out, not_260_out, not_261_out, not_262_out, not_263_out, not_264_out, F5, not_265_out, not_266_out, not_267_out, not_268_out, not_269_out);
  and and_45 (and_45_out, not_270_out, not_271_out, not_272_out, not_273_out, not_274_out, not_275_out, F5, not_276_out, not_277_out, not_278_out, not_279_out, F0);
  and and_46 (and_46_out, not_280_out, not_281_out, not_282_out, not_283_out, not_284_out, not_285_out, F5, not_286_out, not_287_out, not_288_out, F1, not_289_out);
  and and_47 (and_47_out, not_290_out, not_291_out, not_292_out, not_293_out, not_294_out, not_295_out, F5, not_296_out, not_297_out, F2, not_298_out, not_299_out);
  and and_48 (and_48_out, not_300_out, not_301_out, not_302_out, not_303_out, not_304_out, not_305_out, F5, not_306_out, not_307_out, F2, not_308_out, F0);
  and and_49 (and_49_out, not_309_out, not_310_out, not_311_out, not_312_out, not_313_out, not_314_out, F5, not_315_out, not_316_out, F2, F1, F0);
  and and_50 (and_50_out, not_317_out, not_318_out, not_319_out, not_320_out, not_321_out, not_322_out, F5, not_323_out, F3, not_324_out, F1, not_325_out);
  and and_51 (and_51_out, not_326_out, not_327_out, not_328_out, not_329_out, not_330_out, not_331_out, F5, not_332_out, F3, not_333_out, F1, F0);
  and and_52 (and_52_out, not_334_out, not_335_out, not_336_out, not_337_out, not_338_out, not_339_out, F5, not_340_out, not_341_out, not_342_out, F1, F0);
  and and_53 (BEQ, not_343_out, not_344_out, not_345_out, OP2, not_346_out, not_347_out);
  and and_54 (BNE, not_348_out, not_349_out, not_350_out, OP2, not_351_out, OP0);
  and and_55 (JR, not_352_out, not_353_out, not_354_out, not_355_out, not_356_out, not_357_out, not_358_out, not_359_out, F3, not_360_out, not_361_out, not_362_out);
  and and_56 (and_56_out, not_363_out, not_364_out, not_365_out, not_366_out, not_367_out, not_368_out, not_369_out, not_370_out, F3, not_371_out, not_372_out, not_373_out);
  and and_57 (and_57_out, not_374_out, not_375_out, not_376_out, not_377_out, OP1, not_378_out);
  and and_58 (and_58_out, not_379_out, not_380_out, not_381_out, not_382_out, OP1, OP0);
  and and_59 (JAL, not_383_out, not_384_out, not_385_out, not_386_out, OP1, OP0);
  and and_60 (ERET, ~OP0, ~OP1, ~OP2, ~OP3, OP4, ~OP5, ~F0, ~F1, ~F2, F3, F4, ~F5, MF4);  // AND_Gate
  and and_61 (MFC0, ~OP0, ~OP1, ~OP2, ~OP3, OP4, ~OP5, ~MF4, ~MF3, ~MF2, ~MF1, ~MF0);  // AND_Gate
  and and_62 (MTC0, ~OP0, ~OP1, ~OP2, ~OP3, OP4, ~OP5, ~MF4, ~MF3, MF2, ~MF1, ~MF0);  // AND_Gate
  or or_1 (MemToReg, and_1_out, and_2_out);
  or or_2 (ALU_SRC, and_4_out, and_5_out, and_6_out, and_7_out, and_8_out, and_9_out, and_10_out);
  or or_3 (SignedExt, and_33_out, and_34_out, and_35_out, and_36_out, and_37_out, and_38_out, and_39_out, and_40_out);
  or or_4 (JUMP, and_56_out, and_57_out, and_58_out);
  or or_5 (RegWrite, and_11_out, and_12_out, and_13_out, and_14_out, and_15_out, and_16_out, and_17_out, and_18_out, and_19_out, and_20_out, and_22_out, and_23_out, and_24_out, and_25_out, and_26_out, and_27_out, and_28_out, and_29_out, and_30_out, and_31_out, MFC0);
  or or_6 (RegDst, and_41_out, and_42_out, and_43_out, and_44_out, and_45_out, and_46_out, and_47_out, and_48_out, and_49_out, and_50_out, and_51_out, and_52_out);

  // Other names for the same wires on the sheet: tunnel = MFC0
endmodule

// ALU
module MIPS_ALU (
  input  [4:0] shamt,
  input  [31:0] X,
  input  [31:0] Y,
  input  [3:0] AluOP,
  output Equal,
  output [31:0] Result,
  output [31:0] Result_2
);

  wire [0:0] comparator_1_lt, comparator_2_lt;
  wire [31:0] adder_1_out, AND_out, divider_1_out, divider_1_rem, multiplier_1_cout, multiplier_1_out,
       NOR_out, OR_out, shifter_1_out, shifter_2_out, shifter_3_out, subtractor_1_out, XOR_out;

  assign AND_out = X & Y;  // AND_Gate AND, 32 bits wide
  assign OR_out = X | Y;  // OR_Gate OR, 32 bits wide
  Shifter #(.width(32), .shift("ll")) shifter_1 (.in(Y), .\dist (shamt), .out(shifter_1_out));
  Shifter #(.width(32), .shift("ar")) shifter_2 (.in(Y), .\dist (shamt), .out(shifter_2_out));
  Shifter #(.width(32), .shift("lr")) shifter_3 (.in(Y), .\dist (shamt), .out(shifter_3_out));
  Multiplier #(.width(32)) multiplier_1 (.a(X), .b(Y), .out(multiplier_1_out), .cout(multiplier_1_cout));  // open: cin
  Divider #(.width(32)) divider_1 (.a(X), .b(Y), .out(divider_1_out), .rem(divider_1_rem));  // open: upper
  Adder #(.width(32)) adder_1 (.a(X), .b(Y), .out(adder_1_out));  // open: cin, cout
  Subtractor #(.width(32)) subtractor_1 (.a(X), .b(Y), .out(subtractor_1_out));  // open: bin, bout
  assign XOR_out = X ^ Y;  // XOR_Gate XOR, 32 bits wide
  assign NOR_out = ~(X | Y);  // NOR_Gate NOR, 32 bits wide
  Comparator #(.width(32), .mode("twosComplement")) comparator_1 (
    .a(X), .b(Y), .eq(Equal), .lt(comparator_1_lt[0]));  // open: gt
  Comparator #(.width(32), .mode("unsigned")) comparator_2 (.a(X), .b(Y), .lt(comparator_2_lt[0]));  // open: gt, eq
  Multiplexer #(.select(4), .width(32), .disabled("Z"), .enable("false")) multiplexer_1 (
    .in0(shifter_1_out), .in1(shifter_2_out), .in2(shifter_3_out), .in3(multiplier_1_out),
    .in4(divider_1_out), .in5(adder_1_out), .in6(subtractor_1_out), .in7(AND_out), .in8(OR_out),
    .in9(XOR_out), .in10(NOR_out), .in11({{31{1'b0}}, comparator_1_lt[0]}),
    .in12({{31{1'b0}}, comparator_2_lt[0]}), .in13({32{1'b0}}), .in14({32{1'b0}}), .in15({32{1'b0}}),
    .out(Result), .sel(AluOP));
  Multiplexer #(.select(4), .width(32), .disabled("Z"), .enable("false")) multiplexer_2 (
    .in0({32{1'b0}}), .in1({32{1'b0}}), .in2({32{1'b0}}), .in3(multiplier_1_cout), .in4(divider_1_rem),
    .in5({32{1'b0}}), .in6({32{1'b0}}), .in7({32{1'b0}}), .in8({32{1'b0}}), .in9({32{1'b0}}),
    .in10({32{1'b0}}), .in11({32{1'b0}}), .in12({32{1'b0}}), .in13({32{1'b0}}), .in14({32{1'b0}}),
    .in15({32{1'b0}}), .out(Result_2), .sel(AluOP));

  // Other names for the same wires on the sheet: Result2[31:0] = Result_2; S[3:0] = AluOP

  // Notes on the sheet:
  //   不要改变此引脚区域内容，也不要改变ALU封装形式
  //   输入引脚
  //   输出引脚
endmodule

module MIPS_Regifile (
  input  [31:0] Din,
  input  Clk,
  input  WE,
  input  [4:0] R1_num,
  input  [4:0] W_num,
  input  [4:0] R2_num,
  output [31:0] R1,
  output [31:0] R2
);

  // RegisterFile registerfile_1: pin names not known; wires that end beside it: Din, Clk, WE, W_num, R1_num, R2_num, R1, R2
endmodule

module \下降沿Regifile  (
  input  [31:0] Din,
  input  Clk,
  input  WE,
  input  [4:0] R1_num,
  input  [4:0] W_num,
  input  [4:0] R2_num,
  output [31:0] R1,
  output [31:0] R2
);

  // RegisterFile registerfile_1: pin names not known; wires that end beside it: Din, Clk, WE, W_num, R1_num, R2_num, R1, R2
endmodule

module \理想流水线  (
  output RegWrite,
  output MemWrite,
  output [31:0] IF_PC,
  output [31:0] ID_PC,
  output [31:0] EX_PC,
  output [31:0] M_PC,
  output [31:0] WB_PC,
  output [31:0] RDin,
  output [31:0] MDin,
  output [31:0] LedData
);

  wire and_1_out, and_2_out, and_3_out, and_4_out, and_5_out, and_6_out, CLK, comparator_1_eq,
       comparator_2_gt, ex_mem_1_halt_2, ex_mem_1_lh_3, ex_mem_1_memtoreg_2, ex_mem_1_regwrite_2, Go, Halt,
       id_ex_1_alusrcb_2, id_ex_1_beq_2, id_ex_1_bne_2, id_ex_1_eret_3, id_ex_1_lh_2, id_ex_1_memtoreg_2,
       id_ex_1_memwrite_2, id_ex_1_regwrite_2, IR1, IR2, IR3, mem_wb_1_lh_2, mem_wb_1_memtoreg_2,
       mips_alu_1_equal, nor_1_out, not_1_out, not_2_out, not_3_out, or_1_out, register_1_q, RST, Signed,
       Syscall, W1, W2, W3, \单周期硬布线控制器_1_alu_src , \单周期硬布线控制器_1_beq , \单周期硬布线控制器_1_blez , \单周期硬布线控制器_1_bne ,
       \单周期硬布线控制器_1_jal , \单周期硬布线控制器_1_jmp , \单周期硬布线控制器_1_jr , \单周期硬布线控制器_1_lh , \单周期硬布线控制器_1_lui ,
       \单周期硬布线控制器_1_memtoreg , \单周期硬布线控制器_1_memwrite , \单周期硬布线控制器_1_regdst , \单周期硬布线控制器_1_regwrite ;
  wire [3:0] id_ex_1_aluop_2, \单周期硬布线控制器_1_alu_op ;
  wire [4:0] ex_mem_1_w_num_2, id_ex_1_shamt_2, id_ex_1_w_num_2, multiplexer_1_out, multiplexer_3_out,
       multiplexer_4_out, multiplexer_5_out, W_num;
  wire [9:0] mem_wb_1_addr_2;
  wire [15:0] \LoadUse次数 , multiplexer_13_out, \总周期数 , \插入气泡数 , \无条件分支数 , \条件分支成功数 ;
  wire [31:0] a0, adder_1_out, adder_2_out, adder_3_out, adder_4_out, adder_5_out, bit_extender_1_out,
       bit_extender_2_out, bit_extender_3_out, bit_extender_4_out, controlled_buffer_1_out, EX_IR,
       ex_mem_1_alu_2, ex_mem_1_lh_4, id_ex_1_imm_2, ID_IR, IF_IR, MEM_IR, mem_wb_1_alu_2, mem_wb_1_md_2,
       mips_alu_1_result, mips_regifile_1_r1, mips_regifile_1_r2, multiplexer_6_out, multiplexer_7_out,
       multiplexer_8_out, multiplexer_9_out, multiplexer_10_out, multiplexer_11_out, multiplexer_12_out,
       ram_1_data, shifter_1_out, v0, WB_IR;

  Button \u_总复位  (.out(RST));
  Button _1 (.out(IR1));
  Button _2 (.out(IR2));
  Button _3 (.out(IR3));
  // Probe on \总周期数 
  // Probe on \总周期数 
  Button \u_继续运行  (.out(Go));
  LED #(.active("true")) led_1 (.in(W1));
  LED #(.active("true")) led_2 (.in(W2));
  LED #(.active("true")) led_3 (.in(W3));
  nor nor_1 (nor_1_out, or_1_out, \单周期硬布线控制器_1_jmp );
  Hex_Digit_Display hex_digit_display_1 (.value(LedData[31:28]));  // open: dp
  // Probe on IF_PC[19:0]
  // Mips_Probe mips_probe_1: pin names not known; wires that end beside it: IF_IR
  and and_1 (and_1_out, \单周期硬布线控制器_1_jmp , ~\单周期硬布线控制器_1_jr );  // AND_Gate
  assign controlled_buffer_1_out = and_1_out ? {IF_PC[31:28], ID_IR[25:0], 2'b00} : 32'bz;  // Controlled_Buffer controlled_buffer_1
  assign controlled_buffer_1_out = \单周期硬布线控制器_1_jr  ? v0 : 32'bz;  // Controlled_Buffer controlled_buffer_2
  assign controlled_buffer_1_out = or_1_out ? adder_1_out : 32'bz;  // Controlled_Buffer controlled_buffer_3
  and and_2 (and_2_out, nor_1_out, ~\单周期硬布线控制器_1_blez );  // AND_Gate
  Hex_Digit_Display hex_digit_display_2 (.value(LedData[27:24]));  // open: dp
  Hex_Digit_Display hex_digit_display_3 (.value(LedData[23:20]));  // open: dp
  // Probe on ID_PC[19:0]
  // Mips_Probe mips_probe_2: pin names not known; wires that end beside it: ID_IR
  Register #(.width(32), .trigger("rising"), .Select("low")) PC (
    .D(controlled_buffer_1_out), .en(not_1_out), .Q(IF_PC), .clk(CLK));  // open: clr
  not not_1 (not_1_out, Halt);
  assign controlled_buffer_1_out = and_2_out ? adder_2_out : 32'bz;  // Controlled_Buffer controlled_buffer_4
  assign controlled_buffer_1_out = \单周期硬布线控制器_1_blez  ? adder_3_out : 32'bz;  // Controlled_Buffer controlled_buffer_5
  Adder #(.width(32)) adder_1 (.a(adder_5_out), .b(32'h4), .out(adder_1_out));  // open: cin, cout
  Hex_Digit_Display hex_digit_display_4 (.value(LedData[15:12]));  // open: dp
  Hex_Digit_Display hex_digit_display_5 (.value(LedData[19:16]));  // open: dp
  Hex_Digit_Display hex_digit_display_6 (.value(LedData[7:4]));  // open: dp
  Hex_Digit_Display hex_digit_display_7 (.value(LedData[11:8]));  // open: dp
  Clock #(.highDuration(1), .lowDuration(1)) clock_1 (.out(CLK));
  // Probe on EX_PC[19:0]
  // Mips_Probe mips_probe_3: pin names not known; wires that end beside it: EX_IR
  Adder #(.width(32)) adder_2 (.a(IF_PC), .b(32'h4), .out(adder_2_out));  // open: cin, cout
  Hex_Digit_Display hex_digit_display_8 (.value(LedData[3:0]));  // open: dp
  // Mips_Probe mips_probe_4: pin names not known; wires that end beside it: IF_IR
  ROM #(.addrWidth(10), .dataWidth(32), .Select("high")) rom_1 (.addr(IF_PC[11:2]), .data(IF_IR));
  IF_ID if_id_1 (.IR(IF_IR), .IR_2(ID_IR), .PC_4(IF_PC), .PC_4_2(ID_PC), .CLK(CLK));  // open: 同步清零_高电平有效, 使能端_低电平有效
  // Probe on \总周期数 
  // Probe on M_PC[19:0]
  // Mips_Probe mips_probe_5: pin names not known; wires that end beside it: MEM_IR
  Multiplexer #(.select(1), .width(5), .disabled("Z"), .enable("false")) multiplexer_1 (
    .in0(ID_IR[20:16]), .in1(ID_IR[15:11]), .out(multiplexer_1_out), .sel(\单周期硬布线控制器_1_regdst ));
  Multiplexer #(.select(1), .width(32), .disabled("Z"), .enable("false")) multiplexer_2 (
    .in0(adder_2_out), .in1(multiplexer_12_out), .out(RDin), .sel(not_2_out));
  // Probe on \总周期数 
  // Probe on \无条件分支数 
  // Probe on \条件分支成功数 
  // Probe on \插入气泡数 
  // Probe on \LoadUse次数 
  \单周期硬布线控制器  \u_单周期硬布线控制器_1  (
    .Func(ID_IR[5:0]), .OP(ID_IR[31:26]), .ALU_OP(\单周期硬布线控制器_1_alu_op ), .MemToReg(\单周期硬布线控制器_1_memtoreg ),
    .MemWrite(\单周期硬布线控制器_1_memwrite ), .ALU_SRC(\单周期硬布线控制器_1_alu_src ), .RegWrite(\单周期硬布线控制器_1_regwrite ),
    .SysCALL(Syscall), .SignedExt(Signed), .RegDst(\单周期硬布线控制器_1_regdst ), .JR(\单周期硬布线控制器_1_jr ),
    .JMP(\单周期硬布线控制器_1_jmp ), .Beq(\单周期硬布线控制器_1_beq ), .JAL(\单周期硬布线控制器_1_jal ), .Bne(\单周期硬布线控制器_1_bne ),
    .BLEZ(\单周期硬布线控制器_1_blez ), .LUI(\单周期硬布线控制器_1_lui ), .LH(\单周期硬布线控制器_1_lh ));  // open: MF, ERET, MFC0, MTC0
  Multiplexer #(.select(1), .width(5), .disabled("Z"), .enable("false")) multiplexer_3 (
    .in0(ID_IR[25:21]), .in1(5'b00010), .out(multiplexer_3_out), .sel(Syscall));
  Multiplexer #(.select(1), .width(5), .disabled("Z"), .enable("false")) multiplexer_4 (
    .in0(ID_IR[20:16]), .in1(5'b00100), .out(multiplexer_4_out), .sel(Syscall));
  assign bit_extender_1_out = {{16{1'b0}}, ID_IR[15:0]};  // Bit_Extender bit_extender_1
  not not_2 (not_2_out, \单周期硬布线控制器_1_jal );
  // Probe on IF_PC[11:0]
  // Probe on WB_PC[19:0]
  // Mips_Probe mips_probe_6: pin names not known; wires that end beside it: WB_IR
  Multiplexer #(.select(1), .width(5), .disabled("Z"), .enable("false")) multiplexer_5 (
    .in0(multiplexer_1_out), .in1({5{1'b1}}), .out(multiplexer_5_out), .sel(\单周期硬布线控制器_1_jal ));
  Multiplexer #(.select(1), .width(32), .disabled("Z"), .enable("false")) multiplexer_6 (
    .in0(bit_extender_3_out), .in1({32{1'b0}}), .out(multiplexer_6_out), .sel(comparator_2_gt));
  // Probe on ID_PC[11:0]
  // Probe on EX_PC[11:0]
  Multiplexer #(.select(1), .width(32), .disabled("Z"), .enable("false")) multiplexer_7 (
    .in0(RDin), .in1({ID_IR[15:0], {16{1'b0}}}), .out(multiplexer_7_out), .sel(\单周期硬布线控制器_1_lui ));
  assign bit_extender_2_out = {{16{ID_IR[15]}}, ID_IR[15:0]};  // Bit_Extender bit_extender_2
  assign bit_extender_3_out = {{14{ID_IR[15]}}, {ID_IR[15:0], 2'b00}};  // Bit_Extender bit_extender_3
  Adder #(.width(32)) adder_3 (.a(multiplexer_6_out), .b(adder_2_out), .out(adder_3_out));  // open: cin, cout
  // Probe on M_PC[11:0]
  MIPS_Regifile mips_regifile_1 (
    .Din(multiplexer_7_out), .Clk(CLK), .R1(mips_regifile_1_r1), .R2(mips_regifile_1_r2), .WE(RegWrite),
    .W_num(W_num), .R1_num(multiplexer_3_out), .R2_num(multiplexer_4_out));
  Multiplexer #(.select(1), .width(32), .disabled("Z"), .enable("false")) multiplexer_8 (
    .in0(bit_extender_1_out), .in1(bit_extender_2_out), .out(multiplexer_8_out), .sel(Signed));
  // Probe on WB_PC[11:0]
  or or_1 (or_1_out, and_5_out, and_4_out);
  ID_EX id_ex_1 (
    .LH(\单周期硬布线控制器_1_lh ), .LH_2(id_ex_1_lh_2), .RegWrite(\单周期硬布线控制器_1_regwrite ),
    .RegWrite_2(id_ex_1_regwrite_2), .W_num(multiplexer_5_out), .W_num_2(id_ex_1_w_num_2),
    .MemToReg(\单周期硬布线控制器_1_memtoreg ), .MemToReg_2(id_ex_1_memtoreg_2), .MemWrite(\单周期硬布线控制器_1_memwrite ),
    .MemWrite_2(id_ex_1_memwrite_2), .AluOP(\单周期硬布线控制器_1_alu_op ), .AluOP_2(id_ex_1_aluop_2),
    .AluSrcB(\单周期硬布线控制器_1_alu_src ), .R1(mips_regifile_1_r1), .R1_2(v0), .R2(mips_regifile_1_r2), .R2_2(a0),
    .Imm(multiplexer_8_out), .Imm_2(id_ex_1_imm_2), .PC_4(ID_PC), .PC_4_2(EX_PC), .IR(ID_IR), .IR_2(EX_IR),
    .CLK(CLK), .Beq(\单周期硬布线控制器_1_beq ), .Beq_2(id_ex_1_beq_2), .Bne(\单周期硬布线控制器_1_bne ),
    .Bne_2(id_ex_1_bne_2), .Shamt(ID_IR[10:6]), .Shamt_2(id_ex_1_shamt_2), .AluSrcB_2(id_ex_1_alusrcb_2),
    .eret(id_ex_1_eret_3), .eret_3(id_ex_1_eret_3));  // open: 同步清零_高电平有效, 使能端_低电平有效, JAL, JAL_2, JR, JR_2, JMP, JMP_2, _26, _26_2, Sys, Sys_2, f1, f1_2, f2, f2_2, eret_2, eret_4
  and and_3 (and_3_out, ~comparator_1_eq, Syscall);  // AND_Gate
  Comparator #(.width(32), .mode("twosComplement")) comparator_1 (
    .a(v0), .b(32'h22), .eq(comparator_1_eq));  // open: gt, lt
  and and_4 (and_4_out, mips_alu_1_equal, id_ex_1_beq_2);
  Multiplexer #(.select(1), .width(32), .disabled("Z"), .enable("false")) multiplexer_9 (
    .in0(a0), .in1(id_ex_1_imm_2), .out(multiplexer_9_out), .sel(id_ex_1_alusrcb_2));
  Shifter #(.width(32), .shift("ll")) shifter_1 (.in(id_ex_1_imm_2), .\dist (5'b00010), .out(shifter_1_out));
  Register #(.width(1), .trigger("rising"), .Select("low")) register_1 (
    .D(and_3_out), .en(and_3_out), .Q(register_1_q), .clk(CLK), .clr(Go));
  and and_5 (and_5_out, ~mips_alu_1_equal, id_ex_1_bne_2);  // AND_Gate
  MIPS_ALU mips_alu_1 (
    .X(v0), .Y(multiplexer_9_out), .AluOP(id_ex_1_aluop_2), .Equal(mips_alu_1_equal),
    .Result(mips_alu_1_result), .shamt(id_ex_1_shamt_2));  // open: Result_2
  Adder #(.width(32)) adder_4 (.a(v0), .b(id_ex_1_imm_2), .out(adder_4_out));  // open: cin, cout
  Adder #(.width(32)) adder_5 (.a(shifter_1_out), .b(EX_PC), .out(adder_5_out));  // open: cin, cout
  Comparator #(.width(32), .mode("twosComplement")) comparator_2 (
    .a(v0), .b({32{1'b0}}), .gt(comparator_2_gt));  // open: eq, lt
  Register #(.width(32), .trigger("rising"), .Select("low")) register_2 (
    .D(a0), .en(comparator_1_eq), .Q(LedData), .clk(CLK));  // open: clr
  EX_MEM ex_mem_1 (
    .LH(id_ex_1_lh_2), .LH_3(ex_mem_1_lh_3), .RegWrite(id_ex_1_regwrite_2), .RegWrite_2(ex_mem_1_regwrite_2),
    .W_num(id_ex_1_w_num_2), .W_num_2(ex_mem_1_w_num_2), .MemToReg(id_ex_1_memtoreg_2),
    .MemToReg_2(ex_mem_1_memtoreg_2), .MemWrite(id_ex_1_memwrite_2), .MemWrite_2(MemWrite),
    .Halt(register_1_q), .Halt_2(ex_mem_1_halt_2), .LH_2(adder_4_out), .LH_4(ex_mem_1_lh_4),
    .Alu(mips_alu_1_result), .Alu_2(ex_mem_1_alu_2), .R2(a0), .R2_2(MDin), .PC_4(EX_PC), .PC_4_2(M_PC),
    .IR(EX_IR), .IR_2(MEM_IR), .CLK(CLK));  // open: 同步清零_高电平有效, 使能端_低电平有效, JAL, Halt_3
  Multiplexer #(.select(1), .width(32), .disabled("Z"), .enable("false")) multiplexer_10 (
    .in0(ex_mem_1_alu_2), .in1(ex_mem_1_lh_4), .out(multiplexer_10_out), .sel(ex_mem_1_lh_3));
  // Probe on multiplexer_12_out
  Counter #(.width(16), .max('hffff), .ongoal("wrap"), .trigger("rising"), .behavior("old")) counter_1 (
    .Q(\总周期数 ), .clk(and_6_out));  // open: load, D, count, carry, clr, preset
  and and_6 (and_6_out, ~Halt, CLK);  // AND_Gate
  not not_3 (not_3_out, Halt);
  MEM_WB mem_wb_1 (
    .LH(ex_mem_1_lh_3), .LH_2(mem_wb_1_lh_2), .RegWrite(ex_mem_1_regwrite_2), .RegWrite_2(RegWrite),
    .W_num(ex_mem_1_w_num_2), .W_num_2(W_num), .MemToReg(ex_mem_1_memtoreg_2),
    .MemToReg_2(mem_wb_1_memtoreg_2), .Addr(multiplexer_10_out[11:2]), .Addr_2(mem_wb_1_addr_2),
    .Halt(ex_mem_1_halt_2), .Halt_2(Halt), .Alu(ex_mem_1_alu_2), .Alu_2(mem_wb_1_alu_2), .MD(ram_1_data),
    .MD_2(mem_wb_1_md_2), .PC_4(M_PC), .PC_4_2(WB_PC), .IR(MEM_IR), .IR_2(WB_IR), .CLK(CLK));  // open: 同步清零_高电平有效, 使能端_低电平有效, JAL, JAL_2
  RAM #(.addrWidth(10), .dataWidth(32), .bus("separate"), .Select("high")) ram_1 (
    .addr(multiplexer_10_out[11:2]), .din(MDin), .data(ram_1_data), .str(MemWrite), .sel(not_3_out), .clk(CLK));  // open: ld, clr
  Multiplexer #(.select(1), .width(32), .disabled("Z"), .enable("false")) multiplexer_11 (
    .in0(mem_wb_1_alu_2), .in1(mem_wb_1_md_2), .out(multiplexer_11_out), .sel(mem_wb_1_memtoreg_2));
  Multiplexer #(.select(1), .width(32), .disabled("Z"), .enable("false")) multiplexer_12 (
    .in0(multiplexer_11_out), .in1(bit_extender_4_out), .out(multiplexer_12_out), .sel(mem_wb_1_lh_2));
  Multiplexer #(.select(1), .width(16), .disabled("Z"), .enable("false")) multiplexer_13 (
    .in0(multiplexer_11_out[15:0]), .in1(multiplexer_11_out[31:16]), .out(multiplexer_13_out),
    .sel(mem_wb_1_addr_2[1]));
  assign bit_extender_4_out = {{16{multiplexer_13_out[15]}}, multiplexer_13_out};  // Bit_Extender bit_extender_4

  // Other names for the same wires on the sheet: IR[31:0] = IF_IR; MEM_PC[31:0] = M_PC

  // Notes on the sheet:
  //   中断源
  //   时空图监测，可删除
  //   中断等待指示
  //   JAL/J
  //   JR
  //   Branch
  //   next
  //   blez
  //   将立即数左移两位得到28位和当前指令的高4位组成跳转地址
  //   数码管输出
  //   指令存储器
  //   contents of rom_1 (hex, n*v repeats v):
  //   20100000 20110000 20120000 20130000 36100000 36310001 36520002 36730003 ae100000 ae110004 ae120008
  //   ae13000c 2002000a 20110000 20120000 20130000 c
  //   LH
  //   BLEZ
  //   JMP
  //   JR
  //   OP
  //   Func
  //   Syscall
  //   rs
  //   rt
  //   rd
  //   立即数
  //   Beq
  //   LUI
  //   Bne
  //   MemToReg
  //   MemWrite
  //   AluOP
  //   AluSrcB
  //   RegWrite
  //   JAL
  //   RegDst
  //   流水调试日志用
  //   中断策略
  //   为方便自动评测，需要输出流水线各段保存的PC值，注意是PC不是PC+4，另外ID段寄存器写入信息，Mem段内存写入信息也要输出
  //   写回
endmodule

module \气泡流水线  (
  output RegWrite,
  output MemWrite,
  output [31:0] IF_PC,
  output [31:0] ID_PC,
  output [31:0] EX_PC,
  output [31:0] M_PC,
  output [31:0] WB_PC,
  output [31:0] RDin,
  output [31:0] MDin,
  output [31:0] LedData
);

  wire and_1_out, and_2_out, and_3_out, and_4_out, and_5_out, clear, CLK, comparator_1_eq, ex_mem_1_halt_2,
       ex_mem_1_halt_3, ex_mem_1_lh_3, ex_mem_1_memtoreg_2, ex_mem_1_regwrite_2, Go, Halt, id_ex_1_alusrcb_2,
       id_ex_1_beq_2, id_ex_1_bne_2, id_ex_1_jal_2, id_ex_1_lh_2, id_ex_1_memtoreg_2, id_ex_1_memwrite_2,
       id_ex_1_regwrite_2, IR1, IR2, IR3, JMP, JR, mem_wb_1_jal_2, mem_wb_1_lh_2, mem_wb_1_memtoreg_2,
       mips_alu_1_equal, nor_1_out, not_1_out, not_2_out, not_3_out, or_1_out, or_2_out, or_3_out, pause,
       register_1_q, RST, Signed, Syscall, W1, W2, W3, \单周期硬布线控制器_1_alu_src , \单周期硬布线控制器_1_beq ,
       \单周期硬布线控制器_1_bne , \单周期硬布线控制器_1_jal , \单周期硬布线控制器_1_jmp , \单周期硬布线控制器_1_jr , \单周期硬布线控制器_1_lh ,
       \单周期硬布线控制器_1_memtoreg , \单周期硬布线控制器_1_memwrite , \单周期硬布线控制器_1_regdst , \单周期硬布线控制器_1_regwrite ,
       \单周期硬布线控制器_1_syscall , \数据相关检测逻辑_1_pause , \数据相关检测逻辑_2_pause ;
  wire [3:0] id_ex_1_aluop_2, \单周期硬布线控制器_1_alu_op ;
  wire [4:0] ex_mem_1_w_num_2, id_ex_1_shamt_2, id_ex_1_w_num_2, multiplexer_1_out, multiplexer_3_out,
       multiplexer_4_out, multiplexer_5_out, W_num;
  wire [9:0] mem_wb_1_addr_2;
  wire [15:0] \LoadUse次数 , multiplexer_10_out, \总周期数 , \插入气泡数 , \无条件分支数 , \条件分支成功数 ;
  wire [27:2] id_ex_1__26_2;
  wire [31:0] a0, adder_1_out, adder_2_out, adder_3_out, adder_4_out, adder_5_out, bit_extender_1_out,
       bit_extender_2_out, bit_extender_3_out, controlled_buffer_1_out, EX_IR, ex_mem_1_alu_2, ex_mem_1_lh_4,
       id_ex_1_imm_2, ID_IR, IF_IR, MEM_IR, mem_wb_1_alu_2, mem_wb_1_md_2, mips_alu_1_result,
       multiplexer_6_out, multiplexer_7_out, multiplexer_8_out, multiplexer_9_out, multiplexer_11_out,
       ram_1_data, shifter_1_out, v0, WB_IR, \下降沿regifile_1_r1 , \下降沿regifile_1_r2 ;

  Button \u_总复位  (.out(RST));
  Button _1 (.out(IR1));
  Button _2 (.out(IR2));
  Button _3 (.out(IR3));
  // Probe on \总周期数 
  // Probe on \总周期数 
  Button \u_继续运行  (.out(Go));
  LED #(.active("true")) led_1 (.in(W1));
  LED #(.active("true")) led_2 (.in(W2));
  LED #(.active("true")) led_3 (.in(W3));
  nor nor_1 (nor_1_out, or_2_out, JMP);
  Hex_Digit_Display hex_digit_display_1 (.value(LedData[31:28]));  // open: dp
  // Probe on IF_PC[19:0]
  // Mips_Probe mips_probe_1: pin names not known; wires that end beside it: IF_IR
  and and_1 (and_1_out, JMP, ~JR);  // AND_Gate
  assign controlled_buffer_1_out = and_1_out ? {EX_PC[31:28], id_ex_1__26_2, 2'b00} : 32'bz;  // Controlled_Buffer controlled_buffer_1
  assign controlled_buffer_1_out = JR ? v0 : 32'bz;  // Controlled_Buffer controlled_buffer_2
  assign controlled_buffer_1_out = or_2_out ? adder_1_out : 32'bz;  // Controlled_Buffer controlled_buffer_3
  assign controlled_buffer_1_out = nor_1_out ? adder_2_out : 32'bz;  // Controlled_Buffer controlled_buffer_4
  Hex_Digit_Display hex_digit_display_2 (.value(LedData[23:20]));  // open: dp
  Hex_Digit_Display hex_digit_display_3 (.value(LedData[27:24]));  // open: dp
  // Probe on ID_PC[19:0]
  // Mips_Probe mips_probe_2: pin names not known; wires that end beside it: ID_IR
  and and_2 (and_2_out, ~Halt, CLK);  // AND_Gate
  Register #(.width(32), .trigger("rising"), .Select("low")) PC (
    .D(controlled_buffer_1_out), .en(not_1_out), .Q(IF_PC), .clk(CLK));  // open: clr
  not not_1 (not_1_out, or_1_out);
  or or_1 (or_1_out, Halt, pause);
  Adder #(.width(32)) adder_1 (.a(adder_5_out), .b(32'h4), .out(adder_1_out));  // open: cin, cout
  Hex_Digit_Display hex_digit_display_4 (.value(LedData[19:16]));  // open: dp
  Hex_Digit_Display hex_digit_display_5 (.value(LedData[15:12]));  // open: dp
  Counter #(.width(16), .max('hffff), .ongoal("wrap"), .trigger("rising"), .behavior("old")) counter_1 (
    .Q(\总周期数 ), .clk(and_2_out));  // open: load, D, count, carry, clr, preset
  Hex_Digit_Display hex_digit_display_6 (.value(LedData[11:8]));  // open: dp
  Hex_Digit_Display hex_digit_display_7 (.value(LedData[7:4]));  // open: dp
  Clock #(.highDuration(1), .lowDuration(1)) clock_1 (.out(CLK));
  // Probe on EX_PC[19:0]
  // Mips_Probe mips_probe_3: pin names not known; wires that end beside it: EX_IR
  Adder #(.width(32)) adder_2 (.a(IF_PC), .b(32'h4), .out(adder_2_out));  // open: cin, cout
  Hex_Digit_Display hex_digit_display_8 (.value(LedData[3:0]));  // open: dp
  // Mips_Probe mips_probe_4: pin names not known; wires that end beside it: IF_IR
  ROM #(.addrWidth(10), .dataWidth(32), .Select("high")) rom_1 (.addr(IF_PC[11:2]), .data(IF_IR));
  IF_ID if_id_1 (
    .IR(IF_IR), .IR_2(ID_IR), .PC_4(IF_PC), .PC_4_2(ID_PC), .CLK(CLK), .\同步清零_高电平有效 (clear),
    .\使能端_低电平有效 (pause));
  // Probe on \总周期数 
  // Probe on M_PC[19:0]
  // Mips_Probe mips_probe_5: pin names not known; wires that end beside it: MEM_IR
  Multiplexer #(.select(1), .width(5), .disabled("Z"), .enable("false")) multiplexer_1 (
    .in0(ID_IR[20:16]), .in1(ID_IR[15:11]), .out(multiplexer_1_out), .sel(\单周期硬布线控制器_1_regdst ));
  Multiplexer #(.select(1), .width(32), .disabled("Z"), .enable("false")) multiplexer_2 (
    .in0(adder_3_out), .in1(multiplexer_11_out), .out(RDin), .sel(not_2_out));
  Adder #(.width(32)) adder_3 (.a(WB_PC), .b(32'h4), .out(adder_3_out));  // open: cin, cout
  // Probe on \总周期数 
  // Probe on \无条件分支数 
  // Probe on \条件分支成功数 
  // Probe on \插入气泡数 
  // Probe on \LoadUse次数 
  \单周期硬布线控制器  \u_单周期硬布线控制器_1  (
    .Func(ID_IR[5:0]), .OP(ID_IR[31:26]), .ALU_OP(\单周期硬布线控制器_1_alu_op ), .MemToReg(\单周期硬布线控制器_1_memtoreg ),
    .MemWrite(\单周期硬布线控制器_1_memwrite ), .ALU_SRC(\单周期硬布线控制器_1_alu_src ), .RegWrite(\单周期硬布线控制器_1_regwrite ),
    .SysCALL(\单周期硬布线控制器_1_syscall ), .SignedExt(Signed), .RegDst(\单周期硬布线控制器_1_regdst ),
    .JR(\单周期硬布线控制器_1_jr ), .JMP(\单周期硬布线控制器_1_jmp ), .Beq(\单周期硬布线控制器_1_beq ), .JAL(\单周期硬布线控制器_1_jal ),
    .Bne(\单周期硬布线控制器_1_bne ), .LH(\单周期硬布线控制器_1_lh ));  // open: BLEZ, LUI, MF, ERET, MFC0, MTC0
  Multiplexer #(.select(1), .width(5), .disabled("Z"), .enable("false")) multiplexer_3 (
    .in0(ID_IR[25:21]), .in1(5'b00010), .out(multiplexer_3_out), .sel(\单周期硬布线控制器_1_syscall ));
  Multiplexer #(.select(1), .width(5), .disabled("Z"), .enable("false")) multiplexer_4 (
    .in0(ID_IR[20:16]), .in1(5'b00100), .out(multiplexer_4_out), .sel(\单周期硬布线控制器_1_syscall ));
  assign bit_extender_1_out = {{16{1'b0}}, ID_IR[15:0]};  // Bit_Extender bit_extender_1
  not not_2 (not_2_out, mem_wb_1_jal_2);
  // Probe on IF_PC[11:0]
  // Probe on WB_PC[19:0]
  // Mips_Probe mips_probe_6: pin names not known; wires that end beside it: WB_IR
  Multiplexer #(.select(1), .width(5), .disabled("Z"), .enable("false")) multiplexer_5 (
    .in0(multiplexer_1_out), .in1({5{1'b1}}), .out(multiplexer_5_out), .sel(\单周期硬布线控制器_1_jal ));
  assign bit_extender_2_out = {{16{ID_IR[15]}}, ID_IR[15:0]};  // Bit_Extender bit_extender_2
  // Probe on ID_PC[11:0]
  // Probe on EX_PC[11:0]
  // Probe on M_PC[11:0]
  or or_2 (or_2_out, and_5_out, and_4_out);
  \下降沿Regifile  \u_下降沿regifile_1  (
    .Din(RDin), .Clk(CLK), .R1(\下降沿regifile_1_r1 ), .R2(\下降沿regifile_1_r2 ), .WE(RegWrite), .W_num(W_num),
    .R1_num(multiplexer_3_out), .R2_num(multiplexer_4_out));
  Multiplexer #(.select(1), .width(32), .disabled("Z"), .enable("false")) multiplexer_6 (
    .in0(bit_extender_1_out), .in1(bit_extender_2_out), .out(multiplexer_6_out), .sel(Signed));
  or or_3 (or_3_out, clear, pause);
  // Probe on WB_PC[11:0]
  ID_EX id_ex_1 (
    .LH(\单周期硬布线控制器_1_lh ), .LH_2(id_ex_1_lh_2), .RegWrite(\单周期硬布线控制器_1_regwrite ),
    .RegWrite_2(id_ex_1_regwrite_2), .W_num(multiplexer_5_out), .W_num_2(id_ex_1_w_num_2),
    .MemToReg(\单周期硬布线控制器_1_memtoreg ), .MemToReg_2(id_ex_1_memtoreg_2), .MemWrite(\单周期硬布线控制器_1_memwrite ),
    .MemWrite_2(id_ex_1_memwrite_2), .AluOP(\单周期硬布线控制器_1_alu_op ), .AluOP_2(id_ex_1_aluop_2),
    .AluSrcB(\单周期硬布线控制器_1_alu_src ), .R1(\下降沿regifile_1_r1 ), .R1_2(v0), .R2(\下降沿regifile_1_r2 ), .R2_2(a0),
    .Imm(multiplexer_6_out), .Imm_2(id_ex_1_imm_2), .PC_4(ID_PC), .PC_4_2(EX_PC), .IR(ID_IR), .IR_2(EX_IR),
    .CLK(CLK), .\同步清零_高电平有效 (or_3_out), .Beq(\单周期硬布线控制器_1_beq ), .Beq_2(id_ex_1_beq_2),
    .Bne(\单周期硬布线控制器_1_bne ), .Bne_2(id_ex_1_bne_2), .JAL(\单周期硬布线控制器_1_jal ), .JAL_2(id_ex_1_jal_2),
    .Shamt(ID_IR[10:6]), .Shamt_2(id_ex_1_shamt_2), .JR(\单周期硬布线控制器_1_jr ), .JR_2(JR),
    .JMP(\单周期硬布线控制器_1_jmp ), .JMP_2(JMP), ._26(ID_IR[25:0]), ._26_2(id_ex_1__26_2),
    .Sys(\单周期硬布线控制器_1_syscall ), .Sys_2(Syscall), .AluSrcB_2(id_ex_1_alusrcb_2));  // open: 使能端_低电平有效, f1, f1_2, f2, f2_2, eret, eret_3, eret_2, eret_4
  and and_3 (and_3_out, ~comparator_1_eq, Syscall);  // AND_Gate
  Comparator #(.width(32), .mode("twosComplement")) comparator_1 (
    .a(v0), .b(32'h22), .eq(comparator_1_eq));  // open: gt, lt
  and and_4 (and_4_out, mips_alu_1_equal, id_ex_1_beq_2);
  Multiplexer #(.select(1), .width(32), .disabled("Z"), .enable("false")) multiplexer_7 (
    .in0(a0), .in1(id_ex_1_imm_2), .out(multiplexer_7_out), .sel(id_ex_1_alusrcb_2));
  Shifter #(.width(32), .shift("ll")) shifter_1 (.in(id_ex_1_imm_2), .\dist (5'b00010), .out(shifter_1_out));
  Register #(.width(1), .trigger("rising"), .Select("low")) register_1 (
    .D(and_3_out), .en(and_3_out), .Q(register_1_q), .clk(CLK), .clr(Go));
  Register #(.width(32), .trigger("rising"), .Select("low")) register_2 (
    .D(a0), .en(comparator_1_eq), .Q(LedData), .clk(CLK));  // open: clr
  or or_4 (clear, JMP, JR, and_4_out, and_5_out, id_ex_1_jal_2);
  and and_5 (and_5_out, ~mips_alu_1_equal, id_ex_1_bne_2);  // AND_Gate
  MIPS_ALU mips_alu_1 (
    .X(v0), .Y(multiplexer_7_out), .AluOP(id_ex_1_aluop_2), .Equal(mips_alu_1_equal),
    .Result(mips_alu_1_result), .shamt(id_ex_1_shamt_2));  // open: Result_2
  Adder #(.width(32)) adder_4 (.a(v0), .b(id_ex_1_imm_2), .out(adder_4_out));  // open: cin, cout
  Adder #(.width(32)) adder_5 (.a(shifter_1_out), .b(EX_PC), .out(adder_5_out));  // open: cin, cout
  \数据相关检测逻辑  \u_数据相关检测逻辑_1  (.ID_IR(ID_IR), .EX_RW(id_ex_1_regwrite_2), .EX_IR(EX_IR), .pause(\数据相关检测逻辑_1_pause ));
  EX_MEM ex_mem_1 (
    .LH(id_ex_1_lh_2), .LH_3(ex_mem_1_lh_3), .RegWrite(id_ex_1_regwrite_2), .RegWrite_2(ex_mem_1_regwrite_2),
    .W_num(id_ex_1_w_num_2), .W_num_2(ex_mem_1_w_num_2), .MemToReg(id_ex_1_memtoreg_2),
    .MemToReg_2(ex_mem_1_memtoreg_2), .MemWrite(id_ex_1_memwrite_2), .MemWrite_2(MemWrite),
    .Halt(register_1_q), .Halt_2(ex_mem_1_halt_2), .LH_2(adder_4_out), .LH_4(ex_mem_1_lh_4),
    .Alu(mips_alu_1_result), .Alu_2(ex_mem_1_alu_2), .R2(a0), .R2_2(MDin), .PC_4(EX_PC), .PC_4_2(M_PC),
    .IR(EX_IR), .IR_2(MEM_IR), .CLK(CLK), .JAL(id_ex_1_jal_2), .Halt_3(ex_mem_1_halt_3));  // open: 同步清零_高电平有效, 使能端_低电平有效
  Multiplexer #(.select(1), .width(32), .disabled("Z"), .enable("false")) multiplexer_8 (
    .in0(ex_mem_1_alu_2), .in1(ex_mem_1_lh_4), .out(multiplexer_8_out), .sel(ex_mem_1_lh_3));
  // Probe on multiplexer_11_out
  or or_5 (pause, \数据相关检测逻辑_1_pause , \数据相关检测逻辑_2_pause );
  not not_3 (not_3_out, Halt);
  MEM_WB mem_wb_1 (
    .LH(ex_mem_1_lh_3), .LH_2(mem_wb_1_lh_2), .RegWrite(ex_mem_1_regwrite_2), .RegWrite_2(RegWrite),
    .W_num(ex_mem_1_w_num_2), .W_num_2(W_num), .MemToReg(ex_mem_1_memtoreg_2),
    .MemToReg_2(mem_wb_1_memtoreg_2), .Addr(multiplexer_8_out[11:2]), .Addr_2(mem_wb_1_addr_2),
    .Halt(ex_mem_1_halt_2), .Halt_2(Halt), .Alu(ex_mem_1_alu_2), .Alu_2(mem_wb_1_alu_2), .MD(ram_1_data),
    .MD_2(mem_wb_1_md_2), .PC_4(M_PC), .PC_4_2(WB_PC), .IR(MEM_IR), .IR_2(WB_IR), .CLK(CLK),
    .JAL(ex_mem_1_halt_3), .JAL_2(mem_wb_1_jal_2));  // open: 同步清零_高电平有效, 使能端_低电平有效
  RAM #(.addrWidth(10), .dataWidth(32), .bus("separate"), .Select("high")) ram_1 (
    .addr(multiplexer_8_out[11:2]), .din(MDin), .data(ram_1_data), .str(MemWrite), .sel(not_3_out), .clk(CLK));  // open: ld, clr
  \数据相关检测逻辑  \u_数据相关检测逻辑_2  (.ID_IR(ID_IR), .EX_RW(ex_mem_1_regwrite_2), .EX_IR(MEM_IR), .pause(\数据相关检测逻辑_2_pause ));
  Multiplexer #(.select(1), .width(32), .disabled("Z"), .enable("false")) multiplexer_9 (
    .in0(mem_wb_1_alu_2), .in1(mem_wb_1_md_2), .out(multiplexer_9_out), .sel(mem_wb_1_memtoreg_2));
  // Probe on multiplexer_8_out[11:2]
  Multiplexer #(.select(1), .width(16), .disabled("Z"), .enable("false")) multiplexer_10 (
    .in0(multiplexer_9_out[15:0]), .in1(multiplexer_9_out[31:16]), .out(multiplexer_10_out),
    .sel(mem_wb_1_addr_2[1]));
  Multiplexer #(.select(1), .width(32), .disabled("Z"), .enable("false")) multiplexer_11 (
    .in0(multiplexer_9_out), .in1(bit_extender_3_out), .out(multiplexer_11_out), .sel(mem_wb_1_lh_2));
  assign bit_extender_3_out = {{16{multiplexer_10_out[15]}}, multiplexer_10_out};  // Bit_Extender bit_extender_3

  // Other names for the same wires on the sheet: IR[31:0] = IF_IR; MEM_PC[31:0] = M_PC

  // Notes on the sheet:
  //   中断源
  //   中断等待指示
  //   JAL/J
  //   JR
  //   Branch
  //   next
  //   将立即数左移两位得到28位和当前指令的高4位组成跳转地址
  //   数码管输出
  //   指令存储器
  //   contents of rom_1 (hex, n*v repeats v):
  //   20110001 8000c05 20110001 20120002 20130003 8000c09 20110001 20120002 20130003 8000c0d 20110001
  //   20120002 20130003 8000c11 20110001 20120002 20130003 c000cb8 20100001 20110001 118fc0 112020
  //   20020022 c 118882 12200001 8000c15 112020 20020022 c 20110001 118880 112020 20020022 c 12200001
  //   8000c1f 20110001 118fc0 112020 20020022 c 1188c3 112020 20020022 c 118903 112020 20020022 c 118903
  //   112020 20020022 c 118903 112020 20020022 c 118903 112020 20020022 c 118903 112020 20020022 c 118903
  //   112020 20020022 c 118903 112020 20020022 c 20100001 109fc0 139fc3 8021 2012000c 24160003 26100001
  //   3210000f 20080008 20090001 139900 2709825 132020 20020022 c 1094022 1500fff9 22100001 2018000f
  //   2188024 108700 20080008 20090001 139902 2709825 132021 20020022 c 1094022 1500fff9 108702 2c9b022
  //   12c00001 8000c50 4020 1084027 84400 3508ffff 82021 20020022 c 2010ffff 20110000 ae300000 22100001
  //   22310004 ae300000 22100001 22310004 ae300000 22100001 22310004 ae300000 22100001 22310004 ae300000
  //   22100001 22310004 ae300000 22100001 22310004 ae300000 22100001 22310004 ae300000 22100001 22310004
  //   ae300000 22100001 22310004 ae300000 22100001 22310004 ae300000 22100001 22310004 ae300000 22100001
  //   22310004 ae300000 22100001 22310004 ae300000 22100001 22310004 ae300000 22100001 22310004 ae300000
  //   22100001 22310004 22100001 8020 2011003c 8e130000 8e340000 274402a 11000002 ae330000 ae140000
  //   2231fffc 1611fff8 102020 20020022 c 22100004 2011003c 1611fff2 20020032 c 20100000 22100001 102020
  //   20020022 c 22100002 102020 20020022 c 22100003 102020 20020022 c 22100004 102020 20020022 c 22100005
  //   102020 20020022 c 22100006 102020 20020022 c 22100007 102020 20020022 c 22100008 102020 20020022
  //   20020022 c 3e00008
  //   LH
  //   JMP
  //   JR
  //   OP
  //   Func
  //   Syscall
  //   rs
  //   rt
  //   rd
  //   立即数
  //   Beq
  //   Bne
  //   MemToReg
  //   MemWrite
  //   AluOP
  //   AluSrcB
  //   RegWrite
  //   JAL
  //   RegDst
  //   流水调试日志用
  //   中断策略
  //   JMP/JR/JAL/Bne/Beq
  //   为方便自动评测，需要输出流水线各段保存的PC值，注意是PC不是PC+4，另外ID段寄存器写入信息，Mem段内存写入信息也要输出
  //   写回
endmodule
module \重定向流水线  (
  output RegWrite,
  output MemWrite,
  output [31:0] IF_PC,
  output [31:0] ID_PC,
  output [31:0] EX_PC,
  output [31:0] M_PC,
  output [31:0] WB_PC,
  output [31:0] RDin,
  output [31:0] MDin,
  output [31:0] LedData
);

  wire and_1_out, and_2_out, and_3_out, and_4_out, and_5_out, clear, CLK, comparator_1_eq, ex_mem_1_halt_2,
       ex_mem_1_halt_3, ex_mem_1_memtoreg_2, ex_mem_1_regwrite_2, Go, Halt, id_ex_1_alusrcb_2, id_ex_1_beq_2,
       id_ex_1_bne_2, id_ex_1_jal_2, id_ex_1_memtoreg_2, id_ex_1_memwrite_2, id_ex_1_regwrite_2, IR1, IR2,
       IR3, JMP, JR, load_use, mem_wb_1_jal_2, mem_wb_1_memtoreg_2, mips_alu_1_equal, mips_probe_4_p2,
       nor_1_out, not_1_out, not_2_out, not_3_out, or_1_out, or_2_out, or_3_out, register_1_q, RST, Signed,
       Syscall, W1, W2, W3, \重定向控制器_1_alu_src , \重定向控制器_1_beq , \重定向控制器_1_bne , \重定向控制器_1_jal ,
       \重定向控制器_1_jmp , \重定向控制器_1_jr , \重定向控制器_1_memtoreg , \重定向控制器_1_regdst , \重定向控制器_1_regwrite ,
       \重定向控制器_1_syscall ;
  wire [1:0] id_ex_1_f1_2, id_ex_1_f2_2, \重定向控制器_1_f1 , \重定向控制器_1_f2 ;
  wire [3:0] id_ex_1_aluop_2, \重定向控制器_1_alu_op ;
  wire [4:0] ex_mem_1_w_num_2, id_ex_1_shamt_2, id_ex_1_w_num_2, multiplexer_1_out, multiplexer_3_out,
       multiplexer_4_out, multiplexer_5_out, W_num;
  wire [15:0] \LoadUse次数 , \总周期数 , \插入气泡数 , \无条件分支数 , \条件分支成功数 ;
  wire [27:2] id_ex_1__26_2;
  wire [31:0] a0, adder_1_out, adder_2_out, adder_3_out, adder_4_out, adder_5_out, bit_extender_1_out,
       bit_extender_2_out, controlled_buffer_1_out, EX_IR, ex_mem_1_alu_2, id_ex_1_imm_2, id_ex_1_r1_2,
       id_ex_1_r2_2, ID_IR, IF_IR, MEM_IR, mem_wb_1_alu_2, mem_wb_1_md_2, mips_alu_1_result,
       multiplexer_6_out, multiplexer_7_out, multiplexer_10_out, multiplexer_11_out, ram_1_data,
       shifter_1_out, v0, WB_IR, \下降沿regifile_1_r1 , \下降沿regifile_1_r2 ;

  Button \u_总复位  (.out(RST));
  Button _1 (.out(IR1));
  Button _2 (.out(IR2));
  Button _3 (.out(IR3));
  // Probe on \总周期数 
  // Probe on \总周期数 
  Button \u_继续运行  (.out(Go));
  LED #(.active("true")) led_1 (.in(W1));
  LED #(.active("true")) led_2 (.in(W2));
  LED #(.active("true")) led_3 (.in(W3));
  nor nor_1 (nor_1_out, or_2_out, JMP);
  Hex_Digit_Display hex_digit_display_1 (.value(LedData[31:28]));  // open: dp
  // Probe on IF_PC[19:0]
  // Mips_Probe mips_probe_1: pin names not known; wires that end beside it: IF_IR
  and and_1 (and_1_out, JMP, ~JR);  // AND_Gate
  assign controlled_buffer_1_out = and_1_out ? {EX_PC[31:28], id_ex_1__26_2, 2'b00} : 32'bz;  // Controlled_Buffer controlled_buffer_1
  assign controlled_buffer_1_out = JR ? id_ex_1_r1_2 : 32'bz;  // Controlled_Buffer controlled_buffer_2
  assign controlled_buffer_1_out = or_2_out ? adder_1_out : 32'bz;  // Controlled_Buffer controlled_buffer_3
  assign controlled_buffer_1_out = nor_1_out ? adder_2_out : 32'bz;  // Controlled_Buffer controlled_buffer_4
  Hex_Digit_Display hex_digit_display_2 (.value(LedData[27:24]));  // open: dp
  Hex_Digit_Display hex_digit_display_3 (.value(LedData[23:20]));  // open: dp
  // Probe on ID_PC[19:0]
  // Mips_Probe mips_probe_2: pin names not known; wires that end beside it: ID_IR
  Register #(.width(32), .trigger("rising"), .Select("low")) PC (
    .D(controlled_buffer_1_out), .en(not_1_out), .Q(IF_PC), .clk(CLK));  // open: clr
  not not_1 (not_1_out, or_1_out);
  or or_1 (or_1_out, Halt, load_use);
  Adder #(.width(32)) adder_1 (.a(adder_4_out), .b(32'h4), .out(adder_1_out));  // open: cin, cout
  Hex_Digit_Display hex_digit_display_4 (.value(LedData[19:16]));  // open: dp
  Hex_Digit_Display hex_digit_display_5 (.value(LedData[15:12]));  // open: dp
  Counter #(.width(16), .max('hffff), .ongoal("wrap"), .trigger("rising"), .behavior("old")) counter_1 (
    .Q(\总周期数 ), .clk(and_2_out));  // open: load, D, count, carry, clr, preset
  and and_2 (and_2_out, ~Halt, CLK);  // AND_Gate
  Hex_Digit_Display hex_digit_display_6 (.value(LedData[11:8]));  // open: dp
  Hex_Digit_Display hex_digit_display_7 (.value(LedData[7:4]));  // open: dp
  Clock #(.highDuration(1), .lowDuration(1)) clock_1 (.out(CLK));
  // Probe on EX_PC[19:0]
  // Mips_Probe mips_probe_3: pin names not known; wires that end beside it: EX_IR
  Adder #(.width(32)) adder_2 (.a(IF_PC), .b(32'h4), .out(adder_2_out));  // open: cin, cout
  Hex_Digit_Display hex_digit_display_8 (.value(LedData[3:0]));  // open: dp
  // Mips_Probe mips_probe_4: pin names not known; wires that end beside it: IF_IR, mips_probe_4_p2
  IF_ID if_id_1 (
    .IR(IF_IR), .IR_2(ID_IR), .PC_4(IF_PC), .PC_4_2(ID_PC), .CLK(CLK), .\同步清零_高电平有效 (clear),
    .\使能端_低电平有效 (load_use));
  ROM #(.addrWidth(10), .dataWidth(32), .Select("high")) rom_1 (.addr(IF_PC[11:2]), .data(IF_IR));
  // Probe on \总周期数 
  // Probe on M_PC[19:0]
  // Mips_Probe mips_probe_5: pin names not known; wires that end beside it: MEM_IR
  Multiplexer #(.select(1), .width(5), .disabled("Z"), .enable("false")) multiplexer_1 (
    .in0(ID_IR[20:16]), .in1(ID_IR[15:11]), .out(multiplexer_1_out), .sel(\重定向控制器_1_regdst ));
  Multiplexer #(.select(1), .width(32), .disabled("Z"), .enable("false")) multiplexer_2 (
    .in0(adder_3_out), .in1(multiplexer_10_out), .out(RDin), .sel(not_3_out));
  Adder #(.width(32)) adder_3 (.a(WB_PC), .b(32'h4), .out(adder_3_out));  // open: cin, cout
  // Probe on \总周期数 
  // Probe on \无条件分支数 
  // Probe on \条件分支成功数 
  // Probe on \插入气泡数 
  // Probe on \LoadUse次数 
  \重定向控制器  \u_重定向控制器_1  (
    .MemToReg(\重定向控制器_1_memtoreg ), .ALU_SRC(\重定向控制器_1_alu_src ), .RegWrite(\重定向控制器_1_regwrite ),
    .SysCALL(\重定向控制器_1_syscall ), .SignedExt(Signed), .RegDst(\重定向控制器_1_regdst ), .Beq(\重定向控制器_1_beq ),
    .Bne(\重定向控制器_1_bne ), .JR(\重定向控制器_1_jr ), .JMP(\重定向控制器_1_jmp ), .JAL(\重定向控制器_1_jal ),
    .load_use(load_use), .ex_ir(EX_IR), .mem_ir(MEM_IR), .f1(\重定向控制器_1_f1 ), .f2(\重定向控制器_1_f2 ), .IR(ID_IR),
    .ALU_OP(\重定向控制器_1_alu_op ), .MemWrite(mips_probe_4_p2));
  Multiplexer #(.select(1), .width(5), .disabled("Z"), .enable("false")) multiplexer_3 (
    .in0(ID_IR[25:21]), .in1(5'b00010), .out(multiplexer_3_out), .sel(\重定向控制器_1_syscall ));
  Multiplexer #(.select(1), .width(5), .disabled("Z"), .enable("false")) multiplexer_4 (
    .in0(ID_IR[20:16]), .in1(5'b00100), .out(multiplexer_4_out), .sel(\重定向控制器_1_syscall ));
  assign bit_extender_1_out = {{16{1'b0}}, ID_IR[15:0]};  // Bit_Extender bit_extender_1
  // Probe on IF_PC[11:0]
  // Probe on WB_PC[19:0]
  // Mips_Probe mips_probe_6: pin names not known; wires that end beside it: WB_IR
  Multiplexer #(.select(1), .width(5), .disabled("Z"), .enable("false")) multiplexer_5 (
    .in0(multiplexer_1_out), .in1({5{1'b1}}), .out(multiplexer_5_out), .sel(\重定向控制器_1_jal ));
  assign bit_extender_2_out = {{16{ID_IR[15]}}, ID_IR[15:0]};  // Bit_Extender bit_extender_2
  // Probe on EX_PC[11:0]
  // Probe on ID_PC[11:0]
  // Probe on M_PC[11:0]
  or or_2 (or_2_out, and_5_out, and_4_out);
  \下降沿Regifile  \u_下降沿regifile_1  (
    .Din(RDin), .Clk(CLK), .R1(\下降沿regifile_1_r1 ), .R2(\下降沿regifile_1_r2 ), .WE(RegWrite), .W_num(W_num),
    .R1_num(multiplexer_3_out), .R2_num(multiplexer_4_out));
  Multiplexer #(.select(1), .width(32), .disabled("Z"), .enable("false")) multiplexer_6 (
    .in0(bit_extender_1_out), .in1(bit_extender_2_out), .out(multiplexer_6_out), .sel(Signed));
  or or_3 (or_3_out, clear, load_use);
  // Probe on WB_PC[11:0]
  ID_EX id_ex_1 (
    .RegWrite(\重定向控制器_1_regwrite ), .RegWrite_2(id_ex_1_regwrite_2), .W_num(multiplexer_5_out),
    .W_num_2(id_ex_1_w_num_2), .MemToReg(\重定向控制器_1_memtoreg ), .MemToReg_2(id_ex_1_memtoreg_2),
    .MemWrite(mips_probe_4_p2), .MemWrite_2(id_ex_1_memwrite_2), .AluOP(\重定向控制器_1_alu_op ),
    .AluOP_2(id_ex_1_aluop_2), .AluSrcB(\重定向控制器_1_alu_src ), .R1(\下降沿regifile_1_r1 ), .R1_2(id_ex_1_r1_2),
    .R2(\下降沿regifile_1_r2 ), .R2_2(id_ex_1_r2_2), .Imm(multiplexer_6_out), .Imm_2(id_ex_1_imm_2),
    .PC_4(ID_PC), .PC_4_2(EX_PC), .IR(ID_IR), .IR_2(EX_IR), .CLK(CLK), .\同步清零_高电平有效 (or_3_out),
    .Beq(\重定向控制器_1_beq ), .Beq_2(id_ex_1_beq_2), .Bne(\重定向控制器_1_bne ), .Bne_2(id_ex_1_bne_2),
    .JAL(\重定向控制器_1_jal ), .JAL_2(id_ex_1_jal_2), .Shamt(ID_IR[10:6]), .Shamt_2(id_ex_1_shamt_2),
    .JR(\重定向控制器_1_jr ), .JR_2(JR), .JMP(\重定向控制器_1_jmp ), .JMP_2(JMP), ._26(ID_IR[25:0]),
    ._26_2(id_ex_1__26_2), .Sys(\重定向控制器_1_syscall ), .Sys_2(Syscall), .AluSrcB_2(id_ex_1_alusrcb_2),
    .f1(\重定向控制器_1_f1 ), .f1_2(id_ex_1_f1_2), .f2(\重定向控制器_1_f2 ), .f2_2(id_ex_1_f2_2));  // open: LH, LH_2, 使能端_低电平有效, eret, eret_3, eret_2, eret_4
  and and_3 (and_3_out, ~comparator_1_eq, Syscall);  // AND_Gate
  Comparator #(.width(32), .mode("twosComplement")) comparator_1 (
    .a(v0), .b(32'h22), .eq(comparator_1_eq));  // open: gt, lt
  and and_4 (and_4_out, mips_alu_1_equal, id_ex_1_beq_2);
  // Probe on id_ex_1_f2_2
  // Probe on id_ex_1_f1_2
  Multiplexer #(.select(2), .width(32), .disabled("Z"), .enable("false")) multiplexer_7 (
    .in0(id_ex_1_r2_2), .in1(multiplexer_11_out), .in2(mem_wb_1_md_2), .in3(ex_mem_1_alu_2),
    .out(multiplexer_7_out), .sel(id_ex_1_f2_2));
  Shifter #(.width(32), .shift("ll")) shifter_1 (.in(id_ex_1_imm_2), .\dist (5'b00010), .out(shifter_1_out));
  Register #(.width(1), .trigger("rising"), .Select("low")) register_1 (
    .D(and_3_out), .en(and_3_out), .Q(register_1_q), .clk(CLK), .clr(Go));
  Register #(.width(32), .trigger("rising"), .Select("low")) register_2 (
    .D(a0), .en(comparator_1_eq), .Q(LedData), .clk(CLK));  // open: clr
  or or_4 (clear, JMP, JR, and_4_out, and_5_out, id_ex_1_jal_2);
  and and_5 (and_5_out, ~mips_alu_1_equal, id_ex_1_bne_2);  // AND_Gate
  Multiplexer #(.select(2), .width(32), .disabled("Z"), .enable("false")) multiplexer_8 (
    .in0(id_ex_1_r1_2), .in1(multiplexer_11_out), .in2(mem_wb_1_md_2), .in3(ex_mem_1_alu_2), .out(v0),
    .sel(id_ex_1_f1_2));
  Multiplexer #(.select(1), .width(32), .disabled("Z"), .enable("false")) multiplexer_9 (
    .in0(multiplexer_7_out), .in1(id_ex_1_imm_2), .out(a0), .sel(id_ex_1_alusrcb_2));
  Adder #(.width(32)) adder_4 (.a(shifter_1_out), .b(EX_PC), .out(adder_4_out));  // open: cin, cout
  EX_MEM ex_mem_1 (
    .RegWrite(id_ex_1_regwrite_2), .RegWrite_2(ex_mem_1_regwrite_2), .W_num(id_ex_1_w_num_2),
    .W_num_2(ex_mem_1_w_num_2), .MemToReg(id_ex_1_memtoreg_2), .MemToReg_2(ex_mem_1_memtoreg_2),
    .MemWrite(id_ex_1_memwrite_2), .MemWrite_2(MemWrite), .Halt(register_1_q), .Halt_2(ex_mem_1_halt_2),
    .Alu(mips_alu_1_result), .Alu_2(ex_mem_1_alu_2), .R2(multiplexer_7_out), .R2_2(MDin), .PC_4(EX_PC),
    .PC_4_2(M_PC), .IR(EX_IR), .IR_2(MEM_IR), .CLK(CLK), .JAL(id_ex_1_jal_2), .Halt_3(ex_mem_1_halt_3));  // open: LH, LH_3, LH_2, LH_4, 同步清零_高电平有效, 使能端_低电平有效
  MIPS_ALU mips_alu_1 (
    .X(v0), .Y(a0), .AluOP(id_ex_1_aluop_2), .Equal(mips_alu_1_equal), .Result(mips_alu_1_result),
    .shamt(id_ex_1_shamt_2));  // open: Result_2
  // Probe on v0
  // Probe on ex_mem_1_alu_2
  // Probe on multiplexer_10_out
  // Probe on a0
  // Probe on ex_mem_1_alu_2
  not not_2 (not_2_out, Halt);
  RAM #(.addrWidth(10), .dataWidth(32), .bus("separate"), .Select("high")) ram_1 (
    .addr(ex_mem_1_alu_2[11:2]), .din(MDin), .data(ram_1_data), .str(MemWrite), .sel(not_2_out), .clk(CLK));  // open: ld, clr
  MEM_WB mem_wb_1 (
    .RegWrite(ex_mem_1_regwrite_2), .RegWrite_2(RegWrite), .W_num(ex_mem_1_w_num_2), .W_num_2(W_num),
    .MemToReg(ex_mem_1_memtoreg_2), .MemToReg_2(mem_wb_1_memtoreg_2), .Halt(ex_mem_1_halt_2), .Halt_2(Halt),
    .Alu(ex_mem_1_alu_2), .Alu_2(mem_wb_1_alu_2), .MD(ram_1_data), .MD_2(mem_wb_1_md_2), .PC_4(M_PC),
    .PC_4_2(WB_PC), .IR(MEM_IR), .IR_2(WB_IR), .CLK(CLK), .JAL(ex_mem_1_halt_3), .JAL_2(mem_wb_1_jal_2));  // open: LH, LH_2, Addr, Addr_2, 同步清零_高电平有效, 使能端_低电平有效
  not not_3 (not_3_out, mem_wb_1_jal_2);
  Adder #(.width(32)) adder_5 (.a(32'h4), .b(WB_PC), .out(adder_5_out));  // open: cin, cout
  Multiplexer #(.select(1), .width(32), .disabled("Z"), .enable("false")) multiplexer_10 (
    .in0(mem_wb_1_alu_2), .in1(mem_wb_1_md_2), .out(multiplexer_10_out), .sel(mem_wb_1_memtoreg_2));
  Multiplexer #(.select(1), .width(32), .disabled("Z"), .enable("false")) multiplexer_11 (
    .in0(adder_5_out), .in1(mem_wb_1_alu_2), .out(multiplexer_11_out), .sel(not_3_out));

  // Other names for the same wires on the sheet: IR[31:0] = IF_IR; MEM_PC[31:0] = M_PC

  // Notes on the sheet:
  //   中断源
  //   时空图监测，可删除
  //   中断等待指示
  //   JAL/J
  //   JR
  //   Branch
  //   next
  //   将立即数左移两位得到28位和当前指令的高4位组成跳转地址
  //   数码管输出
  //   指令存储器
  //   IR
  //   contents of rom_1 (hex, n*v repeats v):
  //   20110001 8000c05 20110001 20120002 20130003 8000c09 20110001 20120002 20130003 8000c0d 20110001
  //   20120002 20130003 8000c11 20110001 20120002 20130003 c000cb8 20100001 20110001 118fc0 112020
  //   20020022 c 118882 12200001 8000c15 112020 20020022 c 20110001 118880 112020 20020022 c 12200001
  //   8000c1f 20110001 118fc0 112020 20020022 c 1188c3 112020 20020022 c 118903 112020 20020022 c 118903
  //   112020 20020022 c 118903 112020 20020022 c 118903 112020 20020022 c 118903 112020 20020022 c 118903
  //   112020 20020022 c 118903 112020 20020022 c 20100001 109fc0 139fc3 8021 2012000c 24160003 26100001
  //   3210000f 20080008 20090001 139900 2709825 132020 20020022 c 1094022 1500fff9 22100001 2018000f
  //   2188024 108700 20080008 20090001 139902 2709825 132021 20020022 c 1094022 1500fff9 108702 2c9b022
  //   12c00001 8000c50 4020 1084027 84400 3508ffff 82021 20020022 c 2010ffff 20110000 ae300000 22100001
  //   22310004 ae300000 22100001 22310004 ae300000 22100001 22310004 ae300000 22100001 22310004 ae300000
  //   22100001 22310004 ae300000 22100001 22310004 ae300000 22100001 22310004 ae300000 22100001 22310004
  //   ae300000 22100001 22310004 ae300000 22100001 22310004 ae300000 22100001 22310004 ae300000 22100001
  //   22310004 ae300000 22100001 22310004 ae300000 22100001 22310004 ae300000 22100001 22310004 ae300000
  //   22100001 22310004 22100001 8020 2011003c 8e130000 8e340000 274402a 11000002 ae330000 ae140000
  //   2231fffc 1611fff8 102020 20020022 c 22100004 2011003c 1611fff2 20020032 c 20100000 22100001 102020
  //   20020022 c 22100002 102020 20020022 c 22100003 102020 20020022 c 22100004 102020 20020022 c 22100005
  //   102020 20020022 c 22100006 102020 20020022 c 22100007 102020 20020022 c 22100008 102020 20020022
  //   20020022 c 3e00008
  //   JMP
  //   JR
  //   Syscall
  //   rs
  //   rt
  //   rd
  //   立即数
  //   Beq
  //   RegWrite
  //   Bne
  //   MemToReg
  //   MemWrite
  //   AluOP
  //   AluSrcB
  //   JAL
  //   RegDst
  //   流水调试日志用
  //   中断策略
  //   为方便自动评测，需要输出流水线各段保存的PC值，注意是PC不是PC+4，另外ID段寄存器写入信息，Mem段内存写入信息也要输出
  //   JAL并入ALU
  //   写回
endmodule

module \中断按键参考电路  (
  input  \同步清零信号 ,
  output \与中断屏蔽位与 
);

  wire \_1号中断_out , and_1_out, clock_1_out, d_ff_1_q, or_1_out, or_2_out;

  Clock #(.highDuration(1), .lowDuration(1)) clock_1 (.out(clock_1_out));
  Button \_1号中断  (.out(\_1号中断_out ));
  LED #(.active("true")) \_1号中断等待指示灯  (.in(or_1_out));
  or or_1 (or_1_out, \与中断屏蔽位与 , d_ff_1_q);
  D_Flip_Flop #(.trigger("rising"), .Pre_Clr_Positions("LEGACY"), .NegatePresetClear("false"), .enable("true"), .NewFFLayout("false")) d_ff_1 (
    .clk(\_1号中断_out ), .D(1'b1), .Q(d_ff_1_q), .reset(\与中断屏蔽位与 ));  // open: Qn, preset, en
  or or_2 (or_2_out, d_ff_1_q, \与中断屏蔽位与 );
  and and_1 (and_1_out, or_2_out, ~\同步清零信号 );  // AND_Gate
  D_Flip_Flop #(.trigger("rising"), .Pre_Clr_Positions("LEGACY"), .NegatePresetClear("false"), .enable("true"), .NewFFLayout("false")) IR1 (
    .clk(clock_1_out), .D(and_1_out), .Q(\与中断屏蔽位与 ));  // open: Qn, preset, en, reset

  // Notes on the sheet:
  //   中断信号采样参考电路
  //   Reset 
endmodule

module \单周期MIPS_单级中断  (
  input  IR1,
  input  IR2,
  input  IR3,
  output RegWrite,
  output MemWrite,
  output [31:0] PC,
  output [31:0] IR,
  output [31:0] RDin,
  output [31:0] MDin,
  output [31:0] LedData
);

  wire and_1_out, and_2_out, and_3_out, and_4_out, and_5_out, and_6_out, and_7_out, and_8_out, and_9_out,
       and_10_out, and_11_out, CLK, comparator_1_eq, comparator_2_eq, comparator_3_eq, comparator_4_eq,
       comparator_5_eq, comparator_6_eq, d_ff_1_q, d_ff_2_q, d_ff_3_q, decoder_1_out1, decoder_1_out2,
       decoder_1_out3, ERET, Go, Halt, IE, IR1_2_q, IR1_3_q, IR1_q, IR1_t, IR2_t, IR3_t, IRA, IRB, IRC,
       mips_alu_1_equal, nor_1_out, not_1_out, not_2_out, not_3_out, not_4_out, not_5_out, or_4_out,
       or_8_out, or_9_out, or_10_out, or_11_out, or_12_out, or_13_out, sig, SignedExt, Syscall, W1, W2, W3,
       \单周期硬布线控制器_1_alu_src , \单周期硬布线控制器_1_beq , \单周期硬布线控制器_1_bne , \单周期硬布线控制器_1_jal , \单周期硬布线控制器_1_jmp ,
       \单周期硬布线控制器_1_jr , \单周期硬布线控制器_1_memtoreg , \单周期硬布线控制器_1_regdst ;
  wire [1:0] priority_encoder_1_out, register_3_q;
  wire [3:0] \单周期硬布线控制器_1_alu_op ;
  wire [4:0] multiplexer_4_out, multiplexer_5_out, multiplexer_6_out, multiplexer_7_out;
  wire [15:0] \总周期数 ;
  wire [31:0] adder_1_out, adder_2_out, bit_extender_1_out, bit_extender_2_out, controlled_buffer_1_out,
       EPC_q, \int , mips_alu_1_result, multiplexer_1_out, multiplexer_2_out, multiplexer_8_out,
       multiplexer_9_out, multiplexer_10_out, ram_1_data, shifter_1_out, v0;

  Clock #(.highDuration(1), .lowDuration(1)) clock_1 (.out(CLK));
  Button _1 ();  // open: out
  Button _2 ();  // open: out
  Button _3 ();  // open: out
  Button \u_继续运行  (.out(Go));
  LED #(.active("true")) led_1 (.in(W1));
  LED #(.active("true")) led_2 (.in(W2));
  LED #(.active("true")) led_3 (.in(W3));
  and and_1 (and_1_out, \单周期硬布线控制器_1_jmp , ~\单周期硬布线控制器_1_jr );  // AND_Gate
  assign controlled_buffer_1_out = and_1_out ? {PC[31:28], IR[25:0], 2'b00} : 32'bz;  // Controlled_Buffer controlled_buffer_1
  nor nor_1 (nor_1_out, or_4_out, \单周期硬布线控制器_1_jmp );
  assign controlled_buffer_1_out = \单周期硬布线控制器_1_jr  ? v0 : 32'bz;  // Controlled_Buffer controlled_buffer_2
  assign controlled_buffer_1_out = or_4_out ? adder_2_out : 32'bz;  // Controlled_Buffer controlled_buffer_3
  assign controlled_buffer_1_out = nor_1_out ? adder_1_out : 32'bz;  // Controlled_Buffer controlled_buffer_4
  Hex_Digit_Display hex_digit_display_1 (.value(LedData[31:28]));  // open: dp
  // Probe on controlled_buffer_1_out
  Multiplexer #(.select(1), .width(32), .disabled("Z"), .enable("false")) multiplexer_1 (
    .in0(controlled_buffer_1_out), .in1(\int ), .out(multiplexer_1_out), .sel(sig));
  Hex_Digit_Display hex_digit_display_2 (.value(LedData[23:20]));  // open: dp
  Hex_Digit_Display hex_digit_display_3 (.value(LedData[27:24]));  // open: dp
  Register #(.width(32), .trigger("rising"), .Select("low")) EPC (
    .D(controlled_buffer_1_out), .en(sig), .Q(EPC_q), .clk(CLK));  // open: clr
  Multiplexer #(.select(1), .width(32), .disabled("Z"), .enable("false")) multiplexer_2 (
    .in0(multiplexer_1_out), .in1(EPC_q), .out(multiplexer_2_out), .sel(ERET));
  not not_1 (not_1_out, Halt);
  Hex_Digit_Display hex_digit_display_4 (.value(LedData[15:12]));  // open: dp
  Hex_Digit_Display hex_digit_display_5 (.value(LedData[19:16]));  // open: dp
  Comparator #(.width(32), .mode("twosComplement")) comparator_1 (
    .a(v0), .b(32'h22), .eq(comparator_1_eq));  // open: gt, lt
  Register #(.width(32), .trigger("rising"), .Select("low")) u_PC (
    .D(multiplexer_2_out), .en(not_1_out), .Q(PC), .clk(CLK));  // open: clr
  Hex_Digit_Display hex_digit_display_6 (.value(LedData[7:4]));  // open: dp
  Hex_Digit_Display hex_digit_display_7 (.value(LedData[11:8]));  // open: dp
  // Probe on \总周期数 
  Register #(.width(32), .trigger("rising"), .Select("low")) register_1 (
    .D(MDin), .en(comparator_1_eq), .Q(LedData), .clk(CLK));  // open: clr
  and and_2 (and_2_out, ~comparator_1_eq, Syscall);  // AND_Gate
  Hex_Digit_Display hex_digit_display_8 (.value(LedData[3:0]));  // open: dp
  // Mips_Probe mips_probe_1: pin names not known; wires that end beside it: PC[11:2], IR
  Register #(.width(1), .trigger("rising"), .Select("low")) register_2 (
    .D(and_2_out), .en(and_2_out), .Q(Halt), .clk(CLK), .clr(Go));
  ROM #(.addrWidth(10), .dataWidth(32), .Select("high")) rom_1 (.addr(PC[11:2]), .data(IR));
  Adder #(.width(32)) adder_1 (.a(PC), .b(32'h4), .out(adder_1_out));  // open: cin, cout
  Multiplexer #(.select(1), .width(32), .disabled("Z"), .enable("false")) multiplexer_3 (
    .in0(adder_1_out), .in1(multiplexer_10_out), .out(RDin), .sel(not_2_out));
  or or_1 (IR1_t, IR1, IRA);
  \单周期硬布线控制器  \u_单周期硬布线控制器_1  (
    .Func(IR[5:0]), .OP(IR[31:26]), .ALU_OP(\单周期硬布线控制器_1_alu_op ), .MemToReg(\单周期硬布线控制器_1_memtoreg ),
    .MemWrite(MemWrite), .ALU_SRC(\单周期硬布线控制器_1_alu_src ), .RegWrite(RegWrite), .SysCALL(Syscall),
    .SignedExt(SignedExt), .RegDst(\单周期硬布线控制器_1_regdst ), .JR(\单周期硬布线控制器_1_jr ), .JMP(\单周期硬布线控制器_1_jmp ),
    .Beq(\单周期硬布线控制器_1_beq ), .JAL(\单周期硬布线控制器_1_jal ), .Bne(\单周期硬布线控制器_1_bne ), .MF(IR[25:21]), .ERET(ERET));  // open: BLEZ, LUI, LH, MFC0, MTC0
  Multiplexer #(.select(1), .width(5), .disabled("Z"), .enable("false")) multiplexer_4 (
    .in0(IR[25:21]), .in1(5'b00010), .out(multiplexer_4_out), .sel(Syscall));
  Multiplexer #(.select(1), .width(5), .disabled("Z"), .enable("false")) multiplexer_5 (
    .in0(IR[20:16]), .in1(5'b00100), .out(multiplexer_5_out), .sel(Syscall));
  Multiplexer #(.select(1), .width(5), .disabled("Z"), .enable("false")) multiplexer_6 (
    .in0(IR[20:16]), .in1(IR[15:11]), .out(multiplexer_6_out), .sel(\单周期硬布线控制器_1_regdst ));
  assign bit_extender_1_out = {{16{1'b0}}, IR[15:0]};  // Bit_Extender bit_extender_1
  not not_2 (not_2_out, \单周期硬布线控制器_1_jal );
  or or_2 (IR2_t, IR2, IRB);
  // Probe on multiplexer_7_out
  Multiplexer #(.select(1), .width(5), .disabled("Z"), .enable("false")) multiplexer_7 (
    .in0(multiplexer_6_out), .in1({5{1'b1}}), .out(multiplexer_7_out), .sel(\单周期硬布线控制器_1_jal ));
  assign bit_extender_2_out = {{16{IR[15]}}, IR[15:0]};  // Bit_Extender bit_extender_2
  or or_3 (IR3_t, IR3, IRC);
  or or_4 (or_4_out, and_4_out, and_3_out);
  MIPS_Regifile mips_regifile_1 (
    .Din(RDin), .Clk(CLK), .R1(v0), .R2(MDin), .WE(RegWrite), .W_num(multiplexer_7_out),
    .R1_num(multiplexer_4_out), .R2_num(multiplexer_5_out));
  Multiplexer #(.select(1), .width(32), .disabled("Z"), .enable("false")) multiplexer_8 (
    .in0(bit_extender_1_out), .in1(bit_extender_2_out), .out(multiplexer_8_out), .sel(SignedExt));
  and and_3 (and_3_out, mips_alu_1_equal, \单周期硬布线控制器_1_beq );
  Multiplexer #(.select(1), .width(32), .disabled("Z"), .enable("false")) multiplexer_9 (
    .in0(MDin), .in1(multiplexer_8_out), .out(multiplexer_9_out), .sel(\单周期硬布线控制器_1_alu_src ));
  Shifter #(.width(32), .shift("ll")) shifter_1 (.in(multiplexer_8_out), .\dist (5'b00010), .out(shifter_1_out));
  MIPS_ALU mips_alu_1 (
    .X(v0), .Y(multiplexer_9_out), .AluOP(\单周期硬布线控制器_1_alu_op ), .Equal(mips_alu_1_equal),
    .Result(mips_alu_1_result), .shamt(IR[10:6]));  // open: Result_2
  and and_4 (and_4_out, ~mips_alu_1_equal, \单周期硬布线控制器_1_bne );  // AND_Gate
  Adder #(.width(32)) adder_2 (.a(shifter_1_out), .b(adder_1_out), .out(adder_2_out));  // open: cin, cout
  not not_3 (not_3_out, Halt);
  Counter #(.width(16), .max('hffff), .ongoal("wrap"), .trigger("rising"), .behavior("old")) counter_1 (
    .Q(\总周期数 ), .clk(and_5_out));  // open: load, D, count, carry, clr, preset
  and and_5 (and_5_out, ~Halt, CLK);  // AND_Gate
  RAM #(.addrWidth(10), .dataWidth(32), .bus("separate"), .Select("high")) ram_1 (
    .addr(mips_alu_1_result[11:2]), .din(MDin), .data(ram_1_data), .str(MemWrite), .sel(not_3_out), .clk(CLK));  // open: ld, clr
  Multiplexer #(.select(1), .width(32), .disabled("Z"), .enable("false")) multiplexer_10 (
    .in0(mips_alu_1_result), .in1(ram_1_data), .out(multiplexer_10_out), .sel(\单周期硬布线控制器_1_memtoreg ));
  D_Flip_Flop #(.trigger("rising"), .Pre_Clr_Positions("LEGACY"), .NegatePresetClear("false"), .enable("true"), .NewFFLayout("false")) d_ff_1 (
    .clk(IR1_t), .D(1'b1), .Q(d_ff_1_q), .reset(IR1_q));  // open: Qn, preset, en
  or or_5 (W1, IR1_q, d_ff_1_q);
  D_Flip_Flop #(.trigger("rising"), .Pre_Clr_Positions("LEGACY"), .NegatePresetClear("false"), .enable("true"), .NewFFLayout("false")) d_ff_2 (
    .clk(IR2_t), .D(1'b1), .Q(d_ff_2_q), .reset(IR1_2_q));  // open: Qn, preset, en
  or or_6 (W2, IR1_2_q, d_ff_2_q);
  D_Flip_Flop #(.trigger("rising"), .Pre_Clr_Positions("LEGACY"), .NegatePresetClear("false"), .enable("true"), .NewFFLayout("false")) d_ff_3 (
    .clk(IR3_t), .D(1'b1), .Q(d_ff_3_q), .reset(IR1_3_q));  // open: Qn, preset, en
  or or_7 (W3, IR1_3_q, d_ff_3_q);
  or or_8 (or_8_out, d_ff_1_q, IR1_q);
  and and_6 (and_6_out, or_8_out, ~and_7_out);  // AND_Gate
  and and_7 (and_7_out, decoder_1_out1, ERET);
  or or_9 (or_9_out, d_ff_2_q, IR1_2_q);
  and and_8 (and_8_out, or_9_out, ~and_9_out);  // AND_Gate
  and and_9 (and_9_out, decoder_1_out2, ERET);
  or or_10 (or_10_out, d_ff_3_q, IR1_3_q);
  and and_10 (and_10_out, or_10_out, ~and_11_out);  // AND_Gate
  and and_11 (and_11_out, ERET, decoder_1_out3);
  Comparator #(.width(16), .mode("twosComplement")) comparator_2 (
    .a(16'h258), .b(\总周期数 ), .eq(comparator_2_eq));  // open: gt, lt
  Comparator #(.width(16), .mode("twosComplement")) comparator_3 (
    .a(\总周期数 ), .b(16'h1), .eq(comparator_3_eq));  // open: gt, lt
  Comparator #(.width(16), .mode("twosComplement")) comparator_4 (
    .a(\总周期数 ), .b(16'h4), .eq(comparator_4_eq));  // open: gt, lt
  Comparator #(.width(16), .mode("twosComplement")) comparator_5 (
    .a(\总周期数 ), .b(16'h7), .eq(comparator_5_eq));  // open: gt, lt
  or or_11 (or_11_out, comparator_5_eq, comparator_6_eq);
  Comparator #(.width(16), .mode("twosComplement")) comparator_6 (
    .a(\总周期数 ), .b(16'h241), .eq(comparator_6_eq));  // open: gt, lt
  D_Flip_Flop #(.trigger("rising"), .Pre_Clr_Positions("LEGACY"), .NegatePresetClear("false"), .enable("true"), .NewFFLayout("false")) u_IR1 (
    .clk(CLK), .D(and_6_out), .Q(IR1_q));  // open: Qn, preset, en, reset
  D_Flip_Flop #(.trigger("rising"), .Pre_Clr_Positions("LEGACY"), .NegatePresetClear("false"), .enable("true"), .NewFFLayout("false")) IR1_2 (
    .clk(CLK), .D(and_8_out), .Q(IR1_2_q));  // open: Qn, preset, en, reset
  D_Flip_Flop #(.trigger("rising"), .Pre_Clr_Positions("LEGACY"), .NegatePresetClear("false"), .enable("true"), .NewFFLayout("false")) IR1_3 (
    .clk(CLK), .D(and_10_out), .Q(IR1_3_q));  // open: Qn, preset, en, reset
  or or_12 (or_12_out, comparator_2_eq, comparator_3_eq);
  Pull_Resistor #(.pull(0)) pull_resistor_1 (.node(IRA));
  assign IRA = or_12_out ? ~CLK : 1'bz;  // Controlled_Inverter controlled_inverter_1
  Pull_Resistor #(.pull(0)) pull_resistor_2 (.node(IRB));
  assign IRB = comparator_4_eq ? ~CLK : 1'bz;  // Controlled_Inverter controlled_inverter_2
  Pull_Resistor #(.pull(0)) pull_resistor_3 (.node(IRC));
  assign IRC = or_11_out ? ~CLK : 1'bz;  // Controlled_Inverter controlled_inverter_3
  not not_4 (not_4_out, IE);
  Priority_Encoder #(.select(2), .disabled("Z")) priority_encoder_1 (
    .in0(1'b1), .in1(IR1_q), .in2(IR1_2_q), .in3(IR1_3_q), .out(priority_encoder_1_out));  // open: gs, en_out, en_in
  or or_13 (or_13_out, IR1_q, IR1_2_q, IR1_3_q);
  Register #(.width(1), .trigger("rising"), .Select("low")) u_IE (
    .D(or_13_out), .en(not_4_out), .Q(IE), .clk(CLK), .clr(ERET));
  not not_5 (not_5_out, IE);
  Multiplexer #(.select(2), .width(32), .disabled("Z"), .enable("false")) multiplexer_11 (
    .in1(32'h30ac), .in2(32'h3150), .in3(32'h31f4), .out(\int ), .sel(priority_encoder_1_out));  // open: in0
  and and_12 (sig, or_13_out, ~IE);  // AND_Gate
  Register #(.width(2), .trigger("rising"), .Select("low")) register_3 (
    .D(priority_encoder_1_out), .en(not_5_out), .Q(register_3_q), .clk(CLK));  // open: clr
  Decoder #(.select(2), .tristate("false"), .disabled("Z"), .enable("false")) decoder_1 (
    .out1(decoder_1_out1), .out2(decoder_1_out2), .out3(decoder_1_out3), .sel(register_3_q));  // open: out0
  // Probe on priority_encoder_1_out

  // Other names for the same wires on the sheet: a0[31:0] = MDin

  // Notes on the sheet:
  //   中断源
  //   中断等待指示
  //   总复位信号应将除ROM以外所有存储组件全部清零
  //   停机策略
  //   JAL/J
  //   JR
  //   Branch
  //   next
  //   数码管输出
  //   数码管输出应该用寄存器锁存，否则显示数据只能一闪而过
  //   指令存储器
  //   指令字
  //   contents of rom_1 (hex, n*v repeats v):
  //   201d07d0 20100001 109fc0 139fc3 8021 2012000c 24160008 26100001 3210000f 20080008 20090001 139900
  //   2709825 132020 20020022 c 1094022 1500fff9 22100001 2018000f 2188024 108700 20080008 20090001 139902
  //   2709825 132021 20020022 c 1094022 1500fff9 108702 2c9b022 12c00001 8000c07 4020 1084027 84400
  //   3508ffff 82021 20020022 c 8000c01 afa20000 23bd0004 afa40000 23bd0004 afb00000 23bd0004 afb30000
  //   23bd0004 afb40000 23bd0004 afb50000 23bd0004 afb60000 23bd0004 20160001 20140003 20150001 168020
  //   108100 2149825 132020 20020022 c 1600fffa 295a022 1680fff7 23bdfffc 8fb60000 23bdfffc 8fb50000
  //   23bdfffc 8fb40000 23bdfffc 8fb30000 23bdfffc 8fb00000 23bdfffc 8fa40000 23bdfffc 8fa20000 42000018
  //   afa20000 23bd0004 afa40000 23bd0004 afb00000 23bd0004 afb30000 23bd0004 afb40000 23bd0004 afb50000
  //   23bd0004 afb60000 23bd0004 20160002 20140003 20150001 168020 108100 2149825 132020 20020022 c
  //   1600fffa 295a022 1680fff7 23bdfffc 8fb60000 23bdfffc 8fb50000 23bdfffc 8fb40000 23bdfffc 8fb30000
  //   23bdfffc 8fb00000 23bdfffc 8fa40000 23bdfffc 8fa20000 42000018 afa20000 23bd0004 afa40000 23bd0004
  //   afb00000 23bd0004 afb30000 23bd0004 afb40000 23bd0004 afb50000 23bd0004 afb60000 23bd0004 20160003
  //   20140003 20150001 168020 108100 2149825 132020 20020022 c 1600fffa 295a022 1680fff7 23bdfffc
  //   8fb60000 23bdfffc 8fb50000 23bdfffc 8fb40000 23bdfffc 8fb30000 23bdfffc 8fb00000 23bdfffc 8fa40000
  //   23bdfffc 8fa20000 42000018
  //   JMP
  //   JR
  //   OP
  //   Func
  //   MF
  //   Syscall
  //   rs
  //   rt
  //   rd
  //   立即数
  //   Beq
  //   Bne
  //   MemToReg
  //   MemWrite
  //   AluOP
  //   AluSrcB
  //   RegWrite
  //   JAL
  //   RegDst
  //   PC+4
  //   为方便自动评测，需要输出PC，IR，寄存器堆写如数据RDin
  //   RAM写使能MemWrite、RAM写入数据MDin等信号
  //   中断策略
  //   信号模拟
  //   Reset 
  //   Reset 
  //   Reset 
  //   0是开
endmodule

module \单周期MIPS_多级中断  (
  input  IR1,
  input  IR2,
  input  IR3,
  output RegWrite,
  output MemWrite,
  output [31:0] PC,
  output [31:0] IR,
  output [31:0] RDin,
  output [31:0] MDin,
  output [31:0] LedData
);

  wire and_1_out, and_2_out, and_3_out, and_4_out, and_5_out, and_6_out, and_7_out, and_8_out, and_9_out,
       and_10_out, and_11_out, CLK, comparator_1_eq, comparator_4_eq, comparator_5_eq, comparator_6_eq,
       comparator_7_eq, comparator_8_eq, comparator_9_lt, d_ff_1_q, d_ff_2_q, d_ff_3_q, demultiplexer_1_out1,
       demultiplexer_1_out2, demultiplexer_1_out3, epc_t, ERET, Go, Halt, IE, ie_t, IR1_2_q, IR1_3_q, IR1_q,
       IR1_t, IR2_t, IR3_t, IRA, IRB, IRC, MFC0, mips_alu_1_equal, MTC0, multiplexer_13_out, nand_1_out,
       nor_1_out, not_1_out, not_3_out, not_4_out, or_1_out, or_5_out, or_9_out, or_10_out, or_11_out,
       or_12_out, or_13_out, or_14_out, sig, SignedExt, Syscall, W1, W2, W3, \单周期硬布线控制器_1_alu_src ,
       \单周期硬布线控制器_1_beq , \单周期硬布线控制器_1_bne , \单周期硬布线控制器_1_jal , \单周期硬布线控制器_1_jmp , \单周期硬布线控制器_1_jr ,
       \单周期硬布线控制器_1_memtoreg , \单周期硬布线控制器_1_regdst ;
  wire [0:0] not_2_out;
  wire [1:0] multiplexer_14_out, priority_encoder_1_out, \上一中断号_peak , \当前中断号_q ;
  wire [3:0] \单周期硬布线控制器_1_alu_op ;
  wire [4:0] multiplexer_6_out, multiplexer_7_out, multiplexer_8_out, multiplexer_9_out;
  wire [15:0] \总周期数 ;
  wire [31:0] adder_1_out, adder_2_out, bit_extender_1_out, bit_extender_2_out, bit_extender_3_out,
       controlled_buffer_1_out, EPC, \int , mips_alu_1_result, multiplexer_1_out, multiplexer_2_out,
       multiplexer_3_out, multiplexer_5_out, multiplexer_10_out, multiplexer_11_out, multiplexer_12_out,
       ram_1_data, shifter_1_out, v0;

  Clock #(.highDuration(1), .lowDuration(1)) clock_1 (.out(CLK));
  Button _1 ();  // open: out
  Button _2 ();  // open: out
  Button _3 ();  // open: out
  Button \u_继续运行  (.out(Go));
  LED #(.active("true")) led_1 (.in(W1));
  LED #(.active("true")) led_2 (.in(W2));
  LED #(.active("true")) led_3 (.in(W3));
  and and_1 (and_1_out, \单周期硬布线控制器_1_jmp , ~\单周期硬布线控制器_1_jr );  // AND_Gate
  assign controlled_buffer_1_out = and_1_out ? {PC[31:28], IR[25:0], 2'b00} : 32'bz;  // Controlled_Buffer controlled_buffer_1
  nor nor_1 (nor_1_out, or_5_out, \单周期硬布线控制器_1_jmp );
  assign controlled_buffer_1_out = \单周期硬布线控制器_1_jr  ? v0 : 32'bz;  // Controlled_Buffer controlled_buffer_2
  assign controlled_buffer_1_out = or_5_out ? adder_2_out : 32'bz;  // Controlled_Buffer controlled_buffer_3
  assign controlled_buffer_1_out = nor_1_out ? adder_1_out : 32'bz;  // Controlled_Buffer controlled_buffer_4
  Hex_Digit_Display hex_digit_display_1 (.value(LedData[31:28]));  // open: dp
  // Probe on controlled_buffer_1_out
  Multiplexer #(.select(1), .width(32), .disabled("Z"), .enable("false")) multiplexer_1 (
    .in0(controlled_buffer_1_out), .in1(\int ), .out(multiplexer_1_out), .sel(sig));
  Hex_Digit_Display hex_digit_display_2 (.value(LedData[27:24]));  // open: dp
  Hex_Digit_Display hex_digit_display_3 (.value(LedData[23:20]));  // open: dp
  and and_2 (and_2_out, MTC0, epc_t);
  Multiplexer #(.select(1), .width(32), .disabled("Z"), .enable("false")) multiplexer_2 (
    .in0(multiplexer_1_out), .in1(EPC), .out(multiplexer_2_out), .sel(ERET));
  not not_1 (not_1_out, Halt);
  Hex_Digit_Display hex_digit_display_4 (.value(LedData[19:16]));  // open: dp
  Hex_Digit_Display hex_digit_display_5 (.value(LedData[15:12]));  // open: dp
  Comparator #(.width(32), .mode("twosComplement")) comparator_1 (
    .a(v0), .b(32'h22), .eq(comparator_1_eq));  // open: gt, lt
  Multiplexer #(.select(1), .width(32), .disabled("Z"), .enable("false")) multiplexer_3 (
    .in0(controlled_buffer_1_out), .in1(MDin), .out(multiplexer_3_out), .sel(and_2_out));
  Register #(.width(32), .trigger("rising"), .Select("low")) u_PC (
    .D(multiplexer_2_out), .en(not_1_out), .Q(PC), .clk(CLK));  // open: clr
  Hex_Digit_Display hex_digit_display_6 (.value(LedData[7:4]));  // open: dp
  Hex_Digit_Display hex_digit_display_7 (.value(LedData[11:8]));  // open: dp
  // Probe on \总周期数 
  Register #(.width(32), .trigger("rising"), .Select("low")) register_1 (
    .D(MDin), .en(comparator_1_eq), .Q(LedData), .clk(CLK));  // open: clr
  and and_3 (and_3_out, ~comparator_1_eq, Syscall);  // AND_Gate
  Register #(.width(32), .trigger("rising"), .Select("low")) u_EPC (
    .D(multiplexer_3_out), .en(or_1_out), .Q(EPC), .clk(CLK));  // open: clr
  or or_1 (or_1_out, and_2_out, sig);
  Comparator #(.width(5), .mode("twosComplement")) comparator_2 (
    .a(IR[15:11]), .b(5'b01100), .eq(ie_t));  // open: gt, lt
  Comparator #(.width(5), .mode("twosComplement")) comparator_3 (
    .a(IR[15:11]), .b(5'b01110), .eq(epc_t));  // open: gt, lt
  Hex_Digit_Display hex_digit_display_8 (.value(LedData[3:0]));  // open: dp
  Register #(.width(1), .trigger("rising"), .Select("low")) register_2 (
    .D(and_3_out), .en(and_3_out), .Q(Halt), .clk(CLK), .clr(Go));
  // Mips_Probe mips_probe_1: pin names not known; wires that end beside it: PC[11:2], IR
  ROM #(.addrWidth(10), .dataWidth(32), .Select("high")) rom_1 (.addr(PC[11:2]), .data(IR));
  // Probe on IR[15:11]
  Adder #(.width(32)) adder_1 (.a(PC), .b(32'h4), .out(adder_1_out));  // open: cin, cout
  assign bit_extender_1_out = {{31{1'b0}}, IE};  // Bit_Extender bit_extender_1
  Multiplexer #(.select(2), .width(32), .disabled("Z"), .enable("false")) multiplexer_4 (
    .in0(adder_1_out), .in1(multiplexer_12_out), .in2(multiplexer_5_out), .in3(multiplexer_5_out),
    .out(RDin), .sel({MFC0, not_2_out[0]}));
  Multiplexer #(.select(1), .width(32), .disabled("Z"), .enable("false")) multiplexer_5 (
    .in0(EPC), .in1(bit_extender_1_out), .out(multiplexer_5_out), .sel(and_4_out));
  and and_4 (and_4_out, MFC0, ie_t);
  or or_2 (IR1_t, IR1, IRA);
  \单周期硬布线控制器  \u_单周期硬布线控制器_1  (
    .Func(IR[5:0]), .OP(IR[31:26]), .ALU_OP(\单周期硬布线控制器_1_alu_op ), .MemToReg(\单周期硬布线控制器_1_memtoreg ),
    .MemWrite(MemWrite), .ALU_SRC(\单周期硬布线控制器_1_alu_src ), .RegWrite(RegWrite), .SysCALL(Syscall),
    .SignedExt(SignedExt), .RegDst(\单周期硬布线控制器_1_regdst ), .JR(\单周期硬布线控制器_1_jr ), .JMP(\单周期硬布线控制器_1_jmp ),
    .Beq(\单周期硬布线控制器_1_beq ), .JAL(\单周期硬布线控制器_1_jal ), .Bne(\单周期硬布线控制器_1_bne ), .MF(IR[25:21]), .ERET(ERET),
    .MFC0(MFC0), .MTC0(MTC0));  // open: BLEZ, LUI, LH
  Multiplexer #(.select(1), .width(5), .disabled("Z"), .enable("false")) multiplexer_6 (
    .in0(IR[25:21]), .in1(5'b00010), .out(multiplexer_6_out), .sel(Syscall));
  Multiplexer #(.select(1), .width(5), .disabled("Z"), .enable("false")) multiplexer_7 (
    .in0(IR[20:16]), .in1(5'b00100), .out(multiplexer_7_out), .sel(Syscall));
  not not_2 (not_2_out[0], \单周期硬布线控制器_1_jal );
  Multiplexer #(.select(1), .width(5), .disabled("Z"), .enable("false")) multiplexer_8 (
    .in0(IR[20:16]), .in1(IR[15:11]), .out(multiplexer_8_out), .sel(\单周期硬布线控制器_1_regdst ));
  assign bit_extender_2_out = {{16{1'b0}}, IR[15:0]};  // Bit_Extender bit_extender_2
  or or_3 (IR2_t, IR2, IRB);
  // Probe on \总周期数 
  // Probe on PC
  // Probe on multiplexer_9_out
  Multiplexer #(.select(1), .width(5), .disabled("Z"), .enable("false")) multiplexer_9 (
    .in0(multiplexer_8_out), .in1({5{1'b1}}), .out(multiplexer_9_out), .sel(\单周期硬布线控制器_1_jal ));
  // Probe on IR
  assign bit_extender_3_out = {{16{IR[15]}}, IR[15:0]};  // Bit_Extender bit_extender_3
  or or_4 (IR3_t, IR3, IRC);
  or or_5 (or_5_out, and_6_out, and_5_out);
  MIPS_Regifile mips_regifile_1 (
    .Din(RDin), .Clk(CLK), .R1(v0), .R2(MDin), .WE(RegWrite), .W_num(multiplexer_9_out),
    .R1_num(multiplexer_6_out), .R2_num(multiplexer_7_out));
  Multiplexer #(.select(1), .width(32), .disabled("Z"), .enable("false")) multiplexer_10 (
    .in0(bit_extender_2_out), .in1(bit_extender_3_out), .out(multiplexer_10_out), .sel(SignedExt));
  and and_5 (and_5_out, mips_alu_1_equal, \单周期硬布线控制器_1_beq );
  Multiplexer #(.select(1), .width(32), .disabled("Z"), .enable("false")) multiplexer_11 (
    .in0(MDin), .in1(multiplexer_10_out), .out(multiplexer_11_out), .sel(\单周期硬布线控制器_1_alu_src ));
  Shifter #(.width(32), .shift("ll")) shifter_1 (.in(multiplexer_10_out), .\dist (5'b00010), .out(shifter_1_out));
  MIPS_ALU mips_alu_1 (
    .X(v0), .Y(multiplexer_11_out), .AluOP(\单周期硬布线控制器_1_alu_op ), .Equal(mips_alu_1_equal),
    .Result(mips_alu_1_result), .shamt(IR[10:6]));  // open: Result_2
  and and_6 (and_6_out, ~mips_alu_1_equal, \单周期硬布线控制器_1_bne );  // AND_Gate
  Adder #(.width(32)) adder_2 (.a(shifter_1_out), .b(adder_1_out), .out(adder_2_out));  // open: cin, cout
  not not_3 (not_3_out, Halt);
  Counter #(.width(16), .max('hffff), .ongoal("wrap"), .trigger("rising"), .behavior("old")) counter_1 (
    .Q(\总周期数 ), .clk(and_7_out));  // open: load, D, count, carry, clr, preset
  and and_7 (and_7_out, ~Halt, CLK);  // AND_Gate
  RAM #(.addrWidth(10), .dataWidth(32), .bus("separate"), .Select("high")) ram_1 (
    .addr(mips_alu_1_result[11:2]), .din(MDin), .data(ram_1_data), .str(MemWrite), .sel(not_3_out), .clk(CLK));  // open: ld, clr
  Multiplexer #(.select(1), .width(32), .disabled("Z"), .enable("false")) multiplexer_12 (
    .in0(mips_alu_1_result), .in1(ram_1_data), .out(multiplexer_12_out), .sel(\单周期硬布线控制器_1_memtoreg ));
  D_Flip_Flop #(.trigger("rising"), .Pre_Clr_Positions("LEGACY"), .NegatePresetClear("false"), .enable("true"), .NewFFLayout("false")) d_ff_1 (
    .clk(IR1_t), .D(1'b1), .Q(d_ff_1_q), .reset(IR1_q));  // open: Qn, preset, en
  or or_6 (W1, IR1_q, d_ff_1_q);
  D_Flip_Flop #(.trigger("rising"), .Pre_Clr_Positions("LEGACY"), .NegatePresetClear("false"), .enable("true"), .NewFFLayout("false")) d_ff_2 (
    .clk(IR2_t), .D(1'b1), .Q(d_ff_2_q), .reset(IR1_2_q));  // open: Qn, preset, en
  or or_7 (W2, IR1_2_q, d_ff_2_q);
  D_Flip_Flop #(.trigger("rising"), .Pre_Clr_Positions("LEGACY"), .NegatePresetClear("false"), .enable("true"), .NewFFLayout("false")) d_ff_3 (
    .clk(IR3_t), .D(1'b1), .Q(d_ff_3_q), .reset(IR1_3_q));  // open: Qn, preset, en
  or or_8 (W3, IR1_3_q, d_ff_3_q);
  or or_9 (or_9_out, d_ff_1_q, IR1_q);
  and and_8 (and_8_out, or_9_out, ~demultiplexer_1_out1);  // AND_Gate
  or or_10 (or_10_out, d_ff_2_q, IR1_2_q);
  and and_9 (and_9_out, or_10_out, ~demultiplexer_1_out2);  // AND_Gate
  or or_11 (or_11_out, d_ff_3_q, IR1_3_q);
  and and_10 (and_10_out, or_11_out, ~demultiplexer_1_out3);  // AND_Gate
  and and_11 (and_11_out, MTC0, ie_t);
  Comparator #(.width(16), .mode("twosComplement")) comparator_4 (
    .a(16'h258), .b(\总周期数 ), .eq(comparator_4_eq));  // open: gt, lt
  Comparator #(.width(16), .mode("twosComplement")) comparator_5 (
    .a(\总周期数 ), .b(16'h1), .eq(comparator_5_eq));  // open: gt, lt
  Comparator #(.width(16), .mode("twosComplement")) comparator_6 (
    .a(\总周期数 ), .b(16'h4), .eq(comparator_6_eq));  // open: gt, lt
  Comparator #(.width(16), .mode("twosComplement")) comparator_7 (
    .a(\总周期数 ), .b(16'h7), .eq(comparator_7_eq));  // open: gt, lt
  or or_12 (or_12_out, comparator_7_eq, comparator_8_eq);
  Comparator #(.width(16), .mode("twosComplement")) comparator_8 (
    .a(\总周期数 ), .b(16'h241), .eq(comparator_8_eq));  // open: gt, lt
  D_Flip_Flop #(.trigger("rising"), .Pre_Clr_Positions("LEGACY"), .NegatePresetClear("false"), .enable("true"), .NewFFLayout("false")) u_IR1 (
    .clk(CLK), .D(and_8_out), .Q(IR1_q));  // open: Qn, preset, en, reset
  D_Flip_Flop #(.trigger("rising"), .Pre_Clr_Positions("LEGACY"), .NegatePresetClear("false"), .enable("true"), .NewFFLayout("false")) IR1_2 (
    .clk(CLK), .D(and_9_out), .Q(IR1_2_q));  // open: Qn, preset, en, reset
  D_Flip_Flop #(.trigger("rising"), .Pre_Clr_Positions("LEGACY"), .NegatePresetClear("false"), .enable("true"), .NewFFLayout("false")) IR1_3 (
    .clk(CLK), .D(and_10_out), .Q(IR1_3_q));  // open: Qn, preset, en, reset
  Multiplexer #(.select(1), .width(1), .disabled("Z"), .enable("false")) multiplexer_13 (
    .in0(comparator_9_lt), .in1(MDin[0]), .out(multiplexer_13_out), .sel(and_11_out));
  or or_13 (or_13_out, comparator_4_eq, comparator_5_eq);
  Pull_Resistor #(.pull(0)) pull_resistor_1 (.node(IRA));
  assign IRA = or_13_out ? ~CLK : 1'bz;  // Controlled_Inverter controlled_inverter_1
  Pull_Resistor #(.pull(0)) pull_resistor_2 (.node(IRB));
  assign IRB = comparator_6_eq ? ~CLK : 1'bz;  // Controlled_Inverter controlled_inverter_2
  Pull_Resistor #(.pull(0)) pull_resistor_3 (.node(IRC));
  assign IRC = or_12_out ? ~CLK : 1'bz;  // Controlled_Inverter controlled_inverter_3
  not not_4 (not_4_out, IE);
  nand nand_1 (nand_1_out, ~and_11_out, IE);  // NAND_Gate
  or or_14 (or_14_out, not_4_out, ERET);
  Priority_Encoder #(.select(2), .disabled("Z")) priority_encoder_1 (
    .in0(1'b1), .in1(IR1_q), .in2(IR1_2_q), .in3(IR1_3_q), .out(priority_encoder_1_out));  // open: gs, en_out, en_in
  Register #(.width(1), .trigger("rising"), .Select("low")) u_IE (
    .D(multiplexer_13_out), .en(nand_1_out), .Q(IE), .clk(CLK), .clr(ERET));
  Multiplexer #(.select(1), .width(2), .disabled("Z"), .enable("false")) multiplexer_14 (
    .in0(priority_encoder_1_out), .in1(\上一中断号_peak ), .out(multiplexer_14_out), .sel(ERET));
  Demultiplexer #(.select(2), .width(1), .tristate("false"), .disabled("Z"), .enable("false")) demultiplexer_1 (
    .out1(demultiplexer_1_out1), .out2(demultiplexer_1_out2), .out3(demultiplexer_1_out3), .in(ERET),
    .sel(\当前中断号_q ));  // open: out0
  Multiplexer #(.select(2), .width(32), .disabled("Z"), .enable("false")) multiplexer_15 (
    .in1(32'h30ac), .in2(32'h3174), .in3(32'h323c), .out(\int ), .sel(priority_encoder_1_out));  // open: in0
  Register #(.width(2), .trigger("rising"), .Select("low")) \u_当前中断号  (
    .D(multiplexer_14_out), .en(or_14_out), .Q(\当前中断号_q ), .clk(CLK));  // open: clr
  // Probe on priority_encoder_1_out
  and and_12 (sig, ~IE, comparator_9_lt);  // AND_Gate
  \中断栈  \u_上一中断号  (.ir(\当前中断号_q ), .clk(CLK), .sig(sig), .eret(ERET), .peak(\上一中断号_peak ));
  Comparator #(.width(2), .mode("unsigned")) comparator_9 (
    .a(\当前中断号_q ), .b(priority_encoder_1_out), .lt(comparator_9_lt));  // open: gt, eq
  // Probe on \上一中断号_peak 

  // Other names for the same wires on the sheet: a0[31:0] = MDin

  // Notes on the sheet:
  //   中断源
  //   中断等待指示
  //   总复位信号应将除ROM以外所有存储组件全部清零
  //   停机策略
  //   JAL/J
  //   JR
  //   Branch
  //   next
  //   数码管输出
  //   数码管输出应该用寄存器锁存，否则显示数据只能一闪而过
  //   指令存储器
  //   指令字
  //   contents of rom_1 (hex, n*v repeats v):
  //   201d07d0 20100001 109fc0 139fc3 8021 2012000c 24160008 26100001 3210000f 20080008 20090001 139900
  //   2709825 132020 20020022 c 1094022 1500fff9 22100001 2018000f 2188024 108700 20080008 20090001 139902
  //   2709825 132021 20020022 c 1094022 1500fff9 108702 2c9b022 12c00001 8000c07 4020 1084027 84400
  //   3508ffff 82021 20020022 c 8000c01 afa20000 23bd0004 afa40000 23bd0004 afb00000 23bd0004 afb30000
  //   23bd0004 afb40000 23bd0004 afb50000 23bd0004 afb60000 23bd0004 40000000 20160001 20140003 20150001
  //   168020 108100 2149825 132020 20020022 c 1600fffa 295a022 1680fff7 40800000 23bdfffc 8fb60000
  //   23bdfffc 8fb50000 23bdfffc 8fb40000 23bdfffc 8fb30000 23bdfffc 8fb00000 23bdfffc 8fa40000 23bdfffc
  //   8fa20000 42000018 afa20000 23bd0004 afa40000 23bd0004 afb00000 23bd0004 afb30000 23bd0004 afb40000
  //   23bd0004 afb50000 23bd0004 afb60000 23bd0004 40000000 20160002 20140003 20150001 168020 108100
  //   2149825 132020 20020022 c 1600fffa 295a022 1680fff7 40800000 23bdfffc 8fb60000 23bdfffc 8fb50000
  //   23bdfffc 8fb40000 23bdfffc 8fb30000 23bdfffc 8fb00000 23bdfffc 8fa40000 23bdfffc 8fa20000 42000018
  //   afa20000 23bd0004 afa40000 23bd0004 afb00000 23bd0004 afb30000 23bd0004 afb40000 23bd0004 afb50000
  //   23bd0004 afb60000 23bd0004 40000000 20160003 20140003 20150001 168020 108100 2149825 132020 20020022
  //   c 1600fffa 295a022 1680fff7 40800000 23bdfffc 8fb60000 23bdfffc 8fb50000 23bdfffc 8fb40000 23bdfffc
  //   8fb30000 23bdfffc 8fb00000 23bdfffc 8fa40000 23bdfffc 8fa20000 42000018 1680fff7 20160001 40966000
  //   23bdfffc 8fb60000 40967000 23bdfffc 8fb60000 23bdfffc 8fb50000 23bdfffc 8fb40000 23bdfffc 8fb30000
  //   23bdfffc 8fb00000 23bdfffc 8fa40000 23bdfffc 8fa20000 42000018
  //   JMP
  //   JR
  //   OP
  //   Func
  //   MF
  //   Syscall
  //   rs
  //   rt
  //   rd
  //   立即数
  //   Beq
  //   Bne
  //   MemToReg
  //   MemWrite
  //   AluOP
  //   AluSrcB
  //   RegWrite
  //   JAL
  //   RegDst
  //   PC+4
  //   为方便自动评测，需要输出PC，IR，寄存器堆写如数据RDin
  //   RAM写使能MemWrite、RAM写入数据MDin等信号
  //   中断策略
  //   rt
  //   信号模拟
  //   Reset 
  //   Reset 
  //   Reset 
  //   0是开
endmodule

module \气泡流水单级中断  (
  output RegWrite,
  output MemWrite,
  output [31:0] IF_PC,
  output [31:0] ID_PC,
  output [31:0] EX_PC,
  output [31:0] M_PC,
  output [31:0] WB_PC,
  output [31:0] RDin,
  output [31:0] MDin,
  output [31:0] LedData
);

  wire and_1_out, and_2_out, and_3_out, and_4_out, and_5_out, and_6_out, and_7_out, and_8_out, and_9_out,
       and_10_out, and_11_out, and_12_out, and_13_out, and_14_out, and_15_out, and_16_out, and_17_out,
       and_18_out, and_19_out, and_20_out, clear, CLK, comparator_1_eq, comparator_2_eq, comparator_3_eq,
       comparator_4_eq, comparator_5_eq, comparator_6_eq, d_ff_1_q, d_ff_2_q, d_ff_3_q, decoder_1_out1,
       decoder_1_out2, decoder_1_out3, e, ERET, eret_q, ex_mem_1_halt_2, ex_mem_1_halt_3, ex_mem_1_lh_3,
       ex_mem_1_memtoreg_2, ex_mem_1_regwrite_2, Go, Halt, id_ex_1_alusrcb_2, id_ex_1_beq_2, id_ex_1_bne_2,
       id_ex_1_eret_4, id_ex_1_jal_2, id_ex_1_lh_2, id_ex_1_memtoreg_2, id_ex_1_memwrite_2,
       id_ex_1_regwrite_2, IE, IR1, IR1_2_q, IR1_3_q, IR1_q, IR2, IR3, JMP, JR, mem_wb_1_jal_2,
       mem_wb_1_lh_2, mem_wb_1_memtoreg_2, mips_alu_1_equal, nor_1_out, nor_2_out, not_1_out, not_2_out,
       not_3_out, not_4_out, or_1_out, or_2_out, or_3_out, or_4_out, or_6_out, or_13_out, or_14_out,
       or_15_out, or_16_out, or_17_out, or_18_out, pause, pause1_q, pause2_q, register_1_q, RST, s, sig,
       sig1_q, sig2_q, Signed, Syscall, W1, W2, W3, \单周期硬布线控制器_1_alu_src , \单周期硬布线控制器_1_beq ,
       \单周期硬布线控制器_1_bne , \单周期硬布线控制器_1_eret , \单周期硬布线控制器_1_jal , \单周期硬布线控制器_1_jmp , \单周期硬布线控制器_1_jr ,
       \单周期硬布线控制器_1_lh , \单周期硬布线控制器_1_memtoreg , \单周期硬布线控制器_1_memwrite , \单周期硬布线控制器_1_regdst ,
       \单周期硬布线控制器_1_regwrite , \单周期硬布线控制器_1_syscall , \数据相关检测逻辑_1_pause , \数据相关检测逻辑_2_pause ;
  wire [1:0] priority_encoder_1_out, register_3_q;
  wire [3:0] id_ex_1_aluop_2, \单周期硬布线控制器_1_alu_op ;
  wire [4:0] ex_mem_1_w_num_2, id_ex_1_shamt_2, id_ex_1_w_num_2, multiplexer_3_out, multiplexer_5_out,
       multiplexer_6_out, multiplexer_7_out, W_num;
  wire [9:0] mem_wb_1_addr_2;
  wire [15:0] \LoadUse次数 , multiplexer_13_out, \总周期数 , \插入气泡数 , \无条件分支数 , \条件分支成功数 ;
  wire [27:2] id_ex_1__26_2;
  wire [31:0] a0, adder_1_out, adder_2_out, adder_3_out, adder_4_out, adder_5_out, bit_extender_1_out,
       bit_extender_2_out, bit_extender_3_out, controlled_buffer_1_out, EPC_q, EX_IR, ex_mem_1_alu_2,
       ex_mem_1_lh_4, id_ex_1_imm_2, ID_IR, IF_IR, \int , MEM_IR, mem_wb_1_alu_2, mem_wb_1_md_2,
       mips_alu_1_result, multiplexer_1_out, multiplexer_2_out, multiplexer_8_out, multiplexer_9_out,
       multiplexer_10_out, multiplexer_11_out, multiplexer_12_out, ram_1_data, shifter_1_out,
       subtractor_1_out, v0, WB_IR, \下降沿regifile_1_r1 , \下降沿regifile_1_r2 ;

  Button \u_总复位  (.out(RST));
  Button _1 ();  // open: out
  Button _2 ();  // open: out
  Button _3 ();  // open: out
  // Probe on \总周期数 
  // Probe on \总周期数 
  Button \u_继续运行  (.out(Go));
  LED #(.active("true")) led_1 (.in(W1));
  LED #(.active("true")) led_2 (.in(W2));
  LED #(.active("true")) led_3 (.in(W3));
  and and_1 (and_1_out, ~Halt, CLK);  // AND_Gate
  and and_2 (and_2_out, JMP, ~JR);  // AND_Gate
  assign controlled_buffer_1_out = and_2_out ? {EX_PC[31:28], id_ex_1__26_2, 2'b00} : 32'bz;  // Controlled_Buffer controlled_buffer_1
  nor nor_1 (nor_1_out, or_2_out, JMP);
  assign controlled_buffer_1_out = JR ? v0 : 32'bz;  // Controlled_Buffer controlled_buffer_2
  assign controlled_buffer_1_out = or_2_out ? adder_1_out : 32'bz;  // Controlled_Buffer controlled_buffer_3
  assign controlled_buffer_1_out = nor_1_out ? adder_2_out : 32'bz;  // Controlled_Buffer controlled_buffer_4
  Hex_Digit_Display hex_digit_display_1 (.value(LedData[31:28]));  // open: dp
  // Probe on IF_PC[19:0]
  // Mips_Probe mips_probe_1: pin names not known; wires that end beside it: IR1, IR2, IR3, IF_IR
  Counter #(.width(16), .max('hffff), .ongoal("wrap"), .trigger("rising"), .behavior("old")) counter_1 (
    .Q(\总周期数 ), .clk(and_1_out));  // open: load, D, count, carry, clr, preset
  // Probe on multiplexer_2_out
  Subtractor #(.width(32)) subtractor_1 (
    .a(controlled_buffer_1_out), .b(32'h4), .out(subtractor_1_out));  // open: bin, bout
  Register #(.width(32), .trigger("rising"), .Select("low")) EPC (
    .D(subtractor_1_out), .en(s), .Q(EPC_q), .clk(CLK));  // open: clr
  Multiplexer #(.select(1), .width(32), .disabled("Z"), .enable("false")) multiplexer_1 (
    .in0(controlled_buffer_1_out), .in1(\int ), .out(multiplexer_1_out), .sel(sig));
  Hex_Digit_Display hex_digit_display_2 (.value(LedData[23:20]));  // open: dp
  Hex_Digit_Display hex_digit_display_3 (.value(LedData[27:24]));  // open: dp
  // Probe on ID_PC[19:0]
  // Mips_Probe mips_probe_2: pin names not known; wires that end beside it: ID_IR
  Register #(.width(32), .trigger("rising"), .Select("low")) PC (
    .D(multiplexer_2_out), .en(not_1_out), .Q(IF_PC), .clk(CLK));  // open: clr
  not not_1 (not_1_out, or_1_out);
  or or_1 (or_1_out, Halt, pause);
  Multiplexer #(.select(1), .width(32), .disabled("Z"), .enable("false")) multiplexer_2 (
    .in0(multiplexer_1_out), .in1(EPC_q), .out(multiplexer_2_out), .sel(ERET));
  Adder #(.width(32)) adder_1 (.a(adder_5_out), .b(32'h4), .out(adder_1_out));  // open: cin, cout
  Hex_Digit_Display hex_digit_display_4 (.value(LedData[15:12]));  // open: dp
  Hex_Digit_Display hex_digit_display_5 (.value(LedData[19:16]));  // open: dp
  Adder #(.width(32)) adder_2 (.a(IF_PC), .b(32'h4), .out(adder_2_out));  // open: cin, cout
  Hex_Digit_Display hex_digit_display_6 (.value(LedData[11:8]));  // open: dp
  Hex_Digit_Display hex_digit_display_7 (.value(LedData[7:4]));  // open: dp
  Clock #(.highDuration(1), .lowDuration(1)) clock_1 (.out(CLK));
  // Probe on EX_PC[19:0]
  // Mips_Probe mips_probe_3: pin names not known; wires that end beside it: EX_IR
  ROM #(.addrWidth(10), .dataWidth(32), .Select("high")) rom_1 (.addr(IF_PC[11:2]), .data(IF_IR));
  Hex_Digit_Display hex_digit_display_8 (.value(LedData[3:0]));  // open: dp
  // Mips_Probe mips_probe_4: pin names not known; wires that end beside it: IF_IR
  IF_ID if_id_1 (
    .IR(IF_IR), .IR_2(ID_IR), .PC_4(IF_PC), .PC_4_2(ID_PC), .CLK(CLK), .\同步清零_高电平有效 (clear),
    .\使能端_低电平有效 (pause));
  // Probe on \总周期数 
  // Probe on M_PC[19:0]
  // Mips_Probe mips_probe_5: pin names not known; wires that end beside it: MEM_IR
  Multiplexer #(.select(1), .width(5), .disabled("Z"), .enable("false")) multiplexer_3 (
    .in0(ID_IR[20:16]), .in1(ID_IR[15:11]), .out(multiplexer_3_out), .sel(\单周期硬布线控制器_1_regdst ));
  Multiplexer #(.select(1), .width(32), .disabled("Z"), .enable("false")) multiplexer_4 (
    .in0(adder_3_out), .in1(multiplexer_12_out), .out(RDin), .sel(not_2_out));
  Adder #(.width(32)) adder_3 (.a(WB_PC), .b(32'h4), .out(adder_3_out));  // open: cin, cout
  // Probe on \总周期数 
  // Probe on \无条件分支数 
  // Probe on \条件分支成功数 
  // Probe on \插入气泡数 
  // Probe on \LoadUse次数 
  \单周期硬布线控制器  \u_单周期硬布线控制器_1  (
    .Func(ID_IR[5:0]), .OP(ID_IR[31:26]), .ALU_OP(\单周期硬布线控制器_1_alu_op ), .MemToReg(\单周期硬布线控制器_1_memtoreg ),
    .MemWrite(\单周期硬布线控制器_1_memwrite ), .ALU_SRC(\单周期硬布线控制器_1_alu_src ), .RegWrite(\单周期硬布线控制器_1_regwrite ),
    .SysCALL(\单周期硬布线控制器_1_syscall ), .SignedExt(Signed), .RegDst(\单周期硬布线控制器_1_regdst ),
    .JR(\单周期硬布线控制器_1_jr ), .JMP(\单周期硬布线控制器_1_jmp ), .Beq(\单周期硬布线控制器_1_beq ), .JAL(\单周期硬布线控制器_1_jal ),
    .Bne(\单周期硬布线控制器_1_bne ), .LH(\单周期硬布线控制器_1_lh ), .MF(ID_IR[25:21]), .ERET(\单周期硬布线控制器_1_eret ));  // open: BLEZ, LUI, MFC0, MTC0
  Multiplexer #(.select(1), .width(5), .disabled("Z"), .enable("false")) multiplexer_5 (
    .in0(ID_IR[25:21]), .in1(5'b00010), .out(multiplexer_5_out), .sel(\单周期硬布线控制器_1_syscall ));
  Multiplexer #(.select(1), .width(5), .disabled("Z"), .enable("false")) multiplexer_6 (
    .in0(ID_IR[20:16]), .in1(5'b00100), .out(multiplexer_6_out), .sel(\单周期硬布线控制器_1_syscall ));
  assign bit_extender_1_out = {{16{1'b0}}, ID_IR[15:0]};  // Bit_Extender bit_extender_1
  not not_2 (not_2_out, mem_wb_1_jal_2);
  // Probe on IF_PC[11:0]
  // Probe on WB_PC[19:0]
  // Mips_Probe mips_probe_6: pin names not known; wires that end beside it: WB_IR
  Multiplexer #(.select(1), .width(5), .disabled("Z"), .enable("false")) multiplexer_7 (
    .in0(multiplexer_3_out), .in1({5{1'b1}}), .out(multiplexer_7_out), .sel(\单周期硬布线控制器_1_jal ));
  assign bit_extender_2_out = {{16{ID_IR[15]}}, ID_IR[15:0]};  // Bit_Extender bit_extender_2
  // Probe on ID_PC[11:0]
  // Probe on EX_PC[11:0]
  Multiplexer #(.select(1), .width(32), .disabled("Z"), .enable("false")) multiplexer_8 (
    .in0(bit_extender_1_out), .in1(bit_extender_2_out), .out(multiplexer_8_out), .sel(Signed));
  // Probe on M_PC[11:0]
  or or_2 (or_2_out, and_7_out, and_5_out);
  ID_EX id_ex_1 (
    .LH(\单周期硬布线控制器_1_lh ), .LH_2(id_ex_1_lh_2), .RegWrite(\单周期硬布线控制器_1_regwrite ),
    .RegWrite_2(id_ex_1_regwrite_2), .W_num(multiplexer_7_out), .W_num_2(id_ex_1_w_num_2),
    .MemToReg(\单周期硬布线控制器_1_memtoreg ), .MemToReg_2(id_ex_1_memtoreg_2), .MemWrite(\单周期硬布线控制器_1_memwrite ),
    .MemWrite_2(id_ex_1_memwrite_2), .AluOP(\单周期硬布线控制器_1_alu_op ), .AluOP_2(id_ex_1_aluop_2),
    .AluSrcB(\单周期硬布线控制器_1_alu_src ), .R1(\下降沿regifile_1_r1 ), .R1_2(v0), .R2(\下降沿regifile_1_r2 ), .R2_2(a0),
    .Imm(multiplexer_8_out), .Imm_2(id_ex_1_imm_2), .PC_4(ID_PC), .PC_4_2(EX_PC), .IR(ID_IR), .IR_2(EX_IR),
    .CLK(CLK), .\同步清零_高电平有效 (or_3_out), .Beq(\单周期硬布线控制器_1_beq ), .Beq_2(id_ex_1_beq_2),
    .Bne(\单周期硬布线控制器_1_bne ), .Bne_2(id_ex_1_bne_2), .JAL(\单周期硬布线控制器_1_jal ), .JAL_2(id_ex_1_jal_2),
    .Shamt(ID_IR[10:6]), .Shamt_2(id_ex_1_shamt_2), .JR(\单周期硬布线控制器_1_jr ), .JR_2(JR),
    .JMP(\单周期硬布线控制器_1_jmp ), .JMP_2(JMP), ._26(ID_IR[25:0]), ._26_2(id_ex_1__26_2),
    .Sys(\单周期硬布线控制器_1_syscall ), .Sys_2(Syscall), .AluSrcB_2(id_ex_1_alusrcb_2), .eret(\单周期硬布线控制器_1_eret ),
    .eret_3(e), .eret_2(s), .eret_4(id_ex_1_eret_4));  // open: 使能端_低电平有效, f1, f1_2, f2, f2_2
  \下降沿Regifile  \u_下降沿regifile_1  (
    .Din(RDin), .Clk(CLK), .R1(\下降沿regifile_1_r1 ), .R2(\下降沿regifile_1_r2 ), .WE(RegWrite), .W_num(W_num),
    .R1_num(multiplexer_5_out), .R2_num(multiplexer_6_out));
  or or_3 (or_3_out, clear, pause);
  // Probe on WB_PC[11:0]
  and and_3 (and_3_out, eret_q, pause1_q);
  and and_4 (and_4_out, pause, e);
  and and_5 (and_5_out, mips_alu_1_equal, id_ex_1_beq_2);
  Multiplexer #(.select(1), .width(32), .disabled("Z"), .enable("false")) multiplexer_9 (
    .in0(a0), .in1(id_ex_1_imm_2), .out(multiplexer_9_out), .sel(id_ex_1_alusrcb_2));
  and and_6 (and_6_out, ~comparator_1_eq, Syscall);  // AND_Gate
  Comparator #(.width(32), .mode("twosComplement")) comparator_1 (
    .a(v0), .b(32'h22), .eq(comparator_1_eq));  // open: gt, lt
  or or_4 (or_4_out, and_3_out, and_4_out);
  Register #(.width(1), .trigger("rising"), .Select("low")) sig1 (
    .D(id_ex_1_eret_4), .Q(sig1_q), .clk(CLK));  // open: en, clr
  MIPS_ALU mips_alu_1 (
    .X(v0), .Y(multiplexer_9_out), .AluOP(id_ex_1_aluop_2), .Equal(mips_alu_1_equal),
    .Result(mips_alu_1_result), .shamt(id_ex_1_shamt_2));  // open: Result_2
  Shifter #(.width(32), .shift("ll")) shifter_1 (.in(id_ex_1_imm_2), .\dist (5'b00010), .out(shifter_1_out));
  Register #(.width(1), .trigger("rising"), .Select("low")) register_1 (
    .D(and_6_out), .en(and_6_out), .Q(register_1_q), .clk(CLK), .clr(Go));
  Register #(.width(32), .trigger("rising"), .Select("low")) register_2 (
    .D(a0), .en(comparator_1_eq), .Q(LedData), .clk(CLK));  // open: clr
  or or_5 (clear, JMP, or_4_out, JR, sig, and_5_out, and_7_out, id_ex_1_jal_2);
  or or_6 (or_6_out, ERET, pause);
  and and_7 (and_7_out, ~mips_alu_1_equal, id_ex_1_bne_2);  // AND_Gate
  Register #(.width(1), .trigger("rising"), .Select("low")) sig2 (
    .D(sig1_q), .Q(sig2_q), .clk(CLK), .preset(sig1_q));  // open: en, clr, cs
  Adder #(.width(32)) adder_4 (.a(v0), .b(id_ex_1_imm_2), .out(adder_4_out));  // open: cin, cout
  Adder #(.width(32)) adder_5 (.a(shifter_1_out), .b(EX_PC), .out(adder_5_out));  // open: cin, cout
  \数据相关检测逻辑  \u_数据相关检测逻辑_1  (.ID_IR(ID_IR), .EX_RW(id_ex_1_regwrite_2), .EX_IR(EX_IR), .pause(\数据相关检测逻辑_1_pause ));
  Register #(.width(1), .trigger("rising"), .Select("low")) u_eret (
    .D(e), .en(or_6_out), .Q(eret_q), .clk(CLK), .preset(e));  // open: clr, cs
  Register #(.width(1), .trigger("rising"), .Select("low")) pause1 (
    .D(pause), .Q(pause1_q), .clk(CLK));  // open: en, clr
  EX_MEM ex_mem_1 (
    .LH(id_ex_1_lh_2), .LH_3(ex_mem_1_lh_3), .RegWrite(id_ex_1_regwrite_2), .RegWrite_2(ex_mem_1_regwrite_2),
    .W_num(id_ex_1_w_num_2), .W_num_2(ex_mem_1_w_num_2), .MemToReg(id_ex_1_memtoreg_2),
    .MemToReg_2(ex_mem_1_memtoreg_2), .MemWrite(id_ex_1_memwrite_2), .MemWrite_2(MemWrite),
    .Halt(register_1_q), .Halt_2(ex_mem_1_halt_2), .LH_2(adder_4_out), .LH_4(ex_mem_1_lh_4),
    .Alu(mips_alu_1_result), .Alu_2(ex_mem_1_alu_2), .R2(a0), .R2_2(MDin), .PC_4(EX_PC), .PC_4_2(M_PC),
    .IR(EX_IR), .IR_2(MEM_IR), .CLK(CLK), .JAL(id_ex_1_jal_2), .Halt_3(ex_mem_1_halt_3));  // open: 同步清零_高电平有效, 使能端_低电平有效
  Multiplexer #(.select(1), .width(32), .disabled("Z"), .enable("false")) multiplexer_10 (
    .in0(ex_mem_1_alu_2), .in1(ex_mem_1_lh_4), .out(multiplexer_10_out), .sel(ex_mem_1_lh_3));
  or or_7 (pause, \数据相关检测逻辑_1_pause , \数据相关检测逻辑_2_pause );
  and and_8 (and_8_out, ~pause, e);  // AND_Gate
  and and_9 (and_9_out, eret_q, pause1_q);
  and and_10 (and_10_out, ~pause, id_ex_1_eret_4);  // AND_Gate
  and and_11 (and_11_out, pause1_q, sig1_q);
  and and_12 (and_12_out, sig2_q, pause2_q);
  // Probe on multiplexer_12_out
  or or_8 (ERET, and_8_out, and_9_out);
  Register #(.width(1), .trigger("rising"), .Select("low")) pause2 (
    .D(pause1_q), .Q(pause2_q), .clk(CLK));  // open: en, clr
  or or_9 (sig, and_10_out, and_11_out, and_12_out);
  not not_3 (not_3_out, Halt);
  or or_10 (W1, IR1_q, d_ff_1_q);
  or or_11 (W2, IR1_2_q, d_ff_2_q);
  or or_12 (W3, IR1_3_q, d_ff_3_q);
  MEM_WB mem_wb_1 (
    .LH(ex_mem_1_lh_3), .LH_2(mem_wb_1_lh_2), .RegWrite(ex_mem_1_regwrite_2), .RegWrite_2(RegWrite),
    .W_num(ex_mem_1_w_num_2), .W_num_2(W_num), .MemToReg(ex_mem_1_memtoreg_2),
    .MemToReg_2(mem_wb_1_memtoreg_2), .Addr(multiplexer_10_out[11:2]), .Addr_2(mem_wb_1_addr_2),
    .Halt(ex_mem_1_halt_2), .Halt_2(Halt), .Alu(ex_mem_1_alu_2), .Alu_2(mem_wb_1_alu_2), .MD(ram_1_data),
    .MD_2(mem_wb_1_md_2), .PC_4(M_PC), .PC_4_2(WB_PC), .IR(MEM_IR), .IR_2(WB_IR), .CLK(CLK),
    .JAL(ex_mem_1_halt_3), .JAL_2(mem_wb_1_jal_2));  // open: 同步清零_高电平有效, 使能端_低电平有效
  RAM #(.addrWidth(10), .dataWidth(32), .bus("separate"), .Select("high")) ram_1 (
    .addr(multiplexer_10_out[11:2]), .din(MDin), .data(ram_1_data), .str(MemWrite), .sel(not_3_out), .clk(CLK));  // open: ld, clr
  \数据相关检测逻辑  \u_数据相关检测逻辑_2  (.ID_IR(ID_IR), .EX_RW(ex_mem_1_regwrite_2), .EX_IR(MEM_IR), .pause(\数据相关检测逻辑_2_pause ));
  D_Flip_Flop #(.trigger("rising"), .Pre_Clr_Positions("LEGACY"), .NegatePresetClear("false"), .enable("true"), .NewFFLayout("false")) d_ff_1 (
    .clk(IR1), .D(1'b1), .Q(d_ff_1_q), .reset(IR1_q));  // open: Qn, preset, en
  D_Flip_Flop #(.trigger("rising"), .Pre_Clr_Positions("LEGACY"), .NegatePresetClear("false"), .enable("true"), .NewFFLayout("false")) d_ff_2 (
    .clk(IR2), .D(1'b1), .Q(d_ff_2_q), .reset(IR1_2_q));  // open: Qn, preset, en
  D_Flip_Flop #(.trigger("rising"), .Pre_Clr_Positions("LEGACY"), .NegatePresetClear("false"), .enable("true"), .NewFFLayout("false")) d_ff_3 (
    .clk(IR3), .D(1'b1), .Q(d_ff_3_q), .reset(IR1_3_q));  // open: Qn, preset, en
  Multiplexer #(.select(1), .width(32), .disabled("Z"), .enable("false")) multiplexer_11 (
    .in0(mem_wb_1_alu_2), .in1(mem_wb_1_md_2), .out(multiplexer_11_out), .sel(mem_wb_1_memtoreg_2));
  Multiplexer #(.select(1), .width(32), .disabled("Z"), .enable("false")) multiplexer_12 (
    .in0(multiplexer_11_out), .in1(bit_extender_3_out), .out(multiplexer_12_out), .sel(mem_wb_1_lh_2));
  or or_13 (or_13_out, d_ff_1_q, IR1_q);
  or or_14 (or_14_out, d_ff_2_q, IR1_2_q);
  or or_15 (or_15_out, d_ff_3_q, IR1_3_q);
  Multiplexer #(.select(1), .width(16), .disabled("Z"), .enable("false")) multiplexer_13 (
    .in0(multiplexer_11_out[15:0]), .in1(multiplexer_11_out[31:16]), .out(multiplexer_13_out),
    .sel(mem_wb_1_addr_2[1]));
  assign bit_extender_3_out = {{16{multiplexer_13_out[15]}}, multiplexer_13_out};  // Bit_Extender bit_extender_3
  and and_13 (and_13_out, or_13_out, ~and_14_out);  // AND_Gate
  and and_14 (and_14_out, decoder_1_out1, ERET);
  and and_15 (and_15_out, or_14_out, ~and_16_out);  // AND_Gate
  and and_16 (and_16_out, decoder_1_out2, ERET);
  and and_17 (and_17_out, or_15_out, ~and_18_out);  // AND_Gate
  and and_18 (and_18_out, ERET, decoder_1_out3);
  D_Flip_Flop #(.trigger("rising"), .Pre_Clr_Positions("LEGACY"), .NegatePresetClear("false"), .enable("true"), .NewFFLayout("false")) u_IR1 (
    .clk(CLK), .D(and_13_out), .Q(IR1_q));  // open: Qn, preset, en, reset
  D_Flip_Flop #(.trigger("rising"), .Pre_Clr_Positions("LEGACY"), .NegatePresetClear("false"), .enable("true"), .NewFFLayout("false")) IR1_2 (
    .clk(CLK), .D(and_15_out), .Q(IR1_2_q));  // open: Qn, preset, en, reset
  D_Flip_Flop #(.trigger("rising"), .Pre_Clr_Positions("LEGACY"), .NegatePresetClear("false"), .enable("true"), .NewFFLayout("false")) IR1_3 (
    .clk(CLK), .D(and_17_out), .Q(IR1_3_q));  // open: Qn, preset, en, reset
  and and_19 (and_19_out, ~pause, or_16_out);  // AND_Gate
  Register #(.width(1), .trigger("rising"), .Select("low")) u_IE (
    .D(and_19_out), .en(not_4_out), .Q(IE), .clk(CLK), .clr(ERET));
  not not_4 (not_4_out, IE);
  Comparator #(.width(16), .mode("twosComplement")) comparator_2 (
    .a(\总周期数 ), .b(16'h555), .eq(comparator_2_eq));  // open: gt, lt
  Comparator #(.width(16), .mode("twosComplement")) comparator_3 (
    .a(\总周期数 ), .b(16'h555), .eq(comparator_3_eq));  // open: gt, lt
  nor nor_2 (nor_2_out, IE, ERET, pause);
  Priority_Encoder #(.select(2), .disabled("Z")) priority_encoder_1 (
    .in0(1'b1), .in1(IR1_q), .in2(IR1_2_q), .in3(IR1_3_q), .out(priority_encoder_1_out));  // open: gs, en_out, en_in
  Multiplexer #(.select(2), .width(32), .disabled("Z"), .enable("false")) multiplexer_14 (
    .in1(32'h30ac), .in2(32'h3150), .in3(32'h31f4), .out(\int ), .sel(priority_encoder_1_out));  // open: in0
  or or_16 (or_16_out, IR1_q, IR1_2_q, IR1_3_q);
  and and_20 (and_20_out, pause, e);
  Comparator #(.width(16), .mode("twosComplement")) comparator_4 (
    .a(16'h555), .b(\总周期数 ), .eq(comparator_4_eq));  // open: gt, lt
  or or_17 (or_17_out, comparator_4_eq, comparator_5_eq);
  Comparator #(.width(16), .mode("twosComplement")) comparator_5 (
    .a(\总周期数 ), .b(16'h5d), .eq(comparator_5_eq));  // open: gt, lt
  Comparator #(.width(16), .mode("twosComplement")) comparator_6 (
    .a(\总周期数 ), .b(16'h6d), .eq(comparator_6_eq));  // open: gt, lt
  or or_18 (or_18_out, comparator_2_eq, comparator_3_eq);
  Register #(.width(2), .trigger("rising"), .Select("low")) register_3 (
    .D(priority_encoder_1_out), .en(nor_2_out), .Q(register_3_q), .clk(CLK));  // open: clr
  and and_21 (s, or_16_out, ~IE, ~ERET, ~and_20_out);  // AND_Gate
  Pull_Resistor #(.pull(0)) pull_resistor_1 (.node(IR1));
  assign IR1 = or_17_out ? ~CLK : 1'bz;  // Controlled_Inverter controlled_inverter_1
  Pull_Resistor #(.pull(0)) pull_resistor_2 (.node(IR2));
  assign IR2 = comparator_6_eq ? ~CLK : 1'bz;  // Controlled_Inverter controlled_inverter_2
  Pull_Resistor #(.pull(0)) pull_resistor_3 (.node(IR3));
  assign IR3 = or_18_out ? ~CLK : 1'bz;  // Controlled_Inverter controlled_inverter_3
  Decoder #(.select(2), .tristate("false"), .disabled("Z"), .enable("false")) decoder_1 (
    .out1(decoder_1_out1), .out2(decoder_1_out2), .out3(decoder_1_out3), .sel(register_3_q));  // open: out0
  // Probe on priority_encoder_1_out

  // Other names for the same wires on the sheet: IR[31:0] = IF_IR; MEM_PC[31:0] = M_PC

  // Notes on the sheet:
  //   中断源
  //   中断等待指示
  //   JAL/J
  //   JR
  //   Branch
  //   next
  //   将立即数左移两位得到28位和当前指令的高4位组成跳转地址
  //   数码管输出
  //   指令存储器
  //   contents of rom_1 (hex, n*v repeats v):
  //   201d07d0 20100001 109fc0 139fc3 8021 2012000c 24160008 26100001 3210000f 20080008 20090001 139900
  //   2709825 132020 20020022 c 1094022 1500fff9 22100001 2018000f 2188024 108700 20080008 20090001 139902
  //   2709825 132021 20020022 c 1094022 1500fff9 108702 2c9b022 12c00001 8000c07 4020 1084027 84400
  //   3508ffff 82021 20020022 c 8000c01 afa20000 23bd0004 afa40000 23bd0004 afb00000 23bd0004 afb30000
  //   23bd0004 afb40000 23bd0004 afb50000 23bd0004 afb60000 23bd0004 20160001 20140003 20150001 168020
  //   108100 2149825 132020 20020022 c 1600fffa 295a022 1680fff7 23bdfffc 8fb60000 23bdfffc 8fb50000
  //   23bdfffc 8fb40000 23bdfffc 8fb30000 23bdfffc 8fb00000 23bdfffc 8fa40000 23bdfffc 8fa20000 42000018
  //   afa20000 23bd0004 afa40000 23bd0004 afb00000 23bd0004 afb30000 23bd0004 afb40000 23bd0004 afb50000
  //   23bd0004 afb60000 23bd0004 20160002 20140003 20150001 168020 108100 2149825 132020 20020022 c
  //   1600fffa 295a022 1680fff7 23bdfffc 8fb60000 23bdfffc 8fb50000 23bdfffc 8fb40000 23bdfffc 8fb30000
  //   23bdfffc 8fb00000 23bdfffc 8fa40000 23bdfffc 8fa20000 42000018 afa20000 23bd0004 afa40000 23bd0004
  //   afb00000 23bd0004 afb30000 23bd0004 afb40000 23bd0004 afb50000 23bd0004 afb60000 23bd0004 20160003
  //   20140003 20150001 168020 108100 2149825 132020 20020022 c 1600fffa 295a022 1680fff7 23bdfffc
  //   8fb60000 23bdfffc 8fb50000 23bdfffc 8fb40000 23bdfffc 8fb30000 23bdfffc 8fb00000 23bdfffc 8fa40000
  //   23bdfffc 8fa20000 42000018
  //   rs
  //   rt
  //   rd
  //   立即数
  //   LH
  //   JMP
  //   JR
  //   OP
  //   Func
  //   MF
  //   Syscall
  //   Beq
  //   Bne
  //   MemToReg
  //   MemWrite
  //   AluOP
  //   AluSrcB
  //   RegWrite
  //   JAL
  //   RegDst
  //   流水调试日志用
  //   中断策略
  //   puase时不能eret
  //   为方便自动评测，需要输出流水线各段保存的PC值，注意是PC不是PC+4，另外ID段寄存器写入信息，Mem段内存写入信息也要输出
  //   中断策略
  //   写回
  //   Reset 
  //   Reset 
  //   Reset 
  //   0是开
  //   信号模拟
  //   s=sig
  //   e=eret
endmodule

// 扩展
module \控制器生成_1  (
  input  OP0,
  input  OP1,
  input  OP2,
  input  OP3,
  input  OP4,
  input  OP5,
  output LUI,
  output LH,
  output BLEZ
);

  wire not_1_out, not_2_out, not_3_out, not_4_out, not_5_out, not_6_out, not_7_out, not_8_out, not_9_out,
       not_10_out;

  not not_1 (not_1_out, OP5);
  not not_2 (not_2_out, OP4);
  not not_3 (not_3_out, OP4);
  not not_4 (not_4_out, OP3);
  not not_5 (not_5_out, OP2);
  not not_6 (not_6_out, OP1);
  not not_7 (not_7_out, OP5);
  not not_8 (not_8_out, OP4);
  not not_9 (not_9_out, OP3);
  not not_10 (not_10_out, OP0);
  and and_1 (LUI, not_1_out, not_2_out, OP3, OP2, OP1, OP0);
  and and_2 (LH, OP5, not_3_out, not_4_out, not_5_out, not_6_out, OP0);
  and and_3 (BLEZ, not_7_out, not_8_out, not_9_out, OP2, OP1, not_10_out);
endmodule

module IF_ID (
  input  [31:0] IR,
  input  [31:0] PC_4,
  input  CLK,
  input  \同步清零_高电平有效 ,
  input  \使能端_低电平有效 ,
  output [31:0] IR_2,
  output [31:0] PC_4_2
);

  wire pull_resistor_2_node;
  wire [31:0] multiplexer_1_out, multiplexer_2_out;

  Multiplexer #(.select(1), .width(32), .disabled("Z"), .enable("false")) multiplexer_1 (
    .in0(IR), .in1({32{1'b0}}), .out(multiplexer_1_out), .sel(\同步清零_高电平有效 ));
  Multiplexer #(.select(1), .width(32), .disabled("Z"), .enable("false")) multiplexer_2 (
    .in0(PC_4), .in1({32{1'b0}}), .out(multiplexer_2_out), .sel(\同步清零_高电平有效 ));
  Pull_Resistor #(.pull(0)) pull_resistor_1 (.node(\同步清零_高电平有效 ));
  Register #(.width(32), .trigger("rising"), .Select("low")) register_1 (
    .D(multiplexer_1_out), .en(pull_resistor_2_node), .Q(IR_2), .clk(CLK));  // open: clr
  Register #(.width(32), .trigger("rising"), .Select("low")) register_2 (
    .D(multiplexer_2_out), .en(pull_resistor_2_node), .Q(PC_4_2), .clk(CLK));  // open: clr
  Pull_Resistor #(.pull(0)) pull_resistor_2 (.node(pull_resistor_2_node));
  not not_1 (pull_resistor_2_node, \使能端_低电平有效 );

  // Notes on the sheet:
  //   同步清零_高电平有效: pull=down
  //   使能端_低电平有效: pull=down
endmodule

module ID_EX (
  input  LH,
  input  RegWrite,
  input  [4:0] W_num,
  input  MemToReg,
  input  Beq,
  input  Bne,
  input  JAL,
  input  [4:0] Shamt,
  input  JR,
  input  JMP,
  input  MemWrite,
  input  [3:0] AluOP,
  input  AluSrcB,
  input  Sys,
  input  eret,
  input  eret_2,
  input  [1:0] f1,
  input  [1:0] f2,
  input  [31:0] R1,
  input  [31:0] R2,
  input  [31:0] Imm,
  input  [31:0] PC_4,
  input  [31:0] IR,
  input  [25:0] _26,
  input  CLK,
  input  \同步清零_高电平有效 ,
  input  \使能端_低电平有效 ,
  output LH_2,
  output RegWrite_2,
  output [4:0] W_num_2,
  output MemToReg_2,
  output Beq_2,
  output Bne_2,
  output JAL_2,
  output [4:0] Shamt_2,
  output JR_2,
  output JMP_2,
  output MemWrite_2,
  output [3:0] AluOP_2,
  output AluSrcB_2,
  output Sys_2,
  output eret_3,
  output eret_4,
  output [1:0] f1_2,
  output [1:0] f2_2,
  output [31:0] R1_2,
  output [31:0] R2_2,
  output [31:0] Imm_2,
  output [31:0] PC_4_2,
  output [31:0] IR_2,
  output [25:0] _26_2
);

  wire multiplexer_1_out, multiplexer_2_out, multiplexer_4_out, multiplexer_5_out, multiplexer_6_out,
       multiplexer_7_out, multiplexer_9_out, multiplexer_10_out, multiplexer_11_out, multiplexer_13_out,
       multiplexer_14_out, multiplexer_15_out, multiplexer_16_out, pull_resistor_2_node;
  wire [1:0] multiplexer_17_out, multiplexer_18_out;
  wire [3:0] multiplexer_12_out;
  wire [4:0] multiplexer_3_out, multiplexer_8_out;
  wire [25:0] multiplexer_24_out;
  wire [31:0] multiplexer_19_out, multiplexer_20_out, multiplexer_21_out, multiplexer_22_out,
       multiplexer_23_out;

  Multiplexer #(.select(1), .width(1), .disabled("Z"), .enable("false")) multiplexer_1 (
    .in0(LH), .in1(1'b0), .out(multiplexer_1_out), .sel(\同步清零_高电平有效 ));
  Multiplexer #(.select(1), .width(1), .disabled("Z"), .enable("false")) multiplexer_2 (
    .in0(RegWrite), .in1(1'b0), .out(multiplexer_2_out), .sel(\同步清零_高电平有效 ));
  Multiplexer #(.select(1), .width(5), .disabled("Z"), .enable("false")) multiplexer_3 (
    .in0(W_num), .in1({5{1'b0}}), .out(multiplexer_3_out), .sel(\同步清零_高电平有效 ));
  Multiplexer #(.select(1), .width(1), .disabled("Z"), .enable("false")) multiplexer_4 (
    .in0(MemToReg), .in1(1'b0), .out(multiplexer_4_out), .sel(\同步清零_高电平有效 ));
  Multiplexer #(.select(1), .width(1), .disabled("Z"), .enable("false")) multiplexer_5 (
    .in0(Beq), .in1(1'b0), .out(multiplexer_5_out), .sel(\同步清零_高电平有效 ));
  Multiplexer #(.select(1), .width(1), .disabled("Z"), .enable("false")) multiplexer_6 (
    .in0(Bne), .in1(1'b0), .out(multiplexer_6_out), .sel(\同步清零_高电平有效 ));
  Multiplexer #(.select(1), .width(1), .disabled("Z"), .enable("false")) multiplexer_7 (
    .in0(JAL), .in1(1'b0), .out(multiplexer_7_out), .sel(\同步清零_高电平有效 ));
  Multiplexer #(.select(1), .width(5), .disabled("Z"), .enable("false")) multiplexer_8 (
    .in0(Shamt), .in1({5{1'b0}}), .out(multiplexer_8_out), .sel(\同步清零_高电平有效 ));
  Multiplexer #(.select(1), .width(1), .disabled("Z"), .enable("false")) multiplexer_9 (
    .in0(JR), .in1(1'b0), .out(multiplexer_9_out), .sel(\同步清零_高电平有效 ));
  Multiplexer #(.select(1), .width(1), .disabled("Z"), .enable("false")) multiplexer_10 (
    .in0(JMP), .in1(1'b0), .out(multiplexer_10_out), .sel(\同步清零_高电平有效 ));
  Multiplexer #(.select(1), .width(1), .disabled("Z"), .enable("false")) multiplexer_11 (
    .in0(MemWrite), .in1(1'b0), .out(multiplexer_11_out), .sel(\同步清零_高电平有效 ));
  Multiplexer #(.select(1), .width(4), .disabled("Z"), .enable("false")) multiplexer_12 (
    .in0(AluOP), .in1(4'b0000), .out(multiplexer_12_out), .sel(\同步清零_高电平有效 ));
  Multiplexer #(.select(1), .width(1), .disabled("Z"), .enable("false")) multiplexer_13 (
    .in0(AluSrcB), .in1(1'b0), .out(multiplexer_13_out), .sel(\同步清零_高电平有效 ));
  Multiplexer #(.select(1), .width(1), .disabled("Z"), .enable("false")) multiplexer_14 (
    .in0(Sys), .in1(1'b0), .out(multiplexer_14_out), .sel(\同步清零_高电平有效 ));
  Multiplexer #(.select(1), .width(1), .disabled("Z"), .enable("false")) multiplexer_15 (
    .in0(eret), .in1(1'b0), .out(multiplexer_15_out), .sel(\同步清零_高电平有效 ));
  Multiplexer #(.select(1), .width(1), .disabled("Z"), .enable("false")) multiplexer_16 (
    .in0(eret_2), .in1(1'b0), .out(multiplexer_16_out), .sel(\同步清零_高电平有效 ));
  Multiplexer #(.select(1), .width(2), .disabled("Z"), .enable("false")) multiplexer_17 (
    .in0(f1), .in1(2'b00), .out(multiplexer_17_out), .sel(\同步清零_高电平有效 ));
  Multiplexer #(.select(1), .width(2), .disabled("Z"), .enable("false")) multiplexer_18 (
    .in0(f2), .in1(2'b00), .out(multiplexer_18_out), .sel(\同步清零_高电平有效 ));
  Multiplexer #(.select(1), .width(32), .disabled("Z"), .enable("false")) multiplexer_19 (
    .in0(R1), .in1({32{1'b0}}), .out(multiplexer_19_out), .sel(\同步清零_高电平有效 ));
  Multiplexer #(.select(1), .width(32), .disabled("Z"), .enable("false")) multiplexer_20 (
    .in0(R2), .in1({32{1'b0}}), .out(multiplexer_20_out), .sel(\同步清零_高电平有效 ));
  Multiplexer #(.select(1), .width(32), .disabled("Z"), .enable("false")) multiplexer_21 (
    .in0(Imm), .in1({32{1'b0}}), .out(multiplexer_21_out), .sel(\同步清零_高电平有效 ));
  Multiplexer #(.select(1), .width(32), .disabled("Z"), .enable("false")) multiplexer_22 (
    .in0(PC_4), .in1({32{1'b0}}), .out(multiplexer_22_out), .sel(\同步清零_高电平有效 ));
  Multiplexer #(.select(1), .width(32), .disabled("Z"), .enable("false")) multiplexer_23 (
    .in0(IR), .in1({32{1'b0}}), .out(multiplexer_23_out), .sel(\同步清零_高电平有效 ));
  Multiplexer #(.select(1), .width(26), .disabled("Z"), .enable("false")) multiplexer_24 (
    .in0(_26), .in1({26{1'b0}}), .out(multiplexer_24_out), .sel(\同步清零_高电平有效 ));
  Pull_Resistor #(.pull(0)) pull_resistor_1 (.node(\同步清零_高电平有效 ));
  Pull_Resistor #(.pull(0)) pull_resistor_2 (.node(pull_resistor_2_node));
  not not_1 (pull_resistor_2_node, \使能端_低电平有效 );
  Register #(.width(1), .trigger("rising"), .Select("low")) register_1 (
    .D(multiplexer_1_out), .en(pull_resistor_2_node), .Q(LH_2), .clk(CLK));  // open: clr
  Register #(.width(1), .trigger("rising"), .Select("low")) register_2 (
    .D(multiplexer_2_out), .en(pull_resistor_2_node), .Q(RegWrite_2), .clk(CLK));  // open: clr
  Register #(.width(5), .trigger("rising"), .Select("low")) register_3 (
    .D(multiplexer_3_out), .en(pull_resistor_2_node), .Q(W_num_2), .clk(CLK));  // open: clr
  Register #(.width(1), .trigger("rising"), .Select("low")) register_4 (
    .D(multiplexer_4_out), .en(pull_resistor_2_node), .Q(MemToReg_2), .clk(CLK));  // open: clr
  Register #(.width(1), .trigger("rising"), .Select("low")) register_5 (
    .D(multiplexer_5_out), .en(pull_resistor_2_node), .Q(Beq_2), .clk(CLK));  // open: clr
  Register #(.width(1), .trigger("rising"), .Select("low")) register_6 (
    .D(multiplexer_6_out), .en(pull_resistor_2_node), .Q(Bne_2), .clk(CLK));  // open: clr
  Register #(.width(1), .trigger("rising"), .Select("low")) register_7 (
    .D(multiplexer_7_out), .en(pull_resistor_2_node), .Q(JAL_2), .clk(CLK));  // open: clr
  Register #(.width(5), .trigger("rising"), .Select("low")) register_8 (
    .D(multiplexer_8_out), .en(pull_resistor_2_node), .Q(Shamt_2), .clk(CLK));  // open: clr
  Register #(.width(1), .trigger("rising"), .Select("low")) register_9 (
    .D(multiplexer_9_out), .en(pull_resistor_2_node), .Q(JR_2), .clk(CLK));  // open: clr
  Register #(.width(1), .trigger("rising"), .Select("low")) register_10 (
    .D(multiplexer_10_out), .en(pull_resistor_2_node), .Q(JMP_2), .clk(CLK));  // open: clr
  Register #(.width(1), .trigger("rising"), .Select("low")) register_11 (
    .D(multiplexer_11_out), .en(pull_resistor_2_node), .Q(MemWrite_2), .clk(CLK));  // open: clr
  Register #(.width(4), .trigger("rising"), .Select("low")) register_12 (
    .D(multiplexer_12_out), .en(pull_resistor_2_node), .Q(AluOP_2), .clk(CLK));  // open: clr
  Register #(.width(1), .trigger("rising"), .Select("low")) register_13 (
    .D(multiplexer_13_out), .en(pull_resistor_2_node), .Q(AluSrcB_2), .clk(CLK));  // open: clr
  Register #(.width(1), .trigger("rising"), .Select("low")) register_14 (
    .D(multiplexer_14_out), .en(pull_resistor_2_node), .Q(Sys_2), .clk(CLK));  // open: clr
  Register #(.width(1), .trigger("rising"), .Select("low")) register_15 (
    .D(multiplexer_15_out), .en(pull_resistor_2_node), .Q(eret_3), .clk(CLK));  // open: clr
  Register #(.width(1), .trigger("rising"), .Select("low")) register_16 (
    .D(multiplexer_16_out), .en(pull_resistor_2_node), .Q(eret_4), .clk(CLK));  // open: clr
  Register #(.width(2), .trigger("rising"), .Select("low")) register_17 (
    .D(multiplexer_17_out), .en(pull_resistor_2_node), .Q(f1_2), .clk(CLK));  // open: clr
  Register #(.width(2), .trigger("rising"), .Select("low")) register_18 (
    .D(multiplexer_18_out), .en(pull_resistor_2_node), .Q(f2_2), .clk(CLK));  // open: clr
  Register #(.width(32), .trigger("rising"), .Select("low")) register_19 (
    .D(multiplexer_19_out), .en(pull_resistor_2_node), .Q(R1_2), .clk(CLK));  // open: clr
  Register #(.width(32), .trigger("rising"), .Select("low")) register_20 (
    .D(multiplexer_20_out), .en(pull_resistor_2_node), .Q(R2_2), .clk(CLK));  // open: clr
  Register #(.width(32), .trigger("rising"), .Select("low")) register_21 (
    .D(multiplexer_21_out), .en(pull_resistor_2_node), .Q(Imm_2), .clk(CLK));  // open: clr
  Register #(.width(32), .trigger("rising"), .Select("low")) register_22 (
    .D(multiplexer_22_out), .en(pull_resistor_2_node), .Q(PC_4_2), .clk(CLK));  // open: clr
  Register #(.width(32), .trigger("rising"), .Select("low")) register_23 (
    .D(multiplexer_23_out), .en(pull_resistor_2_node), .Q(IR_2), .clk(CLK));  // open: clr
  Register #(.width(26), .trigger("rising"), .Select("low")) register_24 (
    .D(multiplexer_24_out), .en(pull_resistor_2_node), .Q(_26_2), .clk(CLK));  // open: clr

  // Notes on the sheet:
  //   使能端_低电平有效: pull=down
  //   同步清零_高电平有效: pull=down
endmodule

module EX_MEM (
  input  LH,
  input  RegWrite,
  input  [4:0] W_num,
  input  MemToReg,
  input  MemWrite,
  input  Halt,
  input  JAL,
  input  [31:0] LH_2,
  input  [31:0] Alu,
  input  [31:0] R2,
  input  [31:0] PC_4,
  input  [31:0] IR,
  input  CLK,
  input  \同步清零_高电平有效 ,
  input  \使能端_低电平有效 ,
  output LH_3,
  output RegWrite_2,
  output [4:0] W_num_2,
  output MemToReg_2,
  output MemWrite_2,
  output Halt_2,
  output Halt_3,
  output [31:0] LH_4,
  output [31:0] Alu_2,
  output [31:0] R2_2,
  output [31:0] PC_4_2,
  output [31:0] IR_2
);

  wire multiplexer_1_out, multiplexer_2_out, multiplexer_4_out, multiplexer_5_out, multiplexer_6_out,
       multiplexer_7_out, pull_resistor_2_node;
  wire [4:0] multiplexer_3_out;
  wire [31:0] multiplexer_8_out, multiplexer_9_out, multiplexer_10_out, multiplexer_11_out,
       multiplexer_12_out;

  Multiplexer #(.select(1), .width(1), .disabled("Z"), .enable("false")) multiplexer_1 (
    .in0(LH), .in1(1'b0), .out(multiplexer_1_out), .sel(\同步清零_高电平有效 ));
  Multiplexer #(.select(1), .width(1), .disabled("Z"), .enable("false")) multiplexer_2 (
    .in0(RegWrite), .in1(1'b0), .out(multiplexer_2_out), .sel(\同步清零_高电平有效 ));
  Multiplexer #(.select(1), .width(5), .disabled("Z"), .enable("false")) multiplexer_3 (
    .in0(W_num), .in1({5{1'b0}}), .out(multiplexer_3_out), .sel(\同步清零_高电平有效 ));
  Multiplexer #(.select(1), .width(1), .disabled("Z"), .enable("false")) multiplexer_4 (
    .in0(MemToReg), .in1(1'b0), .out(multiplexer_4_out), .sel(\同步清零_高电平有效 ));
  Multiplexer #(.select(1), .width(1), .disabled("Z"), .enable("false")) multiplexer_5 (
    .in0(MemWrite), .in1(1'b0), .out(multiplexer_5_out), .sel(\同步清零_高电平有效 ));
  Multiplexer #(.select(1), .width(1), .disabled("Z"), .enable("false")) multiplexer_6 (
    .in0(Halt), .in1(1'b0), .out(multiplexer_6_out), .sel(\同步清零_高电平有效 ));
  Multiplexer #(.select(1), .width(1), .disabled("Z"), .enable("false")) multiplexer_7 (
    .in0(JAL), .in1(1'b0), .out(multiplexer_7_out), .sel(\同步清零_高电平有效 ));
  Multiplexer #(.select(1), .width(32), .disabled("Z"), .enable("false")) multiplexer_8 (
    .in0(LH_2), .in1({32{1'b0}}), .out(multiplexer_8_out), .sel(\同步清零_高电平有效 ));
  Multiplexer #(.select(1), .width(32), .disabled("Z"), .enable("false")) multiplexer_9 (
    .in0(Alu), .in1({32{1'b0}}), .out(multiplexer_9_out), .sel(\同步清零_高电平有效 ));
  Multiplexer #(.select(1), .width(32), .disabled("Z"), .enable("false")) multiplexer_10 (
    .in0(R2), .in1({32{1'b0}}), .out(multiplexer_10_out), .sel(\同步清零_高电平有效 ));
  Multiplexer #(.select(1), .width(32), .disabled("Z"), .enable("false")) multiplexer_11 (
    .in0(PC_4), .in1({32{1'b0}}), .out(multiplexer_11_out), .sel(\同步清零_高电平有效 ));
  Multiplexer #(.select(1), .width(32), .disabled("Z"), .enable("false")) multiplexer_12 (
    .in0(IR), .in1({32{1'b0}}), .out(multiplexer_12_out), .sel(\同步清零_高电平有效 ));
  Pull_Resistor #(.pull(0)) pull_resistor_1 (.node(\同步清零_高电平有效 ));
  Pull_Resistor #(.pull(0)) pull_resistor_2 (.node(pull_resistor_2_node));
  not not_1 (pull_resistor_2_node, \使能端_低电平有效 );
  Register #(.width(1), .trigger("rising"), .Select("low")) register_1 (
    .D(multiplexer_1_out), .en(pull_resistor_2_node), .Q(LH_3), .clk(CLK));  // open: clr
  Register #(.width(1), .trigger("rising"), .Select("low")) register_2 (
    .D(multiplexer_2_out), .en(pull_resistor_2_node), .Q(RegWrite_2), .clk(CLK));  // open: clr
  Register #(.width(5), .trigger("rising"), .Select("low")) register_3 (
    .D(multiplexer_3_out), .en(pull_resistor_2_node), .Q(W_num_2), .clk(CLK));  // open: clr
  Register #(.width(1), .trigger("rising"), .Select("low")) register_4 (
    .D(multiplexer_4_out), .en(pull_resistor_2_node), .Q(MemToReg_2), .clk(CLK));  // open: clr
  Register #(.width(1), .trigger("rising"), .Select("low")) register_5 (
    .D(multiplexer_5_out), .en(pull_resistor_2_node), .Q(MemWrite_2), .clk(CLK));  // open: clr
  Register #(.width(1), .trigger("rising"), .Select("low")) register_6 (
    .D(multiplexer_6_out), .en(pull_resistor_2_node), .Q(Halt_2), .clk(CLK));  // open: clr
  Register #(.width(1), .trigger("rising"), .Select("low")) register_7 (
    .D(multiplexer_7_out), .en(pull_resistor_2_node), .Q(Halt_3), .clk(CLK));  // open: clr
  Register #(.width(32), .trigger("rising"), .Select("low")) register_8 (
    .D(multiplexer_8_out), .en(pull_resistor_2_node), .Q(LH_4), .clk(CLK));  // open: clr
  Register #(.width(32), .trigger("rising"), .Select("low")) register_9 (
    .D(multiplexer_9_out), .en(pull_resistor_2_node), .Q(Alu_2), .clk(CLK));  // open: clr
  Register #(.width(32), .trigger("rising"), .Select("low")) register_10 (
    .D(multiplexer_10_out), .en(pull_resistor_2_node), .Q(R2_2), .clk(CLK));  // open: clr
  Register #(.width(32), .trigger("rising"), .Select("low")) register_11 (
    .D(multiplexer_11_out), .en(pull_resistor_2_node), .Q(PC_4_2), .clk(CLK));  // open: clr
  Register #(.width(32), .trigger("rising"), .Select("low")) register_12 (
    .D(multiplexer_12_out), .en(pull_resistor_2_node), .Q(IR_2), .clk(CLK));  // open: clr

  // Notes on the sheet:
  //   使能端_低电平有效: pull=down
  //   同步清零_高电平有效: pull=down
endmodule

module MEM_WB (
  input  LH,
  input  RegWrite,
  input  [4:0] W_num,
  input  MemToReg,
  input  [9:0] Addr,
  input  Halt,
  input  JAL,
  input  [31:0] Alu,
  input  [31:0] MD,
  input  [31:0] PC_4,
  input  [31:0] IR,
  input  CLK,
  input  \同步清零_高电平有效 ,
  input  \使能端_低电平有效 ,
  output LH_2,
  output RegWrite_2,
  output [4:0] W_num_2,
  output MemToReg_2,
  output [9:0] Addr_2,
  output Halt_2,
  output JAL_2,
  output [31:0] Alu_2,
  output [31:0] MD_2,
  output [31:0] PC_4_2,
  output [31:0] IR_2
);

  wire multiplexer_1_out, multiplexer_2_out, multiplexer_4_out, multiplexer_6_out, multiplexer_7_out,
       not_1_out;
  wire [4:0] multiplexer_3_out;
  wire [9:0] multiplexer_5_out;
  wire [31:0] multiplexer_8_out, multiplexer_9_out, multiplexer_10_out, multiplexer_11_out;

  Multiplexer #(.select(1), .width(1), .disabled("Z"), .enable("false")) multiplexer_1 (
    .in0(LH), .in1(1'b0), .out(multiplexer_1_out), .sel(\同步清零_高电平有效 ));
  Multiplexer #(.select(1), .width(1), .disabled("Z"), .enable("false")) multiplexer_2 (
    .in0(RegWrite), .in1(1'b0), .out(multiplexer_2_out), .sel(\同步清零_高电平有效 ));
  Multiplexer #(.select(1), .width(5), .disabled("Z"), .enable("false")) multiplexer_3 (
    .in0(W_num), .in1({5{1'b0}}), .out(multiplexer_3_out), .sel(\同步清零_高电平有效 ));
  Multiplexer #(.select(1), .width(1), .disabled("Z"), .enable("false")) multiplexer_4 (
    .in0(MemToReg), .in1(1'b0), .out(multiplexer_4_out), .sel(\同步清零_高电平有效 ));
  Multiplexer #(.select(1), .width(10), .disabled("Z"), .enable("false")) multiplexer_5 (
    .in0(Addr), .in1({10{1'b0}}), .out(multiplexer_5_out), .sel(\同步清零_高电平有效 ));
  Multiplexer #(.select(1), .width(1), .disabled("Z"), .enable("false")) multiplexer_6 (
    .in0(Halt), .in1(1'b0), .out(multiplexer_6_out), .sel(\同步清零_高电平有效 ));
  Multiplexer #(.select(1), .width(1), .disabled("Z"), .enable("false")) multiplexer_7 (
    .in0(JAL), .in1(1'b0), .out(multiplexer_7_out), .sel(\同步清零_高电平有效 ));
  Multiplexer #(.select(1), .width(32), .disabled("Z"), .enable("false")) multiplexer_8 (
    .in0(Alu), .in1({32{1'b0}}), .out(multiplexer_8_out), .sel(\同步清零_高电平有效 ));
  Multiplexer #(.select(1), .width(32), .disabled("Z"), .enable("false")) multiplexer_9 (
    .in0(MD), .in1({32{1'b0}}), .out(multiplexer_9_out), .sel(\同步清零_高电平有效 ));
  Multiplexer #(.select(1), .width(32), .disabled("Z"), .enable("false")) multiplexer_10 (
    .in0(PC_4), .in1({32{1'b0}}), .out(multiplexer_10_out), .sel(\同步清零_高电平有效 ));
  Multiplexer #(.select(1), .width(32), .disabled("Z"), .enable("false")) multiplexer_11 (
    .in0(IR), .in1({32{1'b0}}), .out(multiplexer_11_out), .sel(\同步清零_高电平有效 ));
  Pull_Resistor #(.pull(0)) pull_resistor_1 (.node(\同步清零_高电平有效 ));
  not not_1 (not_1_out, \使能端_低电平有效 );
  Register #(.width(1), .trigger("rising"), .Select("low")) register_1 (
    .D(multiplexer_1_out), .en(not_1_out), .Q(LH_2), .clk(CLK));  // open: clr
  Register #(.width(1), .trigger("rising"), .Select("low")) register_2 (
    .D(multiplexer_2_out), .en(not_1_out), .Q(RegWrite_2), .clk(CLK));  // open: clr
  Register #(.width(5), .trigger("rising"), .Select("low")) register_3 (
    .D(multiplexer_3_out), .en(not_1_out), .Q(W_num_2), .clk(CLK));  // open: clr
  Register #(.width(1), .trigger("rising"), .Select("low")) register_4 (
    .D(multiplexer_4_out), .en(not_1_out), .Q(MemToReg_2), .clk(CLK));  // open: clr
  Register #(.width(10), .trigger("rising"), .Select("low")) register_5 (
    .D(multiplexer_5_out), .en(not_1_out), .Q(Addr_2), .clk(CLK));  // open: clr
  Register #(.width(1), .trigger("rising"), .Select("low")) register_6 (
    .D(multiplexer_6_out), .en(not_1_out), .Q(Halt_2), .clk(CLK));  // open: clr
  Register #(.width(1), .trigger("rising"), .Select("low")) register_7 (
    .D(multiplexer_7_out), .en(not_1_out), .Q(JAL_2), .clk(CLK));  // open: clr
  Register #(.width(32), .trigger("rising"), .Select("low")) register_8 (
    .D(multiplexer_8_out), .en(not_1_out), .Q(Alu_2), .clk(CLK));  // open: clr
  Register #(.width(32), .trigger("rising"), .Select("low")) register_9 (
    .D(multiplexer_9_out), .en(not_1_out), .Q(MD_2), .clk(CLK));  // open: clr
  Register #(.width(32), .trigger("rising"), .Select("low")) register_10 (
    .D(multiplexer_10_out), .en(not_1_out), .Q(PC_4_2), .clk(CLK));  // open: clr
  Register #(.width(32), .trigger("rising"), .Select("low")) register_11 (
    .D(multiplexer_11_out), .en(not_1_out), .Q(IR_2), .clk(CLK));  // open: clr
  Pull_Resistor #(.pull(0)) pull_resistor_2 (.node(not_1_out));

  // Notes on the sheet:
  //   使能端_低电平有效: pull=down
  //   同步清零_高电平有效: pull=down
endmodule

module \数据相关检测逻辑  (
  input  [31:0] ID_IR,
  input  EX_RW,
  input  [31:0] EX_IR,
  output pause
);

  wire and_7_out, and_8_out, and_9_out, and_10_out, and_11_out, and_12_out, and_13_out, and_14_out,
       and_15_out, and_16_out, and_17_out, and_18_out, comparator_2_eq, comparator_7_eq, comparator_8_eq,
       comparator_9_eq, comparator_10_eq, comparator_15_eq, comparator_16_eq, comparator_17_eq,
       comparator_18_eq, comparator_19_eq, comparator_20_eq, comparator_21_eq, comparator_22_eq,
       comparator_23_eq, comparator_24_eq, comparator_25_eq, comparator_26_eq, comparator_27_eq,
       comparator_28_eq, ex_beq, ex_bne, ex_I, ex_jal, ex_jr, ex_R, ex_rd, ex_rt, ex_sw, ex_sys, id_beq,
       id_bne, id_I, id_jr, id_R, id_rs, id_rt, id_sw, id_sys, nor_1_out, nor_2_out, or_1_out, or_3_out;

  // Mips_Probe mips_probe_1: pin names not known; wires that end beside it: EX_IR
  // Mips_Probe mips_probe_2: pin names not known; wires that end beside it: ID_IR
  Comparator #(.width(6), .mode("twosComplement")) comparator_1 (
    .a(6'b000011), .b(EX_IR[31:26]), .eq(ex_jal));  // open: gt, lt
  Comparator #(.width(6), .mode("twosComplement")) comparator_2 (
    .a(6'b000010), .b(EX_IR[31:26]), .eq(comparator_2_eq));  // open: gt, lt
  Comparator #(.width(6), .mode("twosComplement")) comparator_3 (
    .a(6'b101011), .b(EX_IR[31:26]), .eq(ex_sw));  // open: gt, lt
  Comparator #(.width(6), .mode("twosComplement")) comparator_4 (
    .a(6'b000100), .b(EX_IR[31:26]), .eq(ex_beq));  // open: gt, lt
  Comparator #(.width(6), .mode("twosComplement")) comparator_5 (
    .a(6'b000101), .b(EX_IR[31:26]), .eq(ex_bne));  // open: gt, lt
  Comparator #(.width(6), .mode("twosComplement")) comparator_6 (
    .a({6{1'b0}}), .b(EX_IR[31:26]), .eq(ex_R));  // open: gt, lt
  Comparator #(.width(6), .mode("twosComplement")) comparator_7 (
    .a(6'b001000), .b(EX_IR[5:0]), .eq(comparator_7_eq));  // open: gt, lt
  Comparator #(.width(6), .mode("twosComplement")) comparator_8 (
    .a(EX_IR[5:0]), .b(6'b001100), .eq(comparator_8_eq));  // open: gt, lt
  // Probe on EX_IR[20:16]
  Comparator #(.width(6), .mode("twosComplement")) comparator_9 (
    .a(6'b000011), .b(ID_IR[31:26]), .eq(comparator_9_eq));  // open: gt, lt
  Comparator #(.width(6), .mode("twosComplement")) comparator_10 (
    .a(6'b000010), .b(ID_IR[31:26]), .eq(comparator_10_eq));  // open: gt, lt
  Comparator #(.width(6), .mode("twosComplement")) comparator_11 (
    .a(6'b101011), .b(ID_IR[31:26]), .eq(id_sw));  // open: gt, lt
  Comparator #(.width(6), .mode("twosComplement")) comparator_12 (
    .a(6'b000100), .b(ID_IR[31:26]), .eq(id_beq));  // open: gt, lt
  Comparator #(.width(6), .mode("twosComplement")) comparator_13 (
    .a(6'b000101), .b(ID_IR[31:26]), .eq(id_bne));  // open: gt, lt
  Comparator #(.width(6), .mode("twosComplement")) comparator_14 (
    .a({6{1'b0}}), .b(ID_IR[31:26]), .eq(id_R));  // open: gt, lt
  Comparator #(.width(6), .mode("twosComplement")) comparator_15 (
    .a(6'b001100), .b(ID_IR[5:0]), .eq(comparator_15_eq));  // open: gt, lt
  Comparator #(.width(6), .mode("twosComplement")) comparator_16 (
    .a(ID_IR[5:0]), .b(6'b001000), .eq(comparator_16_eq));  // open: gt, lt
  nor nor_1 (nor_1_out, ex_jal, comparator_2_eq);
  and and_1 (ex_jr, ex_R, comparator_7_eq);
  and and_2 (ex_sys, ex_R, comparator_8_eq);
  nor nor_2 (nor_2_out, comparator_9_eq, comparator_10_eq);
  and and_3 (id_sys, id_R, comparator_15_eq);
  and and_4 (id_jr, id_R, comparator_16_eq);
  and and_5 (id_I, nor_2_out, ~id_R);  // AND_Gate
  Comparator #(.width(5), .mode("twosComplement")) comparator_17 (
    .a({5{1'b0}}), .b(ID_IR[20:16]), .eq(comparator_17_eq));  // open: gt, lt
  Comparator #(.width(5), .mode("twosComplement")) comparator_18 (
    .a(5'b00010), .b(EX_IR[20:16]), .eq(comparator_18_eq));  // open: gt, lt
  Comparator #(.width(5), .mode("twosComplement")) comparator_19 (
    .a(5'b00010), .b(EX_IR[15:11]), .eq(comparator_19_eq));  // open: gt, lt
  Comparator #(.width(5), .mode("twosComplement")) comparator_20 (
    .a(5'b00100), .b(EX_IR[20:16]), .eq(comparator_20_eq));  // open: gt, lt
  Comparator #(.width(5), .mode("twosComplement")) comparator_21 (
    .a(5'b00100), .b(EX_IR[15:11]), .eq(comparator_21_eq));  // open: gt, lt
  and and_6 (ex_I, nor_1_out, ~ex_R);  // AND_Gate
  or or_1 (or_1_out, id_sw, id_beq, id_bne);
  Comparator #(.width(5), .mode("twosComplement")) comparator_22 (
    .a(ID_IR[20:16]), .b(EX_IR[20:16]), .eq(comparator_22_eq));  // open: gt, lt
  Comparator #(.width(5), .mode("twosComplement")) comparator_23 (
    .a(ID_IR[20:16]), .b(EX_IR[15:11]), .eq(comparator_23_eq));  // open: gt, lt
  Comparator #(.width(5), .mode("twosComplement")) comparator_24 (
    .a(ID_IR[25:21]), .b(EX_IR[20:16]), .eq(comparator_24_eq));  // open: gt, lt
  Comparator #(.width(5), .mode("twosComplement")) comparator_25 (
    .a(ID_IR[25:21]), .b(EX_IR[15:11]), .eq(comparator_25_eq));  // open: gt, lt
  and and_7 (and_7_out, id_I, or_1_out);
  and and_8 (and_8_out, ~id_sys, id_R, ~id_jr, ~comparator_17_eq);  // AND_Gate
  Comparator #(.width(5), .mode("twosComplement")) comparator_26 (
    .a({5{1'b0}}), .b(ID_IR[25:21]), .eq(comparator_26_eq));  // open: gt, lt
  and and_9 (and_9_out, ex_rt, id_sys, comparator_18_eq);
  and and_10 (and_10_out, ex_rd, id_sys, comparator_19_eq);
  and and_11 (and_11_out, ex_rt, id_sys, comparator_20_eq);
  and and_12 (and_12_out, ex_rd, id_sys, comparator_21_eq);
  Comparator #(.width(5), .mode("twosComplement")) comparator_27 (
    .a(ID_IR[25:21]), .b({5{1'b1}}), .eq(comparator_27_eq));  // open: gt, lt
  Comparator #(.width(5), .mode("twosComplement")) comparator_28 (
    .a({5{1'b1}}), .b(ID_IR[20:16]), .eq(comparator_28_eq));  // open: gt, lt
  nor nor_3 (ex_rt, ~nor_1_out, ex_sw, ex_beq, ex_bne, ex_R);  // NOR_Gate
  nor nor_4 (ex_rd, ~nor_1_out, ex_I, ex_jr, ex_sys);  // NOR_Gate
  or or_2 (id_rt, and_7_out, and_8_out);
  nor nor_5 (id_rs, ~nor_2_out, id_sys, comparator_26_eq);  // NOR_Gate
  and and_13 (and_13_out, id_rs, comparator_27_eq, ex_jal);
  and and_14 (and_14_out, id_rt, comparator_28_eq, ex_jal);
  and and_15 (and_15_out, ex_rt, comparator_22_eq, id_rt);
  and and_16 (and_16_out, ex_rd, comparator_23_eq, id_rt);
  and and_17 (and_17_out, ex_rt, comparator_24_eq, id_rs);
  and and_18 (and_18_out, ex_rd, comparator_25_eq, id_rs);
  or or_3 (or_3_out, and_9_out, and_10_out, and_11_out, and_12_out, and_13_out, and_14_out, and_15_out, and_16_out, and_17_out, and_18_out);
  and and_19 (pause, EX_RW, or_3_out);

  // Notes on the sheet:
  //   OP
  //   Func
  //   rt
  //   rd
  //   OP
  //   Func
  //   rs
  //   rt
  //   JAL
  //   非J
  //   非J
  //   02 = ex.rt
  //   02 = ex.rd
  //   04 = ex.rt
  //   04 = ex.rd
  //   I型
  //   id.rt = ex.rt
  //   id.rt = ex.rd
  //   id.rs = ex.rt
  //   id.rs = ex.rd
  //   JAL
endmodule
// 重定向硬布线控制器
module \重定向控制器  (
  input  [31:0] IR,
  input  [31:0] mem_ir,
  input  [31:0] ex_ir,
  output [3:0] ALU_OP,
  output MemToReg,
  output MemWrite,
  output ALU_SRC,
  output RegWrite,
  output SysCALL,
  output SignedExt,
  output RegDst,
  output Beq,
  output Bne,
  output JR,
  output JMP,
  output JAL,
  output [1:0] f1,
  output [1:0] f2,
  output load_use
);

  wire and_10_out, and_11_out, and_12_out, and_13_out, and_14_out, and_15_out, and_16_out, and_17_out,
       and_18_out, and_19_out, and_20_out, and_21_out, and_22_out, and_23_out, and_24_out, and_25_out,
       and_26_out, and_27_out, and_28_out, and_29_out, and_30_out, and_31_out, and_32_out, and_33_out,
       and_34_out, and_35_out, and_36_out, and_37_out, and_38_out, and_39_out, comparator_3_eq,
       comparator_8_eq, comparator_9_eq, comparator_12_eq, comparator_17_eq, comparator_18_eq,
       comparator_19_eq, comparator_20_eq, comparator_25_eq, comparator_26_eq, comparator_27_eq,
       comparator_28_eq, comparator_29_eq, comparator_30_eq, comparator_31_eq, comparator_32_eq,
       comparator_33_eq, comparator_34_eq, comparator_35_eq, comparator_36_eq, comparator_37_eq,
       comparator_38_eq, comparator_39_eq, comparator_40_eq, comparator_41_eq, comparator_42_eq,
       comparator_43_eq, comparator_44_eq, comparator_45_eq, comparator_46_eq, comparator_47_eq,
       comparator_48_eq, ex_beq, ex_bne, ex_I, ex_jal, ex_jr, ex_mem, ex_R, ex_rd, ex_rt, ex_sw, ex_sys,
       id_beq, id_bne, id_I, id_jr, id_mem, id_R, id_rs, id_rt, id_sw, id_sys, mem_beq, mem_bne, mem_I,
       mem_jal, mem_jr, mem_R, mem_rd, mem_rt, mem_sw, mem_sys, nor_1_out, nor_2_out, nor_3_out, or_1_out,
       or_3_out, or_4_out, or_5_out, or_6_out;

  // Mips_Probe mips_probe_1: pin names not known; wires that end beside it: IR
  Comparator #(.width(6), .mode("twosComplement")) comparator_1 (
    .a(6'b100011), .b(mem_ir[31:26]), .eq(id_mem));  // open: gt, lt
  Comparator #(.width(6), .mode("twosComplement")) comparator_2 (
    .a(6'b000011), .b(mem_ir[31:26]), .eq(mem_jal));  // open: gt, lt
  Comparator #(.width(6), .mode("twosComplement")) comparator_3 (
    .a(6'b000010), .b(mem_ir[31:26]), .eq(comparator_3_eq));  // open: gt, lt
  Comparator #(.width(6), .mode("twosComplement")) comparator_4 (
    .a(6'b101011), .b(mem_ir[31:26]), .eq(mem_sw));  // open: gt, lt
  Comparator #(.width(6), .mode("twosComplement")) comparator_5 (
    .a(6'b000100), .b(mem_ir[31:26]), .eq(mem_beq));  // open: gt, lt
  Comparator #(.width(6), .mode("twosComplement")) comparator_6 (
    .a(6'b000101), .b(mem_ir[31:26]), .eq(mem_bne));  // open: gt, lt
  Comparator #(.width(6), .mode("twosComplement")) comparator_7 (
    .a({6{1'b0}}), .b(mem_ir[31:26]), .eq(mem_R));  // open: gt, lt
  Comparator #(.width(6), .mode("twosComplement")) comparator_8 (
    .a(6'b001000), .b(mem_ir[5:0]), .eq(comparator_8_eq));  // open: gt, lt
  Comparator #(.width(6), .mode("twosComplement")) comparator_9 (
    .a(mem_ir[5:0]), .b(6'b001100), .eq(comparator_9_eq));  // open: gt, lt
  Comparator #(.width(6), .mode("twosComplement")) comparator_10 (
    .a(6'b100011), .b(ex_ir[31:26]), .eq(ex_mem));  // open: gt, lt
  Comparator #(.width(6), .mode("twosComplement")) comparator_11 (
    .a(6'b000011), .b(ex_ir[31:26]), .eq(ex_jal));  // open: gt, lt
  Comparator #(.width(6), .mode("twosComplement")) comparator_12 (
    .a(6'b000010), .b(ex_ir[31:26]), .eq(comparator_12_eq));  // open: gt, lt
  Comparator #(.width(6), .mode("twosComplement")) comparator_13 (
    .a(6'b101011), .b(ex_ir[31:26]), .eq(ex_sw));  // open: gt, lt
  Comparator #(.width(6), .mode("twosComplement")) comparator_14 (
    .a(6'b000100), .b(ex_ir[31:26]), .eq(ex_beq));  // open: gt, lt
  Comparator #(.width(6), .mode("twosComplement")) comparator_15 (
    .a(6'b000101), .b(ex_ir[31:26]), .eq(ex_bne));  // open: gt, lt
  Comparator #(.width(6), .mode("twosComplement")) comparator_16 (
    .a({6{1'b0}}), .b(ex_ir[31:26]), .eq(ex_R));  // open: gt, lt
  Comparator #(.width(6), .mode("twosComplement")) comparator_17 (
    .a(6'b001000), .b(ex_ir[5:0]), .eq(comparator_17_eq));  // open: gt, lt
  Comparator #(.width(6), .mode("twosComplement")) comparator_18 (
    .a(ex_ir[5:0]), .b(6'b001100), .eq(comparator_18_eq));  // open: gt, lt
  // Probe on ex_ir[15:11]
  \运算控制器自动生成  \u_运算控制器自动生成_1  (
    .OP0(IR[26]), .OP1(IR[27]), .OP2(IR[28]), .OP3(IR[29]), .OP4(IR[30]), .OP5(IR[31]), .F0(IR[0]),
    .F1(IR[1]), .F2(IR[2]), .F3(IR[3]), .F4(IR[4]), .F5(IR[5]), .S0(ALU_OP[0]), .S1(ALU_OP[1]),
    .S2(ALU_OP[2]), .S3(ALU_OP[3]));
  \控制信号自动生成  \u_控制信号自动生成_1  (
    .OP0(IR[26]), .OP1(IR[27]), .OP2(IR[28]), .OP3(IR[29]), .OP4(IR[30]), .OP5(IR[31]), .F0(IR[0]),
    .F1(IR[1]), .F2(IR[2]), .F3(IR[3]), .F4(IR[4]), .F5(IR[5]), .MemToReg(MemToReg), .MemWrite(MemWrite),
    .ALU_SRC(ALU_SRC), .RegWrite(RegWrite), .SysCALL(SysCALL), .SignedExt(SignedExt), .RegDst(RegDst),
    .BEQ(Beq), .BNE(Bne), .JR(JR), .JUMP(JMP), .JAL(JAL));  // open: MF4, MF3, MF2, MF1, MF0, ERET, MFC0, MTC0
  Comparator #(.width(6), .mode("twosComplement")) comparator_19 (
    .a(6'b000011), .b(IR[31:26]), .eq(comparator_19_eq));  // open: gt, lt
  Comparator #(.width(6), .mode("twosComplement")) comparator_20 (
    .a(6'b000010), .b(IR[31:26]), .eq(comparator_20_eq));  // open: gt, lt
  Comparator #(.width(6), .mode("twosComplement")) comparator_21 (
    .a(6'b101011), .b(IR[31:26]), .eq(id_sw));  // open: gt, lt
  Comparator #(.width(6), .mode("twosComplement")) comparator_22 (
    .a(6'b000100), .b(IR[31:26]), .eq(id_beq));  // open: gt, lt
  Comparator #(.width(6), .mode("twosComplement")) comparator_23 (
    .a(6'b000101), .b(IR[31:26]), .eq(id_bne));  // open: gt, lt
  Comparator #(.width(6), .mode("twosComplement")) comparator_24 (
    .a({6{1'b0}}), .b(IR[31:26]), .eq(id_R));  // open: gt, lt
  Comparator #(.width(6), .mode("twosComplement")) comparator_25 (
    .a(6'b001100), .b(IR[5:0]), .eq(comparator_25_eq));  // open: gt, lt
  Comparator #(.width(6), .mode("twosComplement")) comparator_26 (
    .a(IR[5:0]), .b(6'b001000), .eq(comparator_26_eq));  // open: gt, lt
  nor nor_1 (nor_1_out, mem_jal, comparator_3_eq);
  and and_1 (mem_jr, mem_R, comparator_8_eq);
  and and_2 (mem_sys, mem_R, comparator_9_eq);
  nor nor_2 (nor_2_out, ex_jal, comparator_12_eq);
  and and_3 (ex_jr, ex_R, comparator_17_eq);
  and and_4 (ex_sys, ex_R, comparator_18_eq);
  nor nor_3 (nor_3_out, comparator_19_eq, comparator_20_eq);
  and and_5 (id_sys, id_R, comparator_25_eq);
  and and_6 (id_jr, id_R, comparator_26_eq);
  and and_7 (id_I, nor_3_out, ~id_R);  // AND_Gate
  Comparator #(.width(5), .mode("twosComplement")) comparator_27 (
    .a({5{1'b0}}), .b(IR[20:16]), .eq(comparator_27_eq));  // open: gt, lt
  Comparator #(.width(5), .mode("twosComplement")) comparator_28 (
    .a(5'b00010), .b(mem_ir[20:16]), .eq(comparator_28_eq));  // open: gt, lt
  Comparator #(.width(5), .mode("twosComplement")) comparator_29 (
    .a(5'b00010), .b(mem_ir[15:11]), .eq(comparator_29_eq));  // open: gt, lt
  Comparator #(.width(5), .mode("twosComplement")) comparator_30 (
    .a(5'b00100), .b(mem_ir[20:16]), .eq(comparator_30_eq));  // open: gt, lt
  Comparator #(.width(5), .mode("twosComplement")) comparator_31 (
    .a(5'b00100), .b(mem_ir[15:11]), .eq(comparator_31_eq));  // open: gt, lt
  and and_8 (mem_I, nor_1_out, ~mem_R);  // AND_Gate
  Comparator #(.width(5), .mode("twosComplement")) comparator_32 (
    .a(IR[20:16]), .b(mem_ir[20:16]), .eq(comparator_32_eq));  // open: gt, lt
  Comparator #(.width(5), .mode("twosComplement")) comparator_33 (
    .a(IR[20:16]), .b(mem_ir[15:11]), .eq(comparator_33_eq));  // open: gt, lt
  Comparator #(.width(5), .mode("twosComplement")) comparator_34 (
    .a(IR[25:21]), .b(mem_ir[20:16]), .eq(comparator_34_eq));  // open: gt, lt
  Comparator #(.width(5), .mode("twosComplement")) comparator_35 (
    .a(IR[25:21]), .b(mem_ir[15:11]), .eq(comparator_35_eq));  // open: gt, lt
  Comparator #(.width(5), .mode("twosComplement")) comparator_36 (
    .a(5'b00010), .b(ex_ir[20:16]), .eq(comparator_36_eq));  // open: gt, lt
  Comparator #(.width(5), .mode("twosComplement")) comparator_37 (
    .a(5'b00010), .b(ex_ir[15:11]), .eq(comparator_37_eq));  // open: gt, lt
  Comparator #(.width(5), .mode("twosComplement")) comparator_38 (
    .a(5'b00100), .b(ex_ir[20:16]), .eq(comparator_38_eq));  // open: gt, lt
  Comparator #(.width(5), .mode("twosComplement")) comparator_39 (
    .a(5'b00100), .b(ex_ir[15:11]), .eq(comparator_39_eq));  // open: gt, lt
  and and_9 (ex_I, nor_2_out, ~ex_R);  // AND_Gate
  Comparator #(.width(5), .mode("twosComplement")) comparator_40 (
    .a(IR[20:16]), .b(ex_ir[20:16]), .eq(comparator_40_eq));  // open: gt, lt
  Comparator #(.width(5), .mode("twosComplement")) comparator_41 (
    .a(IR[20:16]), .b(ex_ir[15:11]), .eq(comparator_41_eq));  // open: gt, lt
  Comparator #(.width(5), .mode("twosComplement")) comparator_42 (
    .a(IR[25:21]), .b(ex_ir[20:16]), .eq(comparator_42_eq));  // open: gt, lt
  Comparator #(.width(5), .mode("twosComplement")) comparator_43 (
    .a(IR[25:21]), .b(ex_ir[15:11]), .eq(comparator_43_eq));  // open: gt, lt
  or or_1 (or_1_out, id_sw, id_beq, id_bne);
  and and_10 (and_10_out, id_I, or_1_out);
  and and_11 (and_11_out, ~id_sys, id_R, ~id_jr, ~comparator_27_eq);  // AND_Gate
  Comparator #(.width(5), .mode("twosComplement")) comparator_44 (
    .a({5{1'b0}}), .b(IR[25:21]), .eq(comparator_44_eq));  // open: gt, lt
  and and_12 (and_12_out, mem_rt, id_sys, comparator_28_eq);
  and and_13 (and_13_out, mem_rd, id_sys, comparator_29_eq);
  and and_14 (and_14_out, mem_rt, id_sys, comparator_30_eq);
  and and_15 (and_15_out, mem_rd, id_sys, comparator_31_eq);
  Comparator #(.width(5), .mode("twosComplement")) comparator_45 (
    .a(IR[25:21]), .b({5{1'b1}}), .eq(comparator_45_eq));  // open: gt, lt
  Comparator #(.width(5), .mode("twosComplement")) comparator_46 (
    .a({5{1'b1}}), .b(IR[20:16]), .eq(comparator_46_eq));  // open: gt, lt
  nor nor_4 (mem_rt, ~nor_1_out, mem_sw, mem_beq, mem_bne, mem_R);  // NOR_Gate
  nor nor_5 (mem_rd, ~nor_1_out, mem_I, mem_jr, mem_sys);  // NOR_Gate
  and and_16 (and_16_out, mem_rt, comparator_32_eq, id_rt);
  and and_17 (and_17_out, mem_rd, comparator_33_eq, id_rt);
  and and_18 (and_18_out, mem_rt, comparator_34_eq, id_rs);
  and and_19 (and_19_out, mem_rd, comparator_35_eq, id_rs);
  and and_20 (and_20_out, ex_rt, id_sys, comparator_36_eq);
  and and_21 (and_21_out, ex_rd, id_sys, comparator_37_eq);
  and and_22 (and_22_out, ex_rt, id_sys, comparator_38_eq);
  and and_23 (and_23_out, ex_rd, id_sys, comparator_39_eq);
  Comparator #(.width(5), .mode("twosComplement")) comparator_47 (
    .a(IR[25:21]), .b({5{1'b1}}), .eq(comparator_47_eq));  // open: gt, lt
  Comparator #(.width(5), .mode("twosComplement")) comparator_48 (
    .a({5{1'b1}}), .b(IR[20:16]), .eq(comparator_48_eq));  // open: gt, lt
  nor nor_6 (ex_rt, ~nor_2_out, ex_sw, ex_beq, ex_bne, ex_R);  // NOR_Gate
  nor nor_7 (ex_rd, ~nor_2_out, ex_I, ex_jr, ex_sys);  // NOR_Gate
  and and_24 (and_24_out, ex_rt, comparator_40_eq, id_rt);
  and and_25 (and_25_out, ex_rd, comparator_41_eq, id_rt);
  and and_26 (and_26_out, ex_rt, comparator_42_eq, id_rs);
  and and_27 (and_27_out, ex_rd, comparator_43_eq, id_rs);
  or or_2 (id_rt, and_10_out, and_11_out);
  nor nor_8 (id_rs, ~nor_3_out, id_sys, comparator_44_eq);  // NOR_Gate
  and and_28 (and_28_out, id_rs, comparator_45_eq, mem_jal);
  and and_29 (and_29_out, id_rt, comparator_46_eq, mem_jal);
  and and_30 (and_30_out, id_rs, comparator_47_eq, ex_jal);
  and and_31 (and_31_out, id_rt, comparator_48_eq, ex_jal);
  or or_3 (or_3_out, and_12_out, and_13_out, and_28_out, and_18_out, and_19_out);
  or or_4 (or_4_out, and_14_out, and_15_out, and_29_out, and_16_out, and_17_out);
  or or_5 (or_5_out, and_20_out, and_21_out, and_30_out, and_26_out, and_27_out);
  or or_6 (or_6_out, and_22_out, and_23_out, and_31_out, and_24_out, and_25_out);
  and and_32 (and_32_out, or_3_out, ~id_mem);  // AND_Gate
  and and_33 (and_33_out, or_4_out, ~id_mem);  // AND_Gate
  and and_34 (and_34_out, id_mem, and_18_out);
  and and_35 (and_35_out, id_mem, and_16_out);
  and and_36 (and_36_out, or_5_out, ~id_mem);  // AND_Gate
  and and_37 (and_37_out, or_6_out, ~id_mem);  // AND_Gate
  and and_38 (and_38_out, id_mem, and_26_out);
  and and_39 (and_39_out, id_mem, and_24_out);
  or or_7 (load_use, and_38_out, and_39_out);
  Priority_Encoder #(.select(2), .disabled("Z")) priority_encoder_1 (
    .in0(1'b1), .in1(and_32_out), .in2(and_34_out), .in3(and_36_out), .out(f1));  // open: gs, en_out, en_in
  Priority_Encoder #(.select(2), .disabled("Z")) priority_encoder_2 (
    .in0(1'b1), .in1(and_33_out), .in2(and_35_out), .in3(and_37_out), .out(f2));  // open: gs, en_out, en_in

  // Notes on the sheet:
  //   JAL
  //   OP
  //   Func
  //   rt
  //   rd
  //   JAL
  //   OP
  //   Func
  //   rt
  //   rd
  //   OP
  //   Func
  //   rs
  //   rt
  //   非J
  //   非J
  //   id.rt
  //   id.rs
  //   非J
  //   运算器控制器，根据指令生成运算器功能选择信号
  //   02 = mem.rt
  //   02 = mem.rd
  //   04 = mem.rt
  //   04 = mem.rd
  //   02 = ex.rt
  //   02 = ex.rd
  //   04 = ex.rt
  //   04 = ex.rd
  //   I型
  //   id.rt = mem.rt
  //   id.rt = mem.rd
  //   id.rs = mem.rt
  //   id.rs = mem.rd
  //   id.rt = ex.rt
  //   id.rt = ex.rd
  //   id.rs = ex.rt
  //   id.rs = ex.rd
  //   JAL
  //   JAL
  //   load-use
  //   rs.mem.alu
  //   rt.mem.alu
  //   rs.mem.lw
  //   rt.mem.lw
  //   rs.ex.alu
  //   rt.ex.alu
  //   rs.ex.lw
  //   rt.ex.lw
endmodule

module \中断栈  (
  input  [1:0] ir,
  input  clk,
  input  sig,
  input  eret,
  output [1:0] peak
);

  wire and_1_out, and_2_out, and_3_out, decoder_1_out0, decoder_1_out1, decoder_1_out2, or_1_out;
  wire [1:0] counter_1_q, \栈1_q , \栈2_q , \栈3_q ;

  or or_1 (or_1_out, eret, sig);
  Decoder #(.select(2), .tristate("false"), .disabled("Z"), .enable("false")) decoder_1 (
    .out0(decoder_1_out0), .out1(decoder_1_out1), .out2(decoder_1_out2), .sel(counter_1_q));  // open: out3
  Counter #(.width(2), .max('h3), .ongoal("wrap"), .trigger("rising"), .behavior("old")) counter_1 (
    .load(eret), .count(or_1_out), .Q(counter_1_q), .clk(clk));  // open: D, carry, clr, preset
  and and_1 (and_1_out, sig, decoder_1_out0);
  Register #(.width(2), .trigger("rising"), .Select("low")) \u_栈1  (
    .D(ir), .en(and_1_out), .Q(\栈1_q ), .clk(clk));  // open: clr
  and and_2 (and_2_out, sig, decoder_1_out1);
  Register #(.width(2), .trigger("rising"), .Select("low")) \u_栈2  (
    .D(ir), .en(and_2_out), .Q(\栈2_q ), .clk(clk));  // open: clr
  and and_3 (and_3_out, sig, decoder_1_out2);
  Register #(.width(2), .trigger("rising"), .Select("low")) \u_栈3  (
    .D(ir), .en(and_3_out), .Q(\栈3_q ), .clk(clk));  // open: clr
  Multiplexer #(.select(2), .width(2), .disabled("Z"), .enable("false")) multiplexer_1 (
    .in0(2'b00), .in1(\栈1_q ), .in2(\栈2_q ), .in3(\栈3_q ), .out(peak), .sel(counter_1_q));
  // Probe on counter_1_q
endmodule

module \封装正确性测试  (
);

  wire IR1, IR2, IR3, MemW, RegW;
  wire [31:0] EX_PC, ID_PC, IF_PC, IR, LED, MDin, MDinr, MEM_PC, PC, RDin, RDinr, WB_PC;

  \单周期MIPS  \u_单周期mips_1  (
    .RegWrite(RegW), .MemWrite(MemW), .PC(PC), .IR(IR), .RDin(RDin), .MDin(MDin), .LedData(LED));  // open: IR1, IR2, IR3
  \气泡流水线  \u_气泡流水线_1  (
    .RegWrite(RegW), .MemWrite(MemW), .IF_PC(IF_PC), .ID_PC(ID_PC), .EX_PC(EX_PC), .M_PC(MEM_PC),
    .WB_PC(WB_PC), .RDin(RDinr), .MDin(MDinr), .LedData(LED));
  \单周期MIPS_单级中断  \u_单周期mips_单级中断_1  (
    .IR1(IR1), .IR2(IR2), .IR3(IR3), .RegWrite(RegW), .MemWrite(MemW), .PC(PC), .IR(IR), .RDin(RDin),
    .MDin(MDin), .LedData(LED));
  \理想流水线  \u_理想流水线_1  (
    .RegWrite(RegW), .MemWrite(MemW), .IF_PC(IF_PC), .ID_PC(ID_PC), .EX_PC(EX_PC), .M_PC(MEM_PC),
    .WB_PC(WB_PC), .RDin(RDinr), .MDin(MDinr), .LedData(LED));
  \气泡流水线  \u_气泡流水线_2  (
    .RegWrite(RegW), .MemWrite(MemW), .IF_PC(IF_PC), .ID_PC(ID_PC), .EX_PC(EX_PC), .M_PC(MEM_PC),
    .WB_PC(WB_PC), .RDin(RDinr), .MDin(MDinr), .LedData(LED));
  \单周期MIPS_多级中断  \u_单周期mips_多级中断_1  (
    .IR1(IR1), .IR2(IR2), .IR3(IR3), .RegWrite(RegW), .MemWrite(MemW), .PC(PC), .IR(IR), .RDin(RDin),
    .MDin(MDin), .LedData(LED));

  // Notes on the sheet:
  //   单周期封装测试
  //   气泡流水封装测试
  //   单周期+单级中断封装测试
  //   请检查上面封装有无位宽不匹配，引脚标签是否和连接的标签相对应，否则无法在educoder平台上正确测试
  //   理想流水封装测试
  //   重定向流水封装测试
  //   单周期+多级中断封装测试
endmodule
